// Logisim project dunk.circ as structural Verilog: 75 circuits, main circuit main
module main (
);

  wire button_1_out, clock_1_out, control_box_1_clock_out, control_box_1_out_12, control_box_1_reset_out,
       control_unit_1_load, controlled_buffer_1_out, controlled_buffer_2_out, controlled_buffer_3_out,
       controlled_buffer_4_out, instruction_printer_1_clock_out, instruction_printer_1_reset_out,
       io_pins_4_1_out_11, io_pins_4_1_out_12, io_pins_4_1_out_13, io_pins_4_1_out_14, io_pins_4_1_out_15,
       io_pins_4_1_out_16, io_pins_4_1_out_17, io_pins_4_1_out_18, mem_ctrl_1_mem_write,
       mem_ctrl_1_reg_write, pause_out, reset_out, resume_out, toggle_debug_out;
  wire [1:0] mem_ctrl_1_reg_select;
  wire [6:0] instruction_printer_1_ascii_out;
  wire [7:0] input_pins_8_1_out_9;
  wire [11:0] mem_ctrl_1_rom_addr_out;
  wire [15:0] addr_bus_controller_1_addr_bus_out, alu_1_out_6, control_bus_controller_1_control_bus_1,
       control_bus_controller_1_control_bus_2, control_unit_1_addr_bus_out, control_unit_1_control_bus_1_out,
       control_unit_1_control_bus_2_out, control_unit_1_current_instr, control_unit_1_data_bus_out,
       control_unit_1_tmpc_out, control_unit_1_to_pk, data_bus_controller_1_data_bus_out, firmware_data,
       io_pins_4_1_data_bus_out, mem_ctrl_1_data_bus_out, mem_ctrl_1_data_to_mem, mem_ctrl_1_data_to_reg,
       mem_ctrl_1_mem_addr_out, mmio_registers_1_out_7, mmio_registers_1_value_out, ram_1_dout,
       register_unit_1_addr_bus_out, register_unit_1_alu1_out, register_unit_1_alu2_out,
       register_unit_1_data_bus_out, special_registers_1_addr_bus_out, special_registers_1_data_bus_out,
       special_registers_1_offset_out, special_registers_1_program_kounter, special_registers_1_stack_pointer;

  Button pause (.out(pause_out));
  Button resume (.out(resume_out));
  Button reset (.out(reset_out));
  Clock clock_1 (.out(clock_1_out));
  control_box control_box_1 (
    .instr(control_unit_1_current_instr), .clock_in(clock_1_out), .reset_in(reset_out),
    .program_kounter(special_registers_1_program_kounter),
    .control_bus_1(control_bus_controller_1_control_bus_1), .pause(pause_out), .resume(resume_out),
    .clock_out(control_box_1_clock_out), .reset_out(control_box_1_reset_out), .out_12(control_box_1_out_12));  // open: instr_breakpoint, pk_breakpoint
  LED #(.active("false")) led_1 (.in(control_box_1_out_12));
  Button toggle_debug (.out(toggle_debug_out));
  control_bus_controller control_bus_controller_1 (
    .control_1(control_unit_1_control_bus_1_out), .control_2(control_unit_1_control_bus_2_out),
    .clock(control_box_1_clock_out), .reset(control_box_1_reset_out),
    .control_bus_1(control_bus_controller_1_control_bus_1),
    .control_bus_2(control_bus_controller_1_control_bus_2));
  data_bus_controller data_bus_controller_1 (
    .control_bus_2(control_bus_controller_1_control_bus_2), .clock(control_box_1_clock_out),
    .reset(control_box_1_reset_out), .control_bus_1(control_bus_controller_1_control_bus_1),
    .addr_bus_in(addr_bus_controller_1_addr_bus_out), .control_unit_in(control_unit_1_data_bus_out),
    .registers_in(register_unit_1_data_bus_out), .special_registers_in(alu_1_out_6),
    .ALU_in(special_registers_1_data_bus_out), .memory_in(mem_ctrl_1_data_bus_out),
    .io_in(io_pins_4_1_data_bus_out), .data_bus_out(data_bus_controller_1_data_bus_out));
  addr_bus_controller addr_bus_controller_1 (
    .control_bus_1(control_bus_controller_1_control_bus_1),
    .control_bus_2(control_bus_controller_1_control_bus_2), .clock(control_box_1_clock_out),
    .reset(control_box_1_reset_out), .data_bus_in(data_bus_controller_1_data_bus_out),
    .control_unit_in(control_unit_1_addr_bus_out), .registers_in(register_unit_1_addr_bus_out),
    .special_registers_in(special_registers_1_addr_bus_out), .addr_bus_out(addr_bus_controller_1_addr_bus_out));
  instruction_printer instruction_printer_1 (
    .enable(toggle_debug_out), .data_bus(data_bus_controller_1_data_bus_out), .load(control_unit_1_load),
    .clk(control_box_1_clock_out), .reset(control_box_1_reset_out),
    .control_bus_1(control_bus_controller_1_control_bus_1),
    .control_bus_2(control_bus_controller_1_control_bus_2), .pk(special_registers_1_program_kounter),
    .real_addr(mem_ctrl_1_mem_addr_out), .instr(control_unit_1_current_instr),
    .tmpc(control_unit_1_tmpc_out), .ascii_out(instruction_printer_1_ascii_out),
    .clock_out(instruction_printer_1_clock_out), .reset_out(instruction_printer_1_reset_out));
  TTY #(.rows(1)) tty_1 (
    .data(instruction_printer_1_ascii_out), .clk(instruction_printer_1_clock_out),
    .clr(instruction_printer_1_reset_out));  // open: we
  control_unit control_unit_1 (
    .stack_pointer(special_registers_1_stack_pointer), .addr_bus(addr_bus_controller_1_addr_bus_out),
    .control_bus_1(control_bus_controller_1_control_bus_1),
    .control_bus_2(control_bus_controller_1_control_bus_2), .clock(control_box_1_clock_out),
    .reset(control_box_1_reset_out), .RAM_direct(mem_ctrl_1_data_bus_out),
    .data_bus_in(data_bus_controller_1_data_bus_out), .interrupt_pins(input_pins_8_1_out_9),
    .control_bus_1_out(control_unit_1_control_bus_1_out),
    .control_bus_2_out(control_unit_1_control_bus_2_out), .current_instr(control_unit_1_current_instr),
    .tmpc_out(control_unit_1_tmpc_out), .data_bus_out(control_unit_1_data_bus_out),
    .addr_bus_out(control_unit_1_addr_bus_out), .to_pk(control_unit_1_to_pk), .load(control_unit_1_load));
  input_pins_8 input_pins_8_1 (
    .in_8(button_1_out), .out_9(input_pins_8_1_out_9));  // open: in_1, in_2, in_3, in_4, in_5, in_6, in_7
  Button button_1 (.out(button_1_out));
  register_unit register_unit_1 (
    .data_bus_in(data_bus_controller_1_data_bus_out), .clock(control_box_1_clock_out),
    .reset(control_box_1_reset_out), .control_bus_1(control_bus_controller_1_control_bus_1),
    .control_bus_2(control_bus_controller_1_control_bus_2), .data_bus_out(register_unit_1_data_bus_out),
    .addr_bus_out(register_unit_1_addr_bus_out), .alu1_out(register_unit_1_alu1_out),
    .alu2_out(register_unit_1_alu2_out));
  ALU alu_1 (
    .argument1(register_unit_1_alu1_out), .argument2(register_unit_1_alu2_out),
    .clock(control_box_1_clock_out), .reset(control_box_1_reset_out),
    .control_bus(control_bus_controller_1_control_bus_1), .out_6(alu_1_out_6));  // open: out_7
  assign controlled_buffer_1_out = io_pins_4_1_out_12 ? io_pins_4_1_out_11 : 1'bz;  // Controlled_Buffer controlled_buffer_1
  assign controlled_buffer_2_out = io_pins_4_1_out_14 ? io_pins_4_1_out_13 : 1'bz;  // Controlled_Buffer controlled_buffer_2
  assign controlled_buffer_3_out = io_pins_4_1_out_16 ? io_pins_4_1_out_15 : 1'bz;  // Controlled_Buffer controlled_buffer_3
  special_registers special_registers_1 (
    .control_bus_1(control_bus_controller_1_control_bus_1),
    .control_bus_2(control_bus_controller_1_control_bus_2), .temp_register(control_unit_1_to_pk),
    .clock(control_box_1_clock_out), .reset(control_box_1_reset_out),
    .data_bus_in(data_bus_controller_1_data_bus_out), .program_kounter(special_registers_1_program_kounter),
    .data_bus_out(special_registers_1_data_bus_out), .addr_bus_out(special_registers_1_addr_bus_out),
    .stack_pointer(special_registers_1_stack_pointer), .offset_out(special_registers_1_offset_out));  // open: sp_reset_value
  io_pins_4 io_pins_4_1 (
    .in_8(controlled_buffer_3_out), .clock(control_box_1_clock_out), .reset(control_box_1_reset_out),
    .in_9(controlled_buffer_4_out), .control_bus(control_bus_controller_1_control_bus_1),
    .in_6(controlled_buffer_1_out), .data_bus_in(data_bus_controller_1_data_bus_out),
    .in_7(controlled_buffer_2_out), .addr_bus_in(addr_bus_controller_1_addr_bus_out),
    .out_15(io_pins_4_1_out_15), .out_16(io_pins_4_1_out_16), .out_17(io_pins_4_1_out_17),
    .out_18(io_pins_4_1_out_18), .data_bus_out(io_pins_4_1_data_bus_out), .out_11(io_pins_4_1_out_11),
    .out_12(io_pins_4_1_out_12), .out_13(io_pins_4_1_out_13), .out_14(io_pins_4_1_out_14));
  assign controlled_buffer_4_out = io_pins_4_1_out_18 ? io_pins_4_1_out_17 : 1'bz;  // Controlled_Buffer controlled_buffer_4
  mmio_registers mmio_registers_1 (
    .write(mem_ctrl_1_reg_write), .clock(control_box_1_clock_out), .reset(control_box_1_reset_out),
    .data_in(mem_ctrl_1_data_to_reg), .reg_select(mem_ctrl_1_reg_select), .out_7(mmio_registers_1_out_7),
    .value_out(mmio_registers_1_value_out));  // open: out_8, out_9, out_10
  mem_ctrl mem_ctrl_1 (
    .data_bus_in(data_bus_controller_1_data_bus_out), .addr_in(addr_bus_controller_1_addr_bus_out),
    .offset_in(special_registers_1_offset_out), .pk_in(special_registers_1_program_kounter),
    .tmpc_in(control_unit_1_tmpc_out), .sp_in(special_registers_1_stack_pointer), .mem_in(ram_1_dout),
    .rom_in(firmware_data), .mmio_reg_in(mmio_registers_1_value_out),
    .control_bus_1(control_bus_controller_1_control_bus_1),
    .control_bus_2(control_bus_controller_1_control_bus_2), .clock(control_box_1_clock_out),
    .reset(control_box_1_reset_out), .rom_addr_out(mem_ctrl_1_rom_addr_out),
    .reg_select(mem_ctrl_1_reg_select), .data_to_reg(mem_ctrl_1_data_to_reg),
    .reg_write(mem_ctrl_1_reg_write), .data_bus_out(mem_ctrl_1_data_bus_out),
    .data_to_mem(mem_ctrl_1_data_to_mem), .mem_write(mem_ctrl_1_mem_write),
    .mem_addr_out(mem_ctrl_1_mem_addr_out));
  RAM #(.addrWidth(16), .dataWidth(16), .enables("line")) ram_1 (
    .addr(mem_ctrl_1_mem_addr_out), .we(mem_ctrl_1_mem_write), .clk(control_box_1_clock_out),
    .din(mem_ctrl_1_data_to_mem), .dout(ram_1_dout));
  ROM #(.addrWidth(12), .dataWidth(16)) firmware (.addr(mem_ctrl_1_rom_addr_out), .data(firmware_data));
  TTY tty_2 (
    .data(mmio_registers_1_out_7[6:0]), .clk(controlled_buffer_4_out), .clr(control_box_1_reset_out));  // open: we

  // Notes on the sheet:
  //   David's Universal Number Kounter
  //   contents of firmware (hex, n*v repeats v):
  //   f009 f00b f010 f01c f030 f051 f071 f076 f07b 307f 7d 821 fffc 3083 3082 7d 1828 0 1002 f01b 121 fffc
  //   3083 3082 883e 1 f010 7d 25 a 861 7 f023 1 f028 25 61 805d 1 f02b 25 30 805d 821 fffc 3083 3082 7d
  //   1827 927 1002 f040 3e 72 3f 1002 f046 9027 7c f07b 1827 9072 1 f037 1f fffc 30 3083 3082 7d 1078
  //   2127 2061 2006 f050 8127 7c f01c 1 f046 7d 8002 f05f 25 a 2045 2072 8002 f065 9027 7c f07b 9072 1
  //   f057 1f fffc 30 3083 3082 7d 1078 100b f070 104b 30 121 fffc 3083 3082 1 f065 7d 9025 10 7c f030 7d
  //   9025 2 7c f030 7d 25 0 8914 f083 3e 895e 1 f07d 8003 f086 3e 9827 8027 7d ff
endmodule

module instruction_printer (
  input  enable,
  input  load,
  input  clk,
  input  reset,
  input  [15:0] data_bus,
  input  [15:0] pk,
  input  [15:0] real_addr,
  input  [15:0] instr,
  input  [15:0] tmpc,
  input  [15:0] control_bus_1,
  input  [15:0] control_bus_2,
  output [6:0] ascii_out,
  output clock_out,
  output reset_out
);

  wire and_1_out, and_2_out, and_3_out, and_4_out, and_5_out, and_7_out, and_8_out, buffer_1_out,
       buffer_2_out, buffer_3_out, buffer_4_out, buffer_5_out, button_1_out, button_2_out, d_ff_1_q,
       d_ff_2_q, d_ff_3_q, d_ff_4_q, d_ff_5_q, d_ff_6_q, eight_bit_eq_cmp_1_out_3, eight_bit_eq_cmp_2_out_3,
       four_bit_eq_cmp_1_out_3, four_bit_eq_cmp_2_out_3, j_k_ff_1_q, or_1_out, or_2_out, or_3_out, or_4_out,
       or_6_out, or_7_out, or_8_out, parameter_printer_1_done, parameter_printer_2_done,
       parameter_printer_2_nothing_pass_up, parameter_printer_3_nothing_pass_up, pulsey_1_out_2, s_r_ff_1_q,
       sixt_bit_eq_cmp_1_out_3;
  wire [4:0] adder_1_out, and_6_out, register_1_q;
  wire [4:4] not_1_out;
  wire [6:0] or_9_out, or_10_out, parameter_printer_1_out_12, parameter_printer_2_out_12,
       parameter_printer_3_out_12;
  wire [7:0] sixt_bit_gatekeeper_1_out_3, sixt_bit_gatekeeper_1_out_3_2;
  wire [15:0] instr_addr_q, register_2_q, sixt_bit_gatekeeper_2_out_3, sixt_bit_gatekeeper_3_out_3,
       sixt_bit_gatekeeper_4_out_3, subtractor_1_out;
  wire [17:0] rom_1_data;

  or or_1 (or_1_out, enable, button_1_out);
  Button button_1 (.out(button_1_out));
  J_K_Flip_Flop j_k_ff_1 (.J(1'b1), .K(1'b1), .clk(or_1_out), .Q(j_k_ff_1_q));  // open: Qn, preset, reset
  not not_1 (not_1_out[4], j_k_ff_1_q);
  buf buffer_1 (buffer_1_out, not_1_out[4]);
  buf buffer_2 (buffer_2_out, buffer_1_out);
  D_Flip_Flop d_ff_1 (.D(load), .clk(clk), .Q(d_ff_1_q), .reset(reset));  // open: Qn, preset
  Button button_2 (.out(button_2_out));
  buf buffer_3 (buffer_3_out, buffer_2_out);
  buf buffer_4 (buffer_4_out, buffer_3_out);
  buf buffer_5 (buffer_5_out, buffer_4_out);
  and and_1 (and_1_out, buffer_5_out, or_1_out);
  D_Flip_Flop d_ff_2 (.D(d_ff_1_q), .clk(clk), .Q(d_ff_2_q), .reset(reset));  // open: Qn, preset
  or or_2 (or_2_out, button_2_out, and_1_out, or_4_out);
  and and_2 (and_2_out, ~not_1_out[4], or_1_out);  // AND_Gate
  D_Flip_Flop d_ff_3 (.D(d_ff_2_q), .clk(clk), .Q(d_ff_3_q), .reset(reset));  // open: Qn, preset
  and and_3 (and_3_out, or_2_out, not_1_out[4]);
  pulsey pulsey_1 (.in_1(and_3_out), .out_3(clock_out), .out_2(pulsey_1_out_2));
  D_Flip_Flop #(.trigger("falling")) d_ff_4 (.D(d_ff_3_q), .clk(clk), .Q(d_ff_4_q), .reset(reset));  // open: Qn, preset
  and and_4 (and_4_out, ~not_1_out[4], clock_out);  // AND_Gate
  or or_3 (or_3_out, pulsey_1_out_2, reset);
  Register #(.width(5)) register_1 (
    .D(adder_1_out), .en(not_1_out[4]), .clk(clock_out), .Q(register_1_q), .clr(or_6_out));
  or or_4 (or_4_out, d_ff_4_q, d_ff_6_q);
  Register #(.width(16)) instr_addr (.D(pk), .en(d_ff_1_q), .clk(clk), .Q(instr_addr_q), .clr(reset));
  or or_5 (reset_out, or_3_out, and_4_out, and_2_out);
  or or_6 (or_6_out, reset, or_3_out);
  Adder #(.width(5)) adder_1 (.a(register_1_q), .b(5'b00001), .out(adder_1_out));  // open: cin, cout
  Subtractor #(.width(16)) subtractor_1 (.a(real_addr), .b(instr_addr_q), .out(subtractor_1_out));  // open: bin, bout
  sixt_bit_eq_cmp sixt_bit_eq_cmp_1 (.in_1(subtractor_1_out), .in_2(16'h2), .out_3(sixt_bit_eq_cmp_1_out_3));
  ROM #(.addrWidth(13), .dataWidth(18)) rom_1 (.addr({sixt_bit_gatekeeper_1_out_3_2, register_1_q}), .data(rom_1_data));
  sixt_bit_gatekeeper sixt_bit_gatekeeper_1 (
    .in_1(not_1_out[4]), .in_2(instr), .out_3({sixt_bit_gatekeeper_1_out_3, sixt_bit_gatekeeper_1_out_3_2}));
  D_Flip_Flop d_ff_5 (.D(and_5_out), .clk(clk), .Q(d_ff_5_q), .reset(reset));  // open: Qn, preset
  and and_5 (and_5_out, sixt_bit_eq_cmp_1_out_3, or_8_out);
  D_Flip_Flop d_ff_6 (.D(d_ff_5_q), .clk(clk), .Q(d_ff_6_q), .reset(reset));  // open: Qn, preset
  // Probe on rom_1_data
  S_R_Flip_Flop s_r_ff_1 (.Q(s_r_ff_1_q), .reset(or_3_out), .preset(rom_1_data[7]));  // open: S, R, clk, Qn
  sixt_bit_gatekeeper sixt_bit_gatekeeper_2 (
    .in_1(not_1_out[4]), .in_2({sixt_bit_gatekeeper_1_out_3, sixt_bit_gatekeeper_1_out_3_2}),
    .out_3(sixt_bit_gatekeeper_2_out_3));
  assign and_6_out = register_1_q & {5{not_1_out[4]}};  // AND_Gate and_6, 5 bits wide
  sixt_bit_gatekeeper sixt_bit_gatekeeper_3 (.in_1(not_1_out[4]), .in_2(tmpc), .out_3(sixt_bit_gatekeeper_3_out_3));
  Register #(.width(16)) register_2 (.D(data_bus), .en(d_ff_5_q), .clk(clk), .Q(register_2_q), .clr(reset));
  Multiplexer #(.width(7)) multiplexer_1 (.in0(rom_1_data[6:0]), .in1(or_9_out), .out(ascii_out), .sel(s_r_ff_1_q));
  or or_7 (or_7_out, s_r_ff_1_q, rom_1_data[7]);
  // Probe on or_9_out
  sixt_bit_gatekeeper sixt_bit_gatekeeper_4 (
    .in_1(not_1_out[4]), .in_2(register_2_q), .out_3(sixt_bit_gatekeeper_4_out_3));
  or or_8 (or_8_out, and_7_out, and_8_out);
  eight_bit_eq_cmp eight_bit_eq_cmp_1 (.in_1(8'h11), .in_2(control_bus_1[7:0]), .out_3(eight_bit_eq_cmp_1_out_3));
  four_bit_eq_cmp four_bit_eq_cmp_1 (.in_1(control_bus_1[15:12]), .in_2(4'b0000), .out_3(four_bit_eq_cmp_1_out_3));
  assign or_9_out = parameter_printer_1_out_12 | or_10_out;  // OR_Gate or_9, 7 bits wide
  parameter_printer parameter_printer_1 (
    .enable(or_7_out), .counter(and_6_out), .clock(clock_out), .instruction(sixt_bit_gatekeeper_2_out_3),
    .tmpc(sixt_bit_gatekeeper_3_out_3), .tmpd(sixt_bit_gatekeeper_4_out_3), .reset(or_3_out),
    .param_type(rom_1_data[5:0]), .nothing_below(parameter_printer_2_nothing_pass_up),
    .done(parameter_printer_1_done), .out_12(parameter_printer_1_out_12));  // open: prev_done, nothing_pass_up
  assign or_10_out = parameter_printer_2_out_12 | parameter_printer_3_out_12;  // OR_Gate or_10, 7 bits wide
  parameter_printer parameter_printer_2 (
    .prev_done(parameter_printer_1_done), .counter(and_6_out), .clock(clock_out),
    .instruction(sixt_bit_gatekeeper_2_out_3), .tmpc(sixt_bit_gatekeeper_3_out_3),
    .tmpd(sixt_bit_gatekeeper_4_out_3), .reset(or_3_out), .param_type(rom_1_data[11:6]),
    .nothing_below(parameter_printer_3_nothing_pass_up), .done(parameter_printer_2_done),
    .out_12(parameter_printer_2_out_12), .nothing_pass_up(parameter_printer_2_nothing_pass_up));  // open: enable
  parameter_printer parameter_printer_3 (
    .prev_done(parameter_printer_2_done), .counter(and_6_out), .clock(clock_out),
    .instruction(sixt_bit_gatekeeper_2_out_3), .tmpc(sixt_bit_gatekeeper_3_out_3),
    .tmpd(sixt_bit_gatekeeper_4_out_3), .reset(or_3_out), .param_type(rom_1_data[17:12]),
    .out_12(parameter_printer_3_out_12), .nothing_pass_up(parameter_printer_3_nothing_pass_up));  // open: enable, nothing_below, done
  and and_7 (and_7_out, eight_bit_eq_cmp_1_out_3, four_bit_eq_cmp_1_out_3);
  eight_bit_eq_cmp eight_bit_eq_cmp_2 (.in_1(8'h11), .in_2(control_bus_2[7:0]), .out_3(eight_bit_eq_cmp_2_out_3));
  four_bit_eq_cmp four_bit_eq_cmp_2 (.in_1(control_bus_2[15:12]), .in_2(4'b0000), .out_3(four_bit_eq_cmp_2_out_3));
  and and_8 (and_8_out, eight_bit_eq_cmp_2_out_3, four_bit_eq_cmp_2_out_3);

  // Notes on the sheet:
  //   contents of rom_1 (hex, n*v repeats v):
  //   63 68 69 6c 6c 27*0 67 6f 74 6f a0 27*4110 67 6f 74 6f 5f 69 66 5f 7a 65 72 6f a0 19*4402 67 6f 74
  //   6f 5f 69 66 5f 6e 6f 6e 7a 65 72 6f a0 16*4402 67 6f 74 6f 5f 69 66 5f 6e 65 67 61 74 69 76 65 a0
  //   15*4402 67 6f 74 6f 5f 69 66 5f 6e 6f 6e 6e 65 67 61 74 69 76 65 a0 12*4402 67 6f 74 6f 5f 69 66 5f
  //   70 6f 73 69 74 69 76 65 a0 15*4402 67 6f 74 6f 5f 69 66 5f 6e 6f 6e 70 6f 73 69 74 69 76 65 a0
  //   12*4402 67 6f 74 6f 5f 69 66 5f 65 71 75 61 6c a0 18*282 67 6f 74 6f 5f 69 66 5f 75 6e 65 71 75 61
  //   6c a0 16*282 67 6f 74 6f 5f 69 66 5f 6c 65 73 73 a0 19*282 67 6f 74 6f 5f 69 66 5f 67 72 65 61 74 65
  //   72 a0 16*282 67 6f 74 6f 5f 69 66 5f 6c 65 71 a0 20*282 67 6f 74 6f 5f 69 66 5f 67 65 71 a0 20*282
  //   67 6f 74 6f 5f 69 66 5f 65 71 75 61 6c a0 18*602 67 6f 74 6f 5f 69 66 5f 75 6e 65 71 75 61 6c a0
  //   16*602 67 6f 74 6f 5f 69 66 5f 6c 65 73 73 a0 19*602 67 6f 74 6f 5f 69 66 5f 67 72 65 61 74 65 72 a0
  //   16*602 67 6f 74 6f 5f 69 66 5f 6c 65 71 a0 20*602 67 6f 74 6f 5f 69 66 5f 67 65 71 a0 20*602 67 6f
  //   74 6f 5f 69 66 5f 6c 65 73 73 5f 75 6e 73 67 6e a0 13*282 67 6f 74 6f 5f 69 66 5f 67 72 65 61 74 65
  //   72 5f 75 6e 73 67 6e a0 10*282 67 6f 74 6f 5f 69 66 5f 6c 65 71 5f 75 6e 73 67 6e a0 14*282 67 6f 74
  //   6f 5f 69 66 5f 67 65 71 5f 75 6e 73 67 6e a0 14*282 67 6f 74 6f 5f 69 66 5f 65 71 75 61 6c 5f 75 6e
  //   73 67 6e a0 12*602 67 6f 74 6f 5f 69 66 5f 75 6e 65 71 75 61 6c 5f 75 6e 73 67 6e a0 10*602 67 6f 74
  //   6f 5f 69 66 5f 6c 65 73 73 5f 75 6e 73 67 6e a0 13*602 67 6f 74 6f 5f 69 66 5f 67 72 65 61 74 65 72
  //   5f 75 6e 73 67 6e a0 10*602 67 6f 74 6f 5f 69 66 5f 6c 65 71 5f 75 6e 73 67 6e a0 14*602 67 6f 74 6f
  //   5f 69 66 5f 67 65 71 5f 75 6e 73 67 6e a0 14*602 73 77 61 70 a0 27*4282 73 65 74 a0 28*4611 73 65 74
  //   a0 28*4651 73 65 74 a0 28*4291 73 65 74 a0 28*4ad9 73 65 74 a0 28*4391 73 65 74 a0 28*4bd9 73 65 74
  //   a0 28*4402 73 65 74 a0 28*4442 73 65 74 a0 28*4282 73 65 74 a0 28*4ac2 73 65 74 a0 28*4382 73 65 74
  //   a0 28*4bc2 73 65 74 a0 28*4623 73 65 74 a0 28*4063 73 65 74 a0 28*42a3 73 65 74 a0 28*4ee3 73 65 74
  //   a0 28*43a3 73 65 74 a0 28*4fe3 73 65 74 a0 28*4406 73 65 74 a0 28*4446 73 65 74 a0 28*4286 73 65 74
  //   a0 28*4ac6 73 65 74 a0 28*4386 73 65 74 a0 28*4bc6 73 65 74 a0 28*4627 73 65 74 a0 28*4667 73 65 74
  //   a0 28*42a7 73 65 74 a0 28*4ee7 73 65 74 a0 28*43a7 73 65 74 a0 28*4fe7 6e 65 67 a0 28*4102 69 6e 63
  //   a0 28*4102 64 65 63 a0 28*4102 73 67 6e a0 28*4102 6e 6f 74 a0 28*4102 6c 73 68 69 66 74 a0 25*4102
  //   72 73 68 69 66 74 a0 25*4102 6e 65 67 a0 28*4282 69 6e 63 a0 28*4282 64 65 63 a0 28*4282 73 67 6e a0
  //   28*4282 6e 6f 74 a0 28*4282 6c 73 68 69 66 74 a0 25*4282 72 73 68 69 66 74 a0 25*4282 61 64 64 a0
  //   28*4402 73 75 62 a0 28*4402 6d 75 6c a0 28*4402 75 63 6d 70 a0 27*4402 63 6d 70 a0 28*4402 61 6e 64
  //   a0 28*4402 6f 72 a0 29*4402 78 6f 72 a0 28*4402 73 68 69 66 74 a0 26*4402 61 64 64 a0 28*282 73 75
  //   62 a0 28*282 6d 75 6c a0 28*282 75 63 6d 70 a0 27*282 63 6d 70 a0 28*282 61 6e 64 a0 28*282 6f 72 a0
  //   29*282 78 6f 72 a0 28*282 73 68 69 66 74 a0 26*282 61 64 64 a0 28*4282 73 75 62 a0 28*4282 6d 75 6c
  //   a0 28*4282 75 63 6d 70 a0 27*4282 63 6d 70 a0 28*4282 61 6e 64 a0 28*4282 6f 72 a0 29*4282 78 6f 72
  //   a0 28*4282 73 68 69 66 74 a0 26*4282 61 64 64 a0 28*2282 73 75 62 a0 28*2282 6d 75 6c a0 28*2282 75
  //   63 6d 70 a0 27*2282 63 6d 70 a0 28*2282 61 6e 64 a0 28*2282 6f 72 a0 29*2282 78 6f 72 a0 28*2282 73
  //   68 69 66 74 a0 26*2282 70 75 73 68 28*0 70 75 73 68 a0 27*4110 70 75 73 68 a0 27*4101 70 75 73 68 a0
  //   27*4102 70 75 73 68 a0 27*4123 70 75 73 68 a0 27*4106 70 75 73 68 a0 27*4127 70 6f 70 29*0 70 6f 70
  //   a0 28*4111 70 6f 70 a0 28*4102 70 6f 70 a0 28*4123 70 6f 70 a0 28*4106 70 6f 70 a0 28*4127 63 61 6c
  //   6c a0 27*4110 72 65 74 75 72 6e 26*0 70 69 6e 6d 6f 64 65 5f 69 6e 70 75 74 a0 18*4100 70 69 6e 6d
  //   6f 64 65 5f 6f 75 74 70 75 74 a0 17*4100 70 69 6e 6d 6f 64 65 5f 69 6e 70 75 74 a0 18*4102 70 69 6e
  //   6d 6f 64 65 5f 6f 75 74 70 75 74 a0 17*4102 73 65 74 5f 70 69 6e 5f 6c 6f 77 a0 20*4100 73 65 74 5f
  //   70 69 6e 5f 68 69 67 68 a0 19*4100 73 65 74 5f 70 69 6e 5f 6c 6f 77 a0 20*4102 73 65 74 5f 70 69 6e
  //   5f 68 69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
endmodule

module control_unit (
  input  [15:0] RAM_direct,
  input  [15:0] data_bus_in,
  input  [15:0] control_bus_1,
  input  [15:0] control_bus_2,
  input  clock,
  input  reset,
  input  [15:0] stack_pointer,
  input  [15:0] addr_bus,
  input  [7:0] interrupt_pins,
  output [15:0] current_instr,
  output [15:0] tmpc_out,
  output [15:0] data_bus_out,
  output [15:0] addr_bus_out,
  output [15:0] control_bus_1_out,
  output [15:0] to_pk,
  output load,
  output [15:0] control_bus_2_out
);

  wire and_1_out, and_2_out, and_4_out, and_5_out, buffer_1_out, buffer_2_out, buffer_3_out, buffer_4_out,
       button_1_out, comparator_1_gt, comparator_1_lt, d_ff_1_q, eight_bit_eq_cmp_1_out_3,
       eight_bit_eq_cmp_2_out_3, interrupt_queue_1_waiting, nor_1_out, or_1_out, or_4_out, or_5_out,
       or_9_out, register_1_q, register_2_q, register_3_q, sixt_bit_eq_cmp_1_out_3, sixt_bit_eq_cmp_2_out_3,
       sixt_bit_eq_cmp_3_out_3, sixt_bit_eq_cmp_4_out_3, sixt_bit_eq_cmp_5_out_3, sixt_bit_eq_cmp_6_out_3,
       sixt_bit_eq_cmp_7_out_3, sixt_bit_eq_cmp_8_out_3, stacker_1_active, unstacker_2_1_active;
  wire [7:0] interrupt_queue_1_id, multiplexer_2_out;
  wire [15:0] interrupt_table_1_ih_addr, interrupt_table_1_to_data_bus, MAR_q,
       microcode_mixer_1_microcode_out, microcode_mixer_2_microcode_out, multiplexer_1_out,
       multiplexer_3_out, multiplexer_4_out, or_6_out, or_7_out, or_8_out, rom_1_data, rom_2_data,
       rom_3_data, shifter_1_out, shifter_2_out, sixt_bit_gatekeeper_1_out_3, sixt_bit_gatekeeper_2_out_3,
       sixt_bit_gatekeeper_3_out_3, sixt_bit_gatekeeper_4_out_3, sixt_bit_gatekeeper_5_out_3,
       sixt_bit_incrementer_1_out_2, stacker_1_change_mask, stacker_1_control_bus_1_out,
       stacker_1_control_bus_2_out, stacker_1_to_data_bus, temp_registers_1_data_bus_out,
       temp_registers_1_out_9, temp_registers_1_out_11, temp_registers_1_to_sreg,
       unstacker_2_1_control_bus_1_out, unstacker_2_1_control_bus_2_out;
  wire [31:0] tick_counter_1_cycle_count, tick_counter_1_negedge_count;

  Button button_1 (.out(button_1_out));
  sixt_bit_eq_cmp sixt_bit_eq_cmp_1 (.in_1(16'h1), .in_2(rom_2_data), .out_3(sixt_bit_eq_cmp_1_out_3));
  and and_1 (and_1_out, clock, ~sixt_bit_eq_cmp_2_out_3, ~or_1_out);  // AND_Gate
  or or_1 (or_1_out, button_1_out, reset);
  Multiplexer #(.width(16)) multiplexer_1 (.in0(data_bus_in), .in1(16'hfe), .out(multiplexer_1_out), .sel(and_2_out));
  Register #(.trigger("falling"), .width(16)) instr (
    .D(multiplexer_1_out), .en(sixt_bit_eq_cmp_1_out_3), .clk(and_1_out), .Q(current_instr), .clr(or_1_out));
  ROM #(.dataWidth(16)) rom_1 (.addr(multiplexer_2_out), .data(rom_1_data));
  Multiplexer #(.width(8)) multiplexer_2 (
    .in0(data_bus_in[7:0]), .in1(8'hfe), .out(multiplexer_2_out), .sel(and_2_out));
  interrupt_queue interrupt_queue_1 (
    .next_ir(and_4_out), .pins_in(interrupt_pins), .reset(or_1_out), .waiting(interrupt_queue_1_waiting),
    .id(interrupt_queue_1_id));
  // Probe on tmpc_out
  // Probe on temp_registers_1_out_9
  // Probe on temp_registers_1_out_11
  temp_registers temp_registers_1 (
    .clock(and_1_out), .reset(or_1_out), .control_bus_1(control_bus_1), .control_bus_2(control_bus_2),
    .data_bus_in(data_bus_in), .ram_direct(RAM_direct), .out_9(temp_registers_1_out_9),
    .out_11(temp_registers_1_out_11), .out_12(tmpc_out), .data_bus_out(temp_registers_1_data_bus_out),
    .to_sreg(temp_registers_1_to_sreg), .addr_bus_out(addr_bus_out));
  Register #(.width(1)) register_1 (
    .D(interrupt_queue_1_waiting), .clk(and_1_out), .Q(register_1_q), .clr(or_1_out));  // open: en
  sixt_bit_eq_cmp sixt_bit_eq_cmp_2 (.in_1(current_instr), .in_2(16'hff), .out_3(sixt_bit_eq_cmp_2_out_3));
  interrupt_table interrupt_table_1 (
    .control_bus_1(control_bus_1), .control_bus_2(control_bus_2), .id(interrupt_queue_1_id),
    .data_in(data_bus_in), .clk(and_1_out), .reset(or_1_out), .ih_addr(interrupt_table_1_ih_addr),
    .to_data_bus(interrupt_table_1_to_data_bus));
  sixt_bit_gatekeeper sixt_bit_gatekeeper_1 (
    .in_1(register_2_q), .in_2(interrupt_table_1_ih_addr), .out_3(sixt_bit_gatekeeper_1_out_3));
  and and_2 (and_2_out, sixt_bit_eq_cmp_3_out_3, interrupt_queue_1_waiting);
  assign data_bus_out = stacker_1_to_data_bus | interrupt_table_1_to_data_bus | temp_registers_1_data_bus_out;  // OR_Gate or_2, 16 bits wide
  assign to_pk = temp_registers_1_to_sreg | sixt_bit_gatekeeper_1_out_3;  // OR_Gate or_3, 16 bits wide
  Register #(.trigger("falling"), .width(1)) register_2 (
    .D(interrupt_queue_1_waiting), .en(sixt_bit_eq_cmp_3_out_3), .clk(and_1_out), .Q(register_2_q),
    .clr(or_1_out));
  Multiplexer #(.width(16)) multiplexer_3 (
    .in0(sixt_bit_incrementer_1_out_2), .in1(rom_1_data), .out(multiplexer_3_out),
    .sel(sixt_bit_eq_cmp_3_out_3));
  sixt_bit_eq_cmp sixt_bit_eq_cmp_3 (.in_1(16'h1), .in_2(rom_2_data), .out_3(sixt_bit_eq_cmp_3_out_3));
  Multiplexer #(.width(16)) multiplexer_4 (
    .in0(multiplexer_3_out), .in1({16{1'b1}}), .out(multiplexer_4_out), .sel(comparator_1_lt));
  sixt_bit_eq_cmp sixt_bit_eq_cmp_4 (.in_1(16'hfffe), .in_2(rom_2_data), .out_3(sixt_bit_eq_cmp_4_out_3));
  Register #(.trigger("falling"), .width(1)) register_3 (
    .D(stacker_1_active), .en(register_2_q), .clk(and_1_out), .Q(register_3_q), .clr(or_1_out));
  // Probe on multiplexer_4_out
  Register #(.trigger("falling"), .width(16)) MAR (
    .D(multiplexer_4_out), .en(or_5_out), .clk(and_1_out), .Q(MAR_q), .clr(or_4_out));
  or or_4 (or_4_out, sixt_bit_eq_cmp_4_out_3, or_1_out);
  sixt_bit_eq_cmp sixt_bit_eq_cmp_5 (.in_1({16{1'b0}}), .in_2(MAR_q), .out_3(sixt_bit_eq_cmp_5_out_3));
  and and_3 (load, sixt_bit_eq_cmp_5_out_3, or_5_out, ~comparator_1_lt);  // AND_Gate
  buf buffer_1 (buffer_1_out, buffer_4_out);
  buf buffer_2 (buffer_2_out, buffer_1_out);
  buf buffer_3 (buffer_3_out, register_3_q);
  buf buffer_4 (buffer_4_out, buffer_3_out);
  ROM #(.addrWidth(16), .dataWidth(16)) rom_2 (.addr(MAR_q), .data(rom_2_data));
  ROM #(.addrWidth(16), .dataWidth(16)) rom_3 (.addr(MAR_q), .data(rom_3_data));
  and and_4 (and_4_out, ~register_3_q, buffer_2_out);  // AND_Gate
  sixt_bit_incrementer sixt_bit_incrementer_1 (.in_1(MAR_q), .out_2(sixt_bit_incrementer_1_out_2));
  tick_counter tick_counter_1 (
    .clock(and_1_out), .reset(or_1_out), .cycle_count(tick_counter_1_cycle_count),
    .negedge_count(tick_counter_1_negedge_count));  // open: posedge_count
  or or_5 (or_5_out, d_ff_1_q, comparator_1_lt);
  // Probe on tick_counter_1_cycle_count
  Comparator #(.width(32)) comparator_1 (
    .a(tick_counter_1_negedge_count), .b(32'h1), .gt(comparator_1_gt), .lt(comparator_1_lt));  // open: eq
  and and_5 (and_5_out, comparator_1_gt, ~sixt_bit_eq_cmp_2_out_3);  // AND_Gate
  microcode_mixer microcode_mixer_1 (
    .microcode_in(rom_2_data), .instruction(current_instr), .tmpa_in(tmpc_out), .tmpb_in(data_bus_in),
    .microcode_out(microcode_mixer_1_microcode_out));
  microcode_mixer microcode_mixer_2 (
    .microcode_in(rom_3_data), .instruction(current_instr), .tmpa_in(tmpc_out), .tmpb_in(data_bus_in),
    .microcode_out(microcode_mixer_2_microcode_out));
  sixt_bit_gatekeeper sixt_bit_gatekeeper_2 (
    .in_1(and_5_out), .in_2(microcode_mixer_1_microcode_out), .out_3(sixt_bit_gatekeeper_2_out_3));
  sixt_bit_gatekeeper sixt_bit_gatekeeper_3 (
    .in_1(and_5_out), .in_2(microcode_mixer_2_microcode_out), .out_3(sixt_bit_gatekeeper_3_out_3));
  D_Flip_Flop #(.trigger("falling")) d_ff_1 (
    .D(nor_1_out), .clk(and_1_out), .Q(d_ff_1_q), .reset(or_1_out));  // open: Qn, preset
  Multiplexer #(.width(16)) multiplexer_5 (
    .in0(sixt_bit_gatekeeper_2_out_3), .in1(or_7_out), .out(control_bus_1_out), .sel(or_9_out));
  Multiplexer #(.width(16)) multiplexer_6 (
    .in0(sixt_bit_gatekeeper_3_out_3), .in1(or_8_out), .out(control_bus_2_out), .sel(or_9_out));
  nor nor_1 (nor_1_out, unstacker_2_1_active, stacker_1_active);
  eight_bit_eq_cmp eight_bit_eq_cmp_1 (.in_1(8'h24), .in_2(control_bus_1_out[7:0]), .out_3(eight_bit_eq_cmp_1_out_3));
  Shifter #(.width(16)) shifter_1 (.in(16'h1), .\dist (control_bus_1_out[15:12]), .out(shifter_1_out));
  eight_bit_eq_cmp eight_bit_eq_cmp_2 (.in_1(8'h24), .in_2(control_bus_2_out[7:0]), .out_3(eight_bit_eq_cmp_2_out_3));
  Shifter #(.width(16)) shifter_2 (.in(16'h1), .\dist (control_bus_2_out[15:12]), .out(shifter_2_out));
  assign or_6_out = sixt_bit_gatekeeper_4_out_3 | sixt_bit_gatekeeper_5_out_3;  // OR_Gate or_6, 16 bits wide
  sixt_bit_gatekeeper sixt_bit_gatekeeper_4 (
    .in_1(eight_bit_eq_cmp_1_out_3), .in_2(shifter_1_out), .out_3(sixt_bit_gatekeeper_4_out_3));
  sixt_bit_gatekeeper sixt_bit_gatekeeper_5 (
    .in_1(eight_bit_eq_cmp_2_out_3), .in_2(shifter_2_out), .out_3(sixt_bit_gatekeeper_5_out_3));
  sixt_bit_eq_cmp sixt_bit_eq_cmp_6 (.in_1(control_bus_1_out), .in_2(16'h60), .out_3(sixt_bit_eq_cmp_6_out_3));
  // Probe on stacker_1_change_mask
  stacker stacker_1 (
    .clk(and_1_out), .reset(or_1_out), .mem_in(RAM_direct), .register_write(or_6_out),
    .stacking_mask(16'hff), .write_changemask(sixt_bit_eq_cmp_8_out_3), .bypass_mask(register_1_q),
    .enable(sixt_bit_eq_cmp_6_out_3), .control_bus_1_out(stacker_1_control_bus_1_out),
    .control_bus_2_out(stacker_1_control_bus_2_out), .to_data_bus(stacker_1_to_data_bus),
    .active(stacker_1_active), .change_mask(stacker_1_change_mask));
  assign or_7_out = stacker_1_control_bus_1_out | unstacker_2_1_control_bus_1_out;  // OR_Gate or_7, 16 bits wide
  assign or_8_out = stacker_1_control_bus_2_out | unstacker_2_1_control_bus_2_out;  // OR_Gate or_8, 16 bits wide
  or or_9 (or_9_out, stacker_1_active, unstacker_2_1_active);
  sixt_bit_eq_cmp sixt_bit_eq_cmp_7 (.in_1(control_bus_1_out), .in_2(16'h62), .out_3(sixt_bit_eq_cmp_7_out_3));
  // Probe on control_bus_1_out
  sixt_bit_eq_cmp sixt_bit_eq_cmp_8 (
    .in_1(16'h61), .in_2(microcode_mixer_1_microcode_out), .out_3(sixt_bit_eq_cmp_8_out_3));
  unstacker_2 unstacker_2_1 (
    .enable(sixt_bit_eq_cmp_8_out_3), .load_unstacking_mask(sixt_bit_eq_cmp_7_out_3),
    .unstacking_mask(RAM_direct), .clk(and_1_out), .reset(or_1_out), .active(unstacker_2_1_active),
    .control_bus_1_out(unstacker_2_1_control_bus_1_out), .control_bus_2_out(unstacker_2_1_control_bus_2_out));
  // Probe on control_bus_2_out
  // Probe on stack_pointer
  // Probe on addr_bus

  // Notes on the sheet:
  //   contents of rom_1 (hex, n*v repeats v):
  //   2 4 6 9 c f 12 15 18 1b 1e 21 24 27 2a 2e 32 36 3a 3e 42 45 48 4b 4e 52 56 5a 5e 62 66 6b 6f 74 77
  //   7c 7f 84 87 8b 8e 91 94 98 9c a1 a5 aa ae b3 b6 ba bd c1 c4 c8 cc d1 d5 da de 13a 134 137 143 146
  //   152 158 16a 164 167 173 17f 182 188 e3 e7 eb ef f3 f7 fb ff 103 107 10b 10f 113 117 11b 11f 123 127
  //   12b 12e 131 13d 140 149 14c 14f 155 15b 15e 161 16d 170 176 179 17c 185 18b 18d 190 193 196 19a 19d
  //   1a1 1a3 1a7 1aa 1ae 1b1 1b5 1bb 1c0 1c2 1c4 1c8 1cc 1ce 1d6 1da 1dc 1df 1e2 1e7 115*0 1f0 1eb
  //   contents of rom_2 (hex, n*v repeats v):
  //   11 1 0 fffe 4010 fffe 10a0 4010 fffe 10a0 4010 fffe 10a0 4010 fffe 10a0 4010 fffe 10a0 4010 fffe
  //   10a0 4010 fffe 12c7 4010 fffe 12c7 4010 fffe 12c7 4010 fffe 12c7 4010 fffe 12c7 4010 fffe 12c7 4010
  //   fffe 111 102f 4010 fffe 111 102f 4010 fffe 111 102f 4010 fffe 111 102f 4010 fffe 111 102f 4010 fffe
  //   111 102f 4010 fffe 12c6 4010 fffe 12c6 4010 fffe 12c6 4010 fffe 12c6 4010 fffe 111 102f 4010 fffe
  //   111 102f 4010 fffe 111 102f 4010 fffe 111 102f 4010 fffe 111 102f 4010 fffe 111 102f 4010 fffe 10a0
  //   2006 10a4 20a4 fffe 111 50 25 fffe 111 2b 50 25 fffe 4003 25 fffe 111 2a 50 25 fffe 4003 25 fffe 111
  //   2a 50 25 fffe 4002 10a4 fffe 4002 53 10a4 fffe 20a0 10a4 fffe 29 10a4 fffe 2082 10a4 fffe 11 2a 10a4
  //   fffe 5010 50 26 fffe 111 2b 50 29 fffe 5010 20a0 26 fffe 111 2a 50 29 fffe 5010 2082 26 fffe 111 2a
  //   50 29 fffe 4002 1086 fffe 4002 53 1086 fffe 20a0 1086 fffe 11 2a 1086 fffe 2082 1086 fffe 11 2a 1086
  //   fffe 5010 50 26 fffe 111 2b 50 29 fffe 5010 20a0 26 fffe 111 2a 50 29 fffe 5010 2082 26 fffe 111 2a
  //   50 29 fffe 11 10c0 10a4 fffe 11 10c1 10a4 fffe 11 10c2 10a4 fffe 11 10c6 10a4 fffe 11 10c7 10a4 fffe
  //   11 10c9 10a4 fffe 11 10ca 10a4 fffe 11 10cb 10a4 fffe 11 10cf 10a4 fffe 11 12c0 b0a4 fffe 11 12c1
  //   b0a4 fffe 11 12c2 b0a4 fffe 11 12c6 b0a4 fffe 11 12c7 b0a4 fffe 11 12c9 b0a4 fffe 11 12ca b0a4 fffe
  //   11 12cb b0a4 fffe 11 12cf b0a4 fffe 12c0 10a4 fffe 12c1 10a4 fffe 12c2 10a4 fffe 11c3 10a4 fffe 11c4
  //   10a4 fffe 11c5 10a4 fffe 12c6 10a4 fffe 12c7 10a4 fffe 11c8 10a4 fffe 11cc 10a4 fffe 12c9 10a4 fffe
  //   12ca 10a4 fffe 12cb 10a4 fffe 11cd 10a4 fffe 12cf 10a4 fffe 11ce 10a4 fffe 12c0 b0a4 fffe 12c1 b0a4
  //   fffe 12c2 b0a4 fffe 22c3 10a4 fffe 22c4 10a4 fffe 22c5 10a4 fffe 12c6 b0a4 fffe 12c7 b0a4 fffe 22c8
  //   10a4 fffe 12c9 b0a4 fffe 12ca b0a4 fffe 12cb b0a4 fffe 22cc 10a4 fffe 22cd 10a4 fffe 12cf b0a4 fffe
  //   22ce 10a4 fffe 1011 fffe 4002 25 fffe 4004 25 fffe 10a0 25 fffe 10 50 29 fffe 1012 25 fffe 10 50 29
  //   fffe 1010 fffe 10 50 25 fffe 1013 10a4 fffe 10 50 29 fffe 1013 1086 fffe 10 50 29 fffe 10 2 25 4010
  //   60 fffe 62 61 1004 6 fffe 10b0 fffe 10b1 fffe 10a0 4006 10b0 fffe 10a0 4006 10b1 fffe 10b2 fffe 10b3
  //   fffe 10b2 fffe 10a0 4006 b0b3 fffe 10a0 4006 b0b2 fffe 10b3 fffe 10b4 20a4 fffe 20a0 10b5 fffe 10a0
  //   4006 b0b4 20a4 fffe 10a0 4006 b0b5 fffe 1011 2 25 60 fffe 10 2 25 5006 4003 6 60 fffe
  //   contents of rom_3 (hex, n*v repeats v):
  //   0 4 0 0 14 0 10 15 0 10 16 0 10 17 0 10 18 0 10 19 0 10 1a 0 10 15 0 10 16 0 10 17 0 10 19 0 10 1a 0
  //   10 18 0 0 12c7 15 0 0 12c7 16 0 0 12c7 17 0 0 12c7 19 0 0 12c7 1a 0 0 12c7 18 0 10 17 0 10 19 0 10
  //   1a 0 10 18 0 0 12c7 15 0 0 12c7 16 0 0 12c7 17 0 0 12c7 19 0 0 12c7 1a 0 0 12c7 18 0 0 20a0 2002 0 0
  //   0 4003 0 0 0 27 4003 0 0 20a0 10 0 0 2a3 4003 0 0 2082 0 0 0 2085 4003 0 0 0 10 0 0 27 10 4*0 2a3 10
  //   5*0 2085 0 0 111 1a1 0 0 0 27 1a1 26 0 10 1a1 0 0 0 2a3 1a1 26 0 10 1a1 0 0 0 2085 1a1 26 0 0 10 0 0
  //   27 10 5*0 2a3 6*0 2085 0 0 111 1083 0 0 0 27 1083 26 0 10 1083 0 0 0 2a3 1083 26 0 10 1083 0 0 0
  //   2085 1083 26 0 0 102f 0 0 0 102f 0 0 0 102f 0 0 0 102f 0 0 0 102f 0 0 0 102f 0 0 0 102f 0 0 0 102f 0
  //   0 0 102f 0 0 0 102f 0 0 0 102f 0 0 0 102f 0 0 0 102f 0 0 0 102f 0 0 0 102f 0 0 0 102f 0 0 0 102f 0 0
  //   0 102f 100*0 1012 10 0 1012 10 0 1012 0 0 1a2 1012 26 0 1082 0 0 1084 1012 26 0 0 0 1013 4003 5*0
  //   1013 1a1 26 4*0 1013 1083 26 0 0 1012 0 14 0 0 1010 0 1010 45*0 12 1003 1b 0 0 0 1012 7a 0 28
endmodule

module four_bit_incrementer (
  input  [3:0] in_1,
  output [3:0] out_2
);

  wire and_1_out, and_2_out, and_3_out, and_4_out, and_5_out, xor_2_out, xor_3_out, xor_4_out, xor_8_out,
       xor_9_out;

  xor xor_1 (out_2[0], in_1[0], 1'b1);
  and and_1 (and_1_out, in_1[0], 1'b1);
  xor xor_2 (xor_2_out, in_1[1], 1'b0);
  and and_2 (and_2_out, in_1[1], 1'b0);
  xor xor_3 (xor_3_out, in_1[2], 1'b0);
  and and_3 (and_3_out, in_1[2], 1'b0);
  xor xor_4 (xor_4_out, in_1[3], 1'b0);
  xor xor_5 (out_2[1], xor_2_out, and_1_out);
  and and_4 (and_4_out, xor_2_out, and_1_out);
  xor xor_6 (out_2[2], xor_3_out, xor_8_out);
  and and_5 (and_5_out, xor_3_out, xor_8_out);
  xor xor_7 (out_2[3], xor_4_out, xor_9_out);
  xor xor_8 (xor_8_out, and_2_out, and_4_out);
  xor xor_9 (xor_9_out, and_3_out, and_5_out);
endmodule

module special_registers (
  input  [15:0] data_bus_in,
  input  [15:0] control_bus_1,
  input  [15:0] control_bus_2,
  input  [15:0] temp_register,
  input  [15:0] sp_reset_value,
  input  clock,
  input  reset,
  output [15:0] program_kounter,
  output [15:0] data_bus_out,
  output [15:0] addr_bus_out,
  output [15:0] stack_pointer,
  output [15:0] offset_out
);

  wire and_1_out, and_2_out, and_3_out, buffer_1_out, buffer_2_out, buffer_3_out, buffer_4_out, buffer_5_out,
       buffer_6_out, buffer_7_out, d_ff_1_q, not_1_out, offs_to_addr_out, offs_to_data_out, offs_write_out,
       or_1_out, or_2_out, or_3_out, or_4_out, or_5_out, pk_decrement_out, pk_increment_out, pk_to_addr_out,
       pk_to_data_out, pk_write_out, s_r_ff_1_qn, s_r_ff_2_q, s_r_ff_3_q, sixt_bit_eq_zero_1_out_2,
       sp_decrement_out, sp_increment_out, sp_postinc_to_addr_out, sp_predec_to_addr_out, sp_to_addr_out,
       sp_to_data_out, sp_write_out, special_registers_opdec_1_offs_to_addr,
       special_registers_opdec_1_offs_to_data, special_registers_opdec_1_offs_write,
       special_registers_opdec_1_pk_dec, special_registers_opdec_1_pk_inc,
       special_registers_opdec_1_pk_to_addr, special_registers_opdec_1_pk_to_data,
       special_registers_opdec_1_pk_write, special_registers_opdec_1_sp_dec,
       special_registers_opdec_1_sp_inc, special_registers_opdec_1_sp_postinc_to_addr,
       special_registers_opdec_1_sp_predec_to_addr, special_registers_opdec_1_sp_to_addr,
       special_registers_opdec_1_sp_to_data, special_registers_opdec_1_sp_write,
       special_registers_opdec_2_offs_to_addr, special_registers_opdec_2_offs_to_data,
       special_registers_opdec_2_offs_write, special_registers_opdec_2_pk_dec,
       special_registers_opdec_2_pk_inc, special_registers_opdec_2_pk_to_addr,
       special_registers_opdec_2_pk_to_data, special_registers_opdec_2_pk_write,
       special_registers_opdec_2_sp_dec, special_registers_opdec_2_sp_inc,
       special_registers_opdec_2_sp_postinc_to_addr, special_registers_opdec_2_sp_predec_to_addr,
       special_registers_opdec_2_sp_to_addr, special_registers_opdec_2_sp_to_data,
       special_registers_opdec_2_sp_write;
  wire [3:0] pk_param_out, sp_param_out, special_registers_opdec_1_pk_param,
       special_registers_opdec_1_sp_param, special_registers_opdec_2_pk_param,
       special_registers_opdec_2_sp_param;
  wire [15:0] data_to_offs_out, data_to_pk_out, multiplexer_1_out, multiplexer_2_out, or_8_out, or_9_out,
       or_10_out, or_11_out, sixt_bit_gatekeeper_1_out_3, sixt_bit_gatekeeper_2_out_3,
       sixt_bit_gatekeeper_3_out_3, sixt_bit_gatekeeper_4_out_3, sixt_bit_gatekeeper_5_out_3,
       sixt_bit_gatekeeper_6_out_3, special_registers_opdec_1_data_to_offs,
       special_registers_opdec_1_data_to_pk, special_registers_opdec_2_data_to_offs,
       special_registers_opdec_2_data_to_pk, subtractor_1_out;

  Pull_Resistor pull_resistor_1 (.node(sp_reset_value));
  S_R_Flip_Flop s_r_ff_1 (.Qn(s_r_ff_1_qn), .preset(clock));  // open: S, R, clk, Q, reset
  Multiplexer #(.width(16)) multiplexer_1 (
    .in0(16'hefff), .in1(sp_reset_value), .out(multiplexer_1_out), .sel(not_1_out));
  not not_1 (not_1_out, sixt_bit_eq_zero_1_out_2);
  sixt_bit_eq_zero sixt_bit_eq_zero_1 (.in_1(sp_reset_value), .out_2(sixt_bit_eq_zero_1_out_2));
  or or_1 (or_1_out, s_r_ff_1_qn, reset);
  buf buffer_1 (buffer_1_out, clock);
  buf buffer_2 (buffer_2_out, buffer_1_out);
  buf buffer_3 (buffer_3_out, buffer_2_out);
  S_R_Flip_Flop s_r_ff_2 (.Q(s_r_ff_2_q), .reset(and_2_out), .preset(or_1_out));  // open: S, R, clk, Qn
  special_registers_opdec special_registers_opdec_1 (
    .ctrl_unit_in(temp_register), .control(control_bus_2), .data_in(data_bus_in),
    .data_to_offs(special_registers_opdec_1_data_to_offs), .sp_to_data(special_registers_opdec_1_sp_to_data),
    .sp_to_addr(special_registers_opdec_1_sp_to_addr), .sp_write(special_registers_opdec_1_sp_write),
    .sp_param(special_registers_opdec_1_sp_param), .sp_inc(special_registers_opdec_1_sp_inc),
    .sp_dec(special_registers_opdec_1_sp_dec),
    .sp_predec_to_addr(special_registers_opdec_1_sp_predec_to_addr),
    .sp_postinc_to_addr(special_registers_opdec_1_sp_postinc_to_addr),
    .offs_to_data(special_registers_opdec_1_offs_to_data),
    .offs_to_addr(special_registers_opdec_1_offs_to_addr), .offs_write(special_registers_opdec_1_offs_write),
    .data_to_pk(special_registers_opdec_1_data_to_pk), .pk_param(special_registers_opdec_1_pk_param),
    .pk_to_data(special_registers_opdec_1_pk_to_data), .pk_to_addr(special_registers_opdec_1_pk_to_addr),
    .pk_inc(special_registers_opdec_1_pk_inc), .pk_dec(special_registers_opdec_1_pk_dec),
    .pk_write(special_registers_opdec_1_pk_write));
  and and_1 (and_1_out, clock, ~buffer_4_out);  // AND_Gate
  buf buffer_4 (buffer_4_out, buffer_3_out);
  and and_2 (and_2_out, ~s_r_ff_3_q, buffer_7_out, s_r_ff_2_q);  // AND_Gate
  Multiplexer #(.width(16)) multiplexer_2 (
    .in0(data_bus_in), .in1(multiplexer_1_out), .out(multiplexer_2_out), .sel(s_r_ff_2_q));
  D_Flip_Flop d_ff_1 (.D(clock), .clk(s_r_ff_2_q), .Q(d_ff_1_q), .reset(and_1_out));  // open: Qn, preset
  buf buffer_5 (buffer_5_out, and_1_out);
  buf buffer_6 (buffer_6_out, buffer_5_out);
  buf buffer_7 (buffer_7_out, buffer_6_out);
  S_R_Flip_Flop s_r_ff_3 (.Q(s_r_ff_3_q), .reset(and_1_out), .preset(and_3_out));  // open: S, R, clk, Qn
  special_registers_opdec special_registers_opdec_2 (
    .ctrl_unit_in(temp_register), .control(control_bus_1), .data_in(data_bus_in),
    .data_to_offs(special_registers_opdec_2_data_to_offs), .sp_to_data(special_registers_opdec_2_sp_to_data),
    .sp_to_addr(special_registers_opdec_2_sp_to_addr), .sp_write(special_registers_opdec_2_sp_write),
    .sp_param(special_registers_opdec_2_sp_param), .sp_inc(special_registers_opdec_2_sp_inc),
    .sp_dec(special_registers_opdec_2_sp_dec),
    .sp_predec_to_addr(special_registers_opdec_2_sp_predec_to_addr),
    .sp_postinc_to_addr(special_registers_opdec_2_sp_postinc_to_addr),
    .offs_to_data(special_registers_opdec_2_offs_to_data),
    .offs_to_addr(special_registers_opdec_2_offs_to_addr), .offs_write(special_registers_opdec_2_offs_write),
    .data_to_pk(special_registers_opdec_2_data_to_pk), .pk_param(special_registers_opdec_2_pk_param),
    .pk_to_data(special_registers_opdec_2_pk_to_data), .pk_to_addr(special_registers_opdec_2_pk_to_addr),
    .pk_inc(special_registers_opdec_2_pk_inc), .pk_dec(special_registers_opdec_2_pk_dec),
    .pk_write(special_registers_opdec_2_pk_write));
  and and_3 (and_3_out, d_ff_1_q, ~s_r_ff_3_q);  // AND_Gate
  assign data_to_pk_out = special_registers_opdec_2_data_to_pk | special_registers_opdec_1_data_to_pk;  // OR_Gate data_to_pk, 16 bits wide
  or pk_to_addr (pk_to_addr_out, special_registers_opdec_2_pk_to_addr, special_registers_opdec_1_pk_to_addr);
  or pk_to_data (pk_to_data_out, special_registers_opdec_2_pk_to_data, special_registers_opdec_1_pk_to_data);
  assign pk_param_out = special_registers_opdec_2_pk_param | special_registers_opdec_1_pk_param;  // OR_Gate pk_param, 4 bits wide
  or pk_increment (pk_increment_out, special_registers_opdec_2_pk_inc, special_registers_opdec_1_pk_inc);
  or pk_decrement (pk_decrement_out, special_registers_opdec_2_pk_dec, special_registers_opdec_1_pk_dec);
  or pk_write (pk_write_out, special_registers_opdec_2_pk_write, special_registers_opdec_1_pk_write);
  or sp_to_data (sp_to_data_out, special_registers_opdec_2_sp_to_data, special_registers_opdec_1_sp_to_data);
  or sp_to_addr (sp_to_addr_out, special_registers_opdec_2_sp_to_addr, special_registers_opdec_1_sp_to_addr);
  assign sp_param_out = special_registers_opdec_2_sp_param | special_registers_opdec_1_sp_param;  // OR_Gate sp_param, 4 bits wide
  or sp_increment (sp_increment_out, special_registers_opdec_2_sp_inc, special_registers_opdec_1_sp_inc);
  or sp_decrement (sp_decrement_out, special_registers_opdec_2_sp_dec, special_registers_opdec_1_sp_dec);
  or sp_predec_to_addr (sp_predec_to_addr_out, special_registers_opdec_2_sp_predec_to_addr, special_registers_opdec_1_sp_predec_to_addr);
  or sp_postinc_to_addr (sp_postinc_to_addr_out, special_registers_opdec_2_sp_postinc_to_addr, special_registers_opdec_1_sp_postinc_to_addr);
  or sp_write (sp_write_out, special_registers_opdec_2_sp_write, special_registers_opdec_1_sp_write);
  or offs_to_data (offs_to_data_out, special_registers_opdec_2_offs_to_data, special_registers_opdec_1_offs_to_data);
  or offs_to_addr (offs_to_addr_out, special_registers_opdec_2_offs_to_addr, special_registers_opdec_1_offs_to_addr);
  assign data_to_offs_out = special_registers_opdec_2_data_to_offs | special_registers_opdec_1_data_to_offs;  // OR_Gate data_to_offs, 16 bits wide
  or offs_write (offs_write_out, special_registers_opdec_2_offs_write, special_registers_opdec_1_offs_write);
  or or_2 (or_2_out, sp_predec_to_addr_out, sp_decrement_out);
  or or_3 (or_3_out, sp_write_out, s_r_ff_2_q);
  or or_4 (or_4_out, sp_postinc_to_addr_out, sp_increment_out);
  or or_5 (or_5_out, sp_predec_to_addr_out, sp_postinc_to_addr_out, sp_to_addr_out);
  // Probe on data_to_pk_out
  Register #(.width(16)) register_1 (
    .D(data_to_offs_out), .en(offs_write_out), .clk(clock), .Q(offset_out), .clr(or_1_out));
  counting_register counting_register_1 (
    .data_in(data_to_pk_out), .param(pk_param_out), .increment(pk_increment_out),
    .decrement(pk_decrement_out), .write(pk_write_out), .clk(clock), .reset(or_1_out), .out_8(program_kounter));
  sixt_bit_gatekeeper sixt_bit_gatekeeper_1 (
    .in_1(pk_to_data_out), .in_2(program_kounter), .out_3(sixt_bit_gatekeeper_1_out_3));
  counting_register counting_register_2 (
    .data_in(multiplexer_2_out), .param(sp_param_out), .increment(or_4_out), .decrement(or_2_out),
    .write(or_3_out), .clk(clock), .out_8(stack_pointer));  // open: reset
  sixt_bit_gatekeeper sixt_bit_gatekeeper_2 (
    .in_1(or_5_out), .in_2(stack_pointer), .out_3(sixt_bit_gatekeeper_2_out_3));
  assign data_bus_out = sixt_bit_gatekeeper_1_out_3 | or_8_out;  // OR_Gate or_6, 16 bits wide
  assign addr_bus_out = sixt_bit_gatekeeper_3_out_3 | or_10_out;  // OR_Gate or_7, 16 bits wide
  sixt_bit_gatekeeper sixt_bit_gatekeeper_3 (
    .in_1(pk_to_addr_out), .in_2(program_kounter), .out_3(sixt_bit_gatekeeper_3_out_3));
  assign or_8_out = sixt_bit_gatekeeper_4_out_3 | or_9_out;  // OR_Gate or_8, 16 bits wide
  sixt_bit_gatekeeper sixt_bit_gatekeeper_4 (
    .in_1(sp_to_data_out), .in_2(stack_pointer), .out_3(sixt_bit_gatekeeper_4_out_3));
  Subtractor #(.width(16)) subtractor_1 (
    .a(sixt_bit_gatekeeper_2_out_3), .b({16{1'b0}}), .out(subtractor_1_out), .bin(sp_predec_to_addr_out));  // open: bout
  assign or_9_out = sixt_bit_gatekeeper_5_out_3 | sixt_bit_gatekeeper_5_out_3;  // OR_Gate or_9, 16 bits wide
  sixt_bit_gatekeeper sixt_bit_gatekeeper_5 (
    .in_1(offs_to_data_out), .in_2(offset_out), .out_3(sixt_bit_gatekeeper_5_out_3));
  sixt_bit_gatekeeper sixt_bit_gatekeeper_6 (
    .in_1(offs_to_addr_out), .in_2(offset_out), .out_3(sixt_bit_gatekeeper_6_out_3));
  // Probe on program_kounter
  // Probe on stack_pointer
  assign or_10_out = subtractor_1_out | or_11_out;  // OR_Gate or_10, 16 bits wide
  assign or_11_out = sixt_bit_gatekeeper_6_out_3 | sixt_bit_gatekeeper_6_out_3;  // OR_Gate or_11, 16 bits wide

  // Notes on the sheet:
  //   this part handles automatic
  //   resetting of sp to a default
  //   value
  //   --->
endmodule

module temp_registers (
  input  [15:0] data_bus_in,
  input  [15:0] control_bus_1,
  input  [15:0] control_bus_2,
  input  [15:0] ram_direct,
  input  clock,
  input  reset,
  output [15:0] data_bus_out,
  output [15:0] addr_bus_out,
  output [15:0] out_9,
  output [15:0] to_sreg,
  output [15:0] out_11,
  output [15:0] out_12
);

  wire or_1_out, or_2_out, or_3_out, sixt_bit_eq_cmp_1_out_3, sixt_bit_eq_cmp_2_out_3,
       sixt_bit_eq_cmp_3_out_3, special_register_dual_opdec_1_addr_bus_enable,
       special_register_dual_opdec_1_data_bus_enable, special_register_dual_opdec_1_write_enable,
       special_register_dual_opdec_2_addr_bus_enable, special_register_dual_opdec_2_data_bus_enable,
       special_register_dual_opdec_2_write_enable, special_register_dual_opdec_3_addr_bus_enable,
       special_register_dual_opdec_3_data_bus_enable, special_register_dual_opdec_3_write_enable;
  wire [15:0] multiplexer_1_out, register_1_q, sixt_bit_gatekeeper_1_out_3, sixt_bit_gatekeeper_2_out_3,
       sixt_bit_gatekeeper_3_out_3, sixt_bit_gatekeeper_4_out_3, sixt_bit_gatekeeper_5_out_3,
       sixt_bit_gatekeeper_6_out_3, sixt_bit_gatekeeper_7_out_3, sixt_bit_gatekeeper_8_out_3,
       sixt_bit_gatekeeper_9_out_3, special_register_dual_opdec_1_special_functions,
       special_register_dual_opdec_2_special_functions, special_register_dual_opdec_3_special_functions,
       special_register_dual_opdec_4_special_functions;

  Register #(.trigger("falling"), .width(16)) register_1 (
    .D(data_bus_in), .clk(clock), .Q(register_1_q), .clr(reset));  // open: en
  sixt_bit_eq_cmp sixt_bit_eq_cmp_1 (.in_1(control_bus_1), .in_2(16'h13), .out_3(sixt_bit_eq_cmp_1_out_3));
  sixt_bit_eq_cmp sixt_bit_eq_cmp_2 (.in_1(16'h13), .in_2(control_bus_2), .out_3(sixt_bit_eq_cmp_2_out_3));
  sixt_bit_eq_cmp sixt_bit_eq_cmp_3 (.in_1(control_bus_1), .in_2(16'h1), .out_3(sixt_bit_eq_cmp_3_out_3));
  special_register_dual_opdec special_register_dual_opdec_1 (
    .control_bus_2(control_bus_2), .id(4'b0010), .control_bus_1(control_bus_1),
    .data_bus_enable(special_register_dual_opdec_1_data_bus_enable),
    .addr_bus_enable(special_register_dual_opdec_1_addr_bus_enable),
    .write_enable(special_register_dual_opdec_1_write_enable),
    .special_functions(special_register_dual_opdec_1_special_functions));  // open: param
  or or_1 (or_1_out, sixt_bit_eq_cmp_1_out_3, special_register_dual_opdec_1_special_functions[0], sixt_bit_eq_cmp_2_out_3);
  special_register_dual_opdec special_register_dual_opdec_2 (
    .control_bus_2(control_bus_2), .id(4'b0011), .control_bus_1(control_bus_1),
    .data_bus_enable(special_register_dual_opdec_2_data_bus_enable),
    .addr_bus_enable(special_register_dual_opdec_2_addr_bus_enable),
    .write_enable(special_register_dual_opdec_2_write_enable),
    .special_functions(special_register_dual_opdec_2_special_functions));  // open: param
  special_register_dual_opdec special_register_dual_opdec_3 (
    .control_bus_2(control_bus_2), .id(4'b0100), .control_bus_1(control_bus_1),
    .data_bus_enable(special_register_dual_opdec_3_data_bus_enable),
    .addr_bus_enable(special_register_dual_opdec_3_addr_bus_enable),
    .write_enable(special_register_dual_opdec_3_write_enable),
    .special_functions(special_register_dual_opdec_3_special_functions));  // open: param
  or or_2 (or_2_out, special_register_dual_opdec_3_special_functions[0], special_register_dual_opdec_4_special_functions[0]);
  or or_3 (or_3_out, special_register_dual_opdec_3_write_enable, sixt_bit_eq_cmp_3_out_3);
  special_register_dual_opdec special_register_dual_opdec_4 (
    .control_bus_2(control_bus_2), .id(4'b0101), .control_bus_1(control_bus_1),
    .special_functions(special_register_dual_opdec_4_special_functions));  // open: data_bus_enable, addr_bus_enable, write_enable, param
  Register #(.width(16)) register_2 (
    .D(register_1_q), .en(special_register_dual_opdec_1_write_enable), .clk(clock), .Q(out_9), .clr(reset));
  Register #(.width(16)) register_3 (
    .D(register_1_q), .en(special_register_dual_opdec_2_write_enable), .clk(clock), .Q(out_11), .clr(reset));
  Multiplexer #(.width(16)) multiplexer_1 (
    .in0(register_1_q), .in1(ram_direct), .out(multiplexer_1_out), .sel(or_3_out));
  Register #(.width(16)) register_4 (.D(multiplexer_1_out), .en(or_3_out), .clk(clock), .Q(out_12), .clr(reset));
  // Probe on out_12
  sixt_bit_gatekeeper sixt_bit_gatekeeper_1 (
    .in_1(special_register_dual_opdec_1_data_bus_enable), .in_2(out_9), .out_3(sixt_bit_gatekeeper_1_out_3));
  sixt_bit_gatekeeper sixt_bit_gatekeeper_2 (
    .in_1(special_register_dual_opdec_1_addr_bus_enable), .in_2(out_9), .out_3(sixt_bit_gatekeeper_2_out_3));
  sixt_bit_gatekeeper sixt_bit_gatekeeper_3 (.in_1(or_1_out), .in_2(out_9), .out_3(sixt_bit_gatekeeper_3_out_3));
  sixt_bit_gatekeeper sixt_bit_gatekeeper_4 (
    .in_1(special_register_dual_opdec_2_data_bus_enable), .in_2(out_11), .out_3(sixt_bit_gatekeeper_4_out_3));
  sixt_bit_gatekeeper sixt_bit_gatekeeper_5 (
    .in_1(special_register_dual_opdec_2_addr_bus_enable), .in_2(out_11), .out_3(sixt_bit_gatekeeper_5_out_3));
  sixt_bit_gatekeeper sixt_bit_gatekeeper_6 (
    .in_1(special_register_dual_opdec_2_special_functions[0]), .in_2(out_11),
    .out_3(sixt_bit_gatekeeper_6_out_3));
  sixt_bit_gatekeeper sixt_bit_gatekeeper_7 (
    .in_1(special_register_dual_opdec_3_data_bus_enable), .in_2(out_12), .out_3(sixt_bit_gatekeeper_7_out_3));
  sixt_bit_gatekeeper sixt_bit_gatekeeper_8 (
    .in_1(special_register_dual_opdec_3_addr_bus_enable), .in_2(out_12), .out_3(sixt_bit_gatekeeper_8_out_3));
  sixt_bit_gatekeeper sixt_bit_gatekeeper_9 (.in_1(or_2_out), .in_2(out_12), .out_3(sixt_bit_gatekeeper_9_out_3));
  assign data_bus_out = sixt_bit_gatekeeper_1_out_3 | sixt_bit_gatekeeper_4_out_3 | sixt_bit_gatekeeper_7_out_3;  // OR_Gate or_4, 16 bits wide
  assign addr_bus_out = sixt_bit_gatekeeper_2_out_3 | sixt_bit_gatekeeper_8_out_3 | sixt_bit_gatekeeper_5_out_3;  // OR_Gate or_5, 16 bits wide
  assign to_sreg = sixt_bit_gatekeeper_3_out_3 | sixt_bit_gatekeeper_9_out_3 | sixt_bit_gatekeeper_6_out_3;  // OR_Gate or_6, 16 bits wide
endmodule

module register_unit (
  input  [15:0] data_bus_in,
  input  [15:0] control_bus_1,
  input  [15:0] control_bus_2,
  input  clock,
  input  reset,
  output [15:0] data_bus_out,
  output [15:0] addr_bus_out,
  output [15:0] alu1_out,
  output [15:0] alu2_out
);

  wire and_5_out, and_6_out, and_7_out, and_8_out, and_9_out, and_10_out, and_11_out, and_12_out, and_13_out,
       and_14_out, and_15_out, and_16_out, and_17_out, and_18_out, and_19_out, and_20_out, and_21_out,
       and_22_out, and_23_out, and_24_out, eight_bit_eq_cmp_1_out_3, eight_bit_eq_cmp_2_out_3,
       eight_bit_eq_cmp_3_out_3, eight_bit_eq_cmp_4_out_3, eight_bit_eq_cmp_5_out_3,
       eight_bit_eq_cmp_6_out_3, eight_bit_eq_cmp_7_out_3, eight_bit_eq_cmp_8_out_3,
       eight_bit_eq_cmp_9_out_3, eight_bit_eq_cmp_10_out_3, eight_bit_eq_cmp_11_out_3,
       eight_bit_eq_cmp_12_out_3, four_bit_eq_cmp_1_out_3, four_bit_eq_cmp_2_out_3, four_bit_eq_cmp_3_out_3,
       four_bit_eq_cmp_4_out_3, four_bit_eq_cmp_5_out_3, four_bit_eq_cmp_6_out_3, four_bit_eq_cmp_7_out_3,
       four_bit_eq_cmp_8_out_3, four_bit_eq_cmp_9_out_3, four_bit_eq_cmp_10_out_3, four_bit_eq_cmp_11_out_3,
       four_bit_eq_cmp_12_out_3, four_bit_eq_cmp_13_out_3, four_bit_eq_cmp_14_out_3,
       four_bit_eq_cmp_15_out_3, four_bit_eq_cmp_16_out_3, four_bit_eq_cmp_17_out_3,
       four_bit_eq_cmp_18_out_3, four_bit_eq_cmp_19_out_3, four_bit_eq_cmp_20_out_3,
       four_bit_eq_cmp_21_out_3, four_bit_eq_cmp_22_out_3, four_bit_eq_cmp_23_out_3,
       four_bit_eq_cmp_24_out_3, four_bit_eq_cmp_25_out_3, four_bit_eq_cmp_26_out_3,
       four_bit_eq_cmp_27_out_3, four_bit_eq_cmp_28_out_3, four_bit_eq_cmp_29_out_3,
       four_bit_eq_cmp_30_out_3, four_bit_eq_cmp_31_out_3, four_bit_eq_cmp_32_out_3,
       four_bit_eq_cmp_33_out_3, four_bit_eq_cmp_34_out_3, or_1_out, or_2_out, or_3_out, or_4_out, or_5_out,
       or_6_out, or_7_out, or_8_out, or_9_out, or_10_out, or_11_out, or_14_out, or_15_out;
  wire [3:0] and_1_out, and_2_out, and_3_out, and_4_out, bit_extender_1_out, bit_extender_2_out,
       bit_extender_3_out, bit_extender_4_out, or_12_out, or_13_out;
  wire [15:0] and_25_out, and_26_out, and_27_out, and_28_out, and_29_out, and_30_out, and_31_out, and_32_out,
       and_33_out, and_34_out, and_35_out, and_36_out, and_37_out, and_38_out, and_39_out, and_40_out,
       and_41_out, and_42_out, and_43_out, and_44_out, and_45_out, and_46_out, and_47_out, and_48_out,
       and_49_out, and_50_out, and_51_out, and_52_out, and_53_out, and_54_out, and_55_out, and_56_out,
       bit_extender_5_out, bit_extender_6_out, bit_extender_7_out, bit_extender_8_out, bit_extender_9_out,
       bit_extender_10_out, bit_extender_11_out, bit_extender_12_out, bit_extender_13_out,
       bit_extender_14_out, bit_extender_15_out, bit_extender_16_out, bit_extender_17_out,
       bit_extender_18_out, bit_extender_19_out, bit_extender_20_out, bit_extender_21_out,
       bit_extender_22_out, bit_extender_23_out, bit_extender_24_out, bit_extender_25_out,
       bit_extender_26_out, bit_extender_27_out, bit_extender_28_out, bit_extender_29_out,
       bit_extender_30_out, bit_extender_31_out, bit_extender_32_out, bit_extender_33_out,
       bit_extender_34_out, bit_extender_35_out, bit_extender_36_out, or_16_out, or_17_out, or_18_out,
       or_19_out, or_20_out, or_21_out, or_22_out, or_23_out, or_24_out, or_25_out, or_26_out, or_27_out,
       or_28_out, or_29_out, or_30_out, or_31_out, or_32_out, or_33_out, or_34_out, or_35_out, or_36_out,
       or_37_out, or_38_out, or_39_out, or_40_out, or_41_out, or_42_out, or_43_out, or_44_out, or_45_out,
       or_46_out, or_47_out, register_1_q, register_2_q, register_3_q, register_4_q, register_5_q,
       register_6_q, register_7_q, register_8_q, register_9_q, register_10_q, register_11_q, register_12_q,
       register_13_q, register_14_q, register_15_q, register_16_q, register_17_q;

  four_bit_eq_cmp four_bit_eq_cmp_1 (.in_1(control_bus_1[7:4]), .in_2(4'b0100), .out_3(four_bit_eq_cmp_1_out_3));
  eight_bit_eq_cmp eight_bit_eq_cmp_1 (.in_1(control_bus_1[7:0]), .in_2(8'h20), .out_3(eight_bit_eq_cmp_1_out_3));
  eight_bit_eq_cmp eight_bit_eq_cmp_2 (.in_1(control_bus_1[7:0]), .in_2(8'h21), .out_3(eight_bit_eq_cmp_2_out_3));
  eight_bit_eq_cmp eight_bit_eq_cmp_3 (.in_1(control_bus_1[7:0]), .in_2(8'h22), .out_3(eight_bit_eq_cmp_3_out_3));
  eight_bit_eq_cmp eight_bit_eq_cmp_4 (.in_1(control_bus_1[7:0]), .in_2(8'h23), .out_3(eight_bit_eq_cmp_4_out_3));
  eight_bit_eq_cmp eight_bit_eq_cmp_5 (.in_1(control_bus_1[7:0]), .in_2(8'h24), .out_3(eight_bit_eq_cmp_5_out_3));
  eight_bit_eq_cmp eight_bit_eq_cmp_6 (.in_1(control_bus_1[7:0]), .in_2(8'h2f), .out_3(eight_bit_eq_cmp_6_out_3));
  eight_bit_eq_cmp eight_bit_eq_cmp_7 (.in_1(control_bus_2[7:0]), .in_2(8'h20), .out_3(eight_bit_eq_cmp_7_out_3));
  eight_bit_eq_cmp eight_bit_eq_cmp_8 (.in_1(control_bus_2[7:0]), .in_2(8'h21), .out_3(eight_bit_eq_cmp_8_out_3));
  eight_bit_eq_cmp eight_bit_eq_cmp_9 (.in_1(control_bus_2[7:0]), .in_2(8'h22), .out_3(eight_bit_eq_cmp_9_out_3));
  eight_bit_eq_cmp eight_bit_eq_cmp_10 (.in_1(control_bus_2[7:0]), .in_2(8'h23), .out_3(eight_bit_eq_cmp_10_out_3));
  eight_bit_eq_cmp eight_bit_eq_cmp_11 (.in_1(control_bus_2[7:0]), .in_2(8'h24), .out_3(eight_bit_eq_cmp_11_out_3));
  eight_bit_eq_cmp eight_bit_eq_cmp_12 (.in_1(control_bus_2[7:0]), .in_2(8'h2f), .out_3(eight_bit_eq_cmp_12_out_3));
  four_bit_eq_cmp four_bit_eq_cmp_2 (.in_1(control_bus_2[7:4]), .in_2(4'b0100), .out_3(four_bit_eq_cmp_2_out_3));
  Register #(.trigger("falling"), .width(16)) register_1 (
    .D(data_bus_in), .clk(clock), .Q(register_1_q), .clr(reset));  // open: en
  or or_1 (or_1_out, eight_bit_eq_cmp_2_out_3, or_2_out);
  or or_2 (or_2_out, eight_bit_eq_cmp_3_out_3, eight_bit_eq_cmp_4_out_3);
  or or_3 (or_3_out, eight_bit_eq_cmp_1_out_3, four_bit_eq_cmp_1_out_3, eight_bit_eq_cmp_5_out_3);
  or or_4 (or_4_out, eight_bit_eq_cmp_8_out_3, or_5_out);
  or or_5 (or_5_out, eight_bit_eq_cmp_9_out_3, eight_bit_eq_cmp_10_out_3);
  assign bit_extender_1_out = {{3{or_6_out}}, or_6_out};  // Bit_Extender bit_extender_1
  or or_6 (or_6_out, four_bit_eq_cmp_1_out_3, or_1_out);
  assign bit_extender_2_out = {{3{or_3_out}}, or_3_out};  // Bit_Extender bit_extender_2
  assign bit_extender_3_out = {{3{or_7_out}}, or_7_out};  // Bit_Extender bit_extender_3
  or or_7 (or_7_out, four_bit_eq_cmp_2_out_3, or_4_out);
  assign bit_extender_4_out = {{3{or_8_out}}, or_8_out};  // Bit_Extender bit_extender_4
  or or_8 (or_8_out, eight_bit_eq_cmp_7_out_3, four_bit_eq_cmp_2_out_3, eight_bit_eq_cmp_11_out_3);
  assign and_1_out = bit_extender_1_out & control_bus_1[11:8];  // AND_Gate and_1, 4 bits wide
  assign and_2_out = bit_extender_2_out & control_bus_1[15:12];  // AND_Gate and_2, 4 bits wide
  assign and_3_out = bit_extender_3_out & control_bus_2[11:8];  // AND_Gate and_3, 4 bits wide
  assign and_4_out = bit_extender_4_out & control_bus_2[15:12];  // AND_Gate and_4, 4 bits wide
  or or_9 (or_9_out, eight_bit_eq_cmp_1_out_3, eight_bit_eq_cmp_7_out_3);
  or or_10 (or_10_out, or_1_out, or_4_out);
  or or_11 (or_11_out, eight_bit_eq_cmp_5_out_3, eight_bit_eq_cmp_11_out_3);
  assign or_12_out = and_1_out | and_3_out;  // OR_Gate or_12, 4 bits wide
  assign or_13_out = and_2_out | and_4_out;  // OR_Gate or_13, 4 bits wide
  assign bit_extender_5_out = {{15{four_bit_eq_cmp_3_out_3}}, four_bit_eq_cmp_3_out_3};  // Bit_Extender bit_extender_5
  four_bit_eq_cmp four_bit_eq_cmp_3 (.in_1(or_13_out), .in_2(4'b0000), .out_3(four_bit_eq_cmp_3_out_3));
  four_bit_eq_cmp four_bit_eq_cmp_4 (.in_1(or_12_out), .in_2(4'b0000), .out_3(four_bit_eq_cmp_4_out_3));
  assign bit_extender_6_out = {{15{four_bit_eq_cmp_4_out_3}}, four_bit_eq_cmp_4_out_3};  // Bit_Extender bit_extender_6
  assign bit_extender_7_out = {{15{four_bit_eq_cmp_5_out_3}}, four_bit_eq_cmp_5_out_3};  // Bit_Extender bit_extender_7
  four_bit_eq_cmp four_bit_eq_cmp_5 (.in_1(or_13_out), .in_2(4'b0001), .out_3(four_bit_eq_cmp_5_out_3));
  four_bit_eq_cmp four_bit_eq_cmp_6 (.in_1(or_12_out), .in_2(4'b0001), .out_3(four_bit_eq_cmp_6_out_3));
  assign bit_extender_8_out = {{15{four_bit_eq_cmp_6_out_3}}, four_bit_eq_cmp_6_out_3};  // Bit_Extender bit_extender_8
  assign bit_extender_9_out = {{15{four_bit_eq_cmp_7_out_3}}, four_bit_eq_cmp_7_out_3};  // Bit_Extender bit_extender_9
  four_bit_eq_cmp four_bit_eq_cmp_7 (.in_1(or_13_out), .in_2(4'b0010), .out_3(four_bit_eq_cmp_7_out_3));
  four_bit_eq_cmp four_bit_eq_cmp_8 (.in_1(or_12_out), .in_2(4'b0010), .out_3(four_bit_eq_cmp_8_out_3));
  assign bit_extender_10_out = {{15{four_bit_eq_cmp_8_out_3}}, four_bit_eq_cmp_8_out_3};  // Bit_Extender bit_extender_10
  assign bit_extender_11_out = {{15{four_bit_eq_cmp_9_out_3}}, four_bit_eq_cmp_9_out_3};  // Bit_Extender bit_extender_11
  four_bit_eq_cmp four_bit_eq_cmp_9 (.in_1(or_13_out), .in_2(4'b0011), .out_3(four_bit_eq_cmp_9_out_3));
  four_bit_eq_cmp four_bit_eq_cmp_10 (.in_1(or_12_out), .in_2(4'b0011), .out_3(four_bit_eq_cmp_10_out_3));
  assign bit_extender_12_out = {{15{four_bit_eq_cmp_10_out_3}}, four_bit_eq_cmp_10_out_3};  // Bit_Extender bit_extender_12
  assign bit_extender_13_out = {{15{four_bit_eq_cmp_11_out_3}}, four_bit_eq_cmp_11_out_3};  // Bit_Extender bit_extender_13
  four_bit_eq_cmp four_bit_eq_cmp_11 (.in_1(or_13_out), .in_2(4'b0100), .out_3(four_bit_eq_cmp_11_out_3));
  four_bit_eq_cmp four_bit_eq_cmp_12 (.in_1(or_12_out), .in_2(4'b0100), .out_3(four_bit_eq_cmp_12_out_3));
  assign bit_extender_14_out = {{15{four_bit_eq_cmp_12_out_3}}, four_bit_eq_cmp_12_out_3};  // Bit_Extender bit_extender_14
  assign bit_extender_15_out = {{15{four_bit_eq_cmp_13_out_3}}, four_bit_eq_cmp_13_out_3};  // Bit_Extender bit_extender_15
  four_bit_eq_cmp four_bit_eq_cmp_13 (.in_1(or_13_out), .in_2(4'b0101), .out_3(four_bit_eq_cmp_13_out_3));
  four_bit_eq_cmp four_bit_eq_cmp_14 (.in_1(or_12_out), .in_2(4'b0101), .out_3(four_bit_eq_cmp_14_out_3));
  assign bit_extender_16_out = {{15{four_bit_eq_cmp_14_out_3}}, four_bit_eq_cmp_14_out_3};  // Bit_Extender bit_extender_16
  assign bit_extender_17_out = {{15{four_bit_eq_cmp_15_out_3}}, four_bit_eq_cmp_15_out_3};  // Bit_Extender bit_extender_17
  four_bit_eq_cmp four_bit_eq_cmp_15 (.in_1(or_13_out), .in_2(4'b0110), .out_3(four_bit_eq_cmp_15_out_3));
  four_bit_eq_cmp four_bit_eq_cmp_16 (.in_1(or_12_out), .in_2(4'b0110), .out_3(four_bit_eq_cmp_16_out_3));
  assign bit_extender_18_out = {{15{four_bit_eq_cmp_16_out_3}}, four_bit_eq_cmp_16_out_3};  // Bit_Extender bit_extender_18
  assign bit_extender_19_out = {{15{four_bit_eq_cmp_17_out_3}}, four_bit_eq_cmp_17_out_3};  // Bit_Extender bit_extender_19
  four_bit_eq_cmp four_bit_eq_cmp_17 (.in_1(or_13_out), .in_2(4'b0111), .out_3(four_bit_eq_cmp_17_out_3));
  four_bit_eq_cmp four_bit_eq_cmp_18 (.in_1(or_12_out), .in_2(4'b0111), .out_3(four_bit_eq_cmp_18_out_3));
  assign bit_extender_20_out = {{15{four_bit_eq_cmp_18_out_3}}, four_bit_eq_cmp_18_out_3};  // Bit_Extender bit_extender_20
  assign bit_extender_21_out = {{15{four_bit_eq_cmp_19_out_3}}, four_bit_eq_cmp_19_out_3};  // Bit_Extender bit_extender_21
  four_bit_eq_cmp four_bit_eq_cmp_19 (.in_1(or_13_out), .in_2(4'b1000), .out_3(four_bit_eq_cmp_19_out_3));
  four_bit_eq_cmp four_bit_eq_cmp_20 (.in_1(or_12_out), .in_2(4'b1000), .out_3(four_bit_eq_cmp_20_out_3));
  assign bit_extender_22_out = {{15{four_bit_eq_cmp_20_out_3}}, four_bit_eq_cmp_20_out_3};  // Bit_Extender bit_extender_22
  assign bit_extender_23_out = {{15{four_bit_eq_cmp_21_out_3}}, four_bit_eq_cmp_21_out_3};  // Bit_Extender bit_extender_23
  four_bit_eq_cmp four_bit_eq_cmp_21 (.in_1(or_13_out), .in_2(4'b1001), .out_3(four_bit_eq_cmp_21_out_3));
  four_bit_eq_cmp four_bit_eq_cmp_22 (.in_1(or_12_out), .in_2(4'b1001), .out_3(four_bit_eq_cmp_22_out_3));
  assign bit_extender_24_out = {{15{four_bit_eq_cmp_22_out_3}}, four_bit_eq_cmp_22_out_3};  // Bit_Extender bit_extender_24
  assign bit_extender_25_out = {{15{four_bit_eq_cmp_23_out_3}}, four_bit_eq_cmp_23_out_3};  // Bit_Extender bit_extender_25
  four_bit_eq_cmp four_bit_eq_cmp_23 (.in_1(or_13_out), .in_2(4'b1010), .out_3(four_bit_eq_cmp_23_out_3));
  four_bit_eq_cmp four_bit_eq_cmp_24 (.in_1(or_12_out), .in_2(4'b1010), .out_3(four_bit_eq_cmp_24_out_3));
  assign bit_extender_26_out = {{15{four_bit_eq_cmp_24_out_3}}, four_bit_eq_cmp_24_out_3};  // Bit_Extender bit_extender_26
  assign bit_extender_27_out = {{15{four_bit_eq_cmp_25_out_3}}, four_bit_eq_cmp_25_out_3};  // Bit_Extender bit_extender_27
  four_bit_eq_cmp four_bit_eq_cmp_25 (.in_1(or_13_out), .in_2(4'b1011), .out_3(four_bit_eq_cmp_25_out_3));
  four_bit_eq_cmp four_bit_eq_cmp_26 (.in_1(or_12_out), .in_2(4'b1011), .out_3(four_bit_eq_cmp_26_out_3));
  assign bit_extender_28_out = {{15{four_bit_eq_cmp_26_out_3}}, four_bit_eq_cmp_26_out_3};  // Bit_Extender bit_extender_28
  assign bit_extender_29_out = {{15{four_bit_eq_cmp_27_out_3}}, four_bit_eq_cmp_27_out_3};  // Bit_Extender bit_extender_29
  four_bit_eq_cmp four_bit_eq_cmp_27 (.in_1(or_13_out), .in_2(4'b1100), .out_3(four_bit_eq_cmp_27_out_3));
  four_bit_eq_cmp four_bit_eq_cmp_28 (.in_1(or_12_out), .in_2(4'b1100), .out_3(four_bit_eq_cmp_28_out_3));
  assign bit_extender_30_out = {{15{four_bit_eq_cmp_28_out_3}}, four_bit_eq_cmp_28_out_3};  // Bit_Extender bit_extender_30
  assign bit_extender_31_out = {{15{four_bit_eq_cmp_29_out_3}}, four_bit_eq_cmp_29_out_3};  // Bit_Extender bit_extender_31
  four_bit_eq_cmp four_bit_eq_cmp_29 (.in_1(or_13_out), .in_2(4'b1101), .out_3(four_bit_eq_cmp_29_out_3));
  four_bit_eq_cmp four_bit_eq_cmp_30 (.in_1(or_12_out), .in_2(4'b1101), .out_3(four_bit_eq_cmp_30_out_3));
  assign bit_extender_32_out = {{15{four_bit_eq_cmp_30_out_3}}, four_bit_eq_cmp_30_out_3};  // Bit_Extender bit_extender_32
  assign bit_extender_33_out = {{15{four_bit_eq_cmp_31_out_3}}, four_bit_eq_cmp_31_out_3};  // Bit_Extender bit_extender_33
  four_bit_eq_cmp four_bit_eq_cmp_31 (.in_1(or_13_out), .in_2(4'b1110), .out_3(four_bit_eq_cmp_31_out_3));
  four_bit_eq_cmp four_bit_eq_cmp_32 (.in_1(or_12_out), .in_2(4'b1110), .out_3(four_bit_eq_cmp_32_out_3));
  assign bit_extender_34_out = {{15{four_bit_eq_cmp_32_out_3}}, four_bit_eq_cmp_32_out_3};  // Bit_Extender bit_extender_34
  assign bit_extender_35_out = {{15{four_bit_eq_cmp_33_out_3}}, four_bit_eq_cmp_33_out_3};  // Bit_Extender bit_extender_35
  four_bit_eq_cmp four_bit_eq_cmp_33 (.in_1(or_13_out), .in_2(4'b1111), .out_3(four_bit_eq_cmp_33_out_3));
  four_bit_eq_cmp four_bit_eq_cmp_34 (.in_1(or_12_out), .in_2(4'b1111), .out_3(four_bit_eq_cmp_34_out_3));
  assign bit_extender_36_out = {{15{four_bit_eq_cmp_34_out_3}}, four_bit_eq_cmp_34_out_3};  // Bit_Extender bit_extender_36
  and and_5 (and_5_out, or_11_out, four_bit_eq_cmp_3_out_3);
  and and_6 (and_6_out, or_11_out, four_bit_eq_cmp_5_out_3);
  and and_7 (and_7_out, or_11_out, four_bit_eq_cmp_7_out_3);
  and and_8 (and_8_out, or_11_out, four_bit_eq_cmp_9_out_3);
  and and_9 (and_9_out, or_11_out, four_bit_eq_cmp_11_out_3);
  and and_10 (and_10_out, or_11_out, four_bit_eq_cmp_13_out_3);
  and and_11 (and_11_out, or_11_out, four_bit_eq_cmp_15_out_3);
  and and_12 (and_12_out, or_11_out, four_bit_eq_cmp_17_out_3);
  and and_13 (and_13_out, or_11_out, four_bit_eq_cmp_19_out_3);
  and and_14 (and_14_out, or_11_out, four_bit_eq_cmp_21_out_3);
  and and_15 (and_15_out, or_11_out, four_bit_eq_cmp_23_out_3);
  and and_16 (and_16_out, or_11_out, four_bit_eq_cmp_25_out_3);
  and and_17 (and_17_out, or_11_out, four_bit_eq_cmp_27_out_3);
  and and_18 (and_18_out, or_11_out, four_bit_eq_cmp_29_out_3);
  and and_19 (and_19_out, or_11_out, four_bit_eq_cmp_31_out_3);
  and and_20 (and_20_out, or_11_out, four_bit_eq_cmp_33_out_3);
  Register #(.width(16)) register_2 (.D(register_1_q), .en(and_5_out), .clk(clock), .Q(register_2_q), .clr(reset));
  Register #(.width(16)) register_3 (.D(register_1_q), .en(and_6_out), .clk(clock), .Q(register_3_q), .clr(reset));
  Register #(.width(16)) register_4 (.D(register_1_q), .en(and_7_out), .clk(clock), .Q(register_4_q), .clr(reset));
  Register #(.width(16)) register_5 (.D(register_1_q), .en(and_8_out), .clk(clock), .Q(register_5_q), .clr(reset));
  Register #(.width(16)) register_6 (.D(register_1_q), .en(and_9_out), .clk(clock), .Q(register_6_q), .clr(reset));
  Register #(.width(16)) register_7 (.D(register_1_q), .en(and_10_out), .clk(clock), .Q(register_7_q), .clr(reset));
  Register #(.width(16)) register_8 (.D(register_1_q), .en(and_11_out), .clk(clock), .Q(register_8_q), .clr(reset));
  Register #(.width(16)) register_9 (.D(register_1_q), .en(and_12_out), .clk(clock), .Q(register_9_q), .clr(reset));
  Register #(.width(16)) register_10 (.D(register_1_q), .en(and_13_out), .clk(clock), .Q(register_10_q), .clr(reset));
  Register #(.width(16)) register_11 (.D(register_1_q), .en(and_14_out), .clk(clock), .Q(register_11_q), .clr(reset));
  Register #(.width(16)) register_12 (.D(register_1_q), .en(and_15_out), .clk(clock), .Q(register_12_q), .clr(reset));
  Register #(.width(16)) register_13 (.D(register_1_q), .en(and_16_out), .clk(clock), .Q(register_13_q), .clr(reset));
  Register #(.width(16)) register_14 (.D(register_1_q), .en(and_17_out), .clk(clock), .Q(register_14_q), .clr(reset));
  Register #(.width(16)) register_15 (.D(register_1_q), .en(and_18_out), .clk(clock), .Q(register_15_q), .clr(reset));
  Register #(.width(16)) register_16 (.D(register_1_q), .en(and_19_out), .clk(clock), .Q(register_16_q), .clr(reset));
  Register #(.width(16)) register_17 (.D(register_1_q), .en(and_20_out), .clk(clock), .Q(register_17_q), .clr(reset));
  and and_21 (and_21_out, control_bus_1[12], eight_bit_eq_cmp_6_out_3);
  or or_14 (or_14_out, and_24_out, and_22_out);
  and and_22 (and_22_out, ~control_bus_1[12], eight_bit_eq_cmp_6_out_3);  // AND_Gate
  or or_15 (or_15_out, and_21_out, and_23_out);
  and and_23 (and_23_out, control_bus_2[12], eight_bit_eq_cmp_12_out_3);
  and and_24 (and_24_out, ~control_bus_2[12], eight_bit_eq_cmp_12_out_3);  // AND_Gate
  assign and_25_out = register_2_q & bit_extender_5_out;  // AND_Gate and_25, 16 bits wide
  assign or_16_out = and_25_out | and_25_out;  // OR_Gate or_16, 16 bits wide
  assign and_26_out = register_3_q & bit_extender_7_out;  // AND_Gate and_26, 16 bits wide
  assign or_17_out = and_26_out | or_16_out;  // OR_Gate or_17, 16 bits wide
  assign and_27_out = register_4_q & bit_extender_9_out;  // AND_Gate and_27, 16 bits wide
  assign or_18_out = and_27_out | or_17_out;  // OR_Gate or_18, 16 bits wide
  assign and_28_out = register_5_q & bit_extender_11_out;  // AND_Gate and_28, 16 bits wide
  assign or_19_out = and_28_out | or_18_out;  // OR_Gate or_19, 16 bits wide
  assign and_29_out = register_6_q & bit_extender_13_out;  // AND_Gate and_29, 16 bits wide
  assign or_20_out = and_29_out | or_19_out;  // OR_Gate or_20, 16 bits wide
  assign and_30_out = register_7_q & bit_extender_15_out;  // AND_Gate and_30, 16 bits wide
  assign or_21_out = and_30_out | or_20_out;  // OR_Gate or_21, 16 bits wide
  assign and_31_out = register_8_q & bit_extender_17_out;  // AND_Gate and_31, 16 bits wide
  assign or_22_out = and_31_out | or_21_out;  // OR_Gate or_22, 16 bits wide
  assign and_32_out = register_9_q & bit_extender_19_out;  // AND_Gate and_32, 16 bits wide
  assign or_23_out = and_32_out | or_22_out;  // OR_Gate or_23, 16 bits wide
  assign and_33_out = register_10_q & bit_extender_21_out;  // AND_Gate and_33, 16 bits wide
  assign or_24_out = and_33_out | or_23_out;  // OR_Gate or_24, 16 bits wide
  assign and_34_out = register_11_q & bit_extender_23_out;  // AND_Gate and_34, 16 bits wide
  assign or_25_out = and_34_out | or_24_out;  // OR_Gate or_25, 16 bits wide
  assign and_35_out = register_12_q & bit_extender_25_out;  // AND_Gate and_35, 16 bits wide
  assign or_26_out = and_35_out | or_25_out;  // OR_Gate or_26, 16 bits wide
  assign and_36_out = register_13_q & bit_extender_27_out;  // AND_Gate and_36, 16 bits wide
  assign or_27_out = and_36_out | or_26_out;  // OR_Gate or_27, 16 bits wide
  assign and_37_out = register_14_q & bit_extender_29_out;  // AND_Gate and_37, 16 bits wide
  assign or_28_out = and_37_out | or_27_out;  // OR_Gate or_28, 16 bits wide
  assign and_38_out = register_15_q & bit_extender_31_out;  // AND_Gate and_38, 16 bits wide
  assign or_29_out = and_38_out | or_28_out;  // OR_Gate or_29, 16 bits wide
  assign and_39_out = register_16_q & bit_extender_33_out;  // AND_Gate and_39, 16 bits wide
  assign or_30_out = and_39_out | or_29_out;  // OR_Gate or_30, 16 bits wide
  assign and_40_out = register_17_q & bit_extender_35_out;  // AND_Gate and_40, 16 bits wide
  assign or_31_out = and_40_out | or_30_out;  // OR_Gate or_31, 16 bits wide
  assign and_41_out = register_2_q & bit_extender_6_out;  // AND_Gate and_41, 16 bits wide
  assign or_32_out = and_41_out | and_41_out;  // OR_Gate or_32, 16 bits wide
  assign and_42_out = register_3_q & bit_extender_8_out;  // AND_Gate and_42, 16 bits wide
  assign or_33_out = and_42_out | or_32_out;  // OR_Gate or_33, 16 bits wide
  assign and_43_out = register_4_q & bit_extender_10_out;  // AND_Gate and_43, 16 bits wide
  assign or_34_out = and_43_out | or_33_out;  // OR_Gate or_34, 16 bits wide
  assign and_44_out = register_5_q & bit_extender_12_out;  // AND_Gate and_44, 16 bits wide
  assign or_35_out = and_44_out | or_34_out;  // OR_Gate or_35, 16 bits wide
  assign and_45_out = register_6_q & bit_extender_14_out;  // AND_Gate and_45, 16 bits wide
  assign or_36_out = and_45_out | or_35_out;  // OR_Gate or_36, 16 bits wide
  assign and_46_out = register_7_q & bit_extender_16_out;  // AND_Gate and_46, 16 bits wide
  assign or_37_out = and_46_out | or_36_out;  // OR_Gate or_37, 16 bits wide
  assign and_47_out = register_8_q & bit_extender_18_out;  // AND_Gate and_47, 16 bits wide
  assign or_38_out = and_47_out | or_37_out;  // OR_Gate or_38, 16 bits wide
  assign and_48_out = register_9_q & bit_extender_20_out;  // AND_Gate and_48, 16 bits wide
  assign or_39_out = and_48_out | or_38_out;  // OR_Gate or_39, 16 bits wide
  assign and_49_out = register_10_q & bit_extender_22_out;  // AND_Gate and_49, 16 bits wide
  assign or_40_out = and_49_out | or_39_out;  // OR_Gate or_40, 16 bits wide
  assign and_50_out = register_11_q & bit_extender_24_out;  // AND_Gate and_50, 16 bits wide
  assign or_41_out = and_50_out | or_40_out;  // OR_Gate or_41, 16 bits wide
  assign and_51_out = register_12_q & bit_extender_26_out;  // AND_Gate and_51, 16 bits wide
  assign or_42_out = and_51_out | or_41_out;  // OR_Gate or_42, 16 bits wide
  assign and_52_out = register_13_q & bit_extender_28_out;  // AND_Gate and_52, 16 bits wide
  assign or_43_out = and_52_out | or_42_out;  // OR_Gate or_43, 16 bits wide
  assign and_53_out = register_14_q & bit_extender_30_out;  // AND_Gate and_53, 16 bits wide
  assign or_44_out = and_53_out | or_43_out;  // OR_Gate or_44, 16 bits wide
  assign and_54_out = register_15_q & bit_extender_32_out;  // AND_Gate and_54, 16 bits wide
  assign or_45_out = and_54_out | or_44_out;  // OR_Gate or_45, 16 bits wide
  assign and_55_out = register_16_q & bit_extender_34_out;  // AND_Gate and_55, 16 bits wide
  assign or_46_out = and_55_out | or_45_out;  // OR_Gate or_46, 16 bits wide
  assign and_56_out = register_17_q & bit_extender_36_out;  // AND_Gate and_56, 16 bits wide
  assign or_47_out = and_56_out | or_46_out;  // OR_Gate or_47, 16 bits wide
  Multiplexer #(.width(16)) multiplexer_1 (.in0(or_31_out), .in1(register_1_q), .out(alu1_out), .sel(or_14_out));
  Multiplexer #(.width(16)) multiplexer_2 (.in0(or_47_out), .in1(register_1_q), .out(alu2_out), .sel(or_15_out));
  sixt_bit_gatekeeper sixt_bit_gatekeeper_1 (.in_1(or_9_out), .in_2(or_31_out), .out_3(data_bus_out));
  sixt_bit_gatekeeper sixt_bit_gatekeeper_2 (.in_1(or_10_out), .in_2(or_47_out), .out_3(addr_bus_out));
endmodule

module ALU (
  input  [15:0] control_bus,
  input  [15:0] argument1,
  input  [15:0] argument2,
  input  clock,
  input  reset,
  output [15:0] out_6,
  output out_7
);

  wire and_3_out, comparator_1_gt, comparator_1_lt, comparator_2_gt, comparator_2_lt,
       eight_bit_eq_cmp_1_out_3, eight_bit_eq_cmp_2_out_3, eight_bit_eq_cmp_3_out_3,
       eight_bit_eq_cmp_4_out_3, eight_bit_eq_cmp_5_out_3, eight_bit_eq_cmp_6_out_3,
       eight_bit_eq_cmp_7_out_3, eight_bit_eq_cmp_8_out_3, eight_bit_eq_cmp_9_out_3,
       eight_bit_eq_cmp_10_out_3, eight_bit_eq_cmp_11_out_3, eight_bit_eq_cmp_12_out_3,
       eight_bit_eq_cmp_13_out_3, eight_bit_eq_cmp_14_out_3, eight_bit_eq_cmp_15_out_3,
       eight_bit_eq_cmp_16_out_3, four_bit_eq_cmp_1_out_3, nor_1_out, or_1_out,
       sixt_bit_adder_subtractor_1_out_5, sixt_bit_comparator_1_out_3, sixt_bit_comparator_1_out_4;
  wire [15:0] and_2_out, multiplexer_1_out, not_1_out, not_2_out, not_3_out, or_2_out, or_3_out, or_4_out,
       or_5_out, or_6_out, or_7_out, or_8_out, or_9_out, or_10_out, or_11_out, or_12_out, or_13_out,
       or_14_out, or_15_out, or_16_out, or_17_out, or_18_out, or_19_out, shifter_1_out, shifter_2_out,
       shifter_3_out, sixt_bit_adder_subtractor_1_out_4, sixt_bit_decrementer_1_out_2,
       sixt_bit_gatekeeper_1_out_3, sixt_bit_gatekeeper_2_out_3, sixt_bit_gatekeeper_3_out_3,
       sixt_bit_gatekeeper_4_out_3, sixt_bit_gatekeeper_5_out_3, sixt_bit_gatekeeper_6_out_3,
       sixt_bit_gatekeeper_7_out_3, sixt_bit_gatekeeper_8_out_3, sixt_bit_gatekeeper_9_out_3,
       sixt_bit_gatekeeper_10_out_3, sixt_bit_gatekeeper_11_out_3, sixt_bit_gatekeeper_12_out_3,
       sixt_bit_gatekeeper_13_out_3, sixt_bit_gatekeeper_14_out_3, sixt_bit_gatekeeper_15_out_3,
       sixt_bit_gatekeeper_16_out_3, sixt_bit_gatekeeper_17_out_3, sixt_bit_gatekeeper_18_out_3,
       sixt_bit_gatekeeper_19_out_3, sixt_bit_gatekeeper_20_out_3, sixt_bit_gatekeeper_21_out_3,
       sixt_bit_incrementer_1_out_2, sixt_bit_incrementer_2_out_2, sixt_bit_incrementer_3_out_2,
       sixt_bit_multuiplier_1_out_3, xor_1_out;

  four_bit_eq_cmp four_bit_eq_cmp_1 (.in_1(control_bus[7:4]), .in_2(4'b0100), .out_3(four_bit_eq_cmp_1_out_3));
  eight_bit_eq_cmp eight_bit_eq_cmp_1 (
    .in_1({4'b0000, control_bus[3:0]}), .in_2({8{1'b0}}), .out_3(eight_bit_eq_cmp_1_out_3));
  eight_bit_eq_cmp eight_bit_eq_cmp_2 (
    .in_1({4'b0000, control_bus[3:0]}), .in_2(8'h1), .out_3(eight_bit_eq_cmp_2_out_3));
  eight_bit_eq_cmp eight_bit_eq_cmp_3 (
    .in_1({4'b0000, control_bus[3:0]}), .in_2(8'h2), .out_3(eight_bit_eq_cmp_3_out_3));
  eight_bit_eq_cmp eight_bit_eq_cmp_4 (
    .in_1({4'b0000, control_bus[3:0]}), .in_2(8'h3), .out_3(eight_bit_eq_cmp_4_out_3));
  eight_bit_eq_cmp eight_bit_eq_cmp_5 (
    .in_1({4'b0000, control_bus[3:0]}), .in_2(8'h4), .out_3(eight_bit_eq_cmp_5_out_3));
  eight_bit_eq_cmp eight_bit_eq_cmp_6 (
    .in_1({4'b0000, control_bus[3:0]}), .in_2(8'h5), .out_3(eight_bit_eq_cmp_6_out_3));
  eight_bit_eq_cmp eight_bit_eq_cmp_7 (
    .in_1({4'b0000, control_bus[3:0]}), .in_2(8'h6), .out_3(eight_bit_eq_cmp_7_out_3));
  eight_bit_eq_cmp eight_bit_eq_cmp_8 (
    .in_1({4'b0000, control_bus[3:0]}), .in_2(8'h7), .out_3(eight_bit_eq_cmp_8_out_3));
  eight_bit_eq_cmp eight_bit_eq_cmp_9 (
    .in_1({4'b0000, control_bus[3:0]}), .in_2(8'h8), .out_3(eight_bit_eq_cmp_9_out_3));
  eight_bit_eq_cmp eight_bit_eq_cmp_10 (
    .in_1({4'b0000, control_bus[3:0]}), .in_2(8'h9), .out_3(eight_bit_eq_cmp_10_out_3));
  eight_bit_eq_cmp eight_bit_eq_cmp_11 (
    .in_1({4'b0000, control_bus[3:0]}), .in_2(8'ha), .out_3(eight_bit_eq_cmp_11_out_3));
  eight_bit_eq_cmp eight_bit_eq_cmp_12 (
    .in_1({4'b0000, control_bus[3:0]}), .in_2(8'hb), .out_3(eight_bit_eq_cmp_12_out_3));
  eight_bit_eq_cmp eight_bit_eq_cmp_13 (
    .in_1({4'b0000, control_bus[3:0]}), .in_2(8'hc), .out_3(eight_bit_eq_cmp_13_out_3));
  eight_bit_eq_cmp eight_bit_eq_cmp_14 (
    .in_1({4'b0000, control_bus[3:0]}), .in_2(8'hd), .out_3(eight_bit_eq_cmp_14_out_3));
  eight_bit_eq_cmp eight_bit_eq_cmp_15 (
    .in_1({4'b0000, control_bus[3:0]}), .in_2(8'he), .out_3(eight_bit_eq_cmp_15_out_3));
  eight_bit_eq_cmp eight_bit_eq_cmp_16 (
    .in_1({4'b0000, control_bus[3:0]}), .in_2(8'hf), .out_3(eight_bit_eq_cmp_16_out_3));
  sixt_bit_adder_subtractor sixt_bit_adder_subtractor_1 (
    .in_3(eight_bit_eq_cmp_2_out_3), .in_1(argument1), .in_2(argument2),
    .out_5(sixt_bit_adder_subtractor_1_out_5), .out_4(sixt_bit_adder_subtractor_1_out_4));
  // Probe on argument1
  // Probe on argument2
  or or_1 (or_1_out, eight_bit_eq_cmp_2_out_3, eight_bit_eq_cmp_1_out_3);
  sixt_bit_gatekeeper sixt_bit_gatekeeper_1 (
    .in_1(or_1_out), .in_2(sixt_bit_adder_subtractor_1_out_4), .out_3(sixt_bit_gatekeeper_1_out_3));
  and and_1 (out_7, or_1_out, sixt_bit_adder_subtractor_1_out_5);
  sixt_bit_multuiplier sixt_bit_multuiplier_1 (
    .in_1(argument1), .in_2(argument2), .out_3(sixt_bit_multuiplier_1_out_3));
  sixt_bit_gatekeeper sixt_bit_gatekeeper_2 (
    .in_1(eight_bit_eq_cmp_3_out_3), .in_2(sixt_bit_multuiplier_1_out_3), .out_3(sixt_bit_gatekeeper_2_out_3));
  sixt_bit_incrementer sixt_bit_incrementer_1 (.in_1(argument1), .out_2(sixt_bit_incrementer_1_out_2));
  sixt_bit_gatekeeper sixt_bit_gatekeeper_3 (
    .in_1(eight_bit_eq_cmp_4_out_3), .in_2(sixt_bit_incrementer_1_out_2), .out_3(sixt_bit_gatekeeper_3_out_3));
  sixt_bit_decrementer sixt_bit_decrementer_1 (.in_1(argument1), .out_2(sixt_bit_decrementer_1_out_2));
  sixt_bit_gatekeeper sixt_bit_gatekeeper_4 (
    .in_1(eight_bit_eq_cmp_5_out_3), .in_2(sixt_bit_decrementer_1_out_2), .out_3(sixt_bit_gatekeeper_4_out_3));
  assign not_1_out = ~argument1;  // NOT_Gate not_1, 16 bits wide
  sixt_bit_incrementer sixt_bit_incrementer_2 (.in_1(not_1_out), .out_2(sixt_bit_incrementer_2_out_2));
  sixt_bit_gatekeeper sixt_bit_gatekeeper_5 (
    .in_1(eight_bit_eq_cmp_6_out_3), .in_2(sixt_bit_incrementer_2_out_2), .out_3(sixt_bit_gatekeeper_5_out_3));
  sixt_bit_comparator sixt_bit_comparator_1 (
    .in_1(argument1), .in_2(argument2), .out_3(sixt_bit_comparator_1_out_3),
    .out_4(sixt_bit_comparator_1_out_4));
  Comparator #(.width(16)) comparator_1 (
    .a(argument1), .b(argument2), .gt(comparator_1_gt), .lt(comparator_1_lt));  // open: eq
  Comparator #(.width(16)) comparator_2 (
    .a(argument1), .b({16{1'b0}}), .gt(comparator_2_gt), .lt(comparator_2_lt));  // open: eq
  assign and_2_out = argument1 & argument2;  // AND_Gate and_2, 16 bits wide
  sixt_bit_gatekeeper sixt_bit_gatekeeper_6 (
    .in_1(eight_bit_eq_cmp_10_out_3), .in_2(and_2_out), .out_3(sixt_bit_gatekeeper_6_out_3));
  assign or_2_out = argument1 | argument2;  // OR_Gate or_2, 16 bits wide
  sixt_bit_gatekeeper sixt_bit_gatekeeper_7 (
    .in_1(eight_bit_eq_cmp_11_out_3), .in_2(or_2_out), .out_3(sixt_bit_gatekeeper_7_out_3));
  assign xor_1_out = argument1 ^ argument2;  // XOR_Gate xor_1, 16 bits wide
  sixt_bit_gatekeeper sixt_bit_gatekeeper_8 (
    .in_1(eight_bit_eq_cmp_12_out_3), .in_2(xor_1_out), .out_3(sixt_bit_gatekeeper_8_out_3));
  assign not_2_out = ~argument2;  // NOT_Gate not_2, 16 bits wide
  sixt_bit_gatekeeper sixt_bit_gatekeeper_9 (
    .in_1(eight_bit_eq_cmp_13_out_3), .in_2(not_2_out), .out_3(sixt_bit_gatekeeper_9_out_3));
  Shifter #(.width(16)) shifter_1 (.in(argument1), .\dist (4'b0001), .out(shifter_1_out));
  sixt_bit_gatekeeper sixt_bit_gatekeeper_10 (
    .in_1(eight_bit_eq_cmp_14_out_3), .in_2(shifter_1_out), .out_3(sixt_bit_gatekeeper_10_out_3));
  Shifter #(.shift("lr"), .width(16)) shifter_2 (.in(argument1), .\dist (4'b0001), .out(shifter_2_out));
  sixt_bit_gatekeeper sixt_bit_gatekeeper_11 (
    .in_1(eight_bit_eq_cmp_15_out_3), .in_2(shifter_2_out), .out_3(sixt_bit_gatekeeper_11_out_3));
  Multiplexer #(.width(16)) multiplexer_1 (
    .in0(argument2), .in1(sixt_bit_incrementer_3_out_2), .out(multiplexer_1_out), .sel(argument2[15]));
  assign not_3_out = ~argument2;  // NOT_Gate not_3, 16 bits wide
  sixt_bit_incrementer sixt_bit_incrementer_3 (.in_1(not_3_out), .out_2(sixt_bit_incrementer_3_out_2));
  assign or_3_out = sixt_bit_gatekeeper_1_out_3 | sixt_bit_gatekeeper_2_out_3;  // OR_Gate or_3, 16 bits wide
  sixt_bit_gatekeeper sixt_bit_gatekeeper_12 (
    .in_1(sixt_bit_comparator_1_out_3), .in_2(16'h1), .out_3(sixt_bit_gatekeeper_12_out_3));
  sixt_bit_gatekeeper sixt_bit_gatekeeper_13 (
    .in_1(sixt_bit_comparator_1_out_4), .in_2({16{1'b1}}), .out_3(sixt_bit_gatekeeper_13_out_3));
  sixt_bit_gatekeeper sixt_bit_gatekeeper_14 (
    .in_1(comparator_1_gt), .in_2(16'h1), .out_3(sixt_bit_gatekeeper_14_out_3));
  sixt_bit_gatekeeper sixt_bit_gatekeeper_15 (
    .in_1(comparator_1_lt), .in_2({16{1'b1}}), .out_3(sixt_bit_gatekeeper_15_out_3));
  sixt_bit_gatekeeper sixt_bit_gatekeeper_16 (
    .in_1(comparator_2_gt), .in_2(16'h1), .out_3(sixt_bit_gatekeeper_16_out_3));
  sixt_bit_gatekeeper sixt_bit_gatekeeper_17 (
    .in_1(comparator_2_lt), .in_2({16{1'b1}}), .out_3(sixt_bit_gatekeeper_17_out_3));
  nor nor_1 (nor_1_out, multiplexer_1_out[4], multiplexer_1_out[5], multiplexer_1_out[6], multiplexer_1_out[7], multiplexer_1_out[8], multiplexer_1_out[9], multiplexer_1_out[10], multiplexer_1_out[11], multiplexer_1_out[12], multiplexer_1_out[13], multiplexer_1_out[14]);
  assign or_4_out = or_3_out | sixt_bit_gatekeeper_3_out_3;  // OR_Gate or_4, 16 bits wide
  assign or_5_out = sixt_bit_gatekeeper_12_out_3 | sixt_bit_gatekeeper_13_out_3;  // OR_Gate or_5, 16 bits wide
  sixt_bit_gatekeeper sixt_bit_gatekeeper_18 (
    .in_1(eight_bit_eq_cmp_7_out_3), .in_2(or_5_out), .out_3(sixt_bit_gatekeeper_18_out_3));
  assign or_6_out = sixt_bit_gatekeeper_14_out_3 | sixt_bit_gatekeeper_15_out_3;  // OR_Gate or_6, 16 bits wide
  sixt_bit_gatekeeper sixt_bit_gatekeeper_19 (
    .in_1(eight_bit_eq_cmp_8_out_3), .in_2(or_6_out), .out_3(sixt_bit_gatekeeper_19_out_3));
  assign or_7_out = sixt_bit_gatekeeper_16_out_3 | sixt_bit_gatekeeper_17_out_3;  // OR_Gate or_7, 16 bits wide
  sixt_bit_gatekeeper sixt_bit_gatekeeper_20 (
    .in_1(eight_bit_eq_cmp_9_out_3), .in_2(or_7_out), .out_3(sixt_bit_gatekeeper_20_out_3));
  and and_3 (and_3_out, eight_bit_eq_cmp_16_out_3, nor_1_out);
  Shifter #(.width(16)) shifter_3 (.in(argument1), .\dist (multiplexer_1_out[3:0]), .out(shifter_3_out));
  assign or_8_out = or_4_out | sixt_bit_gatekeeper_4_out_3;  // OR_Gate or_8, 16 bits wide
  sixt_bit_gatekeeper sixt_bit_gatekeeper_21 (
    .in_1(and_3_out), .in_2(shifter_3_out), .out_3(sixt_bit_gatekeeper_21_out_3));
  assign or_9_out = or_8_out | sixt_bit_gatekeeper_5_out_3;  // OR_Gate or_9, 16 bits wide
  assign or_10_out = or_9_out | sixt_bit_gatekeeper_18_out_3;  // OR_Gate or_10, 16 bits wide
  assign or_11_out = or_10_out | sixt_bit_gatekeeper_19_out_3;  // OR_Gate or_11, 16 bits wide
  assign or_12_out = or_11_out | sixt_bit_gatekeeper_20_out_3;  // OR_Gate or_12, 16 bits wide
  assign or_13_out = or_12_out | sixt_bit_gatekeeper_6_out_3;  // OR_Gate or_13, 16 bits wide
  assign or_14_out = or_13_out | sixt_bit_gatekeeper_7_out_3;  // OR_Gate or_14, 16 bits wide
  assign or_15_out = or_14_out | sixt_bit_gatekeeper_8_out_3;  // OR_Gate or_15, 16 bits wide
  assign or_16_out = or_15_out | sixt_bit_gatekeeper_9_out_3;  // OR_Gate or_16, 16 bits wide
  assign or_17_out = or_16_out | sixt_bit_gatekeeper_10_out_3;  // OR_Gate or_17, 16 bits wide
  assign or_18_out = or_17_out | sixt_bit_gatekeeper_11_out_3;  // OR_Gate or_18, 16 bits wide
  assign or_19_out = or_18_out | sixt_bit_gatekeeper_21_out_3;  // OR_Gate or_19, 16 bits wide
  sixt_bit_gatekeeper sixt_bit_gatekeeper_22 (.in_1(four_bit_eq_cmp_1_out_3), .in_2(or_19_out), .out_3(out_6));

  // Notes on the sheet:
  //   Unsigned Cmp
  //   Signed Cmp
  //   Add
  //   Subtract
  //   Multiply
  //   Increment
  //   Decrement
  //   Negate
  //   cmp0
  //   AND
  //   OR
  //   XOR
  //   NOT
  //   <<
  //   >>
  //   Bit shift
endmodule

module mmio_registers (
  input  [15:0] data_in,
  input  [1:0] reg_select,
  input  write,
  input  clock,
  input  reset,
  output [15:0] value_out,
  output [15:0] out_7,
  output [15:0] out_8,
  output [15:0] out_9,
  output [15:0] out_10
);

  wire and_1_out, and_2_out, and_3_out, and_4_out, decoder_1_out0, decoder_1_out1, decoder_1_out2,
       decoder_1_out3;
  wire [15:0] sixt_bit_gatekeeper_1_out_3, sixt_bit_gatekeeper_2_out_3, sixt_bit_gatekeeper_3_out_3,
       sixt_bit_gatekeeper_4_out_3;

  Decoder #(.enable("false"), .select(2)) decoder_1 (
    .out0(decoder_1_out0), .out1(decoder_1_out1), .out2(decoder_1_out2), .out3(decoder_1_out3),
    .sel(reg_select));
  Register #(.width(16)) register_1 (.D(data_in), .en(and_1_out), .clk(clock), .Q(out_7), .clr(reset));
  and and_1 (and_1_out, decoder_1_out0, write);
  Register #(.width(16)) register_2 (.D(data_in), .en(and_2_out), .clk(clock), .Q(out_8), .clr(reset));
  and and_2 (and_2_out, decoder_1_out1, write);
  Register #(.width(16)) register_3 (.D(data_in), .en(and_3_out), .clk(clock), .Q(out_9), .clr(reset));
  and and_3 (and_3_out, decoder_1_out2, write);
  Register #(.width(16)) register_4 (.D(data_in), .en(and_4_out), .clk(clock), .Q(out_10), .clr(reset));
  and and_4 (and_4_out, decoder_1_out3, write);
  sixt_bit_gatekeeper sixt_bit_gatekeeper_1 (.in_1(decoder_1_out0), .in_2(out_7), .out_3(sixt_bit_gatekeeper_1_out_3));
  sixt_bit_gatekeeper sixt_bit_gatekeeper_2 (.in_1(decoder_1_out1), .in_2(out_8), .out_3(sixt_bit_gatekeeper_2_out_3));
  sixt_bit_gatekeeper sixt_bit_gatekeeper_3 (.in_1(decoder_1_out2), .in_2(out_9), .out_3(sixt_bit_gatekeeper_3_out_3));
  sixt_bit_gatekeeper sixt_bit_gatekeeper_4 (.in_1(decoder_1_out3), .in_2(out_10), .out_3(sixt_bit_gatekeeper_4_out_3));
  assign value_out = sixt_bit_gatekeeper_1_out_3 | sixt_bit_gatekeeper_2_out_3 | sixt_bit_gatekeeper_3_out_3 | sixt_bit_gatekeeper_4_out_3;  // OR_Gate or_1, 16 bits wide
endmodule

module control_box (
  input  [15:0] program_kounter,
  input  [15:0] control_bus_1,
  input  pause,
  input  resume,
  input  [15:0] instr,
  input  [15:0] instr_breakpoint,
  input  [15:0] pk_breakpoint,
  input  clock_in,
  input  reset_in,
  output clock_out,
  output reset_out,
  output out_12
);

  wire and_1_out, and_2_out, and_3_out, and_4_out, and_5_out, buffer_1_out, buffer_2_out, buffer_3_out,
       buffer_4_out, buffer_5_out, buffer_6_out, buffer_7_out, buffer_8_out, buffer_9_out, buffer_10_out,
       buffer_11_out, buffer_12_out, buffer_13_out, buffer_14_out, buffer_16_out, buffer_17_out,
       buffer_18_out, buffer_19_out, buffer_20_out, buffer_21_out, buffer_22_out, buffer_23_out,
       buffer_24_out, buffer_26_out, buffer_27_out, or_1_out, or_2_out, or_3_out, pull_resistor_2_node,
       sixt_bit_eq_cmp_1_out_3, sixt_bit_eq_cmp_2_out_3, sixt_bit_eq_cmp_3_out_3, sixt_bit_eq_cmp_4_out_3;

  and and_1 (and_1_out, clock_in, ~reset_in);  // AND_Gate
  buf buffer_1 (buffer_1_out, 1'b1);
  buf buffer_2 (buffer_2_out, buffer_1_out);
  buf buffer_3 (buffer_3_out, buffer_2_out);
  buf buffer_4 (buffer_4_out, buffer_5_out);
  buf buffer_5 (buffer_5_out, buffer_6_out);
  buf buffer_6 (buffer_6_out, buffer_7_out);
  buf buffer_7 (buffer_7_out, buffer_13_out);
  buf buffer_8 (buffer_8_out, buffer_4_out);
  buf buffer_9 (buffer_9_out, buffer_8_out);
  buf buffer_10 (buffer_10_out, buffer_9_out);
  Pull_Resistor #(.pull(1)) pull_resistor_1 (.node(instr_breakpoint));
  Pull_Resistor pull_resistor_2 (.node(pull_resistor_2_node));
  buf buffer_11 (buffer_11_out, buffer_3_out);
  buf buffer_12 (buffer_12_out, buffer_11_out);
  buf buffer_13 (buffer_13_out, buffer_12_out);
  buf buffer_14 (buffer_14_out, buffer_10_out);
  buf buffer_15 (pull_resistor_2_node, buffer_14_out);
  sixt_bit_eq_cmp sixt_bit_eq_cmp_1 (.in_1(instr_breakpoint), .in_2(instr), .out_3(sixt_bit_eq_cmp_1_out_3));
  and and_2 (and_2_out, 1'b1, ~pull_resistor_2_node);  // AND_Gate
  sixt_bit_eq_cmp sixt_bit_eq_cmp_2 (.in_1(pk_breakpoint), .in_2({16{1'b1}}), .out_3(sixt_bit_eq_cmp_2_out_3));
  Pull_Resistor #(.pull(1)) pull_resistor_3 (.node(pk_breakpoint));
  or or_1 (or_1_out, reset_in, and_2_out);
  buf buffer_16 (buffer_16_out, or_1_out);
  buf buffer_17 (buffer_17_out, buffer_16_out);
  sixt_bit_eq_cmp sixt_bit_eq_cmp_3 (.in_1(program_kounter), .in_2(pk_breakpoint), .out_3(sixt_bit_eq_cmp_3_out_3));
  buf buffer_18 (buffer_18_out, buffer_17_out);
  buf buffer_19 (buffer_19_out, buffer_18_out);
  buf buffer_20 (buffer_20_out, buffer_19_out);
  buf buffer_21 (buffer_21_out, buffer_20_out);
  sixt_bit_eq_cmp sixt_bit_eq_cmp_4 (.in_1(16'h11), .in_2(control_bus_1), .out_3(sixt_bit_eq_cmp_4_out_3));
  Pull_Resistor pull_resistor_4 (.node(pause));
  and and_3 (and_3_out, ~sixt_bit_eq_cmp_2_out_3, and_4_out);  // AND_Gate
  and and_4 (and_4_out, sixt_bit_eq_cmp_3_out_3, sixt_bit_eq_cmp_4_out_3);
  buf buffer_22 (buffer_22_out, buffer_21_out);
  buf buffer_23 (buffer_23_out, buffer_22_out);
  buf buffer_24 (buffer_24_out, buffer_23_out);
  buf buffer_25 (reset_out, buffer_24_out);
  or or_2 (or_2_out, and_3_out, pause, sixt_bit_eq_cmp_1_out_3);
  buf buffer_26 (buffer_26_out, or_2_out);
  and and_5 (and_5_out, or_2_out, ~buffer_27_out);  // AND_Gate
  buf buffer_27 (buffer_27_out, buffer_26_out);
  S_R_Flip_Flop s_r_ff_1 (.Q(out_12), .reset(or_3_out), .preset(and_5_out));  // open: S, R, clk, Qn
  or or_3 (or_3_out, reset_out, resume);
  Pull_Resistor #(.pull(1)) pull_resistor_5 (.node(resume));
  Pull_Resistor pull_resistor_6 (.node(out_12));
  and and_6 (clock_out, ~out_12, and_1_out);  // AND_Gate
endmodule

module control_bus_controller (
  input  [15:0] control_1,
  input  [15:0] control_2,
  input  clock,
  input  reset,
  output [15:0] control_bus_1,
  output [15:0] control_bus_2
);

  Register #(.width(16)) register_1 (.D(control_1), .clk(clock), .Q(control_bus_1), .clr(reset));  // open: en
  Register #(.width(16)) register_2 (.D(control_2), .clk(clock), .Q(control_bus_2), .clr(reset));  // open: en
endmodule

module data_bus_controller (
  input  [15:0] control_bus_1,
  input  [15:0] control_bus_2,
  input  [15:0] addr_bus_in,
  input  clock,
  input  reset,
  input  [15:0] control_unit_in,
  input  [15:0] registers_in,
  input  [15:0] special_registers_in,
  input  [15:0] ALU_in,
  input  [15:0] memory_in,
  input  [15:0] io_in,
  output [15:0] data_bus_out
);

  wire nor_1_out, or_1_out, sixt_bit_eq_cmp_1_out_3, sixt_bit_eq_cmp_2_out_3, sixt_bit_eq_cmp_3_out_3,
       sixt_bit_eq_cmp_4_out_3;
  wire [15:0] multiplexer_1_out, or_2_out;

  sixt_bit_eq_cmp sixt_bit_eq_cmp_1 (.in_1(control_bus_1), .in_2(16'h50), .out_3(sixt_bit_eq_cmp_1_out_3));
  sixt_bit_eq_cmp sixt_bit_eq_cmp_2 (.in_1(control_bus_1), .in_2(16'h52), .out_3(sixt_bit_eq_cmp_2_out_3));
  sixt_bit_eq_cmp sixt_bit_eq_cmp_3 (.in_1(control_bus_2), .in_2(16'h50), .out_3(sixt_bit_eq_cmp_3_out_3));
  sixt_bit_eq_cmp sixt_bit_eq_cmp_4 (.in_1(control_bus_2), .in_2(16'h52), .out_3(sixt_bit_eq_cmp_4_out_3));
  nor nor_1 (nor_1_out, sixt_bit_eq_cmp_1_out_3, sixt_bit_eq_cmp_3_out_3);
  or or_1 (or_1_out, sixt_bit_eq_cmp_2_out_3, sixt_bit_eq_cmp_4_out_3);
  assign or_2_out = control_unit_in | registers_in | special_registers_in | ALU_in | memory_in | io_in;  // OR_Gate or_2, 16 bits wide
  Register #(.width(16)) register_1 (.D(multiplexer_1_out), .en(nor_1_out), .clk(clock), .Q(data_bus_out), .clr(reset));
  Multiplexer #(.width(16)) multiplexer_1 (.in0(or_2_out), .in1(addr_bus_in), .out(multiplexer_1_out), .sel(or_1_out));
endmodule
module addr_bus_controller (
  input  [15:0] control_bus_1,
  input  [15:0] control_bus_2,
  input  [15:0] data_bus_in,
  input  clock,
  input  reset,
  input  [15:0] control_unit_in,
  input  [15:0] registers_in,
  input  [15:0] special_registers_in,
  output [15:0] addr_bus_out
);

  wire nor_1_out, or_1_out, sixt_bit_eq_cmp_1_out_3, sixt_bit_eq_cmp_2_out_3, sixt_bit_eq_cmp_3_out_3,
       sixt_bit_eq_cmp_4_out_3;
  wire [15:0] multiplexer_1_out, or_2_out;

  sixt_bit_eq_cmp sixt_bit_eq_cmp_1 (.in_1(control_bus_1), .in_2(16'h51), .out_3(sixt_bit_eq_cmp_1_out_3));
  sixt_bit_eq_cmp sixt_bit_eq_cmp_2 (.in_1(control_bus_1), .in_2(16'h53), .out_3(sixt_bit_eq_cmp_2_out_3));
  sixt_bit_eq_cmp sixt_bit_eq_cmp_3 (.in_1(control_bus_2), .in_2(16'h51), .out_3(sixt_bit_eq_cmp_3_out_3));
  sixt_bit_eq_cmp sixt_bit_eq_cmp_4 (.in_1(control_bus_2), .in_2(16'h53), .out_3(sixt_bit_eq_cmp_4_out_3));
  nor nor_1 (nor_1_out, sixt_bit_eq_cmp_1_out_3, sixt_bit_eq_cmp_3_out_3);
  or or_1 (or_1_out, sixt_bit_eq_cmp_2_out_3, sixt_bit_eq_cmp_4_out_3);
  Register #(.trigger("falling"), .width(16)) register_1 (
    .D(multiplexer_1_out), .en(nor_1_out), .clk(clock), .Q(addr_bus_out), .clr(reset));
  assign or_2_out = control_unit_in | registers_in | special_registers_in;  // OR_Gate or_2, 16 bits wide
  Multiplexer #(.width(16)) multiplexer_1 (.in0(or_2_out), .in1(data_bus_in), .out(multiplexer_1_out), .sel(or_1_out));
endmodule

module mem_ctrl (
  input  [15:0] data_bus_in,
  input  [15:0] addr_in,
  input  [15:0] offset_in,
  input  [15:0] pk_in,
  input  [15:0] tmpc_in,
  input  [15:0] sp_in,
  input  [15:0] mem_in,
  input  [15:0] rom_in,
  input  [15:0] mmio_reg_in,
  input  [15:0] control_bus_1,
  input  [15:0] control_bus_2,
  input  clock,
  input  reset,
  output [15:0] mem_addr_out,
  output [15:0] data_to_mem,
  output mem_write,
  output [11:0] rom_addr_out,
  output [1:0] reg_select,
  output [15:0] data_to_reg,
  output reg_write,
  output [15:0] data_bus_out
);

  wire addr_router_1_read_out, addr_router_2_read_out, addr_router_3_read_out,
       mem_ctrl_dual_opdec_1_data_as_addr, mem_ctrl_dual_opdec_1_data_as_offset,
       mem_ctrl_dual_opdec_1_faddrout, mem_ctrl_dual_opdec_1_read, mem_ctrl_dual_opdec_1_sp_to_addr,
       mem_ctrl_dual_opdec_1_tmpc_as_offset, mem_ctrl_dual_opdec_1_use_offset, mem_ctrl_dual_opdec_1_write,
       or_1_out;
  wire [15:0] adder_1_out, addr_router_1_addr_out, multiplexer_1_out, multiplexer_2_out, multiplexer_3_out,
       multiplexer_4_out, multiplexer_5_out, multiplexer_6_out, register_1_q, register_2_q, register_3_q,
       sixt_bit_adder_1_out_3, sixt_bit_gatekeeper_1_out_3, sixt_bit_gatekeeper_2_out_3,
       sixt_bit_gatekeeper_3_out_3, sixt_bit_gatekeeper_4_out_3;
  wire [15:2] addr_router_3_addr_out;
  wire [15:12] addr_router_2_addr_out;

  Register #(.trigger("falling"), .width(16)) register_1 (
    .D(data_bus_in), .clk(clock), .Q(register_1_q), .clr(reset));  // open: en
  Register #(.width(16)) register_2 (
    .D(data_bus_in), .clk(mem_ctrl_dual_opdec_1_write), .Q(register_2_q), .clr(reset));  // open: en
  Register #(.width(16)) register_3 (
    .D(addr_in), .clk(mem_ctrl_dual_opdec_1_write), .Q(register_3_q), .clr(reset));  // open: en
  mem_ctrl_dual_opdec mem_ctrl_dual_opdec_1 (
    .ctl_bus_1(control_bus_1), .ctl_bus_2(control_bus_2), .write(mem_ctrl_dual_opdec_1_write),
    .read(mem_ctrl_dual_opdec_1_read), .faddrout(mem_ctrl_dual_opdec_1_faddrout),
    .sp_to_addr(mem_ctrl_dual_opdec_1_sp_to_addr), .data_as_addr(mem_ctrl_dual_opdec_1_data_as_addr),
    .tmpc_as_offset(mem_ctrl_dual_opdec_1_tmpc_as_offset),
    .data_as_offset(mem_ctrl_dual_opdec_1_data_as_offset), .use_offset(mem_ctrl_dual_opdec_1_use_offset));  // open: load_tmpc
  Multiplexer #(.width(16)) multiplexer_1 (
    .in0(addr_in), .in1(register_3_q), .out(multiplexer_1_out), .sel(mem_ctrl_dual_opdec_1_write));
  Multiplexer #(.width(16)) multiplexer_2 (
    .in0(offset_in), .in1(register_1_q), .out(multiplexer_2_out), .sel(mem_ctrl_dual_opdec_1_data_as_offset));
  Multiplexer #(.width(16)) multiplexer_3 (
    .in0(register_1_q), .in1(register_2_q), .out(multiplexer_3_out), .sel(mem_ctrl_dual_opdec_1_write));
  Multiplexer #(.width(16)) multiplexer_4 (
    .in0(multiplexer_1_out), .in1(register_1_q), .out(multiplexer_4_out),
    .sel(mem_ctrl_dual_opdec_1_data_as_addr));
  sixt_bit_adder sixt_bit_adder_1 (
    .in_1(multiplexer_4_out), .in_2(multiplexer_5_out), .out_3(sixt_bit_adder_1_out_3));  // open: out_4
  Multiplexer #(.width(16)) multiplexer_5 (
    .in0(multiplexer_2_out), .in1(tmpc_in), .out(multiplexer_5_out),
    .sel(mem_ctrl_dual_opdec_1_tmpc_as_offset));
  Multiplexer #(.width(16)) multiplexer_6 (
    .in0(multiplexer_4_out), .in1(sixt_bit_adder_1_out_3), .out(multiplexer_6_out),
    .sel(mem_ctrl_dual_opdec_1_use_offset));
  Adder #(.width(16)) adder_1 (.a(16'hf000), .b({16{1'b0}}), .out(adder_1_out));  // open: cin, cout
  addr_router addr_router_1 (
    .default_if_inactive(1'b1), .waiting_for_addr(clock), .lower_bound({16{1'b0}}), .upper_bound(16'hf000),
    .addr_in(multiplexer_6_out), .data_in(multiplexer_3_out), .read(mem_ctrl_dual_opdec_1_read),
    .write(mem_ctrl_dual_opdec_1_write), .addr_default(pk_in), .read_out(addr_router_1_read_out),
    .write_out(mem_write), .addr_out(addr_router_1_addr_out), .data_out(data_to_mem));  // open: active
  addr_router addr_router_2 (
    .waiting_for_addr(clock), .lower_bound(16'hf000), .upper_bound(16'hfffc), .addr_in(multiplexer_6_out),
    .data_in(multiplexer_3_out), .read(mem_ctrl_dual_opdec_1_read), .write(mem_ctrl_dual_opdec_1_write),
    .addr_default(pk_in), .read_out(addr_router_2_read_out), .addr_out({addr_router_2_addr_out, rom_addr_out}));  // open: default_if_inactive, active, write_out, data_out
  addr_router addr_router_3 (
    .waiting_for_addr(clock), .lower_bound(16'hfffc), .upper_bound({16{1'b1}}), .addr_in(multiplexer_6_out),
    .data_in(multiplexer_3_out), .read(mem_ctrl_dual_opdec_1_read), .write(mem_ctrl_dual_opdec_1_write),
    .read_out(addr_router_3_read_out), .write_out(reg_write),
    .addr_out({addr_router_3_addr_out, reg_select}), .data_out(data_to_reg));  // open: default_if_inactive, addr_default, active
  or or_1 (or_1_out, addr_router_1_read_out, mem_ctrl_dual_opdec_1_sp_to_addr);
  sixt_bit_gatekeeper sixt_bit_gatekeeper_1 (.in_1(or_1_out), .in_2(mem_in), .out_3(sixt_bit_gatekeeper_1_out_3));
  sixt_bit_gatekeeper sixt_bit_gatekeeper_2 (
    .in_1(addr_router_2_read_out), .in_2(rom_in), .out_3(sixt_bit_gatekeeper_2_out_3));
  sixt_bit_gatekeeper sixt_bit_gatekeeper_3 (
    .in_1(addr_router_3_read_out), .in_2(mmio_reg_in), .out_3(sixt_bit_gatekeeper_3_out_3));
  sixt_bit_gatekeeper sixt_bit_gatekeeper_4 (
    .in_1(mem_ctrl_dual_opdec_1_faddrout), .in_2(adder_1_out), .out_3(sixt_bit_gatekeeper_4_out_3));
  assign data_bus_out = sixt_bit_gatekeeper_1_out_3 | sixt_bit_gatekeeper_2_out_3 | sixt_bit_gatekeeper_3_out_3 | sixt_bit_gatekeeper_4_out_3;  // OR_Gate or_2, 16 bits wide
  Multiplexer #(.width(16)) multiplexer_7 (
    .in0(addr_router_1_addr_out), .in1(sp_in), .out(mem_addr_out), .sel(mem_ctrl_dual_opdec_1_sp_to_addr));
endmodule

module addr_router (
  input  default_if_inactive,
  input  waiting_for_addr,
  input  [15:0] addr_default,
  input  [15:0] lower_bound,
  input  [15:0] upper_bound,
  input  [15:0] addr_in,
  input  [15:0] data_in,
  input  read,
  input  write,
  output active,
  output [15:0] addr_out,
  output [15:0] data_out,
  output read_out,
  output write_out
);

  wire and_4_out, comparator_1_lt, comparator_2_lt, not_1_out, or_1_out, or_2_out, or_3_out,
       sixt_bit_eq_cmp_1_out_3;
  wire [15:0] sixt_bit_gatekeeper_1_out_3, subtractor_1_out;

  Pull_Resistor pull_resistor_1 (.node(default_if_inactive));
  Pull_Resistor pull_resistor_2 (.node(waiting_for_addr));
  Pull_Resistor pull_resistor_3 (.node(lower_bound));
  Pull_Resistor #(.pull(1)) pull_resistor_4 (.node(upper_bound));
  sixt_bit_eq_cmp sixt_bit_eq_cmp_1 (.in_1({16{1'b1}}), .in_2(upper_bound), .out_3(sixt_bit_eq_cmp_1_out_3));
  Comparator #(.mode("unsigned"), .width(16)) comparator_1 (
    .a(addr_in), .b(lower_bound), .lt(comparator_1_lt));  // open: gt, eq
  Comparator #(.mode("unsigned"), .width(16)) comparator_2 (
    .a(addr_in), .b(upper_bound), .lt(comparator_2_lt));  // open: gt, eq
  Subtractor #(.width(16)) subtractor_1 (.a(addr_in), .b(lower_bound), .out(subtractor_1_out));  // open: bin, bout
  not not_1 (not_1_out, comparator_1_lt);
  or or_1 (or_1_out, sixt_bit_eq_cmp_1_out_3, comparator_2_lt);
  and and_1 (active, not_1_out, or_1_out, or_2_out);
  or or_2 (or_2_out, read, write);
  or or_3 (or_3_out, waiting_for_addr, ~active);  // OR_Gate
  sixt_bit_gatekeeper sixt_bit_gatekeeper_1 (
    .in_1(active), .in_2(subtractor_1_out), .out_3(sixt_bit_gatekeeper_1_out_3));
  sixt_bit_gatekeeper sixt_bit_gatekeeper_2 (.in_1(active), .in_2(data_in), .out_3(data_out));
  and and_2 (read_out, active, read);
  and and_3 (write_out, active, write);
  Pull_Resistor pull_resistor_5 (.node(addr_default));
  and and_4 (and_4_out, or_3_out, default_if_inactive);
  Multiplexer #(.width(16)) multiplexer_1 (
    .in0(sixt_bit_gatekeeper_1_out_3), .in1(addr_default), .out(addr_out), .sel(and_4_out));
endmodule

module mem_ctrl_opdec (
  input  [15:0] control,
  output load_tmpc,
  output read,
  output write,
  output use_offset,
  output tmpc_as_offset,
  output data_as_offset,
  output data_as_addr,
  output sp_to_addr,
  output firmware_addr_out
);

  wire eight_bit_eq_cmp_1_out_3, eight_bit_eq_cmp_2_out_3, eight_bit_eq_cmp_3_out_3,
       eight_bit_eq_cmp_4_out_3, eight_bit_eq_cmp_5_out_3, eight_bit_eq_cmp_6_out_3,
       eight_bit_eq_cmp_7_out_3, eight_bit_eq_cmp_8_out_3, eight_bit_eq_cmp_9_out_3, or_2_out, or_3_out,
       or_4_out, or_5_out, or_6_out, or_9_out, or_10_out, or_11_out, sixt_bit_eq_cmp_2_out_3;

  sixt_bit_eq_cmp sixt_bit_eq_cmp_1 (.in_1(16'h1), .in_2(control), .out_3(load_tmpc));
  sixt_bit_eq_cmp sixt_bit_eq_cmp_2 (.in_1(control), .in_2(16'h1013), .out_3(sixt_bit_eq_cmp_2_out_3));
  eight_bit_eq_cmp eight_bit_eq_cmp_1 (.in_1(control[7:0]), .in_2(8'h4), .out_3(eight_bit_eq_cmp_1_out_3));
  eight_bit_eq_cmp eight_bit_eq_cmp_2 (.in_1(control[7:0]), .in_2(8'h5), .out_3(eight_bit_eq_cmp_2_out_3));
  eight_bit_eq_cmp eight_bit_eq_cmp_3 (.in_1(control[7:0]), .in_2(8'h11), .out_3(eight_bit_eq_cmp_3_out_3));
  eight_bit_eq_cmp eight_bit_eq_cmp_4 (.in_1(control[7:0]), .in_2(8'h22), .out_3(eight_bit_eq_cmp_4_out_3));
  eight_bit_eq_cmp eight_bit_eq_cmp_5 (.in_1(control[7:0]), .in_2(8'h23), .out_3(eight_bit_eq_cmp_5_out_3));
  eight_bit_eq_cmp eight_bit_eq_cmp_6 (.in_1(control[7:0]), .in_2(8'h25), .out_3(eight_bit_eq_cmp_6_out_3));
  eight_bit_eq_cmp eight_bit_eq_cmp_7 (.in_1(control[7:0]), .in_2(8'h26), .out_3(eight_bit_eq_cmp_7_out_3));
  eight_bit_eq_cmp eight_bit_eq_cmp_8 (.in_1(control[7:0]), .in_2(8'h27), .out_3(eight_bit_eq_cmp_8_out_3));
  eight_bit_eq_cmp eight_bit_eq_cmp_9 (.in_1(control[7:0]), .in_2(8'h28), .out_3(eight_bit_eq_cmp_9_out_3));
  eight_bit_eq_cmp eight_bit_eq_cmp_10 (.in_1(control[7:0]), .in_2(8'h29), .out_3(tmpc_as_offset));
  eight_bit_eq_cmp eight_bit_eq_cmp_11 (.in_1(control[7:0]), .in_2(8'h2a), .out_3(data_as_offset));
  eight_bit_eq_cmp eight_bit_eq_cmp_12 (.in_1(control[7:0]), .in_2(8'h2b), .out_3(data_as_addr));
  eight_bit_eq_cmp eight_bit_eq_cmp_13 (.in_1(control[7:0]), .in_2(8'h62), .out_3(sp_to_addr));
  eight_bit_eq_cmp eight_bit_eq_cmp_14 (.in_1(control[7:0]), .in_2(8'h7a), .out_3(firmware_addr_out));
  or or_1 (read, sixt_bit_eq_cmp_2_out_3, or_2_out);
  or or_2 (or_2_out, eight_bit_eq_cmp_1_out_3, or_3_out);
  or or_3 (or_3_out, eight_bit_eq_cmp_2_out_3, or_4_out);
  or or_4 (or_4_out, eight_bit_eq_cmp_3_out_3, or_5_out);
  or or_5 (or_5_out, eight_bit_eq_cmp_4_out_3, or_6_out);
  or or_6 (or_6_out, eight_bit_eq_cmp_5_out_3, or_9_out);
  or or_7 (write, eight_bit_eq_cmp_6_out_3, eight_bit_eq_cmp_7_out_3);
  or or_8 (use_offset, eight_bit_eq_cmp_2_out_3, or_10_out);
  or or_9 (or_9_out, eight_bit_eq_cmp_8_out_3, eight_bit_eq_cmp_9_out_3);
  or or_10 (or_10_out, eight_bit_eq_cmp_5_out_3, or_11_out);
  or or_11 (or_11_out, eight_bit_eq_cmp_7_out_3, eight_bit_eq_cmp_9_out_3);
endmodule

module mem_ctrl_dual_opdec (
  input  [15:0] ctl_bus_1,
  input  [15:0] ctl_bus_2,
  output faddrout,
  output sp_to_addr,
  output data_as_addr,
  output tmpc_as_offset,
  output data_as_offset,
  output use_offset,
  output write,
  output read,
  output load_tmpc
);

  wire mem_ctrl_opdec_1_data_as_addr, mem_ctrl_opdec_1_data_as_offset, mem_ctrl_opdec_1_firmware_addr_out,
       mem_ctrl_opdec_1_load_tmpc, mem_ctrl_opdec_1_read, mem_ctrl_opdec_1_sp_to_addr,
       mem_ctrl_opdec_1_tmpc_as_offset, mem_ctrl_opdec_1_use_offset, mem_ctrl_opdec_1_write,
       mem_ctrl_opdec_2_data_as_addr, mem_ctrl_opdec_2_data_as_offset, mem_ctrl_opdec_2_firmware_addr_out,
       mem_ctrl_opdec_2_load_tmpc, mem_ctrl_opdec_2_read, mem_ctrl_opdec_2_sp_to_addr,
       mem_ctrl_opdec_2_tmpc_as_offset, mem_ctrl_opdec_2_use_offset, mem_ctrl_opdec_2_write;

  mem_ctrl_opdec mem_ctrl_opdec_1 (
    .control(ctl_bus_1), .load_tmpc(mem_ctrl_opdec_1_load_tmpc), .read(mem_ctrl_opdec_1_read),
    .write(mem_ctrl_opdec_1_write), .use_offset(mem_ctrl_opdec_1_use_offset),
    .tmpc_as_offset(mem_ctrl_opdec_1_tmpc_as_offset), .data_as_offset(mem_ctrl_opdec_1_data_as_offset),
    .data_as_addr(mem_ctrl_opdec_1_data_as_addr), .sp_to_addr(mem_ctrl_opdec_1_sp_to_addr),
    .firmware_addr_out(mem_ctrl_opdec_1_firmware_addr_out));
  mem_ctrl_opdec mem_ctrl_opdec_2 (
    .control(ctl_bus_2), .load_tmpc(mem_ctrl_opdec_2_load_tmpc), .read(mem_ctrl_opdec_2_read),
    .write(mem_ctrl_opdec_2_write), .use_offset(mem_ctrl_opdec_2_use_offset),
    .tmpc_as_offset(mem_ctrl_opdec_2_tmpc_as_offset), .data_as_offset(mem_ctrl_opdec_2_data_as_offset),
    .data_as_addr(mem_ctrl_opdec_2_data_as_addr), .sp_to_addr(mem_ctrl_opdec_2_sp_to_addr),
    .firmware_addr_out(mem_ctrl_opdec_2_firmware_addr_out));
  or or_1 (faddrout, mem_ctrl_opdec_2_firmware_addr_out, mem_ctrl_opdec_1_firmware_addr_out);
  or or_2 (sp_to_addr, mem_ctrl_opdec_2_sp_to_addr, mem_ctrl_opdec_1_sp_to_addr);
  or or_3 (data_as_addr, mem_ctrl_opdec_2_data_as_addr, mem_ctrl_opdec_1_data_as_addr);
  or or_4 (tmpc_as_offset, mem_ctrl_opdec_2_tmpc_as_offset, mem_ctrl_opdec_1_tmpc_as_offset);
  or or_5 (data_as_offset, mem_ctrl_opdec_2_data_as_offset, mem_ctrl_opdec_1_data_as_offset);
  or or_6 (use_offset, mem_ctrl_opdec_2_use_offset, mem_ctrl_opdec_1_use_offset);
  or or_7 (write, mem_ctrl_opdec_1_write, mem_ctrl_opdec_2_write);
  or or_8 (read, mem_ctrl_opdec_1_read, mem_ctrl_opdec_2_read);
  or or_9 (load_tmpc, mem_ctrl_opdec_1_load_tmpc, mem_ctrl_opdec_2_load_tmpc);
endmodule

module counting_register (
  input  [15:0] data_in,
  input  [3:0] param,
  input  increment,
  input  decrement,
  input  write,
  input  clk,
  input  reset,
  output [15:0] out_8
);

  wire or_1_out;
  wire [15:0] adder_1_out, bit_extender_1_out, multiplexer_1_out, multiplexer_2_out, register_1_q,
       subtractor_1_out;

  Register #(.width(16)) register_1 (.D(multiplexer_1_out), .en(or_1_out), .clk(clk), .Q(register_1_q), .clr(reset));
  Multiplexer #(.width(16)) multiplexer_1 (
    .in0(multiplexer_2_out), .in1(data_in), .out(multiplexer_1_out), .sel(write));
  assign bit_extender_1_out = {{12{1'b0}}, param};  // Bit_Extender bit_extender_1
  or or_1 (or_1_out, increment, decrement, write);
  Adder #(.width(16)) adder_1 (.a(register_1_q), .b(bit_extender_1_out), .out(adder_1_out), .cin(1'b1));  // open: cout
  Subtractor #(.width(16)) subtractor_1 (
    .a(register_1_q), .b(bit_extender_1_out), .out(subtractor_1_out), .bin(1'b1));  // open: bout
  Adder #(.width(16)) adder_2 (.a(register_1_q), .b(bit_extender_1_out), .out(out_8));  // open: cin, cout
  Multiplexer #(.width(16)) multiplexer_2 (
    .in0(adder_1_out), .in1(subtractor_1_out), .out(multiplexer_2_out), .sel(decrement));
endmodule

module sixt_bit_adder (
  input  [15:0] in_1,
  input  [15:0] in_2,
  output [15:0] out_3,
  output out_4
);

  wire and_1_out, and_2_out, and_3_out, and_4_out, and_5_out, and_6_out, and_7_out, and_8_out, and_9_out,
       and_10_out, and_11_out, and_12_out, and_13_out, and_14_out, and_15_out, and_16_out, and_17_out,
       and_18_out, and_19_out, and_20_out, and_21_out, and_22_out, and_23_out, and_24_out, and_25_out,
       and_26_out, and_27_out, and_28_out, and_29_out, and_30_out, and_31_out, xor_2_out, xor_3_out,
       xor_4_out, xor_5_out, xor_6_out, xor_7_out, xor_8_out, xor_9_out, xor_10_out, xor_11_out, xor_12_out,
       xor_13_out, xor_14_out, xor_15_out, xor_16_out, xor_32_out, xor_33_out, xor_34_out, xor_35_out,
       xor_36_out, xor_37_out, xor_38_out, xor_39_out, xor_40_out, xor_41_out, xor_42_out, xor_43_out,
       xor_44_out, xor_45_out;

  xor xor_1 (out_3[0], in_1[0], in_2[0]);
  and and_1 (and_1_out, in_1[0], in_2[0]);
  xor xor_2 (xor_2_out, in_1[1], in_2[1]);
  and and_2 (and_2_out, in_1[1], in_2[1]);
  xor xor_3 (xor_3_out, in_1[2], in_2[2]);
  and and_3 (and_3_out, in_1[2], in_2[2]);
  xor xor_4 (xor_4_out, in_1[3], in_2[3]);
  and and_4 (and_4_out, in_1[3], in_2[3]);
  xor xor_5 (xor_5_out, in_1[4], in_2[4]);
  and and_5 (and_5_out, in_1[4], in_2[4]);
  xor xor_6 (xor_6_out, in_1[5], in_2[5]);
  and and_6 (and_6_out, in_1[5], in_2[5]);
  xor xor_7 (xor_7_out, in_1[6], in_2[6]);
  and and_7 (and_7_out, in_1[6], in_2[6]);
  xor xor_8 (xor_8_out, in_1[7], in_2[7]);
  and and_8 (and_8_out, in_1[7], in_2[7]);
  xor xor_9 (xor_9_out, in_1[8], in_2[8]);
  and and_9 (and_9_out, in_1[8], in_2[8]);
  xor xor_10 (xor_10_out, in_1[9], in_2[9]);
  and and_10 (and_10_out, in_1[9], in_2[9]);
  xor xor_11 (xor_11_out, in_1[10], in_2[10]);
  and and_11 (and_11_out, in_1[10], in_2[10]);
  xor xor_12 (xor_12_out, in_1[11], in_2[11]);
  and and_12 (and_12_out, in_1[11], in_2[11]);
  xor xor_13 (xor_13_out, in_1[12], in_2[12]);
  and and_13 (and_13_out, in_1[12], in_2[12]);
  xor xor_14 (xor_14_out, in_1[13], in_2[13]);
  and and_14 (and_14_out, in_1[13], in_2[13]);
  xor xor_15 (xor_15_out, in_1[14], in_2[14]);
  and and_15 (and_15_out, in_1[14], in_2[14]);
  xor xor_16 (xor_16_out, in_1[15], in_2[15]);
  and and_16 (and_16_out, in_1[15], in_2[15]);
  xor xor_17 (out_3[1], xor_2_out, and_1_out);
  and and_17 (and_17_out, xor_2_out, and_1_out);
  xor xor_18 (out_3[2], xor_3_out, xor_32_out);
  and and_18 (and_18_out, xor_3_out, xor_32_out);
  xor xor_19 (out_3[3], xor_4_out, xor_33_out);
  and and_19 (and_19_out, xor_4_out, xor_33_out);
  xor xor_20 (out_3[4], xor_5_out, xor_34_out);
  and and_20 (and_20_out, xor_5_out, xor_34_out);
  xor xor_21 (out_3[5], xor_6_out, xor_35_out);
  and and_21 (and_21_out, xor_6_out, xor_35_out);
  xor xor_22 (out_3[6], xor_7_out, xor_36_out);
  and and_22 (and_22_out, xor_7_out, xor_36_out);
  xor xor_23 (out_3[7], xor_8_out, xor_37_out);
  and and_23 (and_23_out, xor_8_out, xor_37_out);
  xor xor_24 (out_3[8], xor_9_out, xor_38_out);
  and and_24 (and_24_out, xor_9_out, xor_38_out);
  xor xor_25 (out_3[9], xor_10_out, xor_39_out);
  and and_25 (and_25_out, xor_10_out, xor_39_out);
  xor xor_26 (out_3[10], xor_11_out, xor_40_out);
  and and_26 (and_26_out, xor_11_out, xor_40_out);
  xor xor_27 (out_3[11], xor_12_out, xor_41_out);
  and and_27 (and_27_out, xor_12_out, xor_41_out);
  xor xor_28 (out_3[12], xor_13_out, xor_42_out);
  and and_28 (and_28_out, xor_13_out, xor_42_out);
  xor xor_29 (out_3[13], xor_14_out, xor_43_out);
  and and_29 (and_29_out, xor_14_out, xor_43_out);
  xor xor_30 (out_3[14], xor_15_out, xor_44_out);
  and and_30 (and_30_out, xor_15_out, xor_44_out);
  xor xor_31 (out_3[15], xor_16_out, xor_45_out);
  and and_31 (and_31_out, xor_16_out, xor_45_out);
  xor xor_32 (xor_32_out, and_2_out, and_17_out);
  xor xor_33 (xor_33_out, and_3_out, and_18_out);
  xor xor_34 (xor_34_out, and_4_out, and_19_out);
  xor xor_35 (xor_35_out, and_5_out, and_20_out);
  xor xor_36 (xor_36_out, and_6_out, and_21_out);
  xor xor_37 (xor_37_out, and_7_out, and_22_out);
  xor xor_38 (xor_38_out, and_8_out, and_23_out);
  xor xor_39 (xor_39_out, and_9_out, and_24_out);
  xor xor_40 (xor_40_out, and_10_out, and_25_out);
  xor xor_41 (xor_41_out, and_11_out, and_26_out);
  xor xor_42 (xor_42_out, and_12_out, and_27_out);
  xor xor_43 (xor_43_out, and_13_out, and_28_out);
  xor xor_44 (xor_44_out, and_14_out, and_29_out);
  xor xor_45 (xor_45_out, and_15_out, and_30_out);
  xor xor_46 (out_4, and_16_out, and_31_out);
endmodule

module sixt_bit_adder_subtractor (
  input  [15:0] in_1,
  input  [15:0] in_2,
  input  in_3,
  output [15:0] out_4,
  output out_5
);

  wire and_1_out, and_2_out, and_3_out, and_4_out, and_5_out, and_6_out, and_7_out, and_8_out, and_9_out,
       and_10_out, and_11_out, and_12_out, and_13_out, and_14_out, and_15_out, and_16_out, and_17_out,
       and_18_out, and_19_out, and_20_out, and_21_out, and_22_out, and_23_out, and_24_out, and_25_out,
       and_26_out, and_27_out, and_28_out, and_29_out, and_30_out, and_31_out, xor_2_out, xor_4_out,
       xor_6_out, xor_8_out, xor_10_out, xor_12_out, xor_14_out, xor_16_out, xor_18_out, xor_20_out,
       xor_22_out, xor_24_out, xor_26_out, xor_28_out, xor_30_out, xor_32_out, xor_33_out, xor_34_out,
       xor_35_out, xor_36_out, xor_37_out, xor_38_out, xor_39_out, xor_40_out, xor_41_out, xor_42_out,
       xor_43_out, xor_44_out, xor_45_out;
  wire [15:0] not_1_out, sixt_bit_incrementer_1_out_2, sixt_bit_selector_1_out_4;

  assign not_1_out = ~in_2;  // NOT_Gate not_1, 16 bits wide
  sixt_bit_selector sixt_bit_selector_1 (
    .in_3(sixt_bit_incrementer_1_out_2), .in_1(in_3), .in_2(in_2), .out_4(sixt_bit_selector_1_out_4));
  sixt_bit_incrementer sixt_bit_incrementer_1 (.in_1(not_1_out), .out_2(sixt_bit_incrementer_1_out_2));
  xor xor_1 (out_4[0], in_1[0], sixt_bit_selector_1_out_4[0]);
  and and_1 (and_1_out, in_1[0], sixt_bit_selector_1_out_4[0]);
  xor xor_2 (xor_2_out, in_1[1], sixt_bit_selector_1_out_4[1]);
  xor xor_3 (out_4[1], xor_2_out, and_1_out);
  and and_2 (and_2_out, in_1[1], sixt_bit_selector_1_out_4[1]);
  and and_3 (and_3_out, xor_2_out, and_1_out);
  xor xor_4 (xor_4_out, in_1[2], sixt_bit_selector_1_out_4[2]);
  xor xor_5 (out_4[2], xor_4_out, xor_32_out);
  and and_4 (and_4_out, in_1[2], sixt_bit_selector_1_out_4[2]);
  and and_5 (and_5_out, xor_4_out, xor_32_out);
  xor xor_6 (xor_6_out, in_1[3], sixt_bit_selector_1_out_4[3]);
  xor xor_7 (out_4[3], xor_6_out, xor_33_out);
  and and_6 (and_6_out, in_1[3], sixt_bit_selector_1_out_4[3]);
  and and_7 (and_7_out, xor_6_out, xor_33_out);
  xor xor_8 (xor_8_out, in_1[4], sixt_bit_selector_1_out_4[4]);
  xor xor_9 (out_4[4], xor_8_out, xor_34_out);
  and and_8 (and_8_out, in_1[4], sixt_bit_selector_1_out_4[4]);
  and and_9 (and_9_out, xor_8_out, xor_34_out);
  xor xor_10 (xor_10_out, in_1[5], sixt_bit_selector_1_out_4[5]);
  xor xor_11 (out_4[5], xor_10_out, xor_35_out);
  and and_10 (and_10_out, in_1[5], sixt_bit_selector_1_out_4[5]);
  and and_11 (and_11_out, xor_10_out, xor_35_out);
  xor xor_12 (xor_12_out, in_1[6], sixt_bit_selector_1_out_4[6]);
  xor xor_13 (out_4[6], xor_12_out, xor_36_out);
  and and_12 (and_12_out, in_1[6], sixt_bit_selector_1_out_4[6]);
  and and_13 (and_13_out, xor_12_out, xor_36_out);
  xor xor_14 (xor_14_out, in_1[7], sixt_bit_selector_1_out_4[7]);
  xor xor_15 (out_4[7], xor_14_out, xor_37_out);
  and and_14 (and_14_out, in_1[7], sixt_bit_selector_1_out_4[7]);
  and and_15 (and_15_out, xor_14_out, xor_37_out);
  xor xor_16 (xor_16_out, in_1[8], sixt_bit_selector_1_out_4[8]);
  xor xor_17 (out_4[8], xor_16_out, xor_38_out);
  and and_16 (and_16_out, in_1[8], sixt_bit_selector_1_out_4[8]);
  and and_17 (and_17_out, xor_16_out, xor_38_out);
  xor xor_18 (xor_18_out, in_1[9], sixt_bit_selector_1_out_4[9]);
  xor xor_19 (out_4[9], xor_18_out, xor_39_out);
  and and_18 (and_18_out, in_1[9], sixt_bit_selector_1_out_4[9]);
  and and_19 (and_19_out, xor_18_out, xor_39_out);
  xor xor_20 (xor_20_out, in_1[10], sixt_bit_selector_1_out_4[10]);
  xor xor_21 (out_4[10], xor_20_out, xor_40_out);
  and and_20 (and_20_out, in_1[10], sixt_bit_selector_1_out_4[10]);
  and and_21 (and_21_out, xor_20_out, xor_40_out);
  xor xor_22 (xor_22_out, in_1[11], sixt_bit_selector_1_out_4[11]);
  xor xor_23 (out_4[11], xor_22_out, xor_41_out);
  and and_22 (and_22_out, in_1[11], sixt_bit_selector_1_out_4[11]);
  and and_23 (and_23_out, xor_22_out, xor_41_out);
  xor xor_24 (xor_24_out, in_1[12], sixt_bit_selector_1_out_4[12]);
  xor xor_25 (out_4[12], xor_24_out, xor_42_out);
  and and_24 (and_24_out, in_1[12], sixt_bit_selector_1_out_4[12]);
  and and_25 (and_25_out, xor_24_out, xor_42_out);
  xor xor_26 (xor_26_out, in_1[13], sixt_bit_selector_1_out_4[13]);
  xor xor_27 (out_4[13], xor_26_out, xor_43_out);
  and and_26 (and_26_out, in_1[13], sixt_bit_selector_1_out_4[13]);
  and and_27 (and_27_out, xor_26_out, xor_43_out);
  xor xor_28 (xor_28_out, in_1[14], sixt_bit_selector_1_out_4[14]);
  xor xor_29 (out_4[14], xor_28_out, xor_44_out);
  and and_28 (and_28_out, in_1[14], sixt_bit_selector_1_out_4[14]);
  and and_29 (and_29_out, xor_28_out, xor_44_out);
  xor xor_30 (xor_30_out, in_1[15], sixt_bit_selector_1_out_4[15]);
  xor xor_31 (out_4[15], xor_30_out, xor_45_out);
  and and_30 (and_30_out, in_1[15], sixt_bit_selector_1_out_4[15]);
  and and_31 (and_31_out, xor_30_out, xor_45_out);
  xor xor_32 (xor_32_out, and_2_out, and_3_out);
  xor xor_33 (xor_33_out, and_4_out, and_5_out);
  xor xor_34 (xor_34_out, and_6_out, and_7_out);
  xor xor_35 (xor_35_out, and_8_out, and_9_out);
  xor xor_36 (xor_36_out, and_10_out, and_11_out);
  xor xor_37 (xor_37_out, and_12_out, and_13_out);
  xor xor_38 (xor_38_out, and_14_out, and_15_out);
  xor xor_39 (xor_39_out, and_16_out, and_17_out);
  xor xor_40 (xor_40_out, and_18_out, and_19_out);
  xor xor_41 (xor_41_out, and_20_out, and_21_out);
  xor xor_42 (xor_42_out, and_22_out, and_23_out);
  xor xor_43 (xor_43_out, and_24_out, and_25_out);
  xor xor_44 (xor_44_out, and_26_out, and_27_out);
  xor xor_45 (xor_45_out, and_28_out, and_29_out);
  xor xor_46 (out_5, and_30_out, and_31_out);
endmodule

module sixt_bit_incrementer (
  input  [15:0] in_1,
  output [15:0] out_2
);

  sixt_bit_adder sixt_bit_adder_1 (.in_1(16'h1), .in_2(in_1), .out_3(out_2));  // open: out_4
endmodule

module sixt_bit_decrementer (
  input  [15:0] in_1,
  output [15:0] out_2
);

  sixt_bit_adder sixt_bit_adder_1 (.in_1({16{1'b1}}), .in_2(in_1), .out_3(out_2));  // open: out_4
endmodule

module sixt_bit_selector (
  input  in_1,
  input  [15:0] in_2,
  input  [15:0] in_3,
  output [15:0] out_4
);

  wire [15:0] and_1_out, and_2_out;
  wire [15:15] not_1_out;

  not not_1 (not_1_out[15], in_1);
  assign and_1_out = {16{not_1_out[15]}} & in_2;  // AND_Gate and_1, 16 bits wide
  assign and_2_out = in_3 & {16{in_1}};  // AND_Gate and_2, 16 bits wide
  assign out_4 = and_1_out | and_2_out;  // OR_Gate or_1, 16 bits wide
endmodule

module sixt_bit_shift_by_one (
  input  [15:0] in_1,
  output [15:0] out_2
);


  assign out_2 = {in_1[14:0], 1'b0};
endmodule

module sixt_bit_gatekeeper (
  input  in_1,
  input  [15:0] in_2,
  output [15:0] out_3
);

  assign out_3 = {16{in_1}} & in_2;  // AND_Gate and_1, 16 bits wide
endmodule

module sixt_bit_gatekeeper_vert (
  input  in_1,
  input  [15:0] in_2,
  output [15:0] out_3
);

  assign out_3 = {16{in_1}} & in_2;  // AND_Gate and_1, 16 bits wide
endmodule

module sixt_bit_multuiplier (
  input  [15:0] in_1,
  input  [15:0] in_2,
  output [15:0] out_3
);

  wire [15:0] sixt_bit_adder_1_out_3, sixt_bit_adder_2_out_3, sixt_bit_adder_3_out_3, sixt_bit_adder_4_out_3,
       sixt_bit_adder_5_out_3, sixt_bit_adder_6_out_3, sixt_bit_adder_7_out_3, sixt_bit_adder_8_out_3,
       sixt_bit_adder_9_out_3, sixt_bit_adder_10_out_3, sixt_bit_adder_11_out_3, sixt_bit_adder_12_out_3,
       sixt_bit_adder_13_out_3, sixt_bit_adder_14_out_3, sixt_bit_gatekeeper_vert_1_out_3,
       sixt_bit_gatekeeper_vert_2_out_3, sixt_bit_gatekeeper_vert_3_out_3, sixt_bit_gatekeeper_vert_4_out_3,
       sixt_bit_gatekeeper_vert_5_out_3, sixt_bit_gatekeeper_vert_6_out_3, sixt_bit_gatekeeper_vert_7_out_3,
       sixt_bit_gatekeeper_vert_8_out_3, sixt_bit_gatekeeper_vert_9_out_3, sixt_bit_gatekeeper_vert_10_out_3,
       sixt_bit_gatekeeper_vert_11_out_3, sixt_bit_gatekeeper_vert_12_out_3,
       sixt_bit_gatekeeper_vert_13_out_3, sixt_bit_gatekeeper_vert_14_out_3,
       sixt_bit_gatekeeper_vert_15_out_3, sixt_bit_gatekeeper_vert_16_out_3, sixt_bit_shift_by_one_1_out_2,
       sixt_bit_shift_by_one_2_out_2, sixt_bit_shift_by_one_3_out_2, sixt_bit_shift_by_one_4_out_2,
       sixt_bit_shift_by_one_5_out_2, sixt_bit_shift_by_one_6_out_2, sixt_bit_shift_by_one_7_out_2,
       sixt_bit_shift_by_one_8_out_2, sixt_bit_shift_by_one_9_out_2, sixt_bit_shift_by_one_10_out_2,
       sixt_bit_shift_by_one_11_out_2, sixt_bit_shift_by_one_12_out_2, sixt_bit_shift_by_one_13_out_2,
       sixt_bit_shift_by_one_14_out_2, sixt_bit_shift_by_one_15_out_2;

  sixt_bit_gatekeeper_vert sixt_bit_gatekeeper_vert_1 (
    .in_1(in_1[0]), .in_2(in_2), .out_3(sixt_bit_gatekeeper_vert_1_out_3));
  sixt_bit_shift_by_one sixt_bit_shift_by_one_1 (.in_1(in_2), .out_2(sixt_bit_shift_by_one_1_out_2));
  sixt_bit_shift_by_one sixt_bit_shift_by_one_2 (
    .in_1(sixt_bit_shift_by_one_1_out_2), .out_2(sixt_bit_shift_by_one_2_out_2));
  sixt_bit_gatekeeper_vert sixt_bit_gatekeeper_vert_2 (
    .in_1(in_1[1]), .in_2(sixt_bit_shift_by_one_1_out_2), .out_3(sixt_bit_gatekeeper_vert_2_out_3));
  sixt_bit_gatekeeper_vert sixt_bit_gatekeeper_vert_3 (
    .in_1(in_1[2]), .in_2(sixt_bit_shift_by_one_2_out_2), .out_3(sixt_bit_gatekeeper_vert_3_out_3));
  sixt_bit_adder sixt_bit_adder_1 (
    .in_1(sixt_bit_gatekeeper_vert_2_out_3), .in_2(sixt_bit_gatekeeper_vert_1_out_3),
    .out_3(sixt_bit_adder_1_out_3));  // open: out_4
  sixt_bit_shift_by_one sixt_bit_shift_by_one_3 (
    .in_1(sixt_bit_shift_by_one_2_out_2), .out_2(sixt_bit_shift_by_one_3_out_2));
  sixt_bit_gatekeeper_vert sixt_bit_gatekeeper_vert_4 (
    .in_1(in_1[3]), .in_2(sixt_bit_shift_by_one_3_out_2), .out_3(sixt_bit_gatekeeper_vert_4_out_3));
  sixt_bit_adder sixt_bit_adder_2 (
    .in_1(sixt_bit_gatekeeper_vert_3_out_3), .in_2(sixt_bit_adder_1_out_3), .out_3(sixt_bit_adder_2_out_3));  // open: out_4
  sixt_bit_adder sixt_bit_adder_3 (
    .in_1(sixt_bit_gatekeeper_vert_4_out_3), .in_2(sixt_bit_adder_2_out_3), .out_3(sixt_bit_adder_3_out_3));  // open: out_4
  sixt_bit_shift_by_one sixt_bit_shift_by_one_4 (
    .in_1(sixt_bit_shift_by_one_3_out_2), .out_2(sixt_bit_shift_by_one_4_out_2));
  sixt_bit_shift_by_one sixt_bit_shift_by_one_5 (
    .in_1(sixt_bit_shift_by_one_4_out_2), .out_2(sixt_bit_shift_by_one_5_out_2));
  sixt_bit_gatekeeper_vert sixt_bit_gatekeeper_vert_5 (
    .in_1(in_1[4]), .in_2(sixt_bit_shift_by_one_4_out_2), .out_3(sixt_bit_gatekeeper_vert_5_out_3));
  sixt_bit_gatekeeper_vert sixt_bit_gatekeeper_vert_6 (
    .in_1(in_1[5]), .in_2(sixt_bit_shift_by_one_5_out_2), .out_3(sixt_bit_gatekeeper_vert_6_out_3));
  sixt_bit_adder sixt_bit_adder_4 (
    .in_1(sixt_bit_gatekeeper_vert_5_out_3), .in_2(sixt_bit_adder_3_out_3), .out_3(sixt_bit_adder_4_out_3));  // open: out_4
  sixt_bit_shift_by_one sixt_bit_shift_by_one_6 (
    .in_1(sixt_bit_shift_by_one_5_out_2), .out_2(sixt_bit_shift_by_one_6_out_2));
  sixt_bit_gatekeeper_vert sixt_bit_gatekeeper_vert_7 (
    .in_1(in_1[6]), .in_2(sixt_bit_shift_by_one_6_out_2), .out_3(sixt_bit_gatekeeper_vert_7_out_3));
  sixt_bit_gatekeeper_vert sixt_bit_gatekeeper_vert_8 (
    .in_1(in_1[7]), .in_2(sixt_bit_shift_by_one_7_out_2), .out_3(sixt_bit_gatekeeper_vert_8_out_3));
  sixt_bit_adder sixt_bit_adder_5 (
    .in_1(sixt_bit_gatekeeper_vert_6_out_3), .in_2(sixt_bit_adder_4_out_3), .out_3(sixt_bit_adder_5_out_3));  // open: out_4
  sixt_bit_adder sixt_bit_adder_6 (
    .in_1(sixt_bit_gatekeeper_vert_7_out_3), .in_2(sixt_bit_adder_5_out_3), .out_3(sixt_bit_adder_6_out_3));  // open: out_4
  sixt_bit_shift_by_one sixt_bit_shift_by_one_7 (
    .in_1(sixt_bit_shift_by_one_6_out_2), .out_2(sixt_bit_shift_by_one_7_out_2));
  sixt_bit_shift_by_one sixt_bit_shift_by_one_8 (
    .in_1(sixt_bit_shift_by_one_7_out_2), .out_2(sixt_bit_shift_by_one_8_out_2));
  sixt_bit_gatekeeper_vert sixt_bit_gatekeeper_vert_9 (
    .in_1(in_1[8]), .in_2(sixt_bit_shift_by_one_8_out_2), .out_3(sixt_bit_gatekeeper_vert_9_out_3));
  sixt_bit_adder sixt_bit_adder_7 (
    .in_1(sixt_bit_gatekeeper_vert_8_out_3), .in_2(sixt_bit_adder_6_out_3), .out_3(sixt_bit_adder_7_out_3));  // open: out_4
  sixt_bit_adder sixt_bit_adder_8 (
    .in_1(sixt_bit_gatekeeper_vert_9_out_3), .in_2(sixt_bit_adder_7_out_3), .out_3(sixt_bit_adder_8_out_3));  // open: out_4
  sixt_bit_shift_by_one sixt_bit_shift_by_one_9 (
    .in_1(sixt_bit_shift_by_one_8_out_2), .out_2(sixt_bit_shift_by_one_9_out_2));
  sixt_bit_shift_by_one sixt_bit_shift_by_one_10 (
    .in_1(sixt_bit_shift_by_one_9_out_2), .out_2(sixt_bit_shift_by_one_10_out_2));
  sixt_bit_gatekeeper_vert sixt_bit_gatekeeper_vert_10 (
    .in_1(in_1[9]), .in_2(sixt_bit_shift_by_one_9_out_2), .out_3(sixt_bit_gatekeeper_vert_10_out_3));
  sixt_bit_gatekeeper_vert sixt_bit_gatekeeper_vert_11 (
    .in_1(in_1[10]), .in_2(sixt_bit_shift_by_one_10_out_2), .out_3(sixt_bit_gatekeeper_vert_11_out_3));
  sixt_bit_adder sixt_bit_adder_9 (
    .in_1(sixt_bit_gatekeeper_vert_10_out_3), .in_2(sixt_bit_adder_8_out_3), .out_3(sixt_bit_adder_9_out_3));  // open: out_4
  sixt_bit_shift_by_one sixt_bit_shift_by_one_11 (
    .in_1(sixt_bit_shift_by_one_10_out_2), .out_2(sixt_bit_shift_by_one_11_out_2));
  sixt_bit_gatekeeper_vert sixt_bit_gatekeeper_vert_12 (
    .in_1(in_1[11]), .in_2(sixt_bit_shift_by_one_11_out_2), .out_3(sixt_bit_gatekeeper_vert_12_out_3));
  sixt_bit_adder sixt_bit_adder_10 (
    .in_1(sixt_bit_gatekeeper_vert_11_out_3), .in_2(sixt_bit_adder_9_out_3), .out_3(sixt_bit_adder_10_out_3));  // open: out_4
  sixt_bit_adder sixt_bit_adder_11 (
    .in_1(sixt_bit_gatekeeper_vert_12_out_3), .in_2(sixt_bit_adder_10_out_3), .out_3(sixt_bit_adder_11_out_3));  // open: out_4
  sixt_bit_shift_by_one sixt_bit_shift_by_one_12 (
    .in_1(sixt_bit_shift_by_one_11_out_2), .out_2(sixt_bit_shift_by_one_12_out_2));
  sixt_bit_shift_by_one sixt_bit_shift_by_one_13 (
    .in_1(sixt_bit_shift_by_one_12_out_2), .out_2(sixt_bit_shift_by_one_13_out_2));
  sixt_bit_gatekeeper_vert sixt_bit_gatekeeper_vert_13 (
    .in_1(in_1[12]), .in_2(sixt_bit_shift_by_one_12_out_2), .out_3(sixt_bit_gatekeeper_vert_13_out_3));
  sixt_bit_gatekeeper_vert sixt_bit_gatekeeper_vert_14 (
    .in_1(in_1[13]), .in_2(sixt_bit_shift_by_one_13_out_2), .out_3(sixt_bit_gatekeeper_vert_14_out_3));
  sixt_bit_adder sixt_bit_adder_12 (
    .in_1(sixt_bit_gatekeeper_vert_13_out_3), .in_2(sixt_bit_adder_11_out_3), .out_3(sixt_bit_adder_12_out_3));  // open: out_4
  sixt_bit_shift_by_one sixt_bit_shift_by_one_14 (
    .in_1(sixt_bit_shift_by_one_13_out_2), .out_2(sixt_bit_shift_by_one_14_out_2));
  sixt_bit_gatekeeper_vert sixt_bit_gatekeeper_vert_15 (
    .in_1(in_1[14]), .in_2(sixt_bit_shift_by_one_14_out_2), .out_3(sixt_bit_gatekeeper_vert_15_out_3));
  sixt_bit_gatekeeper_vert sixt_bit_gatekeeper_vert_16 (
    .in_1(in_1[15]), .in_2(sixt_bit_shift_by_one_15_out_2), .out_3(sixt_bit_gatekeeper_vert_16_out_3));
  sixt_bit_adder sixt_bit_adder_13 (
    .in_1(sixt_bit_gatekeeper_vert_14_out_3), .in_2(sixt_bit_adder_12_out_3), .out_3(sixt_bit_adder_13_out_3));  // open: out_4
  sixt_bit_adder sixt_bit_adder_14 (
    .in_1(sixt_bit_gatekeeper_vert_15_out_3), .in_2(sixt_bit_adder_13_out_3), .out_3(sixt_bit_adder_14_out_3));  // open: out_4
  sixt_bit_shift_by_one sixt_bit_shift_by_one_15 (
    .in_1(sixt_bit_shift_by_one_14_out_2), .out_2(sixt_bit_shift_by_one_15_out_2));
  sixt_bit_adder sixt_bit_adder_15 (
    .in_1(sixt_bit_gatekeeper_vert_16_out_3), .in_2(sixt_bit_adder_14_out_3), .out_3(out_3));  // open: out_4
endmodule

module sixt_bit_eq_cmp (
  input  [15:0] in_1,
  input  [15:0] in_2,
  output out_3
);

  wire or_1_out;
  wire [15:0] xor_1_out;

  Pull_Resistor #(.pull(1)) pull_resistor_1 (.node(in_1));
  Pull_Resistor pull_resistor_2 (.node(in_2));
  xor xor_1 (xor_1_out[0], in_1[0], in_2[0]);
  xor xor_2 (xor_1_out[1], in_1[1], in_2[1]);
  xor xor_3 (xor_1_out[2], in_1[2], in_2[2]);
  xor xor_4 (xor_1_out[3], in_1[3], in_2[3]);
  xor xor_5 (xor_1_out[4], in_1[4], in_2[4]);
  xor xor_6 (xor_1_out[5], in_1[5], in_2[5]);
  xor xor_7 (xor_1_out[6], in_1[6], in_2[6]);
  xor xor_8 (xor_1_out[7], in_1[7], in_2[7]);
  xor xor_9 (xor_1_out[8], in_1[8], in_2[8]);
  xor xor_10 (xor_1_out[9], in_1[9], in_2[9]);
  xor xor_11 (xor_1_out[10], in_1[10], in_2[10]);
  xor xor_12 (xor_1_out[11], in_1[11], in_2[11]);
  xor xor_13 (xor_1_out[12], in_1[12], in_2[12]);
  xor xor_14 (xor_1_out[13], in_1[13], in_2[13]);
  xor xor_15 (xor_1_out[14], in_1[14], in_2[14]);
  xor xor_16 (xor_1_out[15], in_1[15], in_2[15]);
  or or_1 (or_1_out, xor_1_out[0], xor_1_out[1], xor_1_out[2], xor_1_out[3], xor_1_out[4], xor_1_out[5], xor_1_out[6], xor_1_out[7], xor_1_out[8], xor_1_out[9], xor_1_out[10], xor_1_out[11], xor_1_out[12], xor_1_out[13], xor_1_out[14], xor_1_out[15]);
  not not_1 (out_3, or_1_out);
endmodule

module eight_bit_eq_cmp (
  input  [7:0] in_1,
  input  [7:0] in_2,
  output out_3
);

  wire xor_1_out, xor_2_out, xor_3_out, xor_4_out, xor_5_out, xor_6_out, xor_7_out, xor_8_out;

  xor xor_1 (xor_1_out, in_1[0], in_2[0]);
  xor xor_2 (xor_2_out, in_1[1], in_2[1]);
  xor xor_3 (xor_3_out, in_1[2], in_2[2]);
  xor xor_4 (xor_4_out, in_1[3], in_2[3]);
  xor xor_5 (xor_5_out, in_1[4], in_2[4]);
  xor xor_6 (xor_6_out, in_1[5], in_2[5]);
  xor xor_7 (xor_7_out, in_1[6], in_2[6]);
  xor xor_8 (xor_8_out, in_1[7], in_2[7]);
  nor nor_1 (out_3, xor_1_out, xor_2_out, xor_3_out, xor_4_out, xor_5_out, xor_6_out, xor_7_out, xor_8_out);
endmodule

module four_bit_eq_cmp (
  input  [3:0] in_1,
  input  [3:0] in_2,
  output out_3
);

  wire xor_1_out, xor_2_out, xor_3_out, xor_4_out;

  xor xor_1 (xor_1_out, in_1[0], in_2[0]);
  xor xor_2 (xor_2_out, in_1[1], in_2[1]);
  xor xor_3 (xor_3_out, in_1[2], in_2[2]);
  xor xor_4 (xor_4_out, in_1[3], in_2[3]);
  nor nor_1 (out_3, xor_1_out, xor_2_out, xor_3_out, xor_4_out);
endmodule

module sixt_bit_comparator (
  input  [15:0] in_1,
  input  [15:0] in_2,
  output out_3,
  output out_4
);

  wire and_1_out, and_2_out, and_3_out, and_4_out, and_5_out, and_6_out, and_7_out, and_8_out, and_9_out,
       and_10_out, and_11_out, and_12_out, and_13_out, and_14_out, and_15_out, and_16_out, and_17_out,
       and_18_out, and_19_out, and_20_out, and_21_out, and_22_out, and_23_out, and_24_out, and_25_out,
       and_26_out, and_27_out, and_28_out, and_29_out, and_30_out, or_1_out, or_2_out, or_3_out, or_4_out,
       or_5_out, or_6_out, or_7_out, or_8_out, or_9_out, or_10_out, or_11_out, or_12_out, or_13_out,
       or_14_out, or_15_out, or_17_out, or_18_out, or_19_out, or_20_out, or_21_out, or_22_out, or_23_out,
       or_24_out, or_25_out, or_26_out, or_27_out, or_28_out, or_29_out, or_30_out, xor_1_out, xor_2_out,
       xor_3_out, xor_4_out, xor_5_out, xor_6_out, xor_7_out, xor_8_out, xor_9_out, xor_10_out, xor_11_out,
       xor_12_out, xor_13_out, xor_14_out, xor_15_out, xor_16_out;

  xor xor_1 (xor_1_out, in_1[0], in_2[0]);
  xor xor_2 (xor_2_out, in_1[1], in_2[1]);
  xor xor_3 (xor_3_out, in_1[2], in_2[2]);
  xor xor_4 (xor_4_out, in_1[3], in_2[3]);
  xor xor_5 (xor_5_out, in_1[4], in_2[4]);
  xor xor_6 (xor_6_out, in_1[5], in_2[5]);
  xor xor_7 (xor_7_out, in_1[6], in_2[6]);
  xor xor_8 (xor_8_out, in_1[7], in_2[7]);
  xor xor_9 (xor_9_out, in_1[8], in_2[8]);
  xor xor_10 (xor_10_out, in_1[9], in_2[9]);
  xor xor_11 (xor_11_out, in_1[10], in_2[10]);
  xor xor_12 (xor_12_out, in_1[11], in_2[11]);
  xor xor_13 (xor_13_out, in_1[12], in_2[12]);
  xor xor_14 (xor_14_out, in_1[13], in_2[13]);
  xor xor_15 (xor_15_out, in_1[14], in_2[14]);
  xor xor_16 (xor_16_out, in_1[15], in_2[15]);
  or or_1 (or_1_out, or_2_out, xor_1_out);
  and and_1 (and_1_out, xor_1_out, ~or_2_out);  // AND_Gate
  or or_2 (or_2_out, or_3_out, xor_2_out);
  and and_2 (and_2_out, xor_2_out, ~or_3_out);  // AND_Gate
  or or_3 (or_3_out, or_4_out, xor_3_out);
  and and_3 (and_3_out, xor_3_out, ~or_4_out);  // AND_Gate
  or or_4 (or_4_out, or_5_out, xor_4_out);
  and and_4 (and_4_out, xor_4_out, ~or_5_out);  // AND_Gate
  or or_5 (or_5_out, or_6_out, xor_5_out);
  and and_5 (and_5_out, xor_5_out, ~or_6_out);  // AND_Gate
  or or_6 (or_6_out, or_7_out, xor_6_out);
  and and_6 (and_6_out, xor_6_out, ~or_7_out);  // AND_Gate
  or or_7 (or_7_out, or_8_out, xor_7_out);
  and and_7 (and_7_out, xor_7_out, ~or_8_out);  // AND_Gate
  or or_8 (or_8_out, or_9_out, xor_8_out);
  and and_8 (and_8_out, xor_8_out, ~or_9_out);  // AND_Gate
  or or_9 (or_9_out, or_10_out, xor_9_out);
  and and_9 (and_9_out, xor_9_out, ~or_10_out);  // AND_Gate
  or or_10 (or_10_out, or_11_out, xor_10_out);
  and and_10 (and_10_out, xor_10_out, ~or_11_out);  // AND_Gate
  or or_11 (or_11_out, or_12_out, xor_11_out);
  and and_11 (and_11_out, xor_11_out, ~or_12_out);  // AND_Gate
  or or_12 (or_12_out, or_13_out, xor_12_out);
  and and_12 (and_12_out, xor_12_out, ~or_13_out);  // AND_Gate
  or or_13 (or_13_out, or_14_out, xor_13_out);
  and and_13 (and_13_out, xor_13_out, ~or_14_out);  // AND_Gate
  or or_14 (or_14_out, or_15_out, xor_14_out);
  and and_14 (and_14_out, xor_14_out, ~or_15_out);  // AND_Gate
  or or_15 (or_15_out, xor_16_out, xor_15_out);
  and and_15 (and_15_out, xor_15_out, ~xor_16_out);  // AND_Gate
  and and_16 (and_16_out, and_1_out, in_1[0]);
  or or_16 (out_3, and_16_out, or_17_out);
  and and_17 (and_17_out, and_2_out, in_1[1]);
  or or_17 (or_17_out, and_17_out, or_18_out);
  and and_18 (and_18_out, and_3_out, in_1[2]);
  or or_18 (or_18_out, and_18_out, or_19_out);
  and and_19 (and_19_out, and_4_out, in_1[3]);
  or or_19 (or_19_out, and_19_out, or_20_out);
  and and_20 (and_20_out, and_5_out, in_1[4]);
  or or_20 (or_20_out, and_20_out, or_21_out);
  and and_21 (and_21_out, and_6_out, in_1[5]);
  or or_21 (or_21_out, and_21_out, or_22_out);
  and and_22 (and_22_out, and_7_out, in_1[6]);
  or or_22 (or_22_out, and_22_out, or_23_out);
  and and_23 (and_23_out, and_8_out, in_1[7]);
  or or_23 (or_23_out, and_23_out, or_24_out);
  and and_24 (and_24_out, and_9_out, in_1[8]);
  or or_24 (or_24_out, and_24_out, or_25_out);
  and and_25 (and_25_out, and_10_out, in_1[9]);
  or or_25 (or_25_out, and_25_out, or_26_out);
  and and_26 (and_26_out, and_11_out, in_1[10]);
  or or_26 (or_26_out, and_26_out, or_27_out);
  and and_27 (and_27_out, and_12_out, in_1[11]);
  or or_27 (or_27_out, and_27_out, or_28_out);
  and and_28 (and_28_out, and_13_out, in_1[12]);
  or or_28 (or_28_out, and_28_out, or_29_out);
  and and_29 (and_29_out, and_14_out, in_1[13]);
  or or_29 (or_29_out, and_29_out, or_30_out);
  and and_30 (and_30_out, and_15_out, in_1[14]);
  or or_30 (or_30_out, and_30_out, xor_16_out);
  and and_31 (out_4, ~out_3, or_1_out);  // AND_Gate
endmodule

module sixt_bit_eq_zero (
  input  [15:0] in_1,
  output out_2
);

  wire [15:0] not_1_out;

  assign not_1_out = ~in_1;  // NOT_Gate not_1, 16 bits wide
  and and_1 (out_2, not_1_out[0], not_1_out[1], not_1_out[2], not_1_out[3], not_1_out[4], not_1_out[5], not_1_out[6], not_1_out[7], not_1_out[8], not_1_out[9], not_1_out[10], not_1_out[11], not_1_out[12], not_1_out[13], not_1_out[14], not_1_out[15]);
endmodule

module four_bit_eq_zero (
  input  [3:0] in_1,
  output out_2
);

  nor nor_1 (out_2, in_1[0], in_1[1], in_1[2], in_1[3]);
endmodule

module pulse_extender (
  input  in_1,
  input  in_2,
  input  in_3,
  output out_4,
  output out_5,
  output out_6
);

  wire not_1_out;

  S_R_Flip_Flop s_r_ff_1 (.S(1'b0), .R(not_1_out), .clk(in_2), .Q(out_6), .reset(in_3), .preset(in_1));  // open: Qn
  not not_1 (not_1_out, in_1);

  assign out_4 = in_3;
  assign out_5 = in_2;
endmodule

module four_bit_g8 (
  input  in_1,
  input  [3:0] in_2,
  output [3:0] out_3
);

  assign out_3 = {4{in_1}} & in_2;  // AND_Gate and_1, 4 bits wide
endmodule

module two_ticker (
  input  signal_in,
  input  clock,
  input  reset,
  output out_4
);

  wire and_1_out, and_2_out, and_3_out, and_4_out, and_5_out, and_6_out, and_7_out, buffer_1_out,
       buffer_2_out, buffer_3_out, buffer_4_out, buffer_5_out, buffer_6_out, buffer_7_out, buffer_8_out,
       buffer_9_out, buffer_10_out, buffer_11_out, buffer_12_out, buffer_13_out, buffer_14_out,
       buffer_15_out, buffer_16_out, buffer_17_out, buffer_18_out, clk_at_signal_q, fall_next_q, not_1_out,
       or_1_out, or_2_out, or_3_out, xor_1_out;

  not not_1 (not_1_out, clock);
  buf buffer_1 (buffer_1_out, signal_in);
  buf buffer_2 (buffer_2_out, buffer_1_out);
  buf buffer_3 (buffer_3_out, clock);
  buf buffer_4 (buffer_4_out, buffer_3_out);
  buf buffer_5 (buffer_5_out, not_1_out);
  buf buffer_6 (buffer_6_out, buffer_5_out);
  buf buffer_7 (buffer_7_out, buffer_2_out);
  and and_1 (and_1_out, ~buffer_7_out, signal_in);  // AND_Gate
  buf buffer_8 (buffer_8_out, buffer_4_out);
  and and_2 (and_2_out, ~buffer_8_out, clock);  // AND_Gate
  buf buffer_9 (buffer_9_out, buffer_6_out);
  and and_3 (and_3_out, ~buffer_9_out, not_1_out);  // AND_Gate
  or or_1 (or_1_out, and_2_out, and_3_out);
  and and_4 (and_4_out, ~out_4, and_1_out);  // AND_Gate
  xor xor_1 (xor_1_out, clock, clk_at_signal_q);
  and and_5 (and_5_out, signal_in, and_4_out);
  or or_2 (or_2_out, and_5_out, and_6_out);
  and and_6 (and_6_out, fall_next_q, out_4, or_1_out);
  or or_3 (or_3_out, and_6_out, and_4_out);
  and and_7 (and_7_out, xor_1_out, out_4);
  D_Flip_Flop signal_out (.D(or_2_out), .clk(buffer_12_out), .Q(out_4), .reset(reset));  // open: Qn, preset
  buf buffer_10 (buffer_10_out, or_3_out);
  buf buffer_11 (buffer_11_out, buffer_10_out);
  buf buffer_12 (buffer_12_out, buffer_11_out);
  D_Flip_Flop clk_at_signal (.D(clock), .clk(buffer_15_out), .Q(clk_at_signal_q), .reset(reset));  // open: Qn, preset
  buf buffer_13 (buffer_13_out, and_4_out);
  buf buffer_14 (buffer_14_out, buffer_13_out);
  buf buffer_15 (buffer_15_out, buffer_14_out);
  D_Flip_Flop fall_next (.D(and_7_out), .clk(buffer_18_out), .Q(fall_next_q), .reset(reset));  // open: Qn, preset
  buf buffer_16 (buffer_16_out, or_1_out);
  buf buffer_17 (buffer_17_out, buffer_16_out);
  buf buffer_18 (buffer_18_out, buffer_17_out);
endmodule

module special_register_opdec (
  input  [15:0] control,
  input  [3:0] id,
  output [3:0] param,
  output data_bus_enable,
  output addr_bus_enable,
  output write_enable,
  output [15:0] special_functions
);

  wire and_1_out, and_3_out, and_4_out, and_5_out, eight_bit_eq_cmp_1_out_3, eight_bit_eq_cmp_2_out_3,
       eight_bit_eq_cmp_3_out_3, eight_bit_eq_cmp_4_out_3, eight_bit_eq_cmp_5_out_3,
       eight_bit_eq_cmp_6_out_3, eight_bit_eq_cmp_7_out_3, eight_bit_eq_cmp_8_out_3,
       eight_bit_eq_cmp_9_out_3, eight_bit_eq_cmp_10_out_3, eight_bit_eq_cmp_11_out_3,
       eight_bit_eq_cmp_12_out_3, eight_bit_eq_cmp_13_out_3, eight_bit_eq_cmp_14_out_3,
       eight_bit_eq_cmp_15_out_3, eight_bit_eq_cmp_16_out_3, four_bit_eq_cmp_1_out_3, load_data_bus_out_3,
       or_1_out, to_addr_bus_out_3, to_data_bus_indirect_out_3, to_data_bus_indirect_w_offset_out_3,
       to_data_bus_out_3;

  four_bit_eq_cmp four_bit_eq_cmp_1 (.in_1(control[15:12]), .in_2(id), .out_3(four_bit_eq_cmp_1_out_3));
  eight_bit_eq_cmp to_data_bus (.in_1(control[7:0]), .in_2(8'h2), .out_3(to_data_bus_out_3));
  eight_bit_eq_cmp to_addr_bus (.in_1(control[7:0]), .in_2(8'h3), .out_3(to_addr_bus_out_3));
  eight_bit_eq_cmp to_data_bus_indirect (.in_1(control[7:0]), .in_2(8'h4), .out_3(to_data_bus_indirect_out_3));
  eight_bit_eq_cmp to_data_bus_indirect_w_offset (
    .in_1(control[7:0]), .in_2(8'h5), .out_3(to_data_bus_indirect_w_offset_out_3));
  eight_bit_eq_cmp load_data_bus (.in_1(control[7:0]), .in_2(8'h6), .out_3(load_data_bus_out_3));
  eight_bit_eq_cmp eight_bit_eq_cmp_1 (.in_1(control[7:0]), .in_2(8'h10), .out_3(eight_bit_eq_cmp_1_out_3));
  eight_bit_eq_cmp eight_bit_eq_cmp_2 (.in_1(control[7:0]), .in_2(8'h11), .out_3(eight_bit_eq_cmp_2_out_3));
  eight_bit_eq_cmp eight_bit_eq_cmp_3 (.in_1(control[7:0]), .in_2(8'h12), .out_3(eight_bit_eq_cmp_3_out_3));
  eight_bit_eq_cmp eight_bit_eq_cmp_4 (.in_1(control[7:0]), .in_2(8'h13), .out_3(eight_bit_eq_cmp_4_out_3));
  eight_bit_eq_cmp eight_bit_eq_cmp_5 (.in_1(control[7:0]), .in_2(8'h14), .out_3(eight_bit_eq_cmp_5_out_3));
  eight_bit_eq_cmp eight_bit_eq_cmp_6 (.in_1(control[7:0]), .in_2(8'h15), .out_3(eight_bit_eq_cmp_6_out_3));
  eight_bit_eq_cmp eight_bit_eq_cmp_7 (.in_1(control[7:0]), .in_2(8'h16), .out_3(eight_bit_eq_cmp_7_out_3));
  eight_bit_eq_cmp eight_bit_eq_cmp_8 (.in_1(control[7:0]), .in_2(8'h17), .out_3(eight_bit_eq_cmp_8_out_3));
  eight_bit_eq_cmp eight_bit_eq_cmp_9 (.in_1(control[7:0]), .in_2(8'h18), .out_3(eight_bit_eq_cmp_9_out_3));
  eight_bit_eq_cmp eight_bit_eq_cmp_10 (.in_1(control[7:0]), .in_2(8'h19), .out_3(eight_bit_eq_cmp_10_out_3));
  eight_bit_eq_cmp eight_bit_eq_cmp_11 (.in_1(control[7:0]), .in_2(8'h1a), .out_3(eight_bit_eq_cmp_11_out_3));
  eight_bit_eq_cmp eight_bit_eq_cmp_12 (.in_1(control[7:0]), .in_2(8'h1b), .out_3(eight_bit_eq_cmp_12_out_3));
  eight_bit_eq_cmp eight_bit_eq_cmp_13 (.in_1(control[7:0]), .in_2(8'h1c), .out_3(eight_bit_eq_cmp_13_out_3));
  eight_bit_eq_cmp eight_bit_eq_cmp_14 (.in_1(control[7:0]), .in_2(8'h1d), .out_3(eight_bit_eq_cmp_14_out_3));
  eight_bit_eq_cmp eight_bit_eq_cmp_15 (.in_1(control[7:0]), .in_2(8'h1e), .out_3(eight_bit_eq_cmp_15_out_3));
  eight_bit_eq_cmp eight_bit_eq_cmp_16 (.in_1(control[7:0]), .in_2(8'h1f), .out_3(eight_bit_eq_cmp_16_out_3));
  or or_1 (or_1_out, eight_bit_eq_cmp_1_out_3, eight_bit_eq_cmp_2_out_3, eight_bit_eq_cmp_3_out_3, eight_bit_eq_cmp_4_out_3, eight_bit_eq_cmp_5_out_3, eight_bit_eq_cmp_6_out_3, eight_bit_eq_cmp_7_out_3, eight_bit_eq_cmp_8_out_3, eight_bit_eq_cmp_9_out_3, eight_bit_eq_cmp_10_out_3, eight_bit_eq_cmp_11_out_3, eight_bit_eq_cmp_12_out_3, eight_bit_eq_cmp_13_out_3, eight_bit_eq_cmp_14_out_3, eight_bit_eq_cmp_15_out_3, eight_bit_eq_cmp_16_out_3);
  and and_1 (and_1_out, four_bit_eq_cmp_1_out_3, or_1_out);
  and and_2 (data_bus_enable, four_bit_eq_cmp_1_out_3, to_data_bus_out_3);
  and and_3 (and_3_out, four_bit_eq_cmp_1_out_3, to_addr_bus_out_3);
  and and_4 (and_4_out, four_bit_eq_cmp_1_out_3, to_data_bus_indirect_out_3);
  and and_5 (and_5_out, four_bit_eq_cmp_1_out_3, to_data_bus_indirect_w_offset_out_3);
  and and_6 (write_enable, four_bit_eq_cmp_1_out_3, load_data_bus_out_3);
  and and_7 (special_functions[0], four_bit_eq_cmp_1_out_3, eight_bit_eq_cmp_1_out_3);
  and and_8 (special_functions[1], four_bit_eq_cmp_1_out_3, eight_bit_eq_cmp_2_out_3);
  and and_9 (special_functions[2], four_bit_eq_cmp_1_out_3, eight_bit_eq_cmp_3_out_3);
  and and_10 (special_functions[3], four_bit_eq_cmp_1_out_3, eight_bit_eq_cmp_4_out_3);
  and and_11 (special_functions[4], four_bit_eq_cmp_1_out_3, eight_bit_eq_cmp_5_out_3);
  and and_12 (special_functions[5], four_bit_eq_cmp_1_out_3, eight_bit_eq_cmp_6_out_3);
  and and_13 (special_functions[6], four_bit_eq_cmp_1_out_3, eight_bit_eq_cmp_7_out_3);
  and and_14 (special_functions[7], four_bit_eq_cmp_1_out_3, eight_bit_eq_cmp_8_out_3);
  and and_15 (special_functions[8], four_bit_eq_cmp_1_out_3, eight_bit_eq_cmp_9_out_3);
  and and_16 (special_functions[9], four_bit_eq_cmp_1_out_3, eight_bit_eq_cmp_10_out_3);
  and and_17 (special_functions[10], four_bit_eq_cmp_1_out_3, eight_bit_eq_cmp_11_out_3);
  and and_18 (special_functions[11], four_bit_eq_cmp_1_out_3, eight_bit_eq_cmp_12_out_3);
  and and_19 (special_functions[12], four_bit_eq_cmp_1_out_3, eight_bit_eq_cmp_13_out_3);
  and and_20 (special_functions[13], four_bit_eq_cmp_1_out_3, eight_bit_eq_cmp_14_out_3);
  and and_21 (special_functions[14], four_bit_eq_cmp_1_out_3, eight_bit_eq_cmp_15_out_3);
  and and_22 (special_functions[15], four_bit_eq_cmp_1_out_3, eight_bit_eq_cmp_16_out_3);
  four_bit_g8 four_bit_g8_1 (.in_1(and_1_out), .in_2(control[11:8]), .out_3(param));
  or or_2 (addr_bus_enable, and_3_out, and_4_out, and_5_out);

  // Notes on the sheet:
  //   special functions
endmodule

module special_register_dual_opdec (
  input  [15:0] control_bus_1,
  input  [15:0] control_bus_2,
  input  [3:0] id,
  output data_bus_enable,
  output addr_bus_enable,
  output write_enable,
  output [3:0] param,
  output [15:0] special_functions
);

  wire special_register_opdec_1_addr_bus_enable, special_register_opdec_1_data_bus_enable,
       special_register_opdec_1_write_enable, special_register_opdec_2_addr_bus_enable,
       special_register_opdec_2_data_bus_enable, special_register_opdec_2_write_enable;
  wire [3:0] special_register_opdec_1_param, special_register_opdec_2_param;
  wire [15:0] special_register_opdec_1_special_functions, special_register_opdec_2_special_functions;

  special_register_opdec special_register_opdec_1 (
    .control(control_bus_1), .id(id), .param(special_register_opdec_1_param),
    .data_bus_enable(special_register_opdec_1_data_bus_enable),
    .addr_bus_enable(special_register_opdec_1_addr_bus_enable),
    .write_enable(special_register_opdec_1_write_enable),
    .special_functions(special_register_opdec_1_special_functions));
  special_register_opdec special_register_opdec_2 (
    .control(control_bus_2), .id(id), .param(special_register_opdec_2_param),
    .data_bus_enable(special_register_opdec_2_data_bus_enable),
    .addr_bus_enable(special_register_opdec_2_addr_bus_enable),
    .write_enable(special_register_opdec_2_write_enable),
    .special_functions(special_register_opdec_2_special_functions));
  or or_1 (data_bus_enable, special_register_opdec_2_data_bus_enable, special_register_opdec_1_data_bus_enable);
  or or_2 (addr_bus_enable, special_register_opdec_2_addr_bus_enable, special_register_opdec_1_addr_bus_enable);
  or or_3 (write_enable, special_register_opdec_2_write_enable, special_register_opdec_1_write_enable);
  assign param = special_register_opdec_2_param | special_register_opdec_1_param;  // OR_Gate or_4, 4 bits wide
  assign special_functions = special_register_opdec_2_special_functions | special_register_opdec_1_special_functions;  // OR_Gate or_5, 16 bits wide
endmodule

module special_registers_opdec (
  input  [15:0] data_in,
  input  [15:0] ctrl_unit_in,
  input  [15:0] control,
  output [15:0] data_to_pk,
  output [3:0] pk_param,
  output pk_to_data,
  output pk_to_addr,
  output pk_inc,
  output sp_to_data,
  output sp_to_addr,
  output pk_dec,
  output sp_write,
  output pk_write,
  output [3:0] sp_param,
  output sp_inc,
  output sp_dec,
  output sp_predec_to_addr,
  output sp_postinc_to_addr,
  output [15:0] data_to_offs,
  output offs_to_data,
  output offs_to_addr,
  output offs_write
);

  wire and_1_out, and_2_out, and_3_out, and_4_out, and_5_out, and_6_out, comparator_1_eq, comparator_1_gt,
       comparator_1_lt, or_3_out, special_register_opdec_1_addr_bus_enable,
       special_register_opdec_1_write_enable, special_register_opdec_3_write_enable;
  wire [15:0] multiplexer_2_out, special_register_opdec_1_special_functions,
       special_register_opdec_3_special_functions;
  wire [15:4] special_register_opdec_2_special_functions;

  special_register_opdec special_register_opdec_1 (
    .control(control), .id(4'b0000), .param(pk_param), .data_bus_enable(pk_to_data),
    .addr_bus_enable(special_register_opdec_1_addr_bus_enable),
    .write_enable(special_register_opdec_1_write_enable),
    .special_functions({special_register_opdec_1_special_functions[15:3], pk_dec, special_register_opdec_1_special_functions[1:0]}));
  special_register_opdec special_register_opdec_2 (
    .control(control), .id(4'b0001), .param(sp_param), .data_bus_enable(sp_to_data),
    .addr_bus_enable(sp_to_addr), .write_enable(sp_write),
    .special_functions({special_register_opdec_2_special_functions, sp_postinc_to_addr, sp_predec_to_addr, sp_dec, sp_inc}));
  Multiplexer #(.width(16)) multiplexer_1 (
    .in0(data_in), .in1(ctrl_unit_in), .out(data_to_offs), .sel(special_register_opdec_3_special_functions[0]));
  special_register_opdec special_register_opdec_3 (
    .control(control), .id(4'b0101), .data_bus_enable(offs_to_data), .addr_bus_enable(offs_to_addr),
    .write_enable(special_register_opdec_3_write_enable),
    .special_functions(special_register_opdec_3_special_functions));  // open: param
  or or_1 (offs_write, special_register_opdec_3_write_enable, special_register_opdec_3_special_functions[0]);
  Multiplexer #(.width(16)) multiplexer_2 (.in0(data_in), .in1(ctrl_unit_in), .out(multiplexer_2_out), .sel(or_3_out));
  or or_2 (pk_to_addr, special_register_opdec_1_addr_bus_enable, special_register_opdec_1_special_functions[1]);
  or or_3 (or_3_out, special_register_opdec_1_special_functions[3], special_register_opdec_1_special_functions[4], special_register_opdec_1_special_functions[5], special_register_opdec_1_special_functions[6], special_register_opdec_1_special_functions[7], special_register_opdec_1_special_functions[8], special_register_opdec_1_special_functions[9], special_register_opdec_1_special_functions[10], special_register_opdec_1_special_functions[11]);
  Comparator #(.width(16)) comparator_1 (
    .a(data_in), .b({16{1'b0}}), .gt(comparator_1_gt), .eq(comparator_1_eq), .lt(comparator_1_lt));
  Multiplexer #(.width(16)) multiplexer_3 (.in0({16{1'b0}}), .in1(multiplexer_2_out), .out(data_to_pk), .sel(pk_write));
  or or_4 (pk_write, special_register_opdec_1_special_functions[11], special_register_opdec_1_write_enable, special_register_opdec_1_special_functions[3], special_register_opdec_1_special_functions[4], and_1_out, and_2_out, and_3_out, and_4_out, and_5_out, and_6_out);
  and and_1 (and_1_out, special_register_opdec_1_special_functions[5], comparator_1_eq);
  and and_2 (and_2_out, special_register_opdec_1_special_functions[6], ~comparator_1_eq);  // AND_Gate
  and and_3 (and_3_out, special_register_opdec_1_special_functions[7], comparator_1_lt);
  and and_4 (and_4_out, special_register_opdec_1_special_functions[8], ~comparator_1_lt);  // AND_Gate
  and and_5 (and_5_out, special_register_opdec_1_special_functions[9], comparator_1_gt);
  and and_6 (and_6_out, special_register_opdec_1_special_functions[10], ~comparator_1_gt);  // AND_Gate
  or or_5 (pk_inc, special_register_opdec_1_special_functions[0], special_register_opdec_1_special_functions[1]);

  // Notes on the sheet:
  //   <- the combinatorial logic for conditional gotos
endmodule

module io_pins_4 (
  input  [15:0] control_bus,
  input  [15:0] data_bus_in,
  input  [15:0] addr_bus_in,
  input  clock,
  input  reset,
  input  in_6,
  input  in_7,
  input  in_8,
  input  in_9,
  output [15:0] data_bus_out,
  output out_11,
  output out_12,
  output out_13,
  output out_14,
  output out_15,
  output out_16,
  output out_17,
  output out_18
);

  wire and_1_out, and_2_out, and_3_out, and_4_out, and_5_out, and_6_out, and_7_out, and_8_out, and_9_out,
       and_10_out, and_11_out, and_12_out, comparator_1_eq, comparator_2_eq, comparator_3_eq,
       comparator_4_eq, comparator_5_eq, comparator_6_eq, decoder_1_out0, decoder_1_out1, decoder_1_out2,
       decoder_1_out3, multiplexer_1_out, not_1_out, not_2_out, or_1_out, or_2_out, or_3_out, or_4_out,
       or_5_out, or_6_out;
  wire [0:0] or_7_out;

  not not_1 (not_1_out, clock);
  Comparator comparator_1 (.a(control_bus[7:0]), .b(8'h30), .eq(comparator_1_eq));  // open: gt, lt
  Comparator comparator_2 (.a(control_bus[7:0]), .b(8'h31), .eq(comparator_2_eq));  // open: gt, lt
  Comparator comparator_3 (.a(control_bus[7:0]), .b(8'h32), .eq(comparator_3_eq));  // open: gt, lt
  Comparator comparator_4 (.a(control_bus[7:0]), .b(8'h33), .eq(comparator_4_eq));  // open: gt, lt
  Comparator comparator_5 (.a(control_bus[7:0]), .b(8'h34), .eq(comparator_5_eq));  // open: gt, lt
  Comparator comparator_6 (.a(control_bus[7:0]), .b(8'h35), .eq(comparator_6_eq));  // open: gt, lt
  Decoder #(.enable("false"), .select(2)) decoder_1 (
    .out0(decoder_1_out0), .out1(decoder_1_out1), .out2(decoder_1_out2), .out3(decoder_1_out3),
    .sel(control_bus[13:12]));
  or or_1 (or_1_out, comparator_6_eq, comparator_4_eq, comparator_3_eq);
  or or_2 (or_2_out, comparator_2_eq, comparator_1_eq);
  or or_3 (or_3_out, ~comparator_1_eq, comparator_2_eq);  // OR_Gate
  and and_1 (and_1_out, decoder_1_out0, or_1_out, not_1_out);
  and and_2 (and_2_out, decoder_1_out0, or_2_out, not_1_out);
  Multiplexer #(.enable("true")) multiplexer_1 (
    .in0(or_4_out), .in1(1'b1), .out(multiplexer_1_out), .sel(comparator_4_eq), .en(not_2_out));
  not not_2 (not_2_out, comparator_3_eq);
  D_Flip_Flop d_ff_1 (.D(multiplexer_1_out), .clk(and_1_out), .Q(out_11), .reset(reset));  // open: Qn, preset
  D_Flip_Flop d_ff_2 (.D(or_3_out), .clk(and_2_out), .Q(out_12), .reset(reset));  // open: Qn, preset
  and and_3 (and_3_out, decoder_1_out0, in_6);
  D_Flip_Flop d_ff_3 (.D(multiplexer_1_out), .clk(and_4_out), .Q(out_13), .reset(reset));  // open: Qn, preset
  and and_4 (and_4_out, decoder_1_out1, or_1_out, not_1_out);
  D_Flip_Flop d_ff_4 (.D(or_3_out), .clk(and_5_out), .Q(out_14), .reset(reset));  // open: Qn, preset
  and and_5 (and_5_out, decoder_1_out1, or_2_out, not_1_out);
  or or_4 (or_4_out, data_bus_in[0], data_bus_in[1], data_bus_in[2], data_bus_in[3], data_bus_in[4], data_bus_in[5], data_bus_in[6], data_bus_in[7], data_bus_in[8], data_bus_in[9], data_bus_in[10], data_bus_in[11], data_bus_in[12], data_bus_in[13], data_bus_in[14], data_bus_in[15]);
  and and_6 (and_6_out, decoder_1_out1, in_7);
  or or_5 (or_5_out, and_3_out, and_6_out);
  D_Flip_Flop d_ff_5 (.D(multiplexer_1_out), .clk(and_7_out), .Q(out_15), .reset(reset));  // open: Qn, preset
  and and_7 (and_7_out, decoder_1_out2, or_1_out, not_1_out);
  D_Flip_Flop d_ff_6 (.D(or_3_out), .clk(and_8_out), .Q(out_16), .reset(reset));  // open: Qn, preset
  and and_8 (and_8_out, decoder_1_out2, or_2_out, not_1_out);
  or or_6 (or_6_out, or_5_out, and_9_out);
  and and_9 (and_9_out, decoder_1_out2, in_8);
  and and_10 (and_10_out, decoder_1_out3, or_1_out, not_1_out);
  and and_11 (and_11_out, decoder_1_out3, or_2_out, not_1_out);
  D_Flip_Flop d_ff_7 (.D(multiplexer_1_out), .clk(and_10_out), .Q(out_17), .reset(reset));  // open: Qn, preset
  D_Flip_Flop d_ff_8 (.D(or_3_out), .clk(and_11_out), .Q(out_18), .reset(reset));  // open: Qn, preset
  or or_7 (or_7_out[0], or_6_out, and_12_out);
  and and_12 (and_12_out, decoder_1_out3, in_9);
  sixt_bit_gatekeeper sixt_bit_gatekeeper_1 (
    .in_1(comparator_5_eq), .in_2({{15{1'b0}}, or_7_out[0]}), .out_3(data_bus_out));
endmodule

module clock_division_bell (
  input  [7:0] divisor,
  input  load_divisor,
  input  restart,
  input  clock,
  input  reset,
  output out_6
);

  wire and_1_out, and_2_out, comparator_1_eq, j_k_ff_1_q, nor_1_out, not_1_out, or_1_out, or_2_out,
       rising_edge_delay_1_out_2;
  wire [7:0] adder_1_out, divisor_register_q, kounter_q, multiplexer_1_out, multiplexer_2_out,
       subtractor_1_out, subtractor_2_out;

  Subtractor subtractor_1 (.a(divisor), .b(8'h1), .out(subtractor_1_out));  // open: bin, bout
  Register divisor_register (.D(subtractor_1_out), .en(load_divisor), .clk(clock), .Q(divisor_register_q), .clr(reset));
  not not_1 (not_1_out, nor_1_out);
  Multiplexer #(.width(8)) multiplexer_1 (.in0({8{1'b0}}), .in1(adder_1_out), .out(multiplexer_1_out), .sel(not_1_out));
  Adder adder_1 (.a(kounter_q), .b(8'h1), .out(adder_1_out));  // open: cin, cout
  and and_1 (and_1_out, clock, ~load_divisor);  // AND_Gate
  or or_1 (or_1_out, load_divisor, restart, reset);
  Multiplexer #(.width(8)) multiplexer_2 (
    .in0(multiplexer_1_out), .in1({8{1'b1}}), .out(multiplexer_2_out), .sel(or_1_out));
  and and_2 (and_2_out, and_1_out, ~or_1_out);  // AND_Gate
  rising_edge_delay rising_edge_delay_1 (.in_1(or_1_out), .out_2(rising_edge_delay_1_out_2));
  Register kounter (.D(multiplexer_2_out), .en(1'b1), .clk(or_2_out), .Q(kounter_q));  // open: clr
  or or_2 (or_2_out, and_2_out, rising_edge_delay_1_out_2);
  Subtractor subtractor_2 (.a(kounter_q), .b(divisor_register_q), .out(subtractor_2_out));  // open: bin, bout
  Comparator #(.mode("unsigned")) comparator_1 (.a(divisor), .b({8{1'b0}}), .eq(comparator_1_eq));  // open: gt, lt
  nor nor_1 (nor_1_out, subtractor_2_out[0], subtractor_2_out[1], subtractor_2_out[2], subtractor_2_out[3], subtractor_2_out[4], subtractor_2_out[5], subtractor_2_out[6], subtractor_2_out[7]);
  J_K_Flip_Flop j_k_ff_1 (.J(1'b1), .K(1'b1), .clk(nor_1_out), .Q(j_k_ff_1_q), .reset(or_1_out));  // open: Qn, preset
  Multiplexer multiplexer_3 (.in0(j_k_ff_1_q), .in1(clock), .out(out_6), .sel(comparator_1_eq));
endmodule

module falling_edge_delay (
  input  in_1,
  output out_2
);

  wire buffer_1_out, buffer_2_out, buffer_3_out, buffer_4_out, buffer_5_out, buffer_6_out, buffer_7_out,
       buffer_8_out, buffer_9_out, buffer_10_out, buffer_11_out, buffer_12_out, buffer_13_out, buffer_14_out,
       buffer_15_out, buffer_16_out, buffer_17_out, buffer_18_out, buffer_19_out, buffer_20_out,
       buffer_21_out, buffer_22_out, buffer_23_out, buffer_24_out, buffer_25_out, buffer_26_out,
       buffer_27_out, buffer_28_out, buffer_29_out, buffer_30_out, buffer_31_out, buffer_32_out,
       buffer_33_out, buffer_34_out, buffer_35_out, buffer_36_out, buffer_37_out, buffer_38_out,
       buffer_39_out, buffer_40_out, buffer_41_out, buffer_42_out, buffer_43_out, buffer_44_out,
       buffer_45_out, buffer_46_out, buffer_47_out, buffer_48_out, buffer_49_out, buffer_50_out,
       buffer_51_out, buffer_52_out, buffer_53_out, buffer_54_out, buffer_55_out, buffer_56_out,
       buffer_57_out, buffer_58_out, buffer_59_out, buffer_60_out, buffer_61_out, buffer_62_out,
       buffer_63_out, buffer_64_out;

  buf buffer_1 (buffer_1_out, in_1);
  buf buffer_2 (buffer_2_out, buffer_1_out);
  buf buffer_3 (buffer_3_out, buffer_4_out);
  buf buffer_4 (buffer_4_out, buffer_5_out);
  buf buffer_5 (buffer_5_out, buffer_25_out);
  buf buffer_6 (buffer_6_out, buffer_3_out);
  buf buffer_7 (buffer_7_out, buffer_6_out);
  buf buffer_8 (buffer_8_out, buffer_9_out);
  buf buffer_9 (buffer_9_out, buffer_10_out);
  buf buffer_10 (buffer_10_out, buffer_33_out);
  buf buffer_11 (buffer_11_out, buffer_8_out);
  buf buffer_12 (buffer_12_out, buffer_11_out);
  buf buffer_13 (buffer_13_out, buffer_14_out);
  buf buffer_14 (buffer_14_out, buffer_15_out);
  buf buffer_15 (buffer_15_out, buffer_41_out);
  buf buffer_16 (buffer_16_out, buffer_13_out);
  buf buffer_17 (buffer_17_out, buffer_16_out);
  buf buffer_18 (buffer_18_out, buffer_19_out);
  buf buffer_19 (buffer_19_out, buffer_20_out);
  buf buffer_20 (buffer_20_out, buffer_49_out);
  buf buffer_21 (buffer_21_out, buffer_2_out);
  buf buffer_22 (buffer_22_out, buffer_21_out);
  buf buffer_23 (buffer_23_out, buffer_22_out);
  buf buffer_24 (buffer_24_out, buffer_23_out);
  buf buffer_25 (buffer_25_out, buffer_26_out);
  buf buffer_26 (buffer_26_out, buffer_27_out);
  buf buffer_27 (buffer_27_out, buffer_28_out);
  buf buffer_28 (buffer_28_out, buffer_55_out);
  buf buffer_29 (buffer_29_out, buffer_7_out);
  buf buffer_30 (buffer_30_out, buffer_29_out);
  buf buffer_31 (buffer_31_out, buffer_30_out);
  buf buffer_32 (buffer_32_out, buffer_31_out);
  buf buffer_33 (buffer_33_out, buffer_34_out);
  buf buffer_34 (buffer_34_out, buffer_35_out);
  buf buffer_35 (buffer_35_out, buffer_36_out);
  buf buffer_36 (buffer_36_out, buffer_58_out);
  buf buffer_37 (buffer_37_out, buffer_12_out);
  buf buffer_38 (buffer_38_out, buffer_37_out);
  buf buffer_39 (buffer_39_out, buffer_38_out);
  buf buffer_40 (buffer_40_out, buffer_39_out);
  buf buffer_41 (buffer_41_out, buffer_42_out);
  buf buffer_42 (buffer_42_out, buffer_43_out);
  buf buffer_43 (buffer_43_out, buffer_44_out);
  buf buffer_44 (buffer_44_out, buffer_61_out);
  buf buffer_45 (buffer_45_out, buffer_17_out);
  buf buffer_46 (buffer_46_out, buffer_45_out);
  buf buffer_47 (buffer_47_out, buffer_46_out);
  buf buffer_48 (buffer_48_out, buffer_47_out);
  buf buffer_49 (buffer_49_out, buffer_50_out);
  buf buffer_50 (buffer_50_out, buffer_51_out);
  buf buffer_51 (buffer_51_out, buffer_52_out);
  buf buffer_52 (buffer_52_out, buffer_64_out);
  or or_1 (out_2, buffer_18_out, in_1);
  buf buffer_53 (buffer_53_out, buffer_24_out);
  buf buffer_54 (buffer_54_out, buffer_53_out);
  buf buffer_55 (buffer_55_out, buffer_54_out);
  buf buffer_56 (buffer_56_out, buffer_32_out);
  buf buffer_57 (buffer_57_out, buffer_56_out);
  buf buffer_58 (buffer_58_out, buffer_57_out);
  buf buffer_59 (buffer_59_out, buffer_40_out);
  buf buffer_60 (buffer_60_out, buffer_59_out);
  buf buffer_61 (buffer_61_out, buffer_60_out);
  buf buffer_62 (buffer_62_out, buffer_48_out);
  buf buffer_63 (buffer_63_out, buffer_62_out);
  buf buffer_64 (buffer_64_out, buffer_63_out);
endmodule

module rising_edge_delay (
  input  in_1,
  output out_2
);

  wire buffer_1_out, buffer_2_out, buffer_3_out, buffer_4_out, buffer_5_out, buffer_6_out, buffer_7_out,
       buffer_8_out, buffer_9_out, buffer_10_out, buffer_11_out, buffer_12_out, buffer_13_out, buffer_14_out,
       buffer_15_out, buffer_16_out, buffer_17_out, buffer_18_out, buffer_19_out, buffer_20_out,
       buffer_21_out, buffer_22_out, buffer_23_out, buffer_24_out, buffer_25_out, buffer_26_out,
       buffer_27_out, buffer_28_out, buffer_29_out, buffer_30_out, buffer_31_out, buffer_32_out,
       buffer_33_out, buffer_34_out, buffer_35_out, buffer_36_out, buffer_37_out, buffer_38_out,
       buffer_39_out, buffer_40_out, buffer_41_out, buffer_42_out, buffer_43_out, buffer_44_out,
       buffer_45_out, buffer_46_out, buffer_47_out, buffer_48_out, buffer_49_out, buffer_50_out,
       buffer_51_out, buffer_52_out, buffer_53_out, buffer_54_out, buffer_55_out, buffer_56_out,
       buffer_57_out, buffer_58_out, buffer_59_out, buffer_60_out, buffer_61_out, buffer_62_out,
       buffer_63_out, buffer_64_out;

  buf buffer_1 (buffer_1_out, in_1);
  buf buffer_2 (buffer_2_out, buffer_1_out);
  buf buffer_3 (buffer_3_out, buffer_4_out);
  buf buffer_4 (buffer_4_out, buffer_5_out);
  buf buffer_5 (buffer_5_out, buffer_25_out);
  buf buffer_6 (buffer_6_out, buffer_3_out);
  buf buffer_7 (buffer_7_out, buffer_6_out);
  buf buffer_8 (buffer_8_out, buffer_9_out);
  buf buffer_9 (buffer_9_out, buffer_10_out);
  buf buffer_10 (buffer_10_out, buffer_33_out);
  buf buffer_11 (buffer_11_out, buffer_8_out);
  buf buffer_12 (buffer_12_out, buffer_11_out);
  buf buffer_13 (buffer_13_out, buffer_14_out);
  buf buffer_14 (buffer_14_out, buffer_15_out);
  buf buffer_15 (buffer_15_out, buffer_41_out);
  buf buffer_16 (buffer_16_out, buffer_13_out);
  buf buffer_17 (buffer_17_out, buffer_16_out);
  buf buffer_18 (buffer_18_out, buffer_19_out);
  buf buffer_19 (buffer_19_out, buffer_20_out);
  buf buffer_20 (buffer_20_out, buffer_49_out);
  buf buffer_21 (buffer_21_out, buffer_2_out);
  buf buffer_22 (buffer_22_out, buffer_21_out);
  buf buffer_23 (buffer_23_out, buffer_22_out);
  buf buffer_24 (buffer_24_out, buffer_23_out);
  buf buffer_25 (buffer_25_out, buffer_26_out);
  buf buffer_26 (buffer_26_out, buffer_27_out);
  buf buffer_27 (buffer_27_out, buffer_28_out);
  buf buffer_28 (buffer_28_out, buffer_55_out);
  buf buffer_29 (buffer_29_out, buffer_7_out);
  buf buffer_30 (buffer_30_out, buffer_29_out);
  buf buffer_31 (buffer_31_out, buffer_30_out);
  buf buffer_32 (buffer_32_out, buffer_31_out);
  buf buffer_33 (buffer_33_out, buffer_34_out);
  buf buffer_34 (buffer_34_out, buffer_35_out);
  buf buffer_35 (buffer_35_out, buffer_36_out);
  buf buffer_36 (buffer_36_out, buffer_58_out);
  buf buffer_37 (buffer_37_out, buffer_12_out);
  buf buffer_38 (buffer_38_out, buffer_37_out);
  buf buffer_39 (buffer_39_out, buffer_38_out);
  buf buffer_40 (buffer_40_out, buffer_39_out);
  buf buffer_41 (buffer_41_out, buffer_42_out);
  buf buffer_42 (buffer_42_out, buffer_43_out);
  buf buffer_43 (buffer_43_out, buffer_44_out);
  buf buffer_44 (buffer_44_out, buffer_61_out);
  buf buffer_45 (buffer_45_out, buffer_17_out);
  buf buffer_46 (buffer_46_out, buffer_45_out);
  buf buffer_47 (buffer_47_out, buffer_46_out);
  buf buffer_48 (buffer_48_out, buffer_47_out);
  buf buffer_49 (buffer_49_out, buffer_50_out);
  buf buffer_50 (buffer_50_out, buffer_51_out);
  buf buffer_51 (buffer_51_out, buffer_52_out);
  buf buffer_52 (buffer_52_out, buffer_64_out);
  and and_1 (out_2, buffer_18_out, in_1);
  buf buffer_53 (buffer_53_out, buffer_24_out);
  buf buffer_54 (buffer_54_out, buffer_53_out);
  buf buffer_55 (buffer_55_out, buffer_54_out);
  buf buffer_56 (buffer_56_out, buffer_32_out);
  buf buffer_57 (buffer_57_out, buffer_56_out);
  buf buffer_58 (buffer_58_out, buffer_57_out);
  buf buffer_59 (buffer_59_out, buffer_40_out);
  buf buffer_60 (buffer_60_out, buffer_59_out);
  buf buffer_61 (buffer_61_out, buffer_60_out);
  buf buffer_62 (buffer_62_out, buffer_48_out);
  buf buffer_63 (buffer_63_out, buffer_62_out);
  buf buffer_64 (buffer_64_out, buffer_63_out);

  // Notes on the sheet:
  //   While the falling edge is propagated ASAP
  //   Delays the rising edge from reaching the output for 48 * (buffer propagation delay),
endmodule

module not_or_hasnt (
  input  in_1,
  output out_2
);

  wire and_1_out, s_r_ff_1_q, s_r_ff_2_q;

  S_R_Flip_Flop s_r_ff_1 (.Q(s_r_ff_1_q), .reset(1'b0), .preset(in_1));  // open: S, R, clk, Qn
  and and_1 (and_1_out, s_r_ff_1_q, ~in_1);  // AND_Gate
  S_R_Flip_Flop s_r_ff_2 (.Q(s_r_ff_2_q), .reset(in_1), .preset(and_1_out));  // open: S, R, clk, Qn
  or or_1 (out_2, s_r_ff_2_q, ~s_r_ff_1_q);  // OR_Gate
endmodule

module eight_bit_gate (
  input  enable,
  input  [7:0] data_in,
  output [7:0] data_out
);

  assign data_out = {8{enable}} & data_in;  // AND_Gate and_1, 8 bits wide
endmodule

module microcode_mixer (
  input  [15:0] instruction,
  input  [15:0] tmpa_in,
  input  [15:0] tmpb_in,
  input  [15:0] microcode_in,
  output [15:0] microcode_out
);

  wire [3:0] multiplexer_1_out, multiplexer_2_out;

  Multiplexer #(.select(4), .width(4)) multiplexer_1 (
    .in0(microcode_in[11:8]), .in1(instruction[15:12]), .in2(instruction[11:8]), .in3(instruction[7:4]),
    .in4(instruction[3:0]), .in5(tmpa_in[15:12]), .in6(tmpa_in[11:8]), .in7(tmpa_in[7:4]),
    .in8(tmpa_in[3:0]), .in9(tmpb_in[15:12]), .in10(tmpb_in[11:8]), .in11(tmpb_in[7:4]), .in12(tmpb_in[3:0]),
    .out(multiplexer_1_out));  // open: in13, in14, in15, sel
  Multiplexer #(.select(4), .width(4)) multiplexer_2 (
    .in0(microcode_in[15:12]), .in1(instruction[15:12]), .in2(instruction[11:8]), .in3(instruction[7:4]),
    .in4(instruction[3:0]), .in5(tmpa_in[15:12]), .in6(tmpa_in[11:8]), .in7(tmpa_in[7:4]),
    .in8(tmpa_in[3:0]), .in9(tmpb_in[15:12]), .in10(tmpb_in[11:8]), .in11(tmpb_in[7:4]), .in12(tmpb_in[3:0]),
    .out(multiplexer_2_out));  // open: in13, in14, in15, sel
  Multiplexer #(.width(4)) multiplexer_3 (
    .in0(microcode_in[11:8]), .in1(multiplexer_1_out), .out(microcode_out[11:8]), .sel(microcode_in[7]));
  Multiplexer #(.width(4)) multiplexer_4 (
    .in0(microcode_in[15:12]), .in1(multiplexer_2_out), .out(microcode_out[15:12]), .sel(microcode_in[7]));

  assign microcode_out[7:0] = {1'b0, microcode_in[6:0]};
endmodule

module tick_counter (
  input  clock,
  input  reset,
  output [31:0] posedge_count,
  output [31:0] cycle_count,
  output [31:0] negedge_count
);

  wire [31:0] adder_1_out, adder_2_out;

  Register #(.width(32)) register_1 (.D(adder_1_out), .clk(clock), .Q(posedge_count), .clr(reset));  // open: en
  Adder #(.width(32)) adder_1 (.a(posedge_count), .b(32'h1), .out(adder_1_out));  // open: cin, cout
  Register #(.trigger("falling"), .width(32)) register_2 (
    .D(adder_2_out), .clk(clock), .Q(negedge_count), .clr(reset));  // open: en
  Adder #(.width(32)) adder_2 (.a(negedge_count), .b(32'h1), .out(adder_2_out));  // open: cin, cout
  Adder #(.width(32)) adder_3 (.a(posedge_count), .b(negedge_count), .out(cycle_count));  // open: cin, cout
endmodule

module four_bit_conditional_incrementer (
  input  in_1,
  input  [3:0] in_2,
  output [3:0] out_3
);

  Adder #(.width(4)) adder_1 (.a(in_2), .b(4'b0000), .out(out_3), .cin(in_1));  // open: cout
endmodule

module auto_reset_register (
  input  [15:0] data_in,
  input  write,
  input  [15:0] reset_value,
  input  clock,
  input  reset,
  output [15:0] data_out
);

  wire and_1_out, and_2_out, and_3_out, buffer_1_out, buffer_2_out, buffer_3_out, buffer_4_out, buffer_5_out,
       buffer_6_out, buffer_7_out, d_ff_1_q, not_1_out, or_1_out, or_2_out, s_r_ff_1_qn, s_r_ff_2_q,
       s_r_ff_3_q, sixt_bit_eq_zero_1_out_2;
  wire [15:0] multiplexer_1_out, multiplexer_2_out;

  Pull_Resistor pull_resistor_1 (.node(reset_value));
  sixt_bit_eq_zero sixt_bit_eq_zero_1 (.in_1(reset_value), .out_2(sixt_bit_eq_zero_1_out_2));
  S_R_Flip_Flop s_r_ff_1 (.Qn(s_r_ff_1_qn), .preset(clock));  // open: S, R, clk, Q, reset
  Multiplexer #(.width(16)) multiplexer_1 (
    .in0({16{1'b0}}), .in1(reset_value), .out(multiplexer_1_out), .sel(not_1_out));
  not not_1 (not_1_out, sixt_bit_eq_zero_1_out_2);
  or or_1 (or_1_out, s_r_ff_1_qn, reset);
  buf buffer_1 (buffer_1_out, clock);
  buf buffer_2 (buffer_2_out, buffer_1_out);
  buf buffer_3 (buffer_3_out, buffer_2_out);
  S_R_Flip_Flop s_r_ff_2 (.Q(s_r_ff_2_q), .reset(and_2_out), .preset(or_1_out));  // open: S, R, clk, Qn
  and and_1 (and_1_out, clock, ~buffer_4_out);  // AND_Gate
  buf buffer_4 (buffer_4_out, buffer_3_out);
  and and_2 (and_2_out, ~s_r_ff_3_q, buffer_7_out, s_r_ff_2_q);  // AND_Gate
  Multiplexer #(.width(16)) multiplexer_2 (
    .in0(data_in), .in1(multiplexer_1_out), .out(multiplexer_2_out), .sel(s_r_ff_2_q));
  D_Flip_Flop d_ff_1 (.D(clock), .clk(s_r_ff_2_q), .Q(d_ff_1_q), .reset(and_1_out));  // open: Qn, preset
  S_R_Flip_Flop s_r_ff_3 (.Q(s_r_ff_3_q), .reset(and_1_out), .preset(and_3_out));  // open: S, R, clk, Qn
  buf buffer_5 (buffer_5_out, and_1_out);
  buf buffer_6 (buffer_6_out, buffer_5_out);
  buf buffer_7 (buffer_7_out, buffer_6_out);
  and and_3 (and_3_out, d_ff_1_q, ~s_r_ff_3_q);  // AND_Gate
  Register #(.width(16)) register_1 (.D(multiplexer_2_out), .en(or_2_out), .clk(clock), .Q(data_out));  // open: clr
  or or_2 (or_2_out, s_r_ff_2_q, write);
endmodule

module default_register_00ff (
  input  [15:0] data_in,
  input  write,
  input  [15:0] reset_value,
  input  clock,
  input  reset,
  output [15:0] data_out
);

  wire and_1_out, and_2_out, and_3_out, buffer_1_out, buffer_2_out, buffer_3_out, buffer_4_out, buffer_5_out,
       buffer_6_out, buffer_7_out, d_ff_1_q, not_1_out, or_1_out, or_2_out, s_r_ff_1_qn, s_r_ff_2_q,
       s_r_ff_3_q, sixt_bit_eq_zero_1_out_2;
  wire [15:0] multiplexer_1_out, multiplexer_2_out;

  Pull_Resistor pull_resistor_1 (.node(reset_value));
  sixt_bit_eq_zero sixt_bit_eq_zero_1 (.in_1(reset_value), .out_2(sixt_bit_eq_zero_1_out_2));
  S_R_Flip_Flop s_r_ff_1 (.Qn(s_r_ff_1_qn), .preset(clock));  // open: S, R, clk, Q, reset
  Multiplexer #(.width(16)) multiplexer_1 (.in0(16'hff), .in1(reset_value), .out(multiplexer_1_out), .sel(not_1_out));
  not not_1 (not_1_out, sixt_bit_eq_zero_1_out_2);
  or or_1 (or_1_out, s_r_ff_1_qn, reset);
  buf buffer_1 (buffer_1_out, clock);
  buf buffer_2 (buffer_2_out, buffer_1_out);
  buf buffer_3 (buffer_3_out, buffer_2_out);
  S_R_Flip_Flop s_r_ff_2 (.Q(s_r_ff_2_q), .reset(and_2_out), .preset(or_1_out));  // open: S, R, clk, Qn
  and and_1 (and_1_out, clock, ~buffer_4_out);  // AND_Gate
  buf buffer_4 (buffer_4_out, buffer_3_out);
  buf buffer_5 (buffer_5_out, and_1_out);
  and and_2 (and_2_out, ~s_r_ff_3_q, buffer_7_out, s_r_ff_2_q);  // AND_Gate
  buf buffer_6 (buffer_6_out, buffer_5_out);
  buf buffer_7 (buffer_7_out, buffer_6_out);
  Multiplexer #(.width(16)) multiplexer_2 (
    .in0(data_in), .in1(multiplexer_1_out), .out(multiplexer_2_out), .sel(s_r_ff_2_q));
  D_Flip_Flop d_ff_1 (.D(clock), .clk(s_r_ff_2_q), .Q(d_ff_1_q), .reset(and_1_out));  // open: Qn, preset
  S_R_Flip_Flop s_r_ff_3 (.Q(s_r_ff_3_q), .reset(and_1_out), .preset(and_3_out));  // open: S, R, clk, Qn
  and and_3 (and_3_out, d_ff_1_q, ~s_r_ff_3_q);  // AND_Gate
  Register #(.width(16)) register_1 (.D(multiplexer_2_out), .en(or_2_out), .clk(clock), .Q(data_out));  // open: clr
  or or_2 (or_2_out, s_r_ff_2_q, write);
endmodule
module stacker (
  input  bypass_mask,
  input  enable,
  input  write_changemask,
  input  [15:0] mem_in,
  input  clk,
  input  reset,
  input  [15:0] register_write,
  input  [15:0] stacking_mask,
  output active,
  output [15:0] control_bus_1_out,
  output [15:0] change_mask,
  output [15:0] control_bus_2_out,
  output [15:0] to_data_bus
);

  wire adder_1_out, and_1_out, and_18_out, and_19_out, and_20_out, and_21_out, and_22_out, and_23_out,
       and_24_out, and_25_out, and_26_out, and_27_out, and_28_out, and_29_out, and_30_out, and_31_out,
       and_32_out, and_33_out, and_34_out, and_35_out, and_36_out, and_37_out, and_38_out, and_39_out,
       and_40_out, and_41_out, and_42_out, and_43_out, and_44_out, and_45_out, and_46_out, and_47_out,
       and_48_out, and_49_out, and_50_out, and_51_out, and_52_out, and_53_out, and_54_out, and_55_out,
       and_56_out, and_57_out, and_58_out, and_59_out, and_60_out, and_61_out, and_62_out, and_63_out,
       and_64_out, and_65_out, and_66_out, and_67_out, and_68_out, and_69_out, buffer_1_out, buffer_2_out,
       buffer_3_out, buffer_4_out, buffer_5_out, buffer_6_out, buffer_7_out, buffer_8_out, buffer_9_out,
       buffer_10_out, buffer_11_out, buffer_12_out, buffer_13_out, buffer_14_out, buffer_15_out,
       button_1_out, d_ff_1_q, d_ff_2_q, four_bit_eq_zero_1_out_2, four_bit_eq_zero_2_out_2,
       four_bit_eq_zero_3_out_2, four_bit_eq_zero_4_out_2, four_bit_eq_zero_5_out_2,
       four_bit_eq_zero_6_out_2, four_bit_eq_zero_7_out_2, four_bit_eq_zero_8_out_2,
       four_bit_eq_zero_9_out_2, four_bit_eq_zero_10_out_2, four_bit_eq_zero_11_out_2,
       four_bit_eq_zero_12_out_2, four_bit_eq_zero_13_out_2, four_bit_eq_zero_14_out_2,
       four_bit_eq_zero_15_out_2, four_bit_eq_zero_16_out_2, or_1_out, or_2_out, or_3_out, or_4_out,
       or_5_out, or_6_out, or_7_out, or_8_out, or_9_out, or_10_out, or_11_out, or_12_out, or_13_out,
       or_14_out, or_15_out, or_16_out, or_17_out, or_34_out, register_1_q, register_2_q, register_3_q,
       register_4_q, register_5_q, register_6_q, register_7_q, register_8_q, register_9_q, register_10_q,
       register_11_q, register_12_q, register_13_q, register_14_q, register_15_q, register_16_q,
       register_17_q, s_r_ff_1_q, s_r_ff_19_q;
  wire [3:0] four_bit_conditional_incrementer_1_out_3, four_bit_conditional_incrementer_2_out_3,
       four_bit_conditional_incrementer_3_out_3, four_bit_conditional_incrementer_4_out_3,
       four_bit_conditional_incrementer_5_out_3, four_bit_conditional_incrementer_6_out_3,
       four_bit_conditional_incrementer_7_out_3, four_bit_conditional_incrementer_8_out_3,
       four_bit_conditional_incrementer_9_out_3, four_bit_conditional_incrementer_10_out_3,
       four_bit_conditional_incrementer_11_out_3, four_bit_conditional_incrementer_12_out_3,
       four_bit_conditional_incrementer_13_out_3, four_bit_conditional_incrementer_14_out_3,
       four_bit_conditional_incrementer_15_out_3, four_bit_conditional_incrementer_16_out_3,
       four_bit_g8_1_out_3, four_bit_g8_2_out_3, four_bit_g8_3_out_3, four_bit_g8_4_out_3,
       four_bit_g8_5_out_3, four_bit_g8_6_out_3, four_bit_g8_7_out_3, four_bit_g8_8_out_3,
       four_bit_g8_9_out_3, four_bit_g8_10_out_3, four_bit_g8_11_out_3, four_bit_g8_12_out_3,
       four_bit_g8_13_out_3, four_bit_g8_14_out_3, four_bit_g8_15_out_3, four_bit_g8_16_out_3, or_19_out,
       or_20_out, or_21_out, or_22_out, or_23_out, or_24_out, or_25_out, or_26_out, or_27_out, or_28_out,
       or_29_out, or_30_out, or_31_out, or_32_out, or_33_out;
  wire [15:0] multiplexer_1_out, multiplexer_2_out, multiplexer_3_out, multiplexer_4_out, multiplexer_5_out,
       multiplexer_6_out, multiplexer_7_out, not_1_out, s_r_ff_3_q;
  wire [15:12] or_18_out;

  Button button_1 (.out(button_1_out));
  or or_1 (or_1_out, reset, and_69_out, button_1_out);
  Multiplexer #(.width(16)) multiplexer_1 (
    .in0(register_write), .in1(mem_in), .out(multiplexer_1_out), .sel(s_r_ff_1_q));
  Multiplexer #(.width(16)) multiplexer_2 (
    .in0(stacking_mask), .in1({16{1'b1}}), .out(multiplexer_2_out), .sel(bypass_mask));
  Pull_Resistor pull_resistor_1 (.node(bypass_mask));
  buf buffer_1 (buffer_1_out, write_changemask);
  buf buffer_2 (buffer_2_out, buffer_1_out);
  buf buffer_3 (buffer_3_out, buffer_2_out);
  and and_1 (and_1_out, write_changemask, ~buffer_4_out);  // AND_Gate
  buf buffer_4 (buffer_4_out, buffer_3_out);
  S_R_Flip_Flop s_r_ff_1 (.Q(s_r_ff_1_q), .reset(clk), .preset(and_1_out));  // open: S, R, clk, Qn
  Register #(.width(1)) register_1 (
    .D(multiplexer_1_out[0]), .en(or_2_out), .clk(clk), .Q(register_1_q), .clr(or_1_out));
  or or_2 (or_2_out, multiplexer_1_out[0], s_r_ff_1_q);
  Register #(.width(1)) register_2 (
    .D(multiplexer_1_out[1]), .en(or_3_out), .clk(clk), .Q(register_2_q), .clr(or_1_out));
  or or_3 (or_3_out, multiplexer_1_out[1], s_r_ff_1_q);
  Register #(.width(1)) register_3 (
    .D(multiplexer_1_out[2]), .en(or_4_out), .clk(clk), .Q(register_3_q), .clr(or_1_out));
  or or_4 (or_4_out, multiplexer_1_out[2], s_r_ff_1_q);
  Register #(.width(1)) register_4 (
    .D(multiplexer_1_out[3]), .en(or_5_out), .clk(clk), .Q(register_4_q), .clr(or_1_out));
  or or_5 (or_5_out, multiplexer_1_out[3], s_r_ff_1_q);
  Register #(.width(1)) register_5 (
    .D(multiplexer_1_out[4]), .en(or_6_out), .clk(clk), .Q(register_5_q), .clr(or_1_out));
  or or_6 (or_6_out, multiplexer_1_out[4], s_r_ff_1_q);
  Register #(.width(1)) register_6 (
    .D(multiplexer_1_out[5]), .en(or_7_out), .clk(clk), .Q(register_6_q), .clr(or_1_out));
  or or_7 (or_7_out, multiplexer_1_out[5], s_r_ff_1_q);
  Register #(.width(1)) register_7 (
    .D(multiplexer_1_out[6]), .en(or_8_out), .clk(clk), .Q(register_7_q), .clr(or_1_out));
  or or_8 (or_8_out, multiplexer_1_out[6], s_r_ff_1_q);
  Register #(.width(1)) register_8 (
    .D(multiplexer_1_out[7]), .en(or_9_out), .clk(clk), .Q(register_8_q), .clr(or_1_out));
  or or_9 (or_9_out, multiplexer_1_out[7], s_r_ff_1_q);
  Register #(.width(1)) register_9 (
    .D(multiplexer_1_out[8]), .en(or_10_out), .clk(clk), .Q(register_9_q), .clr(or_1_out));
  or or_10 (or_10_out, multiplexer_1_out[8], s_r_ff_1_q);
  Register #(.width(1)) register_10 (
    .D(multiplexer_1_out[9]), .en(or_11_out), .clk(clk), .Q(register_10_q), .clr(or_1_out));
  or or_11 (or_11_out, multiplexer_1_out[9], s_r_ff_1_q);
  Register #(.width(1)) register_11 (
    .D(multiplexer_1_out[10]), .en(or_12_out), .clk(clk), .Q(register_11_q), .clr(or_1_out));
  or or_12 (or_12_out, multiplexer_1_out[10], s_r_ff_1_q);
  Register #(.width(1)) register_12 (
    .D(multiplexer_1_out[11]), .en(or_13_out), .clk(clk), .Q(register_12_q), .clr(or_1_out));
  or or_13 (or_13_out, multiplexer_1_out[11], s_r_ff_1_q);
  Register #(.width(1)) register_13 (
    .D(multiplexer_1_out[12]), .en(or_14_out), .clk(clk), .Q(register_13_q), .clr(or_1_out));
  or or_14 (or_14_out, multiplexer_1_out[12], s_r_ff_1_q);
  Register #(.width(1)) register_14 (
    .D(multiplexer_1_out[13]), .en(or_15_out), .clk(clk), .Q(register_14_q), .clr(or_1_out));
  or or_15 (or_15_out, multiplexer_1_out[13], s_r_ff_1_q);
  Register #(.width(1)) register_15 (
    .D(multiplexer_1_out[14]), .en(or_16_out), .clk(clk), .Q(register_15_q), .clr(or_1_out));
  or or_16 (or_16_out, multiplexer_1_out[14], s_r_ff_1_q);
  Register #(.width(1)) register_16 (
    .D(multiplexer_1_out[15]), .en(or_17_out), .clk(clk), .Q(register_16_q), .clr(or_1_out));
  or or_17 (or_17_out, multiplexer_1_out[15], s_r_ff_1_q);
  S_R_Flip_Flop s_r_ff_2 (.Q(active), .reset(or_1_out), .preset(and_18_out));  // open: S, R, clk, Qn
  and and_2 (change_mask[0], multiplexer_2_out[0], register_1_q);
  and and_3 (change_mask[1], multiplexer_2_out[1], register_2_q);
  and and_4 (change_mask[2], multiplexer_2_out[2], register_3_q);
  and and_5 (change_mask[3], multiplexer_2_out[3], register_4_q);
  and and_6 (change_mask[4], multiplexer_2_out[4], register_5_q);
  and and_7 (change_mask[5], multiplexer_2_out[5], register_6_q);
  and and_8 (change_mask[6], multiplexer_2_out[6], register_7_q);
  and and_9 (change_mask[7], multiplexer_2_out[7], register_8_q);
  and and_10 (change_mask[8], multiplexer_2_out[8], register_9_q);
  and and_11 (change_mask[9], multiplexer_2_out[9], register_10_q);
  and and_12 (change_mask[10], multiplexer_2_out[10], register_11_q);
  and and_13 (change_mask[11], multiplexer_2_out[11], register_12_q);
  and and_14 (change_mask[12], multiplexer_2_out[12], register_13_q);
  and and_15 (change_mask[13], multiplexer_2_out[13], register_14_q);
  and and_16 (change_mask[14], multiplexer_2_out[14], register_15_q);
  and and_17 (change_mask[15], multiplexer_2_out[15], register_16_q);
  and and_18 (and_18_out, enable, ~active);  // AND_Gate
  assign not_1_out = ~s_r_ff_3_q;  // NOT_Gate not_1, 16 bits wide
  and and_19 (and_19_out, change_mask[0], not_1_out[0]);
  and and_20 (and_20_out, change_mask[1], not_1_out[1]);
  and and_21 (and_21_out, change_mask[2], not_1_out[2]);
  and and_22 (and_22_out, change_mask[3], not_1_out[3]);
  and and_23 (and_23_out, change_mask[4], not_1_out[4]);
  and and_24 (and_24_out, change_mask[5], not_1_out[5]);
  and and_25 (and_25_out, change_mask[6], not_1_out[6]);
  and and_26 (and_26_out, change_mask[7], not_1_out[7]);
  and and_27 (and_27_out, change_mask[8], not_1_out[8]);
  and and_28 (and_28_out, change_mask[9], not_1_out[9]);
  and and_29 (and_29_out, change_mask[10], not_1_out[10]);
  and and_30 (and_30_out, change_mask[11], not_1_out[11]);
  and and_31 (and_31_out, change_mask[12], not_1_out[12]);
  and and_32 (and_32_out, change_mask[13], not_1_out[13]);
  and and_33 (and_33_out, change_mask[14], not_1_out[14]);
  and and_34 (and_34_out, change_mask[15], not_1_out[15]);
  four_bit_conditional_incrementer four_bit_conditional_incrementer_1 (
    .in_2(4'b0000), .in_1(and_19_out), .out_3(four_bit_conditional_incrementer_1_out_3));
  four_bit_eq_zero four_bit_eq_zero_1 (
    .in_1(four_bit_conditional_incrementer_1_out_3), .out_2(four_bit_eq_zero_1_out_2));
  four_bit_conditional_incrementer four_bit_conditional_incrementer_2 (
    .in_2(four_bit_conditional_incrementer_1_out_3), .in_1(and_20_out),
    .out_3(four_bit_conditional_incrementer_2_out_3));
  four_bit_eq_zero four_bit_eq_zero_2 (
    .in_1(four_bit_conditional_incrementer_2_out_3), .out_2(four_bit_eq_zero_2_out_2));
  four_bit_conditional_incrementer four_bit_conditional_incrementer_3 (
    .in_2(four_bit_conditional_incrementer_2_out_3), .in_1(and_21_out),
    .out_3(four_bit_conditional_incrementer_3_out_3));
  four_bit_eq_zero four_bit_eq_zero_3 (
    .in_1(four_bit_conditional_incrementer_3_out_3), .out_2(four_bit_eq_zero_3_out_2));
  four_bit_conditional_incrementer four_bit_conditional_incrementer_4 (
    .in_2(four_bit_conditional_incrementer_3_out_3), .in_1(and_22_out),
    .out_3(four_bit_conditional_incrementer_4_out_3));
  four_bit_eq_zero four_bit_eq_zero_4 (
    .in_1(four_bit_conditional_incrementer_4_out_3), .out_2(four_bit_eq_zero_4_out_2));
  four_bit_conditional_incrementer four_bit_conditional_incrementer_5 (
    .in_2(four_bit_conditional_incrementer_4_out_3), .in_1(and_23_out),
    .out_3(four_bit_conditional_incrementer_5_out_3));
  four_bit_eq_zero four_bit_eq_zero_5 (
    .in_1(four_bit_conditional_incrementer_5_out_3), .out_2(four_bit_eq_zero_5_out_2));
  four_bit_conditional_incrementer four_bit_conditional_incrementer_6 (
    .in_2(four_bit_conditional_incrementer_5_out_3), .in_1(and_24_out),
    .out_3(four_bit_conditional_incrementer_6_out_3));
  four_bit_eq_zero four_bit_eq_zero_6 (
    .in_1(four_bit_conditional_incrementer_6_out_3), .out_2(four_bit_eq_zero_6_out_2));
  four_bit_conditional_incrementer four_bit_conditional_incrementer_7 (
    .in_2(four_bit_conditional_incrementer_6_out_3), .in_1(and_25_out),
    .out_3(four_bit_conditional_incrementer_7_out_3));
  four_bit_eq_zero four_bit_eq_zero_7 (
    .in_1(four_bit_conditional_incrementer_7_out_3), .out_2(four_bit_eq_zero_7_out_2));
  four_bit_conditional_incrementer four_bit_conditional_incrementer_8 (
    .in_2(four_bit_conditional_incrementer_7_out_3), .in_1(and_26_out),
    .out_3(four_bit_conditional_incrementer_8_out_3));
  four_bit_eq_zero four_bit_eq_zero_8 (
    .in_1(four_bit_conditional_incrementer_8_out_3), .out_2(four_bit_eq_zero_8_out_2));
  four_bit_conditional_incrementer four_bit_conditional_incrementer_9 (
    .in_2(four_bit_conditional_incrementer_8_out_3), .in_1(and_27_out),
    .out_3(four_bit_conditional_incrementer_9_out_3));
  four_bit_eq_zero four_bit_eq_zero_9 (
    .in_1(four_bit_conditional_incrementer_9_out_3), .out_2(four_bit_eq_zero_9_out_2));
  four_bit_conditional_incrementer four_bit_conditional_incrementer_10 (
    .in_2(four_bit_conditional_incrementer_9_out_3), .in_1(and_28_out),
    .out_3(four_bit_conditional_incrementer_10_out_3));
  four_bit_eq_zero four_bit_eq_zero_10 (
    .in_1(four_bit_conditional_incrementer_10_out_3), .out_2(four_bit_eq_zero_10_out_2));
  four_bit_conditional_incrementer four_bit_conditional_incrementer_11 (
    .in_2(four_bit_conditional_incrementer_10_out_3), .in_1(and_29_out),
    .out_3(four_bit_conditional_incrementer_11_out_3));
  four_bit_eq_zero four_bit_eq_zero_11 (
    .in_1(four_bit_conditional_incrementer_11_out_3), .out_2(four_bit_eq_zero_11_out_2));
  four_bit_conditional_incrementer four_bit_conditional_incrementer_12 (
    .in_2(four_bit_conditional_incrementer_11_out_3), .in_1(and_30_out),
    .out_3(four_bit_conditional_incrementer_12_out_3));
  four_bit_eq_zero four_bit_eq_zero_12 (
    .in_1(four_bit_conditional_incrementer_12_out_3), .out_2(four_bit_eq_zero_12_out_2));
  four_bit_conditional_incrementer four_bit_conditional_incrementer_13 (
    .in_2(four_bit_conditional_incrementer_12_out_3), .in_1(and_31_out),
    .out_3(four_bit_conditional_incrementer_13_out_3));
  four_bit_eq_zero four_bit_eq_zero_13 (
    .in_1(four_bit_conditional_incrementer_13_out_3), .out_2(four_bit_eq_zero_13_out_2));
  four_bit_conditional_incrementer four_bit_conditional_incrementer_14 (
    .in_2(four_bit_conditional_incrementer_13_out_3), .in_1(and_32_out),
    .out_3(four_bit_conditional_incrementer_14_out_3));
  four_bit_eq_zero four_bit_eq_zero_14 (
    .in_1(four_bit_conditional_incrementer_14_out_3), .out_2(four_bit_eq_zero_14_out_2));
  four_bit_conditional_incrementer four_bit_conditional_incrementer_15 (
    .in_2(four_bit_conditional_incrementer_14_out_3), .in_1(and_33_out),
    .out_3(four_bit_conditional_incrementer_15_out_3));
  four_bit_eq_zero four_bit_eq_zero_15 (
    .in_1(four_bit_conditional_incrementer_15_out_3), .out_2(four_bit_eq_zero_15_out_2));
  four_bit_conditional_incrementer four_bit_conditional_incrementer_16 (
    .in_2(four_bit_conditional_incrementer_15_out_3), .in_1(and_34_out),
    .out_3(four_bit_conditional_incrementer_16_out_3));
  // Probe on four_bit_conditional_incrementer_16_out_3
  and and_35 (and_35_out, four_bit_eq_zero_1_out_2, and_20_out);
  and and_36 (and_36_out, four_bit_eq_zero_2_out_2, and_21_out);
  and and_37 (and_37_out, four_bit_eq_zero_3_out_2, and_22_out);
  and and_38 (and_38_out, four_bit_eq_zero_4_out_2, and_23_out);
  and and_39 (and_39_out, four_bit_eq_zero_5_out_2, and_24_out);
  and and_40 (and_40_out, four_bit_eq_zero_6_out_2, and_25_out);
  and and_41 (and_41_out, four_bit_eq_zero_7_out_2, and_26_out);
  and and_42 (and_42_out, four_bit_eq_zero_8_out_2, and_27_out);
  and and_43 (and_43_out, four_bit_eq_zero_9_out_2, and_28_out);
  and and_44 (and_44_out, four_bit_eq_zero_10_out_2, and_29_out);
  and and_45 (and_45_out, four_bit_eq_zero_11_out_2, and_30_out);
  and and_46 (and_46_out, four_bit_eq_zero_12_out_2, and_31_out);
  and and_47 (and_47_out, four_bit_eq_zero_13_out_2, and_32_out);
  and and_48 (and_48_out, four_bit_eq_zero_14_out_2, and_33_out);
  and and_49 (and_49_out, four_bit_eq_zero_15_out_2, and_34_out);
  and and_50 (and_50_out, register_17_q, and_19_out);
  four_bit_g8 four_bit_g8_1 (.in_1(and_19_out), .in_2(4'b0000), .out_3(four_bit_g8_1_out_3));
  and and_51 (and_51_out, register_17_q, and_35_out);
  four_bit_g8 four_bit_g8_2 (.in_1(and_35_out), .in_2(4'b0001), .out_3(four_bit_g8_2_out_3));
  and and_52 (and_52_out, register_17_q, and_36_out);
  four_bit_g8 four_bit_g8_3 (.in_1(and_36_out), .in_2(4'b0010), .out_3(four_bit_g8_3_out_3));
  and and_53 (and_53_out, register_17_q, and_37_out);
  four_bit_g8 four_bit_g8_4 (.in_1(and_37_out), .in_2(4'b0011), .out_3(four_bit_g8_4_out_3));
  and and_54 (and_54_out, register_17_q, and_38_out);
  four_bit_g8 four_bit_g8_5 (.in_1(and_38_out), .in_2(4'b0100), .out_3(four_bit_g8_5_out_3));
  and and_55 (and_55_out, register_17_q, and_39_out);
  four_bit_g8 four_bit_g8_6 (.in_1(and_39_out), .in_2(4'b0101), .out_3(four_bit_g8_6_out_3));
  and and_56 (and_56_out, register_17_q, and_40_out);
  four_bit_g8 four_bit_g8_7 (.in_1(and_40_out), .in_2(4'b0110), .out_3(four_bit_g8_7_out_3));
  and and_57 (and_57_out, register_17_q, and_41_out);
  four_bit_g8 four_bit_g8_8 (.in_1(and_41_out), .in_2(4'b0111), .out_3(four_bit_g8_8_out_3));
  and and_58 (and_58_out, register_17_q, and_42_out);
  four_bit_g8 four_bit_g8_9 (.in_1(and_42_out), .in_2(4'b1000), .out_3(four_bit_g8_9_out_3));
  and and_59 (and_59_out, register_17_q, and_43_out);
  four_bit_g8 four_bit_g8_10 (.in_1(and_43_out), .in_2(4'b1001), .out_3(four_bit_g8_10_out_3));
  and and_60 (and_60_out, register_17_q, and_44_out);
  four_bit_g8 four_bit_g8_11 (.in_1(and_44_out), .in_2(4'b1010), .out_3(four_bit_g8_11_out_3));
  and and_61 (and_61_out, register_17_q, and_45_out);
  four_bit_g8 four_bit_g8_12 (.in_1(and_45_out), .in_2(4'b1011), .out_3(four_bit_g8_12_out_3));
  and and_62 (and_62_out, register_17_q, and_46_out);
  four_bit_g8 four_bit_g8_13 (.in_1(and_46_out), .in_2(4'b1100), .out_3(four_bit_g8_13_out_3));
  and and_63 (and_63_out, register_17_q, and_47_out);
  four_bit_g8 four_bit_g8_14 (.in_1(and_47_out), .in_2(4'b1101), .out_3(four_bit_g8_14_out_3));
  and and_64 (and_64_out, register_17_q, and_48_out);
  four_bit_g8 four_bit_g8_15 (.in_1(and_48_out), .in_2(4'b1110), .out_3(four_bit_g8_15_out_3));
  and and_65 (and_65_out, register_17_q, and_49_out);
  four_bit_g8 four_bit_g8_16 (.in_1(and_49_out), .in_2(4'b1111), .out_3(four_bit_g8_16_out_3));
  four_bit_eq_zero four_bit_eq_zero_16 (
    .in_1(four_bit_conditional_incrementer_16_out_3), .out_2(four_bit_eq_zero_16_out_2));
  assign or_18_out = four_bit_g8_1_out_3 | or_19_out;  // OR_Gate or_18, 4 bits wide
  assign or_19_out = four_bit_g8_2_out_3 | or_20_out;  // OR_Gate or_19, 4 bits wide
  assign or_20_out = four_bit_g8_3_out_3 | or_21_out;  // OR_Gate or_20, 4 bits wide
  assign or_21_out = four_bit_g8_4_out_3 | or_22_out;  // OR_Gate or_21, 4 bits wide
  assign or_22_out = four_bit_g8_5_out_3 | or_23_out;  // OR_Gate or_22, 4 bits wide
  assign or_23_out = four_bit_g8_6_out_3 | or_24_out;  // OR_Gate or_23, 4 bits wide
  assign or_24_out = four_bit_g8_7_out_3 | or_25_out;  // OR_Gate or_24, 4 bits wide
  assign or_25_out = four_bit_g8_8_out_3 | or_26_out;  // OR_Gate or_25, 4 bits wide
  assign or_26_out = four_bit_g8_9_out_3 | or_27_out;  // OR_Gate or_26, 4 bits wide
  assign or_27_out = four_bit_g8_10_out_3 | or_28_out;  // OR_Gate or_27, 4 bits wide
  assign or_28_out = four_bit_g8_11_out_3 | or_29_out;  // OR_Gate or_28, 4 bits wide
  assign or_29_out = four_bit_g8_12_out_3 | or_30_out;  // OR_Gate or_29, 4 bits wide
  assign or_30_out = four_bit_g8_13_out_3 | or_31_out;  // OR_Gate or_30, 4 bits wide
  assign or_31_out = four_bit_g8_14_out_3 | or_32_out;  // OR_Gate or_31, 4 bits wide
  assign or_32_out = four_bit_g8_15_out_3 | or_33_out;  // OR_Gate or_32, 4 bits wide
  assign or_33_out = four_bit_g8_16_out_3 | four_bit_g8_16_out_3;  // OR_Gate or_33, 4 bits wide
  and and_66 (and_66_out, active, four_bit_eq_zero_16_out_2);
  S_R_Flip_Flop s_r_ff_3 (
    .S(and_50_out), .R(1'b0), .clk(clk), .Q(s_r_ff_3_q[0]), .reset(or_1_out));  // open: Qn, preset
  S_R_Flip_Flop s_r_ff_4 (
    .S(and_51_out), .R(1'b0), .clk(clk), .Q(s_r_ff_3_q[1]), .reset(or_1_out));  // open: Qn, preset
  S_R_Flip_Flop s_r_ff_5 (
    .S(and_52_out), .R(1'b0), .clk(clk), .Q(s_r_ff_3_q[2]), .reset(or_1_out));  // open: Qn, preset
  S_R_Flip_Flop s_r_ff_6 (
    .S(and_53_out), .R(1'b0), .clk(clk), .Q(s_r_ff_3_q[3]), .reset(or_1_out));  // open: Qn, preset
  S_R_Flip_Flop s_r_ff_7 (
    .S(and_54_out), .R(1'b0), .clk(clk), .Q(s_r_ff_3_q[4]), .reset(or_1_out));  // open: Qn, preset
  S_R_Flip_Flop s_r_ff_8 (
    .S(and_55_out), .R(1'b0), .clk(clk), .Q(s_r_ff_3_q[5]), .reset(or_1_out));  // open: Qn, preset
  S_R_Flip_Flop s_r_ff_9 (
    .S(and_56_out), .R(1'b0), .clk(clk), .Q(s_r_ff_3_q[6]), .reset(or_1_out));  // open: Qn, preset
  S_R_Flip_Flop s_r_ff_10 (
    .S(and_57_out), .R(1'b0), .clk(clk), .Q(s_r_ff_3_q[7]), .reset(or_1_out));  // open: Qn, preset
  S_R_Flip_Flop s_r_ff_11 (
    .S(and_58_out), .R(1'b0), .clk(clk), .Q(s_r_ff_3_q[8]), .reset(or_1_out));  // open: Qn, preset
  S_R_Flip_Flop s_r_ff_12 (
    .S(and_59_out), .R(1'b0), .clk(clk), .Q(s_r_ff_3_q[9]), .reset(or_1_out));  // open: Qn, preset
  S_R_Flip_Flop s_r_ff_13 (
    .S(and_60_out), .R(1'b0), .clk(clk), .Q(s_r_ff_3_q[10]), .reset(or_1_out));  // open: Qn, preset
  S_R_Flip_Flop s_r_ff_14 (
    .S(and_61_out), .R(1'b0), .clk(clk), .Q(s_r_ff_3_q[11]), .reset(or_1_out));  // open: Qn, preset
  S_R_Flip_Flop s_r_ff_15 (
    .S(and_62_out), .R(1'b0), .clk(clk), .Q(s_r_ff_3_q[12]), .reset(or_1_out));  // open: Qn, preset
  S_R_Flip_Flop s_r_ff_16 (
    .S(and_63_out), .R(1'b0), .clk(clk), .Q(s_r_ff_3_q[13]), .reset(or_1_out));  // open: Qn, preset
  S_R_Flip_Flop s_r_ff_17 (
    .S(and_64_out), .R(1'b0), .clk(clk), .Q(s_r_ff_3_q[14]), .reset(or_1_out));  // open: Qn, preset
  S_R_Flip_Flop s_r_ff_18 (
    .S(and_65_out), .R(1'b0), .clk(clk), .Q(s_r_ff_3_q[15]), .reset(or_1_out));  // open: Qn, preset
  buf buffer_5 (buffer_5_out, and_66_out);
  buf buffer_6 (buffer_6_out, buffer_5_out);
  and and_67 (and_67_out, and_66_out, buffer_8_out);
  buf buffer_7 (buffer_7_out, buffer_6_out);
  buf buffer_8 (buffer_8_out, buffer_7_out);
  Register #(.width(1)) register_17 (.D(adder_1_out), .en(active), .clk(clk), .Q(register_17_q), .clr(or_34_out));
  or or_34 (or_34_out, or_1_out, and_68_out);
  Multiplexer #(.width(16)) multiplexer_3 (
    .in0({or_18_out, 12'h20}), .in1(16'h25), .out(multiplexer_3_out), .sel(register_17_q));
  Multiplexer #(.width(16)) multiplexer_4 (
    .in0(16'h1012), .in1({16{1'b0}}), .out(multiplexer_4_out), .sel(register_17_q));
  Adder #(.width(1)) adder_1 (.a(register_17_q), .b(1'b1), .out(adder_1_out));  // open: cin, cout
  Multiplexer #(.width(16)) multiplexer_5 (.in0(16'h1012), .in1(16'h25), .out(multiplexer_5_out), .sel(register_17_q));
  S_R_Flip_Flop s_r_ff_19 (.Q(s_r_ff_19_q), .reset(or_1_out), .preset(and_67_out));  // open: S, R, clk, Qn
  buf buffer_9 (buffer_9_out, active);
  buf buffer_10 (buffer_10_out, buffer_9_out);
  buf buffer_11 (buffer_11_out, buffer_10_out);
  and and_68 (and_68_out, active, ~buffer_11_out);  // AND_Gate
  Multiplexer #(.width(16)) multiplexer_6 (
    .in0(multiplexer_3_out), .in1(multiplexer_5_out), .out(multiplexer_6_out), .sel(s_r_ff_19_q));
  Multiplexer #(.width(16)) multiplexer_7 (
    .in0(multiplexer_4_out), .in1({16{1'b0}}), .out(multiplexer_7_out), .sel(s_r_ff_19_q));
  sixt_bit_gatekeeper sixt_bit_gatekeeper_1 (.in_1(active), .in_2(multiplexer_6_out), .out_3(control_bus_1_out));
  sixt_bit_gatekeeper sixt_bit_gatekeeper_2 (.in_1(active), .in_2(multiplexer_7_out), .out_3(control_bus_2_out));
  sixt_bit_gatekeeper sixt_bit_gatekeeper_3 (.in_1(d_ff_1_q), .in_2(change_mask), .out_3(to_data_bus));
  D_Flip_Flop d_ff_1 (.D(s_r_ff_19_q), .clk(clk), .Q(d_ff_1_q), .reset(or_1_out));  // open: Qn, preset
  // Probe on control_bus_1_out
  // Probe on control_bus_2_out
  D_Flip_Flop d_ff_2 (.D(d_ff_1_q), .clk(clk), .Q(d_ff_2_q), .reset(or_1_out));  // open: Qn, preset
  and and_69 (and_69_out, d_ff_2_q, ~buffer_12_out);  // AND_Gate
  buf buffer_12 (buffer_12_out, buffer_13_out);
  buf buffer_13 (buffer_13_out, buffer_14_out);
  buf buffer_14 (buffer_14_out, buffer_15_out);
  buf buffer_15 (buffer_15_out, d_ff_2_q);
endmodule

module unstacker (
  input  enable,
  input  load_unstacking_mask,
  input  clk,
  input  reset,
  input  [15:0] unstacking_mask,
  output active,
  output [15:0] control_bus_1_out,
  output [15:0] control_bus_2_out
);

  wire adder_1_out, and_1_out, and_2_out, and_3_out, and_4_out, and_5_out, and_6_out, and_7_out, and_8_out,
       and_9_out, and_10_out, and_11_out, and_12_out, and_13_out, and_14_out, and_15_out, and_16_out,
       and_17_out, and_18_out, and_19_out, and_20_out, and_21_out, and_22_out, and_23_out, and_24_out,
       and_25_out, and_26_out, and_27_out, and_28_out, and_29_out, and_30_out, and_31_out, and_32_out,
       and_33_out, and_34_out, buffer_1_out, buffer_2_out, buffer_3_out, buffer_4_out, buffer_5_out,
       button_1_out, d_ff_1_q, d_ff_2_q, d_ff_3_q, d_ff_4_q, d_ff_5_q, d_ff_6_q, d_ff_7_q, d_ff_8_q,
       d_ff_9_q, d_ff_10_q, d_ff_11_q, d_ff_12_q, d_ff_13_q, d_ff_14_q, d_ff_15_q, d_ff_16_q, d_ff_17_q,
       four_bit_eq_zero_1_out_2, four_bit_eq_zero_2_out_2, four_bit_eq_zero_3_out_2,
       four_bit_eq_zero_4_out_2, four_bit_eq_zero_5_out_2, four_bit_eq_zero_6_out_2,
       four_bit_eq_zero_7_out_2, four_bit_eq_zero_8_out_2, four_bit_eq_zero_9_out_2,
       four_bit_eq_zero_10_out_2, four_bit_eq_zero_11_out_2, four_bit_eq_zero_12_out_2,
       four_bit_eq_zero_13_out_2, four_bit_eq_zero_14_out_2, four_bit_eq_zero_15_out_2,
       four_bit_eq_zero_16_out_2, or_1_out, or_19_out, register_2_q;
  wire [3:0] four_bit_conditional_incrementer_1_out_3, four_bit_conditional_incrementer_2_out_3,
       four_bit_conditional_incrementer_3_out_3, four_bit_conditional_incrementer_4_out_3,
       four_bit_conditional_incrementer_5_out_3, four_bit_conditional_incrementer_6_out_3,
       four_bit_conditional_incrementer_7_out_3, four_bit_conditional_incrementer_8_out_3,
       four_bit_conditional_incrementer_9_out_3, four_bit_conditional_incrementer_10_out_3,
       four_bit_conditional_incrementer_11_out_3, four_bit_conditional_incrementer_12_out_3,
       four_bit_conditional_incrementer_13_out_3, four_bit_conditional_incrementer_14_out_3,
       four_bit_conditional_incrementer_15_out_3, four_bit_conditional_incrementer_16_out_3,
       four_bit_g8_1_out_3, four_bit_g8_2_out_3, four_bit_g8_3_out_3, four_bit_g8_4_out_3,
       four_bit_g8_5_out_3, four_bit_g8_6_out_3, four_bit_g8_7_out_3, four_bit_g8_8_out_3,
       four_bit_g8_9_out_3, four_bit_g8_10_out_3, four_bit_g8_11_out_3, four_bit_g8_12_out_3,
       four_bit_g8_13_out_3, four_bit_g8_14_out_3, four_bit_g8_15_out_3, four_bit_g8_16_out_3, or_3_out,
       or_4_out, or_5_out, or_6_out, or_7_out, or_8_out, or_9_out, or_10_out, or_11_out, or_12_out,
       or_13_out, or_14_out, or_15_out, or_16_out, or_17_out, register_1_q;
  wire [15:0] bit_extender_1_out, multiplexer_1_out, multiplexer_2_out, or_18_out, s_r_ff_1_q;
  wire [15:12] or_2_out;

  Button button_1 (.out(button_1_out));
  or or_1 (or_1_out, reset, and_2_out, button_1_out);
  and and_1 (and_1_out, load_unstacking_mask, clk);
  D_Flip_Flop #(.trigger("falling")) d_ff_1 (
    .D(unstacking_mask[0]), .clk(and_1_out), .Q(d_ff_1_q), .reset(or_18_out[0]));  // open: Qn, preset
  D_Flip_Flop #(.trigger("falling")) d_ff_2 (
    .D(unstacking_mask[1]), .clk(and_1_out), .Q(d_ff_2_q), .reset(or_18_out[1]));  // open: Qn, preset
  D_Flip_Flop #(.trigger("falling")) d_ff_3 (
    .D(unstacking_mask[2]), .clk(and_1_out), .Q(d_ff_3_q), .reset(or_18_out[2]));  // open: Qn, preset
  D_Flip_Flop #(.trigger("falling")) d_ff_4 (
    .D(unstacking_mask[3]), .clk(and_1_out), .Q(d_ff_4_q), .reset(or_18_out[3]));  // open: Qn, preset
  D_Flip_Flop #(.trigger("falling")) d_ff_5 (
    .D(unstacking_mask[4]), .clk(and_1_out), .Q(d_ff_5_q), .reset(or_18_out[4]));  // open: Qn, preset
  D_Flip_Flop #(.trigger("falling")) d_ff_6 (
    .D(unstacking_mask[5]), .clk(and_1_out), .Q(d_ff_6_q), .reset(or_18_out[5]));  // open: Qn, preset
  D_Flip_Flop #(.trigger("falling")) d_ff_7 (
    .D(unstacking_mask[6]), .clk(and_1_out), .Q(d_ff_7_q), .reset(or_18_out[6]));  // open: Qn, preset
  D_Flip_Flop #(.trigger("falling")) d_ff_8 (
    .D(unstacking_mask[7]), .clk(and_1_out), .Q(d_ff_8_q), .reset(or_18_out[7]));  // open: Qn, preset
  D_Flip_Flop #(.trigger("falling")) d_ff_9 (
    .D(unstacking_mask[8]), .clk(and_1_out), .Q(d_ff_9_q), .reset(or_18_out[8]));  // open: Qn, preset
  D_Flip_Flop #(.trigger("falling")) d_ff_10 (
    .D(unstacking_mask[9]), .clk(and_1_out), .Q(d_ff_10_q), .reset(or_18_out[9]));  // open: Qn, preset
  D_Flip_Flop #(.trigger("falling")) d_ff_11 (
    .D(unstacking_mask[10]), .clk(and_1_out), .Q(d_ff_11_q), .reset(or_18_out[10]));  // open: Qn, preset
  D_Flip_Flop #(.trigger("falling")) d_ff_12 (
    .D(unstacking_mask[11]), .clk(and_1_out), .Q(d_ff_12_q), .reset(or_18_out[11]));  // open: Qn, preset
  D_Flip_Flop #(.trigger("falling")) d_ff_13 (
    .D(unstacking_mask[12]), .clk(and_1_out), .Q(d_ff_13_q), .reset(or_18_out[12]));  // open: Qn, preset
  D_Flip_Flop #(.trigger("falling")) d_ff_14 (
    .D(unstacking_mask[13]), .clk(and_1_out), .Q(d_ff_14_q), .reset(or_18_out[13]));  // open: Qn, preset
  D_Flip_Flop #(.trigger("falling")) d_ff_15 (
    .D(unstacking_mask[14]), .clk(and_1_out), .Q(d_ff_15_q), .reset(or_18_out[14]));  // open: Qn, preset
  D_Flip_Flop #(.trigger("falling")) d_ff_16 (
    .D(unstacking_mask[15]), .clk(and_1_out), .Q(d_ff_16_q), .reset(or_18_out[15]));  // open: Qn, preset
  D_Flip_Flop #(.trigger("falling")) d_ff_17 (
    .D(four_bit_eq_zero_1_out_2), .clk(clk), .Q(d_ff_17_q), .reset(enable));  // open: Qn, preset
  four_bit_eq_zero four_bit_eq_zero_1 (.in_1(register_1_q), .out_2(four_bit_eq_zero_1_out_2));
  and and_2 (and_2_out, d_ff_17_q, clk, ~load_unstacking_mask);  // AND_Gate
  Register #(.trigger("falling"), .width(4)) register_1 (
    .D(four_bit_conditional_incrementer_1_out_3), .clk(clk), .Q(register_1_q));  // open: en, clr
  four_bit_conditional_incrementer four_bit_conditional_incrementer_1 (
    .in_2(four_bit_conditional_incrementer_2_out_3), .in_1(d_ff_1_q),
    .out_3(four_bit_conditional_incrementer_1_out_3));
  four_bit_conditional_incrementer four_bit_conditional_incrementer_2 (
    .in_2(four_bit_conditional_incrementer_3_out_3), .in_1(d_ff_2_q),
    .out_3(four_bit_conditional_incrementer_2_out_3));
  four_bit_eq_zero four_bit_eq_zero_2 (
    .in_1(four_bit_conditional_incrementer_3_out_3), .out_2(four_bit_eq_zero_2_out_2));
  four_bit_conditional_incrementer four_bit_conditional_incrementer_3 (
    .in_2(four_bit_conditional_incrementer_4_out_3), .in_1(d_ff_3_q),
    .out_3(four_bit_conditional_incrementer_3_out_3));
  four_bit_eq_zero four_bit_eq_zero_3 (
    .in_1(four_bit_conditional_incrementer_4_out_3), .out_2(four_bit_eq_zero_3_out_2));
  four_bit_conditional_incrementer four_bit_conditional_incrementer_4 (
    .in_2(four_bit_conditional_incrementer_5_out_3), .in_1(d_ff_4_q),
    .out_3(four_bit_conditional_incrementer_4_out_3));
  four_bit_eq_zero four_bit_eq_zero_4 (
    .in_1(four_bit_conditional_incrementer_5_out_3), .out_2(four_bit_eq_zero_4_out_2));
  four_bit_conditional_incrementer four_bit_conditional_incrementer_5 (
    .in_2(four_bit_conditional_incrementer_6_out_3), .in_1(d_ff_5_q),
    .out_3(four_bit_conditional_incrementer_5_out_3));
  four_bit_eq_zero four_bit_eq_zero_5 (
    .in_1(four_bit_conditional_incrementer_6_out_3), .out_2(four_bit_eq_zero_5_out_2));
  four_bit_conditional_incrementer four_bit_conditional_incrementer_6 (
    .in_2(four_bit_conditional_incrementer_7_out_3), .in_1(d_ff_6_q),
    .out_3(four_bit_conditional_incrementer_6_out_3));
  four_bit_eq_zero four_bit_eq_zero_6 (
    .in_1(four_bit_conditional_incrementer_7_out_3), .out_2(four_bit_eq_zero_6_out_2));
  four_bit_conditional_incrementer four_bit_conditional_incrementer_7 (
    .in_2(four_bit_conditional_incrementer_8_out_3), .in_1(d_ff_7_q),
    .out_3(four_bit_conditional_incrementer_7_out_3));
  four_bit_eq_zero four_bit_eq_zero_7 (
    .in_1(four_bit_conditional_incrementer_8_out_3), .out_2(four_bit_eq_zero_7_out_2));
  four_bit_conditional_incrementer four_bit_conditional_incrementer_8 (
    .in_2(four_bit_conditional_incrementer_9_out_3), .in_1(d_ff_8_q),
    .out_3(four_bit_conditional_incrementer_8_out_3));
  four_bit_eq_zero four_bit_eq_zero_8 (
    .in_1(four_bit_conditional_incrementer_9_out_3), .out_2(four_bit_eq_zero_8_out_2));
  four_bit_conditional_incrementer four_bit_conditional_incrementer_9 (
    .in_2(four_bit_conditional_incrementer_10_out_3), .in_1(d_ff_9_q),
    .out_3(four_bit_conditional_incrementer_9_out_3));
  four_bit_eq_zero four_bit_eq_zero_9 (
    .in_1(four_bit_conditional_incrementer_10_out_3), .out_2(four_bit_eq_zero_9_out_2));
  four_bit_conditional_incrementer four_bit_conditional_incrementer_10 (
    .in_2(four_bit_conditional_incrementer_11_out_3), .in_1(d_ff_10_q),
    .out_3(four_bit_conditional_incrementer_10_out_3));
  four_bit_eq_zero four_bit_eq_zero_10 (
    .in_1(four_bit_conditional_incrementer_11_out_3), .out_2(four_bit_eq_zero_10_out_2));
  four_bit_conditional_incrementer four_bit_conditional_incrementer_11 (
    .in_2(four_bit_conditional_incrementer_12_out_3), .in_1(d_ff_11_q),
    .out_3(four_bit_conditional_incrementer_11_out_3));
  four_bit_eq_zero four_bit_eq_zero_11 (
    .in_1(four_bit_conditional_incrementer_12_out_3), .out_2(four_bit_eq_zero_11_out_2));
  four_bit_conditional_incrementer four_bit_conditional_incrementer_12 (
    .in_2(four_bit_conditional_incrementer_13_out_3), .in_1(d_ff_12_q),
    .out_3(four_bit_conditional_incrementer_12_out_3));
  four_bit_eq_zero four_bit_eq_zero_12 (
    .in_1(four_bit_conditional_incrementer_13_out_3), .out_2(four_bit_eq_zero_12_out_2));
  four_bit_conditional_incrementer four_bit_conditional_incrementer_13 (
    .in_2(four_bit_conditional_incrementer_14_out_3), .in_1(d_ff_13_q),
    .out_3(four_bit_conditional_incrementer_13_out_3));
  four_bit_eq_zero four_bit_eq_zero_13 (
    .in_1(four_bit_conditional_incrementer_14_out_3), .out_2(four_bit_eq_zero_13_out_2));
  four_bit_conditional_incrementer four_bit_conditional_incrementer_14 (
    .in_2(four_bit_conditional_incrementer_15_out_3), .in_1(d_ff_14_q),
    .out_3(four_bit_conditional_incrementer_14_out_3));
  four_bit_eq_zero four_bit_eq_zero_14 (
    .in_1(four_bit_conditional_incrementer_15_out_3), .out_2(four_bit_eq_zero_14_out_2));
  four_bit_conditional_incrementer four_bit_conditional_incrementer_15 (
    .in_2(four_bit_conditional_incrementer_16_out_3), .in_1(d_ff_15_q),
    .out_3(four_bit_conditional_incrementer_15_out_3));
  four_bit_eq_zero four_bit_eq_zero_15 (
    .in_1(four_bit_conditional_incrementer_16_out_3), .out_2(four_bit_eq_zero_15_out_2));
  four_bit_conditional_incrementer four_bit_conditional_incrementer_16 (
    .in_2(4'b0000), .in_1(d_ff_16_q), .out_3(four_bit_conditional_incrementer_16_out_3));
  not not_1 (active, four_bit_eq_zero_1_out_2);
  and and_3 (and_3_out, d_ff_1_q, four_bit_eq_zero_16_out_2);
  four_bit_eq_zero four_bit_eq_zero_16 (
    .in_1(four_bit_conditional_incrementer_2_out_3), .out_2(four_bit_eq_zero_16_out_2));
  and and_4 (and_4_out, four_bit_eq_zero_2_out_2, d_ff_2_q);
  and and_5 (and_5_out, four_bit_eq_zero_3_out_2, d_ff_3_q);
  and and_6 (and_6_out, four_bit_eq_zero_4_out_2, d_ff_4_q);
  and and_7 (and_7_out, four_bit_eq_zero_5_out_2, d_ff_5_q);
  and and_8 (and_8_out, four_bit_eq_zero_6_out_2, d_ff_6_q);
  and and_9 (and_9_out, four_bit_eq_zero_7_out_2, d_ff_7_q);
  and and_10 (and_10_out, four_bit_eq_zero_8_out_2, d_ff_8_q);
  and and_11 (and_11_out, four_bit_eq_zero_9_out_2, d_ff_9_q);
  and and_12 (and_12_out, four_bit_eq_zero_10_out_2, d_ff_10_q);
  and and_13 (and_13_out, four_bit_eq_zero_11_out_2, d_ff_11_q);
  and and_14 (and_14_out, four_bit_eq_zero_12_out_2, d_ff_12_q);
  and and_15 (and_15_out, four_bit_eq_zero_13_out_2, d_ff_13_q);
  and and_16 (and_16_out, four_bit_eq_zero_14_out_2, d_ff_14_q);
  and and_17 (and_17_out, four_bit_eq_zero_15_out_2, d_ff_15_q);
  and and_18 (and_18_out, register_2_q, and_3_out);
  assign or_2_out = four_bit_g8_1_out_3 | or_3_out;  // OR_Gate or_2, 4 bits wide
  four_bit_g8 four_bit_g8_1 (.in_1(and_3_out), .in_2(4'b0000), .out_3(four_bit_g8_1_out_3));
  and and_19 (and_19_out, register_2_q, and_4_out);
  assign or_3_out = four_bit_g8_2_out_3 | or_4_out;  // OR_Gate or_3, 4 bits wide
  four_bit_g8 four_bit_g8_2 (.in_1(and_4_out), .in_2(4'b0001), .out_3(four_bit_g8_2_out_3));
  and and_20 (and_20_out, register_2_q, and_5_out);
  assign or_4_out = four_bit_g8_3_out_3 | or_5_out;  // OR_Gate or_4, 4 bits wide
  four_bit_g8 four_bit_g8_3 (.in_1(and_5_out), .in_2(4'b0010), .out_3(four_bit_g8_3_out_3));
  and and_21 (and_21_out, register_2_q, and_6_out);
  assign or_5_out = four_bit_g8_4_out_3 | or_6_out;  // OR_Gate or_5, 4 bits wide
  four_bit_g8 four_bit_g8_4 (.in_1(and_6_out), .in_2(4'b0011), .out_3(four_bit_g8_4_out_3));
  and and_22 (and_22_out, register_2_q, and_7_out);
  assign or_6_out = four_bit_g8_5_out_3 | or_7_out;  // OR_Gate or_6, 4 bits wide
  four_bit_g8 four_bit_g8_5 (.in_1(and_7_out), .in_2(4'b0100), .out_3(four_bit_g8_5_out_3));
  and and_23 (and_23_out, register_2_q, and_8_out);
  assign or_7_out = four_bit_g8_6_out_3 | or_8_out;  // OR_Gate or_7, 4 bits wide
  four_bit_g8 four_bit_g8_6 (.in_1(and_8_out), .in_2(4'b0101), .out_3(four_bit_g8_6_out_3));
  and and_24 (and_24_out, register_2_q, and_9_out);
  assign or_8_out = four_bit_g8_7_out_3 | or_9_out;  // OR_Gate or_8, 4 bits wide
  four_bit_g8 four_bit_g8_7 (.in_1(and_9_out), .in_2(4'b0110), .out_3(four_bit_g8_7_out_3));
  and and_25 (and_25_out, register_2_q, and_10_out);
  assign or_9_out = four_bit_g8_8_out_3 | or_10_out;  // OR_Gate or_9, 4 bits wide
  four_bit_g8 four_bit_g8_8 (.in_1(and_10_out), .in_2(4'b0111), .out_3(four_bit_g8_8_out_3));
  and and_26 (and_26_out, register_2_q, and_11_out);
  assign or_10_out = four_bit_g8_9_out_3 | or_11_out;  // OR_Gate or_10, 4 bits wide
  four_bit_g8 four_bit_g8_9 (.in_1(and_11_out), .in_2(4'b1000), .out_3(four_bit_g8_9_out_3));
  and and_27 (and_27_out, register_2_q, and_12_out);
  assign or_11_out = four_bit_g8_10_out_3 | or_12_out;  // OR_Gate or_11, 4 bits wide
  four_bit_g8 four_bit_g8_10 (.in_1(and_12_out), .in_2(4'b1001), .out_3(four_bit_g8_10_out_3));
  and and_28 (and_28_out, register_2_q, and_13_out);
  assign or_12_out = four_bit_g8_11_out_3 | or_13_out;  // OR_Gate or_12, 4 bits wide
  four_bit_g8 four_bit_g8_11 (.in_1(and_13_out), .in_2(4'b1010), .out_3(four_bit_g8_11_out_3));
  and and_29 (and_29_out, register_2_q, and_14_out);
  assign or_13_out = four_bit_g8_12_out_3 | or_14_out;  // OR_Gate or_13, 4 bits wide
  four_bit_g8 four_bit_g8_12 (.in_1(and_14_out), .in_2(4'b1011), .out_3(four_bit_g8_12_out_3));
  and and_30 (and_30_out, register_2_q, and_15_out);
  assign or_14_out = four_bit_g8_13_out_3 | or_15_out;  // OR_Gate or_14, 4 bits wide
  four_bit_g8 four_bit_g8_13 (.in_1(and_15_out), .in_2(4'b1100), .out_3(four_bit_g8_13_out_3));
  and and_31 (and_31_out, register_2_q, and_16_out);
  assign or_15_out = four_bit_g8_14_out_3 | or_16_out;  // OR_Gate or_15, 4 bits wide
  four_bit_g8 four_bit_g8_14 (.in_1(and_16_out), .in_2(4'b1101), .out_3(four_bit_g8_14_out_3));
  and and_32 (and_32_out, register_2_q, and_17_out);
  assign or_16_out = four_bit_g8_15_out_3 | or_17_out;  // OR_Gate or_16, 4 bits wide
  four_bit_g8 four_bit_g8_15 (.in_1(and_17_out), .in_2(4'b1110), .out_3(four_bit_g8_15_out_3));
  and and_33 (and_33_out, register_2_q, d_ff_16_q);
  assign or_17_out = four_bit_g8_16_out_3 | four_bit_g8_16_out_3;  // OR_Gate or_17, 4 bits wide
  four_bit_g8 four_bit_g8_16 (.in_1(d_ff_16_q), .in_2(4'b1111), .out_3(four_bit_g8_16_out_3));
  S_R_Flip_Flop s_r_ff_1 (
    .S(and_18_out), .R(1'b0), .clk(clk), .Q(s_r_ff_1_q[0]), .reset(or_1_out));  // open: Qn, preset
  S_R_Flip_Flop s_r_ff_2 (
    .S(and_19_out), .R(1'b0), .clk(clk), .Q(s_r_ff_1_q[1]), .reset(or_1_out));  // open: Qn, preset
  S_R_Flip_Flop s_r_ff_3 (
    .S(and_20_out), .R(1'b0), .clk(clk), .Q(s_r_ff_1_q[2]), .reset(or_1_out));  // open: Qn, preset
  S_R_Flip_Flop s_r_ff_4 (
    .S(and_21_out), .R(1'b0), .clk(clk), .Q(s_r_ff_1_q[3]), .reset(or_1_out));  // open: Qn, preset
  S_R_Flip_Flop s_r_ff_5 (
    .S(and_22_out), .R(1'b0), .clk(clk), .Q(s_r_ff_1_q[4]), .reset(or_1_out));  // open: Qn, preset
  S_R_Flip_Flop s_r_ff_6 (
    .S(and_23_out), .R(1'b0), .clk(clk), .Q(s_r_ff_1_q[5]), .reset(or_1_out));  // open: Qn, preset
  S_R_Flip_Flop s_r_ff_7 (
    .S(and_24_out), .R(1'b0), .clk(clk), .Q(s_r_ff_1_q[6]), .reset(or_1_out));  // open: Qn, preset
  S_R_Flip_Flop s_r_ff_8 (
    .S(and_25_out), .R(1'b0), .clk(clk), .Q(s_r_ff_1_q[7]), .reset(or_1_out));  // open: Qn, preset
  S_R_Flip_Flop s_r_ff_9 (
    .S(and_26_out), .R(1'b0), .clk(clk), .Q(s_r_ff_1_q[8]), .reset(or_1_out));  // open: Qn, preset
  S_R_Flip_Flop s_r_ff_10 (
    .S(and_27_out), .R(1'b0), .clk(clk), .Q(s_r_ff_1_q[9]), .reset(or_1_out));  // open: Qn, preset
  S_R_Flip_Flop s_r_ff_11 (
    .S(and_28_out), .R(1'b0), .clk(clk), .Q(s_r_ff_1_q[10]), .reset(or_1_out));  // open: Qn, preset
  S_R_Flip_Flop s_r_ff_12 (
    .S(and_29_out), .R(1'b0), .clk(clk), .Q(s_r_ff_1_q[11]), .reset(or_1_out));  // open: Qn, preset
  S_R_Flip_Flop s_r_ff_13 (
    .S(and_30_out), .R(1'b0), .clk(clk), .Q(s_r_ff_1_q[12]), .reset(or_1_out));  // open: Qn, preset
  S_R_Flip_Flop s_r_ff_14 (
    .S(and_31_out), .R(1'b0), .clk(clk), .Q(s_r_ff_1_q[13]), .reset(or_1_out));  // open: Qn, preset
  S_R_Flip_Flop s_r_ff_15 (
    .S(and_32_out), .R(1'b0), .clk(clk), .Q(s_r_ff_1_q[14]), .reset(or_1_out));  // open: Qn, preset
  S_R_Flip_Flop s_r_ff_16 (
    .S(and_33_out), .R(1'b0), .clk(clk), .Q(s_r_ff_1_q[15]), .reset(or_1_out));  // open: Qn, preset
  assign or_18_out = bit_extender_1_out | s_r_ff_1_q;  // OR_Gate or_18, 16 bits wide
  assign bit_extender_1_out = {{15{or_1_out}}, or_1_out};  // Bit_Extender bit_extender_1
  Register #(.width(1)) register_2 (.D(adder_1_out), .en(active), .clk(clk), .Q(register_2_q), .clr(or_19_out));
  or or_19 (or_19_out, or_1_out, and_34_out);
  Multiplexer #(.width(16)) multiplexer_1 (
    .in0(16'h1004), .in1({or_2_out, 12'h24}), .out(multiplexer_1_out), .sel(register_2_q));
  Multiplexer #(.width(16)) multiplexer_2 (
    .in0({16{1'b0}}), .in1(16'h1010), .out(multiplexer_2_out), .sel(register_2_q));
  Adder #(.width(1)) adder_1 (.a(register_2_q), .b(1'b1), .out(adder_1_out));  // open: cin, cout
  buf buffer_1 (buffer_1_out, enable);
  buf buffer_2 (buffer_2_out, buffer_1_out);
  buf buffer_3 (buffer_3_out, buffer_2_out);
  buf buffer_4 (buffer_4_out, buffer_3_out);
  buf buffer_5 (buffer_5_out, buffer_4_out);
  and and_34 (and_34_out, enable, ~buffer_5_out);  // AND_Gate
  // Probe on control_bus_1_out
  sixt_bit_gatekeeper sixt_bit_gatekeeper_1 (.in_1(active), .in_2(multiplexer_1_out), .out_3(control_bus_1_out));
  // Probe on control_bus_2_out
  sixt_bit_gatekeeper sixt_bit_gatekeeper_2 (.in_1(active), .in_2(multiplexer_2_out), .out_3(control_bus_2_out));
endmodule

module L (
  input  in_1,
  output out_2
);

  wire buffer_1_out, buffer_2_out, buffer_3_out;

  buf buffer_1 (buffer_1_out, in_1);
  buf buffer_2 (buffer_2_out, buffer_1_out);
  buf buffer_3 (buffer_3_out, buffer_2_out);
  and and_1 (out_2, in_1, ~buffer_3_out);  // AND_Gate
endmodule

module eight_bit_conditional_incrementer (
  input  in_1,
  input  [7:0] in_2,
  output [7:0] out_3
);

  Adder adder_1 (.a(in_2), .b({8{1'b0}}), .out(out_3), .cin(in_1));  // open: cout
endmodule

module which_bit (
  input  [7:0] in_1,
  output [7:0] out_2
);

  wire or_1_out, or_2_out, or_3_out, or_4_out, or_5_out, or_6_out, or_7_out;
  wire [7:0] eight_bit_conditional_incrementer_1_out_3, eight_bit_conditional_incrementer_2_out_3,
       eight_bit_conditional_incrementer_3_out_3, eight_bit_conditional_incrementer_4_out_3,
       eight_bit_conditional_incrementer_5_out_3, eight_bit_conditional_incrementer_6_out_3,
       eight_bit_conditional_incrementer_7_out_3;

  or or_1 (or_1_out, in_1[7], in_1[6]);
  eight_bit_conditional_incrementer eight_bit_conditional_incrementer_1 (
    .in_2({8{1'b0}}), .in_1(in_1[7]), .out_3(eight_bit_conditional_incrementer_1_out_3));
  eight_bit_conditional_incrementer eight_bit_conditional_incrementer_2 (
    .in_2(eight_bit_conditional_incrementer_1_out_3), .in_1(or_1_out),
    .out_3(eight_bit_conditional_incrementer_2_out_3));
  or or_2 (or_2_out, or_1_out, in_1[5]);
  eight_bit_conditional_incrementer eight_bit_conditional_incrementer_3 (
    .in_2(eight_bit_conditional_incrementer_2_out_3), .in_1(or_2_out),
    .out_3(eight_bit_conditional_incrementer_3_out_3));
  or or_3 (or_3_out, or_2_out, in_1[4]);
  or or_4 (or_4_out, or_3_out, in_1[3]);
  eight_bit_conditional_incrementer eight_bit_conditional_incrementer_4 (
    .in_2(eight_bit_conditional_incrementer_3_out_3), .in_1(or_3_out),
    .out_3(eight_bit_conditional_incrementer_4_out_3));
  or or_5 (or_5_out, or_4_out, in_1[2]);
  eight_bit_conditional_incrementer eight_bit_conditional_incrementer_5 (
    .in_2(eight_bit_conditional_incrementer_4_out_3), .in_1(or_4_out),
    .out_3(eight_bit_conditional_incrementer_5_out_3));
  eight_bit_conditional_incrementer eight_bit_conditional_incrementer_6 (
    .in_2(eight_bit_conditional_incrementer_5_out_3), .in_1(or_5_out),
    .out_3(eight_bit_conditional_incrementer_6_out_3));
  or or_6 (or_6_out, or_5_out, in_1[1]);
  eight_bit_conditional_incrementer eight_bit_conditional_incrementer_7 (
    .in_2(eight_bit_conditional_incrementer_6_out_3), .in_1(or_6_out),
    .out_3(eight_bit_conditional_incrementer_7_out_3));
  or or_7 (or_7_out, or_6_out, in_1[0]);
  eight_bit_conditional_incrementer eight_bit_conditional_incrementer_8 (
    .in_2(eight_bit_conditional_incrementer_7_out_3), .in_1(or_7_out), .out_3(out_2));
endmodule

module interrupt_queue (
  input  next_ir,
  input  [7:0] pins_in,
  input  reset,
  output waiting,
  output [7:0] id
);

  wire and_1_out, buffer_1_out, buffer_2_out, buffer_3_out, buffer_4_out, buffer_5_out, buffer_6_out,
       buffer_7_out, buffer_8_out, buffer_9_out, button_1_out, or_1_out, or_2_out;
  wire [7:0] l_8_out_2, multiplexer_1_out, multiplexer_2_out, multiplexer_3_out, multiplexer_4_out,
       multiplexer_5_out, multiplexer_6_out, multiplexer_7_out, multiplexer_8_out, register_2_q,
       register_3_q, register_4_q, register_5_q, register_6_q, register_7_q, register_8_q;

  L l_1 (.in_1(pins_in[7]), .out_2(l_8_out_2[7]));
  Button button_1 (.out(button_1_out));
  L l_2 (.in_1(pins_in[6]), .out_2(l_8_out_2[6]));
  L l_3 (.in_1(pins_in[5]), .out_2(l_8_out_2[5]));
  or or_1 (or_1_out, reset, button_1_out);
  buf buffer_1 (buffer_1_out, next_ir);
  buf buffer_2 (buffer_2_out, buffer_1_out);
  L l_4 (.in_1(pins_in[4]), .out_2(l_8_out_2[4]));
  L l_5 (.in_1(pins_in[3]), .out_2(l_8_out_2[3]));
  L l_6 (.in_1(pins_in[2]), .out_2(l_8_out_2[2]));
  buf buffer_3 (buffer_3_out, buffer_2_out);
  buf buffer_4 (buffer_4_out, buffer_3_out);
  buf buffer_5 (buffer_5_out, buffer_4_out);
  buf buffer_6 (buffer_6_out, buffer_5_out);
  L l_7 (.in_1(pins_in[1]), .out_2(l_8_out_2[1]));
  L l_8 (.in_1(pins_in[0]), .out_2(l_8_out_2[0]));
  and and_1 (and_1_out, ~buffer_6_out, next_ir);  // AND_Gate
  or or_2 (or_2_out, and_1_out, l_8_out_2[0], l_8_out_2[1], l_8_out_2[2], l_8_out_2[3], l_8_out_2[4], l_8_out_2[5], l_8_out_2[6], l_8_out_2[7]);
  buf buffer_7 (buffer_7_out, or_2_out);
  Multiplexer #(.width(8)) multiplexer_1 (
    .in0(l_8_out_2), .in1(register_2_q), .out(multiplexer_1_out), .sel(and_1_out));
  buf buffer_8 (buffer_8_out, buffer_7_out);
  buf buffer_9 (buffer_9_out, buffer_8_out);
  Register register_1 (.D(multiplexer_1_out), .clk(buffer_9_out), .Q(id), .clr(or_1_out));  // open: en
  Register register_2 (.D(multiplexer_2_out), .clk(buffer_9_out), .Q(register_2_q), .clr(or_1_out));  // open: en
  Multiplexer #(.width(8)) multiplexer_2 (.in0(id), .in1(register_3_q), .out(multiplexer_2_out), .sel(and_1_out));
  Multiplexer #(.width(8)) multiplexer_3 (
    .in0(register_2_q), .in1(register_4_q), .out(multiplexer_3_out), .sel(and_1_out));
  Register register_3 (.D(multiplexer_3_out), .clk(buffer_9_out), .Q(register_3_q), .clr(or_1_out));  // open: en
  Register register_4 (.D(multiplexer_4_out), .clk(buffer_9_out), .Q(register_4_q), .clr(or_1_out));  // open: en
  Multiplexer #(.width(8)) multiplexer_4 (
    .in0(register_3_q), .in1(register_5_q), .out(multiplexer_4_out), .sel(and_1_out));
  Register register_5 (.D(multiplexer_5_out), .clk(buffer_9_out), .Q(register_5_q), .clr(or_1_out));  // open: en
  Multiplexer #(.width(8)) multiplexer_5 (
    .in0(register_4_q), .in1(register_6_q), .out(multiplexer_5_out), .sel(and_1_out));
  Register register_6 (.D(multiplexer_6_out), .clk(buffer_9_out), .Q(register_6_q), .clr(or_1_out));  // open: en
  Multiplexer #(.width(8)) multiplexer_6 (
    .in0(register_5_q), .in1(register_7_q), .out(multiplexer_6_out), .sel(and_1_out));
  Register register_7 (.D(multiplexer_7_out), .clk(buffer_9_out), .Q(register_7_q), .clr(or_1_out));  // open: en
  Multiplexer #(.width(8)) multiplexer_7 (
    .in0(register_6_q), .in1(register_8_q), .out(multiplexer_7_out), .sel(and_1_out));
  or or_3 (waiting, id[0], id[1], id[2], id[3], id[4], id[5], id[6], id[7]);
  Register register_8 (.D(multiplexer_8_out), .clk(buffer_9_out), .Q(register_8_q), .clr(or_1_out));  // open: en
  Multiplexer #(.width(8)) multiplexer_8 (
    .in0(register_7_q), .in1({8{1'b0}}), .out(multiplexer_8_out), .sel(and_1_out));
endmodule

module interrupt_table (
  input  [15:0] control_bus_1,
  input  [15:0] control_bus_2,
  input  [7:0] id,
  input  [15:0] data_in,
  input  clk,
  input  reset,
  output [15:0] ih_addr,
  output [15:0] to_data_bus
);

  wire or_1_out, or_2_out, or_3_out, or_4_out, or_5_out, or_6_out, or_7_out, or_8_out, or_9_out, or_10_out,
       or_11_out, or_12_out, or_13_out, or_14_out, or_15_out, or_16_out, or_17_out, sixt_bit_eq_cmp_1_out_3,
       sixt_bit_eq_cmp_2_out_3, sixt_bit_eq_cmp_3_out_3, sixt_bit_eq_cmp_4_out_3, sixt_bit_eq_cmp_5_out_3,
       sixt_bit_eq_cmp_6_out_3, sixt_bit_eq_cmp_7_out_3, sixt_bit_eq_cmp_8_out_3, sixt_bit_eq_cmp_9_out_3,
       sixt_bit_eq_cmp_10_out_3, sixt_bit_eq_cmp_11_out_3, sixt_bit_eq_cmp_12_out_3,
       sixt_bit_eq_cmp_13_out_3, sixt_bit_eq_cmp_14_out_3, sixt_bit_eq_cmp_15_out_3,
       sixt_bit_eq_cmp_16_out_3, sixt_bit_eq_cmp_17_out_3, sixt_bit_eq_cmp_18_out_3,
       sixt_bit_eq_cmp_19_out_3, sixt_bit_eq_cmp_20_out_3, sixt_bit_eq_cmp_21_out_3,
       sixt_bit_eq_cmp_22_out_3, sixt_bit_eq_cmp_23_out_3, sixt_bit_eq_cmp_24_out_3,
       sixt_bit_eq_cmp_25_out_3, sixt_bit_eq_cmp_26_out_3, sixt_bit_eq_cmp_27_out_3,
       sixt_bit_eq_cmp_28_out_3, sixt_bit_eq_cmp_29_out_3, sixt_bit_eq_cmp_30_out_3,
       sixt_bit_eq_cmp_31_out_3, sixt_bit_eq_cmp_32_out_3, sixt_bit_eq_cmp_33_out_3, sixt_bit_eq_cmp_34_out_3;
  wire [3:0] subtractor_1_out;
  wire [7:0] which_bit_1_out_2;
  wire [15:0] or_18_out, or_19_out, or_20_out, or_21_out, or_22_out, or_23_out, or_24_out, register_1_q,
       register_2_q, register_3_q, register_4_q, register_5_q, register_6_q, register_7_q, register_8_q,
       register_9_q, sixt_bit_gatekeeper_1_out_3, sixt_bit_gatekeeper_2_out_3, sixt_bit_gatekeeper_3_out_3,
       sixt_bit_gatekeeper_4_out_3, sixt_bit_gatekeeper_5_out_3, sixt_bit_gatekeeper_6_out_3,
       sixt_bit_gatekeeper_7_out_3, sixt_bit_gatekeeper_8_out_3;

  Register #(.trigger("falling"), .width(16)) register_1 (
    .D(data_in), .clk(clk), .Q(register_1_q), .clr(reset));  // open: en
  sixt_bit_eq_cmp sixt_bit_eq_cmp_1 (.in_1(control_bus_1), .in_2(16'h8002), .out_3(sixt_bit_eq_cmp_1_out_3));
  sixt_bit_eq_cmp sixt_bit_eq_cmp_2 (.in_1(control_bus_2), .in_2(16'h8002), .out_3(sixt_bit_eq_cmp_2_out_3));
  sixt_bit_eq_cmp sixt_bit_eq_cmp_3 (.in_1(control_bus_1), .in_2(16'h8006), .out_3(sixt_bit_eq_cmp_3_out_3));
  sixt_bit_eq_cmp sixt_bit_eq_cmp_4 (.in_1(control_bus_2), .in_2(16'h8006), .out_3(sixt_bit_eq_cmp_4_out_3));
  sixt_bit_eq_cmp sixt_bit_eq_cmp_5 (.in_1(control_bus_1), .in_2(16'h9002), .out_3(sixt_bit_eq_cmp_5_out_3));
  sixt_bit_eq_cmp sixt_bit_eq_cmp_6 (.in_1(control_bus_2), .in_2(16'h9002), .out_3(sixt_bit_eq_cmp_6_out_3));
  sixt_bit_eq_cmp sixt_bit_eq_cmp_7 (.in_1(control_bus_1), .in_2(16'h9006), .out_3(sixt_bit_eq_cmp_7_out_3));
  sixt_bit_eq_cmp sixt_bit_eq_cmp_8 (.in_1(control_bus_2), .in_2(16'h9006), .out_3(sixt_bit_eq_cmp_8_out_3));
  sixt_bit_eq_cmp sixt_bit_eq_cmp_9 (.in_1(control_bus_1), .in_2(16'ha002), .out_3(sixt_bit_eq_cmp_9_out_3));
  sixt_bit_eq_cmp sixt_bit_eq_cmp_10 (.in_1(control_bus_2), .in_2(16'ha002), .out_3(sixt_bit_eq_cmp_10_out_3));
  sixt_bit_eq_cmp sixt_bit_eq_cmp_11 (.in_1(control_bus_1), .in_2(16'ha006), .out_3(sixt_bit_eq_cmp_11_out_3));
  sixt_bit_eq_cmp sixt_bit_eq_cmp_12 (.in_1(control_bus_2), .in_2(16'ha006), .out_3(sixt_bit_eq_cmp_12_out_3));
  sixt_bit_eq_cmp sixt_bit_eq_cmp_13 (.in_1(control_bus_1), .in_2(16'hb002), .out_3(sixt_bit_eq_cmp_13_out_3));
  sixt_bit_eq_cmp sixt_bit_eq_cmp_14 (.in_1(control_bus_2), .in_2(16'hb002), .out_3(sixt_bit_eq_cmp_14_out_3));
  sixt_bit_eq_cmp sixt_bit_eq_cmp_15 (.in_1(control_bus_1), .in_2(16'hb006), .out_3(sixt_bit_eq_cmp_15_out_3));
  sixt_bit_eq_cmp sixt_bit_eq_cmp_16 (.in_1(control_bus_2), .in_2(16'hb006), .out_3(sixt_bit_eq_cmp_16_out_3));
  sixt_bit_eq_cmp sixt_bit_eq_cmp_17 (.in_1(control_bus_1), .in_2(16'hc002), .out_3(sixt_bit_eq_cmp_17_out_3));
  sixt_bit_eq_cmp sixt_bit_eq_cmp_18 (.in_1(control_bus_2), .in_2(16'hc002), .out_3(sixt_bit_eq_cmp_18_out_3));
  sixt_bit_eq_cmp sixt_bit_eq_cmp_19 (.in_1(control_bus_1), .in_2(16'hc006), .out_3(sixt_bit_eq_cmp_19_out_3));
  sixt_bit_eq_cmp sixt_bit_eq_cmp_20 (.in_1(control_bus_2), .in_2(16'hc006), .out_3(sixt_bit_eq_cmp_20_out_3));
  sixt_bit_eq_cmp sixt_bit_eq_cmp_21 (.in_1(control_bus_1), .in_2(16'hd002), .out_3(sixt_bit_eq_cmp_21_out_3));
  sixt_bit_eq_cmp sixt_bit_eq_cmp_22 (.in_1(control_bus_2), .in_2(16'hd002), .out_3(sixt_bit_eq_cmp_22_out_3));
  sixt_bit_eq_cmp sixt_bit_eq_cmp_23 (.in_1(control_bus_1), .in_2(16'hd006), .out_3(sixt_bit_eq_cmp_23_out_3));
  sixt_bit_eq_cmp sixt_bit_eq_cmp_24 (.in_1(control_bus_2), .in_2(16'hd006), .out_3(sixt_bit_eq_cmp_24_out_3));
  sixt_bit_eq_cmp sixt_bit_eq_cmp_25 (.in_1(control_bus_1), .in_2(16'he002), .out_3(sixt_bit_eq_cmp_25_out_3));
  sixt_bit_eq_cmp sixt_bit_eq_cmp_26 (.in_1(control_bus_2), .in_2(16'he002), .out_3(sixt_bit_eq_cmp_26_out_3));
  sixt_bit_eq_cmp sixt_bit_eq_cmp_27 (.in_1(control_bus_1), .in_2(16'he006), .out_3(sixt_bit_eq_cmp_27_out_3));
  sixt_bit_eq_cmp sixt_bit_eq_cmp_28 (.in_1(control_bus_2), .in_2(16'he006), .out_3(sixt_bit_eq_cmp_28_out_3));
  sixt_bit_eq_cmp sixt_bit_eq_cmp_29 (.in_1(control_bus_1), .in_2(16'hf002), .out_3(sixt_bit_eq_cmp_29_out_3));
  sixt_bit_eq_cmp sixt_bit_eq_cmp_30 (.in_1(control_bus_2), .in_2(16'hf002), .out_3(sixt_bit_eq_cmp_30_out_3));
  sixt_bit_eq_cmp sixt_bit_eq_cmp_31 (.in_1(control_bus_1), .in_2(16'hf006), .out_3(sixt_bit_eq_cmp_31_out_3));
  sixt_bit_eq_cmp sixt_bit_eq_cmp_32 (.in_1(control_bus_2), .in_2(16'hf006), .out_3(sixt_bit_eq_cmp_32_out_3));
  sixt_bit_eq_cmp sixt_bit_eq_cmp_33 (.in_1(16'h1b), .in_2(control_bus_1), .out_3(sixt_bit_eq_cmp_33_out_3));
  or or_1 (or_1_out, sixt_bit_eq_cmp_33_out_3, sixt_bit_eq_cmp_34_out_3);
  sixt_bit_eq_cmp sixt_bit_eq_cmp_34 (.in_1(16'h1b), .in_2(control_bus_2), .out_3(sixt_bit_eq_cmp_34_out_3));
  which_bit which_bit_1 (.in_1(id), .out_2(which_bit_1_out_2));
  or or_2 (or_2_out, sixt_bit_eq_cmp_1_out_3, sixt_bit_eq_cmp_2_out_3);
  or or_3 (or_3_out, sixt_bit_eq_cmp_3_out_3, sixt_bit_eq_cmp_4_out_3);
  or or_4 (or_4_out, sixt_bit_eq_cmp_5_out_3, sixt_bit_eq_cmp_6_out_3);
  or or_5 (or_5_out, sixt_bit_eq_cmp_7_out_3, sixt_bit_eq_cmp_8_out_3);
  or or_6 (or_6_out, sixt_bit_eq_cmp_9_out_3, sixt_bit_eq_cmp_10_out_3);
  or or_7 (or_7_out, sixt_bit_eq_cmp_11_out_3, sixt_bit_eq_cmp_12_out_3);
  or or_8 (or_8_out, sixt_bit_eq_cmp_13_out_3, sixt_bit_eq_cmp_14_out_3);
  or or_9 (or_9_out, sixt_bit_eq_cmp_15_out_3, sixt_bit_eq_cmp_16_out_3);
  or or_10 (or_10_out, sixt_bit_eq_cmp_17_out_3, sixt_bit_eq_cmp_18_out_3);
  or or_11 (or_11_out, sixt_bit_eq_cmp_19_out_3, sixt_bit_eq_cmp_20_out_3);
  or or_12 (or_12_out, sixt_bit_eq_cmp_21_out_3, sixt_bit_eq_cmp_22_out_3);
  or or_13 (or_13_out, sixt_bit_eq_cmp_23_out_3, sixt_bit_eq_cmp_24_out_3);
  or or_14 (or_14_out, sixt_bit_eq_cmp_25_out_3, sixt_bit_eq_cmp_26_out_3);
  or or_15 (or_15_out, sixt_bit_eq_cmp_27_out_3, sixt_bit_eq_cmp_28_out_3);
  or or_16 (or_16_out, sixt_bit_eq_cmp_29_out_3, sixt_bit_eq_cmp_30_out_3);
  or or_17 (or_17_out, sixt_bit_eq_cmp_31_out_3, sixt_bit_eq_cmp_32_out_3);
  Register #(.width(16)) register_2 (.D(register_1_q), .en(or_3_out), .clk(clk), .Q(register_2_q), .clr(reset));
  Register #(.width(16)) register_3 (.D(register_1_q), .en(or_5_out), .clk(clk), .Q(register_3_q), .clr(reset));
  Register #(.width(16)) register_4 (.D(register_1_q), .en(or_7_out), .clk(clk), .Q(register_4_q), .clr(reset));
  Register #(.width(16)) register_5 (.D(register_1_q), .en(or_9_out), .clk(clk), .Q(register_5_q), .clr(reset));
  Register #(.width(16)) register_6 (.D(register_1_q), .en(or_11_out), .clk(clk), .Q(register_6_q), .clr(reset));
  Register #(.width(16)) register_7 (.D(register_1_q), .en(or_13_out), .clk(clk), .Q(register_7_q), .clr(reset));
  Register #(.width(16)) register_8 (.D(register_1_q), .en(or_15_out), .clk(clk), .Q(register_8_q), .clr(reset));
  Register #(.width(16)) register_9 (.D(register_1_q), .en(or_17_out), .clk(clk), .Q(register_9_q), .clr(reset));
  Subtractor #(.width(4)) subtractor_1 (
    .a(which_bit_1_out_2[3:0]), .b(4'b0001), .out(subtractor_1_out));  // open: bin, bout
  sixt_bit_gatekeeper sixt_bit_gatekeeper_1 (.in_1(or_2_out), .in_2(register_2_q), .out_3(sixt_bit_gatekeeper_1_out_3));
  assign or_18_out = sixt_bit_gatekeeper_2_out_3 | or_19_out;  // OR_Gate or_18, 16 bits wide
  sixt_bit_gatekeeper sixt_bit_gatekeeper_2 (.in_1(or_4_out), .in_2(register_3_q), .out_3(sixt_bit_gatekeeper_2_out_3));
  assign or_19_out = sixt_bit_gatekeeper_3_out_3 | or_20_out;  // OR_Gate or_19, 16 bits wide
  sixt_bit_gatekeeper sixt_bit_gatekeeper_3 (.in_1(or_6_out), .in_2(register_4_q), .out_3(sixt_bit_gatekeeper_3_out_3));
  assign or_20_out = sixt_bit_gatekeeper_4_out_3 | or_21_out;  // OR_Gate or_20, 16 bits wide
  sixt_bit_gatekeeper sixt_bit_gatekeeper_4 (.in_1(or_8_out), .in_2(register_5_q), .out_3(sixt_bit_gatekeeper_4_out_3));
  assign or_21_out = sixt_bit_gatekeeper_5_out_3 | or_22_out;  // OR_Gate or_21, 16 bits wide
  sixt_bit_gatekeeper sixt_bit_gatekeeper_5 (
    .in_1(or_10_out), .in_2(register_6_q), .out_3(sixt_bit_gatekeeper_5_out_3));
  assign or_22_out = sixt_bit_gatekeeper_6_out_3 | or_23_out;  // OR_Gate or_22, 16 bits wide
  sixt_bit_gatekeeper sixt_bit_gatekeeper_6 (
    .in_1(or_12_out), .in_2(register_7_q), .out_3(sixt_bit_gatekeeper_6_out_3));
  assign or_23_out = sixt_bit_gatekeeper_7_out_3 | sixt_bit_gatekeeper_8_out_3;  // OR_Gate or_23, 16 bits wide
  sixt_bit_gatekeeper sixt_bit_gatekeeper_7 (
    .in_1(or_14_out), .in_2(register_8_q), .out_3(sixt_bit_gatekeeper_7_out_3));
  sixt_bit_gatekeeper sixt_bit_gatekeeper_8 (
    .in_1(or_16_out), .in_2(register_9_q), .out_3(sixt_bit_gatekeeper_8_out_3));
  // Probe on subtractor_1_out[2:0]
  Multiplexer #(.select(3), .width(16)) multiplexer_1 (
    .in0(register_2_q), .in1(register_3_q), .in2(register_4_q), .in3(register_5_q), .in4(register_6_q),
    .in5(register_7_q), .in6(register_8_q), .in7(register_9_q), .out(ih_addr));  // open: sel
  assign or_24_out = sixt_bit_gatekeeper_1_out_3 | or_18_out;  // OR_Gate or_24, 16 bits wide
  sixt_bit_gatekeeper sixt_bit_gatekeeper_9 (.in_1(or_1_out), .in_2(or_24_out), .out_3(to_data_bus));
endmodule

module input_pins_8 (
  input  in_1,
  input  in_2,
  input  in_3,
  input  in_4,
  input  in_5,
  input  in_6,
  input  in_7,
  input  in_8,
  output [7:0] out_9
);

  Pull_Resistor pull_resistor_1 (.node(in_1));
  Pull_Resistor pull_resistor_2 (.node(in_2));
  Pull_Resistor pull_resistor_3 (.node(in_3));
  Pull_Resistor pull_resistor_4 (.node(in_4));
  Pull_Resistor pull_resistor_5 (.node(in_5));
  Pull_Resistor pull_resistor_6 (.node(in_6));
  Pull_Resistor pull_resistor_7 (.node(in_7));
  Pull_Resistor pull_resistor_8 (.node(in_8));

  assign out_9 = {in_1, in_2, in_3, in_4, in_5, in_6, in_7, in_8};
endmodule

module spi_controller (
  input  write,
  input  read,
  input  [15:0] spi_out_config,
  input  [15:0] data_in,
  input  [15:0] spi_in_config,
  input  clock,
  input  reset,
  input  miso,
  output [15:0] data_out,
  output done,
  output cs,
  output clk,
  output mosi
);

  wire and_1_out, and_2_out, and_3_out, and_4_out, and_5_out, and_6_out, and_7_out, and_8_out, and_9_out,
       and_10_out, and_11_out, and_12_out, and_13_out, and_14_out, and_15_out, clock_division_bell_1_out_6,
       comparator_1_gt, comparator_2_eq, comparator_3_lt, comparator_4_gt, comparator_5_eq,
       falling_edge_delay_1_out_2, falling_edge_delay_2_out_2, nor_1_out, not_2_out, not_or_hasnt_1_out_2,
       not_or_hasnt_2_out_2, or_1_out, or_2_out, or_6_out, or_7_out, or_8_out, or_10_out, or_11_out,
       or_12_out, pulse_extender_1_out_6, rising_edge_delay_1_out_2, rising_edge_delay_2_out_2,
       rising_edge_delay_4_out_2, s_r_ff_1_q, s_r_ff_2_q, s_r_ff_3_q, s_r_ff_4_q, shift_register_1_p3,
       shift_register_1_p4, shift_register_2_p1, shift_register_2_p4, shift_register_2_p15,
       shift_register_2_p16, shift_register_3_p1, shift_register_3_p2, shift_register_3_p3,
       two_ticker_1_out_4, two_ticker_2_out_4, two_ticker_3_out_4, two_ticker_4_out_4;
  wire [1:0] bytes_to_write_q;
  wire [4:0] adder_1_out, adder_2_out, kounter_q, multiplexer_1_out, register_2_q;
  wire [15:0] register_1_q, undriven;

  two_ticker two_ticker_1 (.signal_in(s_r_ff_1_q), .clock(clock), .reset(reset), .out_4(two_ticker_1_out_4));
  Register #(.width(2)) bytes_to_write (
    .D(spi_out_config[1:0]), .clk(two_ticker_1_out_4), .Q(bytes_to_write_q), .clr(reset));  // open: en
  clock_division_bell clock_division_bell_1 (
    .divisor(spi_out_config[15:8]), .load_divisor(two_ticker_1_out_4), .restart(two_ticker_1_out_4),
    .clock(clock), .reset(reset), .out_6(clock_division_bell_1_out_6));
  Comparator #(.mode("unsigned"), .width(2)) comparator_1 (
    .a(bytes_to_write_q), .b(2'b01), .gt(comparator_1_gt));  // open: eq, lt
  Register #(.width(16)) register_1 (.D(data_in), .clk(s_r_ff_1_q), .Q(register_1_q), .clr(reset));  // open: en
  // Shift_Register shift_register_1: pin names not known; wires that end beside it: reset, two_ticker_1_out_4, shift_register_1_p3, shift_register_1_p4, 1'b0, register_1_q[0], register_1_q[1], register_1_q[2], register_1_q[3], register_1_q[4], register_1_q[5], register_1_q[6], register_1_q[7]
  or or_1 (or_1_out, s_r_ff_1_q, shift_register_3_p2);
  not not_1 (cs, or_1_out);
  and and_1 (and_1_out, write, ~shift_register_3_p2);  // AND_Gate
  not_or_hasnt not_or_hasnt_1 (.in_1(and_1_out), .out_2(not_or_hasnt_1_out_2));
  and and_2 (and_2_out, and_1_out, falling_edge_delay_1_out_2);
  S_R_Flip_Flop s_r_ff_1 (.Q(s_r_ff_1_q), .reset(or_2_out), .preset(and_2_out));  // open: S, R, clk, Qn
  or or_2 (or_2_out, reset, two_ticker_3_out_4);
  or or_3 (shift_register_1_p3, and_11_out, and_12_out);
  and and_3 (and_3_out, s_r_ff_1_q, clock_division_bell_1_out_6);
  and and_4 (and_4_out, or_12_out, shift_register_3_p2);
  or or_4 (clk, and_3_out, and_4_out);
  falling_edge_delay falling_edge_delay_1 (.in_1(not_or_hasnt_1_out_2), .out_2(falling_edge_delay_1_out_2));
  and and_5 (and_5_out, s_r_ff_1_q, ~rising_edge_delay_4_out_2);  // AND_Gate
  S_R_Flip_Flop #(.trigger("falling")) s_r_ff_2 (
    .S(1'b0), .R(1'b1), .clk(clock), .Q(s_r_ff_2_q), .reset(reset), .preset(and_5_out));  // open: Qn
  and and_6 (and_6_out, shift_register_2_p1, and_11_out);
  or or_5 (mosi, and_6_out, and_8_out);
  or or_6 (or_6_out, reset, two_ticker_3_out_4);
  and and_7 (and_7_out, ~s_r_ff_2_q, clock_division_bell_1_out_6);  // AND_Gate
  // Shift_Register shift_register_2: pin names not known; wires that end beside it: shift_register_2_p1, reset, two_ticker_1_out_4, shift_register_2_p4, shift_register_1_p4, 1'b0, register_1_q[8], register_1_q[9], register_1_q[10], register_1_q[11], register_1_q[12], register_1_q[13], register_1_q[14], register_1_q[15], shift_register_2_p15, shift_register_2_p16
  S_R_Flip_Flop #(.trigger("falling")) s_r_ff_3 (
    .Q(s_r_ff_3_q), .reset(or_6_out), .preset(s_r_ff_2_q));  // open: S, R, clk, Qn
  rising_edge_delay rising_edge_delay_1 (.in_1(s_r_ff_2_q), .out_2(rising_edge_delay_1_out_2));
  rising_edge_delay rising_edge_delay_2 (.in_1(s_r_ff_1_q), .out_2(rising_edge_delay_2_out_2));
  rising_edge_delay rising_edge_delay_3 (.in_1(and_12_out), .out_2(shift_register_2_p4));
  rising_edge_delay rising_edge_delay_4 (.in_1(s_r_ff_3_q), .out_2(rising_edge_delay_4_out_2));
  or or_7 (or_7_out, rising_edge_delay_1_out_2, and_7_out);
  and and_8 (and_8_out, shift_register_2_p15, and_12_out);
  and and_9 (and_9_out, read, ~s_r_ff_1_q);  // AND_Gate
  rising_edge_delay rising_edge_delay_5 (.in_1(or_7_out), .out_2(shift_register_1_p4));
  Register #(.width(5)) kounter (
    .D(adder_1_out), .en(rising_edge_delay_2_out_2), .clk(and_10_out), .Q(kounter_q), .clr(or_8_out));
  and and_10 (and_10_out, clock, s_r_ff_1_q);
  or or_8 (or_8_out, reset, two_ticker_3_out_4);
  // Shift_Register #(.length(16)) shift_register_3: pin names not known; wires that end beside it: shift_register_3_p1, shift_register_3_p2, shift_register_3_p3, miso
  or or_9 (shift_register_3_p1, two_ticker_4_out_4, reset);
  Adder #(.width(5)) adder_1 (.a(kounter_q), .b(5'b00001), .out(adder_1_out));  // open: cin, cout
  Comparator #(.mode("unsigned"), .width(5)) comparator_2 (
    .a(kounter_q), .b(5'b10000), .eq(comparator_2_eq));  // open: gt, lt
  Comparator #(.mode("unsigned"), .width(5)) comparator_3 (
    .a(kounter_q), .b(5'b00001), .lt(comparator_3_lt));  // open: gt, eq
  Comparator #(.mode("unsigned"), .width(5)) comparator_4 (
    .a(kounter_q), .b(5'b01000), .gt(comparator_4_gt));  // open: eq, lt
  and and_11 (and_11_out, ~comparator_3_lt, ~comparator_4_gt);  // AND_Gate
  and and_12 (and_12_out, comparator_4_gt, comparator_1_gt);
  and and_13 (and_13_out, and_9_out, falling_edge_delay_2_out_2);
  S_R_Flip_Flop s_r_ff_4 (.Q(s_r_ff_4_q), .reset(or_11_out), .preset(and_13_out));  // open: S, R, clk, Qn
  two_ticker two_ticker_2 (.signal_in(shift_register_3_p2), .clock(clock), .reset(reset), .out_4(two_ticker_2_out_4));
  and and_14 (and_14_out, comparator_2_eq, comparator_1_gt);
  or or_10 (or_10_out, and_14_out, and_15_out);
  and and_15 (and_15_out, comparator_4_gt, ~comparator_1_gt);  // AND_Gate
  not_or_hasnt not_or_hasnt_2 (.in_1(and_9_out), .out_2(not_or_hasnt_2_out_2));
  S_R_Flip_Flop s_r_ff_5 (
    .S(s_r_ff_4_q), .R(not_2_out), .clk(clock), .Q(shift_register_3_p2), .reset(or_11_out));  // open: Qn, preset
  not not_2 (not_2_out, s_r_ff_4_q);
  two_ticker two_ticker_3 (.signal_in(or_10_out), .clock(clock), .reset(reset), .out_4(two_ticker_3_out_4));
  falling_edge_delay falling_edge_delay_2 (.in_1(not_or_hasnt_2_out_2), .out_2(falling_edge_delay_2_out_2));
  clock_division_bell clock_division_bell_2 (
    .divisor(spi_out_config[15:8]), .load_divisor(two_ticker_2_out_4), .clock(clock), .reset(reset),
    .out_6(shift_register_3_p3));  // open: restart
  nor nor_1 (nor_1_out, spi_in_config[0], spi_in_config[1], spi_in_config[2], spi_in_config[3], spi_in_config[4]);
  Register #(.width(5)) register_2 (
    .D(adder_2_out), .en(shift_register_3_p2), .clk(shift_register_3_p3), .Q(register_2_q), .clr(or_11_out));
  or or_11 (or_11_out, reset, two_ticker_4_out_4);
  Multiplexer #(.width(5)) multiplexer_1 (
    .in0(spi_in_config[4:0]), .in1(5'b01000), .out(multiplexer_1_out), .sel(nor_1_out));
  Adder #(.width(5)) adder_2 (.a(register_2_q), .b(5'b00001), .out(adder_2_out));  // open: cin, cout
  Comparator #(.mode("unsigned"), .width(5)) comparator_5 (
    .a(register_2_q), .b(multiplexer_1_out), .eq(comparator_5_eq));  // open: gt, lt
  pulse_extender pulse_extender_1 (
    .in_1(comparator_5_eq), .in_2(reset), .in_3(or_12_out), .out_6(pulse_extender_1_out_6));  // open: out_4, out_5
  or or_12 (or_12_out, reset, two_ticker_2_out_4);
  two_ticker two_ticker_4 (
    .signal_in(pulse_extender_1_out_6), .clock(clock), .reset(or_12_out), .out_4(two_ticker_4_out_4));
  Register #(.width(16)) register_3 (.D(undriven), .clk(comparator_5_eq), .Q(data_out), .clr(reset));  // open: en
  or or_13 (done, two_ticker_3_out_4, two_ticker_4_out_4);
endmodule

module pulse_daisy (
  input  in_1,
  output out_2,
  output out_3
);

  wire buffer_1_out, buffer_2_out, buffer_3_out, buffer_4_out, buffer_5_out, buffer_6_out, buffer_7_out,
       buffer_8_out, buffer_9_out, buffer_10_out, buffer_11_out, buffer_12_out, buffer_13_out, buffer_14_out,
       buffer_15_out, buffer_16_out, buffer_17_out, buffer_18_out, buffer_19_out, buffer_20_out;

  buf buffer_1 (buffer_1_out, buffer_6_out);
  buf buffer_2 (buffer_2_out, buffer_1_out);
  buf buffer_3 (buffer_3_out, buffer_14_out);
  buf buffer_4 (buffer_4_out, buffer_3_out);
  buf buffer_5 (buffer_5_out, in_1);
  buf buffer_6 (buffer_6_out, buffer_8_out);
  buf buffer_7 (buffer_7_out, buffer_9_out);
  buf buffer_8 (buffer_8_out, buffer_7_out);
  buf buffer_9 (buffer_9_out, buffer_5_out);
  buf buffer_10 (buffer_10_out, buffer_2_out);
  buf buffer_11 (buffer_11_out, buffer_12_out);
  buf buffer_12 (buffer_12_out, buffer_10_out);
  buf buffer_13 (buffer_13_out, buffer_11_out);
  buf buffer_14 (buffer_14_out, buffer_16_out);
  buf buffer_15 (buffer_15_out, buffer_17_out);
  buf buffer_16 (buffer_16_out, buffer_15_out);
  buf buffer_17 (buffer_17_out, buffer_13_out);
  buf buffer_18 (buffer_18_out, buffer_4_out);
  buf buffer_19 (buffer_19_out, buffer_20_out);
  buf buffer_20 (buffer_20_out, buffer_18_out);
  buf buffer_21 (out_3, buffer_19_out);
  and and_1 (out_2, in_1, ~buffer_5_out);  // AND_Gate
endmodule

module pulsey (
  input  in_1,
  output out_2,
  output out_3
);

  wire buffer_1_out, microclock_delay_1_out_2, pulse_daisy_1_out_3, pulse_daisy_2_out_3, pulse_daisy_3_out_3,
       pulse_daisy_4_out_3, pulse_daisy_5_out_3, pulse_daisy_6_out_3, pulse_daisy_7_out_3,
       pulse_daisy_8_out_3, pulse_daisy_9_out_3, pulse_daisy_10_out_3, pulse_daisy_11_out_3,
       pulse_daisy_12_out_3, pulse_daisy_13_out_3, pulse_daisy_14_out_3, pulse_daisy_15_out_3,
       pulse_daisy_16_out_3, pulse_daisy_17_out_3, pulse_daisy_18_out_3, pulse_daisy_19_out_3,
       pulse_daisy_20_out_3, pulse_daisy_21_out_3, pulse_daisy_22_out_3, pulse_daisy_23_out_3,
       pulse_daisy_24_out_3, pulse_daisy_25_out_3, pulse_daisy_26_out_3, pulse_daisy_27_out_3,
       pulse_daisy_28_out_3, pulse_daisy_29_out_3, pulse_daisy_30_out_3, pulse_daisy_31_out_3;
  wire [31:0] pulse_daisy_1_out_2;

  buf buffer_1 (buffer_1_out, in_1);
  microclock_delay microclock_delay_1 (.in_1(buffer_1_out), .out_2(microclock_delay_1_out_2));
  pulse_daisy pulse_daisy_1 (
    .in_1(microclock_delay_1_out_2), .out_3(pulse_daisy_1_out_3), .out_2(pulse_daisy_1_out_2[0]));
  pulse_daisy pulse_daisy_2 (.in_1(pulse_daisy_1_out_3), .out_3(pulse_daisy_2_out_3), .out_2(pulse_daisy_1_out_2[1]));
  pulse_daisy pulse_daisy_3 (.in_1(pulse_daisy_2_out_3), .out_3(pulse_daisy_3_out_3), .out_2(pulse_daisy_1_out_2[2]));
  pulse_daisy pulse_daisy_4 (.in_1(pulse_daisy_3_out_3), .out_3(pulse_daisy_4_out_3), .out_2(pulse_daisy_1_out_2[3]));
  pulse_daisy pulse_daisy_5 (.in_1(pulse_daisy_4_out_3), .out_3(pulse_daisy_5_out_3), .out_2(pulse_daisy_1_out_2[4]));
  pulse_daisy pulse_daisy_6 (.in_1(pulse_daisy_5_out_3), .out_3(pulse_daisy_6_out_3), .out_2(pulse_daisy_1_out_2[5]));
  pulse_daisy pulse_daisy_7 (.in_1(pulse_daisy_6_out_3), .out_3(pulse_daisy_7_out_3), .out_2(pulse_daisy_1_out_2[6]));
  pulse_daisy pulse_daisy_8 (.in_1(pulse_daisy_7_out_3), .out_3(pulse_daisy_8_out_3), .out_2(pulse_daisy_1_out_2[7]));
  pulse_daisy pulse_daisy_9 (.in_1(pulse_daisy_8_out_3), .out_3(pulse_daisy_9_out_3), .out_2(pulse_daisy_1_out_2[8]));
  pulse_daisy pulse_daisy_10 (.in_1(pulse_daisy_9_out_3), .out_3(pulse_daisy_10_out_3), .out_2(pulse_daisy_1_out_2[9]));
  pulse_daisy pulse_daisy_11 (
    .in_1(pulse_daisy_10_out_3), .out_3(pulse_daisy_11_out_3), .out_2(pulse_daisy_1_out_2[10]));
  pulse_daisy pulse_daisy_12 (
    .in_1(pulse_daisy_11_out_3), .out_3(pulse_daisy_12_out_3), .out_2(pulse_daisy_1_out_2[11]));
  pulse_daisy pulse_daisy_13 (
    .in_1(pulse_daisy_12_out_3), .out_3(pulse_daisy_13_out_3), .out_2(pulse_daisy_1_out_2[12]));
  pulse_daisy pulse_daisy_14 (
    .in_1(pulse_daisy_13_out_3), .out_3(pulse_daisy_14_out_3), .out_2(pulse_daisy_1_out_2[13]));
  pulse_daisy pulse_daisy_15 (
    .in_1(pulse_daisy_14_out_3), .out_3(pulse_daisy_15_out_3), .out_2(pulse_daisy_1_out_2[14]));
  pulse_daisy pulse_daisy_16 (
    .in_1(pulse_daisy_15_out_3), .out_3(pulse_daisy_16_out_3), .out_2(pulse_daisy_1_out_2[15]));
  pulse_daisy pulse_daisy_17 (
    .in_1(pulse_daisy_16_out_3), .out_3(pulse_daisy_17_out_3), .out_2(pulse_daisy_1_out_2[16]));
  pulse_daisy pulse_daisy_18 (
    .in_1(pulse_daisy_17_out_3), .out_3(pulse_daisy_18_out_3), .out_2(pulse_daisy_1_out_2[17]));
  pulse_daisy pulse_daisy_19 (
    .in_1(pulse_daisy_18_out_3), .out_3(pulse_daisy_19_out_3), .out_2(pulse_daisy_1_out_2[18]));
  pulse_daisy pulse_daisy_20 (
    .in_1(pulse_daisy_19_out_3), .out_3(pulse_daisy_20_out_3), .out_2(pulse_daisy_1_out_2[19]));
  pulse_daisy pulse_daisy_21 (
    .in_1(pulse_daisy_20_out_3), .out_3(pulse_daisy_21_out_3), .out_2(pulse_daisy_1_out_2[20]));
  pulse_daisy pulse_daisy_22 (
    .in_1(pulse_daisy_21_out_3), .out_3(pulse_daisy_22_out_3), .out_2(pulse_daisy_1_out_2[21]));
  pulse_daisy pulse_daisy_23 (
    .in_1(pulse_daisy_22_out_3), .out_3(pulse_daisy_23_out_3), .out_2(pulse_daisy_1_out_2[22]));
  pulse_daisy pulse_daisy_24 (
    .in_1(pulse_daisy_23_out_3), .out_3(pulse_daisy_24_out_3), .out_2(pulse_daisy_1_out_2[23]));
  pulse_daisy pulse_daisy_25 (
    .in_1(pulse_daisy_24_out_3), .out_3(pulse_daisy_25_out_3), .out_2(pulse_daisy_1_out_2[24]));
  pulse_daisy pulse_daisy_26 (
    .in_1(pulse_daisy_25_out_3), .out_3(pulse_daisy_26_out_3), .out_2(pulse_daisy_1_out_2[25]));
  pulse_daisy pulse_daisy_27 (
    .in_1(pulse_daisy_26_out_3), .out_3(pulse_daisy_27_out_3), .out_2(pulse_daisy_1_out_2[26]));
  pulse_daisy pulse_daisy_28 (
    .in_1(pulse_daisy_27_out_3), .out_3(pulse_daisy_28_out_3), .out_2(pulse_daisy_1_out_2[27]));
  pulse_daisy pulse_daisy_29 (
    .in_1(pulse_daisy_28_out_3), .out_3(pulse_daisy_29_out_3), .out_2(pulse_daisy_1_out_2[28]));
  pulse_daisy pulse_daisy_30 (
    .in_1(pulse_daisy_29_out_3), .out_3(pulse_daisy_30_out_3), .out_2(pulse_daisy_1_out_2[29]));
  pulse_daisy pulse_daisy_31 (
    .in_1(pulse_daisy_30_out_3), .out_3(pulse_daisy_31_out_3), .out_2(pulse_daisy_1_out_2[30]));
  pulse_daisy pulse_daisy_32 (.in_1(pulse_daisy_31_out_3), .out_2(pulse_daisy_1_out_2[31]));  // open: out_3
  and and_1 (out_2, in_1, ~buffer_1_out);  // AND_Gate
  or or_1 (out_3, pulse_daisy_1_out_2[31], pulse_daisy_1_out_2[30], pulse_daisy_1_out_2[29], pulse_daisy_1_out_2[28], pulse_daisy_1_out_2[27], pulse_daisy_1_out_2[26], pulse_daisy_1_out_2[25], pulse_daisy_1_out_2[24], pulse_daisy_1_out_2[23], pulse_daisy_1_out_2[22], pulse_daisy_1_out_2[21], pulse_daisy_1_out_2[20], pulse_daisy_1_out_2[19], pulse_daisy_1_out_2[18], pulse_daisy_1_out_2[17], pulse_daisy_1_out_2[16], pulse_daisy_1_out_2[15], pulse_daisy_1_out_2[14], pulse_daisy_1_out_2[13], pulse_daisy_1_out_2[12], pulse_daisy_1_out_2[11], pulse_daisy_1_out_2[10], pulse_daisy_1_out_2[9], pulse_daisy_1_out_2[8], pulse_daisy_1_out_2[7], pulse_daisy_1_out_2[6], pulse_daisy_1_out_2[5], pulse_daisy_1_out_2[4], pulse_daisy_1_out_2[3], pulse_daisy_1_out_2[2], pulse_daisy_1_out_2[1], pulse_daisy_1_out_2[0], 1'b0);
endmodule

module hex_digits (
  input  [15:0] in_1,
  output [3:0] out_2,
  output [3:0] out_3,
  output [3:0] out_4,
  output [3:0] out_5
);

  wire [3:0] divider_1_rem, divider_1_rem_2, divider_1_rem_3, divider_2_rem, divider_2_rem_2,
       divider_2_rem_3, divider_3_rem, divider_3_rem_2, divider_3_rem_3, divider_4_rem, divider_4_rem_2,
       divider_4_rem_3;
  wire [15:0] divider_1_out, divider_2_out, divider_3_out;

  Divider #(.width(16)) divider_1 (
    .a(in_1), .b(16'h10), .out(divider_1_out), .rem({divider_1_rem_3, divider_1_rem_2, divider_1_rem, out_2}));  // open: upper
  Divider #(.width(16)) divider_2 (
    .a(divider_1_out), .b(16'h10), .out(divider_2_out),
    .rem({divider_2_rem_3, divider_2_rem_2, divider_2_rem, out_3}));  // open: upper
  Divider #(.width(16)) divider_3 (
    .a(divider_2_out), .b(16'h10), .out(divider_3_out),
    .rem({divider_3_rem_3, divider_3_rem_2, divider_3_rem, out_4}));  // open: upper
  Divider #(.width(16)) divider_4 (
    .a(divider_3_out), .b(16'h10), .rem({divider_4_rem_3, divider_4_rem_2, divider_4_rem, out_5}));  // open: out, upper
endmodule

module parameter_printer (
  input  prev_done,
  input  enable,
  input  [5:0] param_type,
  input  [4:0] counter,
  input  clock,
  input  [15:0] instruction,
  input  [15:0] tmpc,
  input  [15:0] tmpd,
  input  reset,
  input  nothing_below,
  output done,
  output [6:0] out_12,
  output nothing_pass_up
);

  wire and_1_out, and_5_out, and_6_out, and_7_out, and_10_out, and_11_out, and_12_out, and_13_out,
       buffer_1_out, buffer_2_out, buffer_3_out, buffer_4_out, buffer_5_out, buffer_6_out, buffer_7_out,
       buffer_8_out, buffer_9_out, buffer_10_out, buffer_11_out, buffer_12_out, buffer_13_out, buffer_14_out,
       buffer_15_out, decoder_1_out0, decoder_1_out1, decoder_1_out2, decoder_1_out3, decoder_1_out4,
       decoder_1_out5, decoder_1_out6, decoder_1_out7, not_1_out, or_1_out, or_3_out, or_4_out, or_5_out,
       or_6_out, or_7_out, or_8_out, or_11_out, or_12_out, or_13_out, s_r_ff_1_q, s_r_ff_2_q, s_r_ff_3_q;
  wire [3:0] four_bit_g8_1_out_3, four_bit_g8_2_out_3, multiplexer_2_out, multiplexer_2_out_2,
       multiplexer_2_out_3, multiplexer_2_out_4, multiplexer_3_out, or_9_out;
  wire [4:0] and_3_out, five_bit_subtractor_1_out_4, register_1_q, register_2_q;
  wire [4:4] d_ff_1_q;
  wire [6:0] bit_extender_2_out;
  wire [6:6] d_ff_2_q;
  wire [7:0] and_8_out, and_9_out, multiplexer_1_out, or_10_out, sub_parameter_printer_1_ascii_out;
  wire [7:7] and_4_out;
  wire [15:0] bit_extender_1_out, or_2_out, sixt_bit_gatekeeper_1_out_3, sixt_bit_gatekeeper_2_out_3;

  Pull_Resistor pull_resistor_1 (.node(prev_done));
  Pull_Resistor pull_resistor_2 (.node(enable));
  D_Flip_Flop d_ff_1 (.D(or_1_out), .clk(clock), .Q(d_ff_1_q[4]), .reset(reset));  // open: Qn, preset
  or or_1 (or_1_out, prev_done, enable);
  Register #(.width(5)) register_1 (.D(counter), .clk(clock), .Q(register_1_q), .clr(reset));  // open: en
  Register #(.width(5)) register_2 (.D(counter), .clk(and_1_out), .Q(register_2_q), .clr(reset));  // open: en
  and and_1 (and_1_out, clock, ~d_ff_1_q[4]);  // AND_Gate
  D_Flip_Flop d_ff_2 (.D(d_ff_1_q[4]), .clk(clock), .Q(d_ff_2_q[6]), .reset(reset));  // open: Qn, preset
  Decoder #(.enable("false"), .select(3)) decoder_1 (
    .out0(decoder_1_out0), .out1(decoder_1_out1), .out2(decoder_1_out2), .out3(decoder_1_out3),
    .out4(decoder_1_out4), .out5(decoder_1_out5), .out6(decoder_1_out6), .out7(decoder_1_out7),
    .sel(param_type[5:3]));
  Pull_Resistor #(.pull(1)) pull_resistor_3 (.node(nothing_below));
  five_bit_subtractor five_bit_subtractor_1 (
    .a(register_1_q), .b(register_2_q), .out_4(five_bit_subtractor_1_out_4));  // open: in_1, out_5
  sixt_bit_gatekeeper sixt_bit_gatekeeper_1 (.in_1(or_4_out), .in_2(tmpc), .out_3(sixt_bit_gatekeeper_1_out_3));
  assign or_2_out = sixt_bit_gatekeeper_1_out_3 | sixt_bit_gatekeeper_2_out_3;  // OR_Gate or_2, 16 bits wide
  sixt_bit_gatekeeper sixt_bit_gatekeeper_2 (.in_1(or_5_out), .in_2(tmpd), .out_3(sixt_bit_gatekeeper_2_out_3));
  and and_2 (nothing_pass_up, nothing_below, and_4_out[7]);
  assign and_3_out = {5{d_ff_1_q[4]}} & five_bit_subtractor_1_out_4;  // AND_Gate and_3, 5 bits wide
  or or_3 (or_3_out, decoder_1_out1, decoder_1_out5);
  or or_4 (or_4_out, decoder_1_out2, decoder_1_out4, decoder_1_out5);
  or or_5 (or_5_out, decoder_1_out3, decoder_1_out6, decoder_1_out7);
  and and_4 (and_4_out[7], param_type[2], ~param_type[1], ~param_type[0]);  // AND_Gate
  and and_5 (and_5_out, nothing_below, ~and_4_out[7]);  // AND_Gate
  Multiplexer #(.width(8)) multiplexer_1 (.in0(8'h20), .in1(8'h80), .out(multiplexer_1_out), .sel(and_5_out));
  or or_6 (or_6_out, decoder_1_out0, decoder_1_out1);
  or or_7 (or_7_out, decoder_1_out2, decoder_1_out3);
  or or_8 (or_8_out, decoder_1_out0, decoder_1_out4);
  four_bit_g8 four_bit_g8_1 (.in_1(or_8_out), .in_2(instruction[15:12]), .out_3(four_bit_g8_1_out_3));
  assign or_9_out = four_bit_g8_1_out_3 | four_bit_g8_2_out_3;  // OR_Gate or_9, 4 bits wide
  four_bit_g8 four_bit_g8_2 (.in_1(or_3_out), .in_2(instruction[11:8]), .out_3(four_bit_g8_2_out_3));
  assign bit_extender_1_out = {{12{1'b0}}, or_9_out};  // Bit_Extender bit_extender_1
  Multiplexer #(.width(16)) multiplexer_2 (
    .in0(or_2_out), .in1(bit_extender_1_out),
    .out({multiplexer_2_out_4, multiplexer_2_out_3, multiplexer_2_out_2, multiplexer_2_out}), .sel(or_6_out));
  and and_6 (and_6_out, param_type[2], ~param_type[1], ~param_type[0]);  // AND_Gate
  Multiplexer #(.width(4)) multiplexer_3 (
    .in0(or_9_out), .in1(multiplexer_2_out), .out(multiplexer_3_out), .sel(or_7_out));
  and and_7 (and_7_out, prev_done, and_6_out);
  buf buffer_1 (buffer_1_out, d_ff_1_q[4]);
  buf buffer_2 (buffer_2_out, buffer_1_out);
  sub_parameter_printer sub_parameter_printer_1 (
    .last(multiplexer_1_out), .param_type(param_type[2:0]), .nibble(multiplexer_3_out),
    .following({multiplexer_2_out_4, multiplexer_2_out_3, multiplexer_2_out_2, multiplexer_2_out}),
    .counter(and_3_out[3:0]), .ascii_out(sub_parameter_printer_1_ascii_out));
  buf buffer_3 (buffer_3_out, buffer_2_out);
  buf buffer_4 (buffer_4_out, buffer_3_out);
  buf buffer_5 (buffer_5_out, buffer_4_out);
  buf buffer_6 (buffer_6_out, buffer_5_out);
  assign and_8_out = ~{8{and_4_out[7]}} & sub_parameter_printer_1_ascii_out;  // AND_Gate and_8, 8 bits wide
  assign and_9_out = {8{and_4_out[7]}} & 8'h80;  // AND_Gate and_9, 8 bits wide
  and and_10 (and_10_out, buffer_6_out, or_10_out[7]);
  assign or_10_out = and_8_out | and_9_out;  // OR_Gate or_10, 8 bits wide
  S_R_Flip_Flop s_r_ff_1 (.Q(s_r_ff_1_q), .reset(or_11_out), .preset(and_10_out));  // open: S, R, clk, Qn
  or or_11 (or_11_out, reset, ~and_10_out, ~d_ff_1_q[4]);  // OR_Gate
  buf buffer_7 (buffer_7_out, buffer_8_out);
  buf buffer_8 (buffer_8_out, buffer_9_out);
  buf buffer_9 (buffer_9_out, s_r_ff_1_q);
  and and_11 (and_11_out, and_10_out, buffer_7_out);
  buf buffer_10 (buffer_10_out, buffer_11_out);
  buf buffer_11 (buffer_11_out, buffer_12_out);
  buf buffer_12 (buffer_12_out, s_r_ff_2_q);
  S_R_Flip_Flop s_r_ff_2 (.Q(s_r_ff_2_q), .reset(or_11_out), .preset(and_11_out));  // open: S, R, clk, Qn
  not not_1 (not_1_out, d_ff_1_q[4]);
  and and_12 (and_12_out, and_10_out, buffer_10_out);
  buf buffer_13 (buffer_13_out, buffer_14_out);
  buf buffer_14 (buffer_14_out, buffer_15_out);
  buf buffer_15 (buffer_15_out, s_r_ff_3_q);
  S_R_Flip_Flop s_r_ff_3 (.Q(s_r_ff_3_q), .reset(or_11_out), .preset(and_12_out));  // open: S, R, clk, Qn
  or or_12 (or_12_out, reset, not_1_out);
  and and_13 (and_13_out, and_10_out, buffer_13_out);
  or or_13 (or_13_out, and_7_out, and_13_out);
  S_R_Flip_Flop s_r_ff_4 (.Q(done), .reset(or_12_out), .preset(or_13_out));  // open: S, R, clk, Qn
  assign bit_extender_2_out = {{6{done}}, done};  // Bit_Extender bit_extender_2
  assign out_12 = ~bit_extender_2_out & {7{d_ff_2_q[6]}} & or_10_out[6:0];  // AND_Gate and_14, 7 bits wide
endmodule
module sub_parameter_printer (
  input  [2:0] param_type,
  input  [3:0] nibble,
  input  [15:0] following,
  input  [7:0] last,
  input  [3:0] counter,
  output [7:0] ascii_out
);

  wire and_1_out, and_2_out, and_3_out, nor_1_out, nor_2_out, nor_3_out, nor_4_out, or_30_out;
  wire [7:0] and_22_out, and_23_out, and_24_out, and_25_out, and_26_out, and_27_out, and_28_out, and_29_out,
       and_30_out, and_31_out, and_32_out, and_33_out, and_34_out, and_35_out, and_36_out, and_37_out,
       and_38_out, and_39_out, and_40_out, and_41_out, and_42_out, and_43_out, and_44_out, and_45_out,
       and_46_out, and_47_out, and_48_out, and_49_out, and_50_out, and_51_out, and_52_out, and_53_out,
       and_54_out, and_55_out, and_56_out, and_57_out, and_58_out, and_59_out, and_60_out, and_61_out,
       and_62_out, and_63_out, and_64_out, and_65_out, and_66_out, and_67_out, and_68_out, and_69_out,
       and_70_out, and_71_out, and_72_out, and_73_out, and_74_out, and_75_out, and_76_out, and_77_out,
       and_78_out, and_79_out, and_80_out, and_81_out, and_82_out, and_83_out, and_84_out, and_85_out,
       and_86_out, and_87_out, and_88_out, and_89_out, and_90_out, byte_gate_1_out_3, byte_gate_2_out_3,
       byte_gate_3_out_3, byte_gate_4_out_3, byte_gate_5_out_3, byte_gate_6_out_3, byte_gate_7_out_3,
       byte_gate_8_out_3, byte_gate_9_out_3, byte_gate_10_out_3, byte_gate_11_out_3, byte_gate_12_out_3,
       byte_gate_13_out_3, byte_gate_14_out_3, byte_gate_15_out_3,
       byte_if_zero_replace_2carry_1_carry_1_carry, byte_if_zero_replace_2carry_1_out_7,
       byte_if_zero_replace_2carry_1_vanishes, byte_if_zero_replace_2carry_2_carry_1_carry,
       byte_if_zero_replace_2carry_2_out_7, byte_if_zero_replace_2carry_2_vanishes,
       byte_if_zero_replace_2carry_3_carry_1_carry, byte_if_zero_replace_2carry_3_out_7,
       byte_if_zero_replace_2carry_3_vanishes, byte_if_zero_replace_2carry_4_carry_1_carry,
       byte_if_zero_replace_2carry_4_out_7, byte_if_zero_replace_2carry_4_vanishes,
       byte_if_zero_replace_2carry_5_carry_1_carry, byte_if_zero_replace_2carry_5_out_7,
       byte_if_zero_replace_2carry_5_vanishes, byte_if_zero_replace_2carry_6_carry_1_carry,
       byte_if_zero_replace_2carry_6_out_7, byte_if_zero_replace_2carry_6_vanishes,
       byte_if_zero_replace_2carry_7_carry_1_carry, byte_if_zero_replace_2carry_7_out_7,
       byte_if_zero_replace_2carry_7_vanishes, byte_if_zero_replace_2carry_8_carry_1_carry,
       byte_if_zero_replace_2carry_8_out_7, byte_if_zero_replace_2carry_8_vanishes,
       byte_if_zero_replace_2carry_9_carry_1_carry, byte_if_zero_replace_2carry_9_out_7,
       byte_if_zero_replace_2carry_9_vanishes, byte_if_zero_replace_2carry_10_carry_1_carry,
       byte_if_zero_replace_2carry_10_out_7, byte_if_zero_replace_2carry_10_vanishes,
       byte_if_zero_replace_2carry_11_carry_1_carry, byte_if_zero_replace_2carry_11_out_7,
       byte_if_zero_replace_2carry_11_vanishes, byte_if_zero_replace_2carry_12_out_7,
       hex_digit_to_ascii_1_out_2, hex_digit_to_ascii_2_out_2, hex_digit_to_ascii_3_out_2,
       hex_digit_to_ascii_4_out_2, hex_digit_to_ascii_5_out_2, or_1_out, or_2_out, or_3_out, or_4_out,
       or_5_out, or_6_out, or_7_out, or_8_out, or_9_out, or_10_out, or_11_out, or_12_out, or_13_out,
       or_14_out, or_15_out, or_16_out, or_17_out, or_18_out, or_19_out, or_20_out, or_21_out, or_22_out,
       or_23_out, or_24_out, or_25_out, or_26_out, or_27_out, or_28_out, or_29_out;
  wire [7:7] and_20_out, and_21_out, not_1_out, not_2_out, not_3_out, not_4_out;
  wire [15:0] and_4_out;

  hex_digit_to_ascii hex_digit_to_ascii_1 (.in_1(nibble), .out_2(hex_digit_to_ascii_1_out_2));
  hex_digit_to_ascii hex_digit_to_ascii_2 (.in_1(following[3:0]), .out_2(hex_digit_to_ascii_2_out_2));
  hex_digit_to_ascii hex_digit_to_ascii_3 (.in_1(following[7:4]), .out_2(hex_digit_to_ascii_3_out_2));
  hex_digit_to_ascii hex_digit_to_ascii_4 (.in_1(following[11:8]), .out_2(hex_digit_to_ascii_4_out_2));
  hex_digit_to_ascii hex_digit_to_ascii_5 (.in_1(following[15:12]), .out_2(hex_digit_to_ascii_5_out_2));
  not not_1 (not_1_out[7], and_1_out);
  and and_1 (and_1_out, nor_1_out, and_2_out);
  nor nor_1 (nor_1_out, following[0], following[1], following[3], following[2]);
  and and_2 (and_2_out, nor_2_out, and_3_out);
  nor nor_2 (nor_2_out, following[4], following[5], following[7], following[6]);
  and and_3 (and_3_out, nor_3_out, nor_4_out);
  nor nor_3 (nor_3_out, following[8], following[9], following[11], following[10]);
  nor nor_4 (nor_4_out, following[12], following[13], following[15], following[14]);
  and and_4 (and_4_out[0], ~counter[0], ~counter[1], ~counter[2], ~counter[3]);  // AND_Gate
  and and_5 (and_4_out[1], counter[0], ~counter[1], ~counter[2], ~counter[3]);  // AND_Gate
  and and_6 (and_4_out[2], ~counter[0], counter[1], ~counter[2], ~counter[3]);  // AND_Gate
  and and_7 (and_4_out[3], counter[0], counter[1], ~counter[2], ~counter[3]);  // AND_Gate
  and and_8 (and_4_out[4], ~counter[0], ~counter[1], counter[2], ~counter[3]);  // AND_Gate
  and and_9 (and_4_out[5], counter[0], ~counter[1], counter[2], ~counter[3]);  // AND_Gate
  and and_10 (and_4_out[6], ~counter[0], counter[1], counter[2], ~counter[3]);  // AND_Gate
  and and_11 (and_4_out[7], counter[0], counter[1], counter[2], ~counter[3]);  // AND_Gate
  and and_12 (and_4_out[8], ~counter[0], ~counter[1], ~counter[2], counter[3]);  // AND_Gate
  and and_13 (and_4_out[9], counter[0], ~counter[1], ~counter[2], counter[3]);  // AND_Gate
  and and_14 (and_4_out[10], ~counter[0], counter[1], ~counter[2], counter[3]);  // AND_Gate
  and and_15 (and_4_out[11], counter[0], counter[1], ~counter[2], counter[3]);  // AND_Gate
  and and_16 (and_4_out[12], ~counter[0], ~counter[1], counter[2], counter[3]);  // AND_Gate
  and and_17 (and_4_out[13], counter[0], ~counter[1], counter[2], counter[3]);  // AND_Gate
  and and_18 (and_4_out[14], ~counter[0], counter[1], counter[2], counter[3]);  // AND_Gate
  and and_19 (and_4_out[15], counter[0], counter[1], counter[2], counter[3]);
  not not_2 (not_2_out[7], and_2_out);
  not not_3 (not_3_out[7], and_3_out);
  not not_4 (not_4_out[7], nor_4_out);
  and and_20 (and_20_out[7], ~param_type[1], ~param_type[2]);  // AND_Gate
  and and_21 (and_21_out[7], param_type[1], ~param_type[2]);  // AND_Gate
  assign or_1_out = {8{and_21_out[7]}} | {8{param_type[2]}};  // OR_Gate or_1, 8 bits wide
  assign and_22_out = {8{and_20_out[7]}} & 8'h30;  // AND_Gate and_22, 8 bits wide
  assign and_23_out = {8{and_21_out[7]}} & 8'h72;  // AND_Gate and_23, 8 bits wide
  assign and_24_out = {8{param_type[2]}} & 8'h73;  // AND_Gate and_24, 8 bits wide
  assign and_25_out = {8{and_20_out[7]}} & 8'h78;  // AND_Gate and_25, 8 bits wide
  assign and_26_out = {8{and_21_out[7]}} & hex_digit_to_ascii_1_out_2;  // AND_Gate and_26, 8 bits wide
  assign and_27_out = {8{param_type[2]}} & 8'h72;  // AND_Gate and_27, 8 bits wide
  assign and_28_out = {8{and_20_out[7]}} & hex_digit_to_ascii_5_out_2;  // AND_Gate and_28, 8 bits wide
  assign and_29_out = {8{param_type[2]}} & hex_digit_to_ascii_1_out_2;  // AND_Gate and_29, 8 bits wide
  assign and_30_out = {8{and_20_out[7]}} & hex_digit_to_ascii_4_out_2;  // AND_Gate and_30, 8 bits wide
  assign and_31_out = {8{and_20_out[7]}} & hex_digit_to_ascii_3_out_2;  // AND_Gate and_31, 8 bits wide
  assign and_32_out = {8{and_20_out[7]}} & hex_digit_to_ascii_2_out_2;  // AND_Gate and_32, 8 bits wide
  assign and_33_out = and_59_out & hex_digit_to_ascii_5_out_2;  // AND_Gate and_33, 8 bits wide
  assign or_2_out = and_33_out | and_34_out;  // OR_Gate or_2, 8 bits wide
  assign and_34_out = ~and_59_out & hex_digit_to_ascii_4_out_2;  // AND_Gate and_34, 8 bits wide
  assign and_35_out = and_59_out & hex_digit_to_ascii_4_out_2;  // AND_Gate and_35, 8 bits wide
  assign or_3_out = and_35_out | and_36_out;  // OR_Gate or_3, 8 bits wide
  assign and_36_out = ~and_59_out & hex_digit_to_ascii_3_out_2;  // AND_Gate and_36, 8 bits wide
  assign and_37_out = and_59_out & hex_digit_to_ascii_3_out_2;  // AND_Gate and_37, 8 bits wide
  assign or_4_out = and_37_out | and_38_out;  // OR_Gate or_4, 8 bits wide
  assign and_38_out = ~and_59_out & hex_digit_to_ascii_2_out_2;  // AND_Gate and_38, 8 bits wide
  assign or_5_out = and_22_out | and_23_out | and_24_out;  // OR_Gate or_5, 8 bits wide
  assign or_6_out = and_25_out | and_26_out | and_27_out;  // OR_Gate or_6, 8 bits wide
  assign or_7_out = and_28_out | and_29_out;  // OR_Gate or_7, 8 bits wide
  assign and_39_out = and_60_out & or_2_out;  // AND_Gate and_39, 8 bits wide
  assign and_40_out = ~and_60_out & hex_digit_to_ascii_3_out_2;  // AND_Gate and_40, 8 bits wide
  assign and_41_out = and_60_out & or_3_out;  // AND_Gate and_41, 8 bits wide
  assign and_42_out = ~and_60_out & hex_digit_to_ascii_2_out_2;  // AND_Gate and_42, 8 bits wide
  assign and_43_out = {8{param_type[0]}} & 8'h2a;  // AND_Gate and_43, 8 bits wide
  assign and_44_out = ~{8{param_type[0]}} & or_5_out;  // AND_Gate and_44, 8 bits wide
  assign and_45_out = {8{param_type[0]}} & or_5_out;  // AND_Gate and_45, 8 bits wide
  assign and_46_out = ~{8{param_type[0]}} & or_6_out;  // AND_Gate and_46, 8 bits wide
  assign and_47_out = {8{param_type[0]}} & or_6_out;  // AND_Gate and_47, 8 bits wide
  assign and_48_out = ~{8{param_type[0]}} & or_7_out;  // AND_Gate and_48, 8 bits wide
  assign and_49_out = {8{param_type[0]}} & or_7_out;  // AND_Gate and_49, 8 bits wide
  assign and_50_out = ~{8{param_type[0]}} & and_30_out;  // AND_Gate and_50, 8 bits wide
  assign and_51_out = {8{param_type[0]}} & and_30_out;  // AND_Gate and_51, 8 bits wide
  assign and_52_out = ~{8{param_type[0]}} & and_31_out;  // AND_Gate and_52, 8 bits wide
  assign and_53_out = {8{param_type[0]}} & and_31_out;  // AND_Gate and_53, 8 bits wide
  assign and_54_out = ~{8{param_type[0]}} & and_32_out;  // AND_Gate and_54, 8 bits wide
  assign and_55_out = {8{param_type[0]}} & and_32_out;  // AND_Gate and_55, 8 bits wide
  assign and_56_out = ~{8{param_type[0]}} & {8{1'b0}};  // AND_Gate and_56, 8 bits wide
  assign or_8_out = and_39_out | and_40_out;  // OR_Gate or_8, 8 bits wide
  assign or_9_out = and_41_out | and_42_out;  // OR_Gate or_9, 8 bits wide
  assign or_10_out = and_43_out | and_44_out;  // OR_Gate or_10, 8 bits wide
  assign or_11_out = and_45_out | and_46_out;  // OR_Gate or_11, 8 bits wide
  assign or_12_out = and_47_out | and_48_out;  // OR_Gate or_12, 8 bits wide
  assign or_13_out = and_49_out | and_50_out;  // OR_Gate or_13, 8 bits wide
  assign or_14_out = and_51_out | and_52_out;  // OR_Gate or_14, 8 bits wide
  assign or_15_out = and_53_out | and_54_out;  // OR_Gate or_15, 8 bits wide
  assign or_16_out = and_55_out | and_56_out;  // OR_Gate or_16, 8 bits wide
  assign and_57_out = and_61_out & or_8_out;  // AND_Gate and_57, 8 bits wide
  assign or_17_out = and_57_out | and_58_out;  // OR_Gate or_17, 8 bits wide
  assign and_58_out = ~and_61_out & hex_digit_to_ascii_2_out_2;  // AND_Gate and_58, 8 bits wide
  assign and_59_out = {8{not_4_out[7]}} & {8{param_type[0]}};  // AND_Gate and_59, 8 bits wide
  assign and_60_out = {8{not_3_out[7]}} & {8{param_type[0]}};  // AND_Gate and_60, 8 bits wide
  assign and_61_out = {8{not_2_out[7]}} & {8{param_type[0]}};  // AND_Gate and_61, 8 bits wide
  assign and_62_out = {8{not_1_out[7]}} & or_1_out & {8{param_type[0]}};  // AND_Gate and_62, 8 bits wide
  assign and_63_out = and_62_out & 8'h29;  // AND_Gate and_63, 8 bits wide
  assign and_64_out = ~and_62_out & last;  // AND_Gate and_64, 8 bits wide
  assign and_65_out = and_62_out & 8'h28;  // AND_Gate and_65, 8 bits wide
  assign and_66_out = ~and_62_out & or_11_out;  // AND_Gate and_66, 8 bits wide
  assign and_67_out = and_62_out & or_11_out;  // AND_Gate and_67, 8 bits wide
  assign and_68_out = ~and_62_out & or_12_out;  // AND_Gate and_68, 8 bits wide
  assign and_69_out = and_62_out & or_12_out;  // AND_Gate and_69, 8 bits wide
  assign and_70_out = ~and_62_out & or_13_out;  // AND_Gate and_70, 8 bits wide
  assign and_71_out = and_62_out & {8{param_type[2]}} & or_13_out;  // AND_Gate and_71, 8 bits wide
  assign and_72_out = and_62_out & ~{8{param_type[2]}} & 8'h2b;  // AND_Gate and_72, 8 bits wide
  assign and_73_out = ~and_62_out & or_14_out;  // AND_Gate and_73, 8 bits wide
  assign and_74_out = and_62_out & {8{param_type[2]}} & 8'h2b;  // AND_Gate and_74, 8 bits wide
  assign and_75_out = and_62_out & ~{8{param_type[2]}} & 8'h30;  // AND_Gate and_75, 8 bits wide
  assign and_76_out = ~and_62_out & or_15_out;  // AND_Gate and_76, 8 bits wide
  assign and_77_out = and_62_out & {8{param_type[2]}} & 8'h30;  // AND_Gate and_77, 8 bits wide
  assign and_78_out = and_62_out & ~{8{param_type[2]}} & 8'h78;  // AND_Gate and_78, 8 bits wide
  assign and_79_out = ~and_62_out & or_16_out;  // AND_Gate and_79, 8 bits wide
  assign and_80_out = and_62_out & {8{param_type[2]}} & 8'h78;  // AND_Gate and_80, 8 bits wide
  assign and_81_out = and_62_out & ~{8{param_type[2]}} & or_17_out;  // AND_Gate and_81, 8 bits wide
  assign and_82_out = or_17_out & and_62_out & {8{param_type[2]}};  // AND_Gate and_82, 8 bits wide
  assign and_83_out = and_62_out & ~{8{param_type[2]}} & and_61_out & or_9_out;  // AND_Gate and_83, 8 bits wide
  assign and_84_out = or_9_out & and_62_out & {8{param_type[2]}} & and_61_out;  // AND_Gate and_84, 8 bits wide
  assign and_85_out = and_62_out & ~{8{param_type[2]}} & or_4_out & and_60_out;  // AND_Gate and_85, 8 bits wide
  assign and_86_out = or_4_out & and_62_out & {8{param_type[2]}} & and_60_out;  // AND_Gate and_86, 8 bits wide
  assign and_87_out = and_62_out & ~{8{param_type[2]}} & hex_digit_to_ascii_2_out_2 & and_59_out;  // AND_Gate and_87, 8 bits wide
  assign and_88_out = hex_digit_to_ascii_2_out_2 & {8{param_type[2]}} & and_62_out & and_59_out;  // AND_Gate and_88, 8 bits wide
  assign or_18_out = and_63_out | and_64_out;  // OR_Gate or_18, 8 bits wide
  assign or_19_out = and_65_out | and_66_out;  // OR_Gate or_19, 8 bits wide
  assign or_20_out = and_67_out | and_68_out;  // OR_Gate or_20, 8 bits wide
  assign or_21_out = and_69_out | and_70_out;  // OR_Gate or_21, 8 bits wide
  assign or_22_out = and_71_out | and_72_out | and_73_out;  // OR_Gate or_22, 8 bits wide
  assign or_23_out = and_74_out | and_75_out | and_76_out;  // OR_Gate or_23, 8 bits wide
  assign or_24_out = and_77_out | and_78_out | and_79_out;  // OR_Gate or_24, 8 bits wide
  assign or_25_out = and_80_out | and_81_out;  // OR_Gate or_25, 8 bits wide
  assign or_26_out = and_82_out | and_83_out;  // OR_Gate or_26, 8 bits wide
  assign or_27_out = and_84_out | and_85_out;  // OR_Gate or_27, 8 bits wide
  assign or_28_out = and_86_out | and_87_out;  // OR_Gate or_28, 8 bits wide
  assign and_89_out = and_62_out & last;  // AND_Gate and_89, 8 bits wide
  assign and_90_out = ~and_62_out & 8'h80;  // AND_Gate and_90, 8 bits wide
  byte_if_zero_replace_2carry byte_if_zero_replace_2carry_1 (
    .if_zero(or_18_out), .carryover(or_29_out), .carryover_2(8'h80), .candidate_1(or_20_out),
    .vanishes(byte_if_zero_replace_2carry_1_vanishes),
    .carry_1_carry(byte_if_zero_replace_2carry_1_carry_1_carry), .out_7(byte_if_zero_replace_2carry_1_out_7));  // open: carry_1, carry_2
  byte_if_zero_replace_2carry byte_if_zero_replace_2carry_2 (
    .if_zero(or_18_out), .carryover(or_29_out), .carryover_2(8'h80), .candidate_1(or_21_out),
    .carry_1(byte_if_zero_replace_2carry_1_vanishes), .carry_2(byte_if_zero_replace_2carry_1_carry_1_carry),
    .vanishes(byte_if_zero_replace_2carry_2_vanishes),
    .carry_1_carry(byte_if_zero_replace_2carry_2_carry_1_carry), .out_7(byte_if_zero_replace_2carry_2_out_7));
  byte_if_zero_replace_2carry byte_if_zero_replace_2carry_3 (
    .if_zero(or_18_out), .carryover(or_29_out), .carryover_2(8'h80), .candidate_1(or_22_out),
    .carry_1(byte_if_zero_replace_2carry_2_vanishes), .carry_2(byte_if_zero_replace_2carry_2_carry_1_carry),
    .vanishes(byte_if_zero_replace_2carry_3_vanishes),
    .carry_1_carry(byte_if_zero_replace_2carry_3_carry_1_carry), .out_7(byte_if_zero_replace_2carry_3_out_7));
  byte_if_zero_replace_2carry byte_if_zero_replace_2carry_4 (
    .if_zero(or_18_out), .carryover(or_29_out), .carryover_2(8'h80), .candidate_1(or_23_out),
    .carry_1(byte_if_zero_replace_2carry_3_vanishes), .carry_2(byte_if_zero_replace_2carry_3_carry_1_carry),
    .vanishes(byte_if_zero_replace_2carry_4_vanishes),
    .carry_1_carry(byte_if_zero_replace_2carry_4_carry_1_carry), .out_7(byte_if_zero_replace_2carry_4_out_7));
  byte_if_zero_replace_2carry byte_if_zero_replace_2carry_5 (
    .if_zero(or_18_out), .carryover(or_29_out), .carryover_2(8'h80), .candidate_1(or_24_out),
    .carry_1(byte_if_zero_replace_2carry_4_vanishes), .carry_2(byte_if_zero_replace_2carry_4_carry_1_carry),
    .vanishes(byte_if_zero_replace_2carry_5_vanishes),
    .carry_1_carry(byte_if_zero_replace_2carry_5_carry_1_carry), .out_7(byte_if_zero_replace_2carry_5_out_7));
  byte_if_zero_replace_2carry byte_if_zero_replace_2carry_6 (
    .if_zero(or_18_out), .carryover(or_29_out), .carryover_2(8'h80), .candidate_1(or_25_out),
    .carry_1(byte_if_zero_replace_2carry_5_vanishes), .carry_2(byte_if_zero_replace_2carry_5_carry_1_carry),
    .vanishes(byte_if_zero_replace_2carry_6_vanishes),
    .carry_1_carry(byte_if_zero_replace_2carry_6_carry_1_carry), .out_7(byte_if_zero_replace_2carry_6_out_7));
  byte_if_zero_replace_2carry byte_if_zero_replace_2carry_7 (
    .if_zero(or_18_out), .carryover(or_29_out), .carryover_2(8'h80), .candidate_1(or_26_out),
    .carry_1(byte_if_zero_replace_2carry_6_vanishes), .carry_2(byte_if_zero_replace_2carry_6_carry_1_carry),
    .vanishes(byte_if_zero_replace_2carry_7_vanishes),
    .carry_1_carry(byte_if_zero_replace_2carry_7_carry_1_carry), .out_7(byte_if_zero_replace_2carry_7_out_7));
  byte_if_zero_replace_2carry byte_if_zero_replace_2carry_8 (
    .if_zero(or_18_out), .carryover(or_29_out), .carryover_2(8'h80), .candidate_1(or_27_out),
    .carry_1(byte_if_zero_replace_2carry_7_vanishes), .carry_2(byte_if_zero_replace_2carry_7_carry_1_carry),
    .vanishes(byte_if_zero_replace_2carry_8_vanishes),
    .carry_1_carry(byte_if_zero_replace_2carry_8_carry_1_carry), .out_7(byte_if_zero_replace_2carry_8_out_7));
  byte_if_zero_replace_2carry byte_if_zero_replace_2carry_9 (
    .if_zero(or_18_out), .carryover(or_29_out), .carryover_2(8'h80), .candidate_1(or_28_out),
    .carry_1(byte_if_zero_replace_2carry_8_vanishes), .carry_2(byte_if_zero_replace_2carry_8_carry_1_carry),
    .vanishes(byte_if_zero_replace_2carry_9_vanishes),
    .carry_1_carry(byte_if_zero_replace_2carry_9_carry_1_carry), .out_7(byte_if_zero_replace_2carry_9_out_7));
  byte_if_zero_replace_2carry byte_if_zero_replace_2carry_10 (
    .if_zero(or_18_out), .carryover(or_29_out), .carryover_2(8'h80), .candidate_1(and_88_out),
    .carry_1(byte_if_zero_replace_2carry_9_vanishes), .carry_2(byte_if_zero_replace_2carry_9_carry_1_carry),
    .vanishes(byte_if_zero_replace_2carry_10_vanishes),
    .carry_1_carry(byte_if_zero_replace_2carry_10_carry_1_carry), .out_7(byte_if_zero_replace_2carry_10_out_7));
  byte_if_zero_replace_2carry byte_if_zero_replace_2carry_11 (
    .if_zero(or_18_out), .carryover(or_29_out), .carryover_2(8'h80), .candidate_1({8{1'b0}}),
    .carry_1(byte_if_zero_replace_2carry_10_vanishes),
    .carry_2(byte_if_zero_replace_2carry_10_carry_1_carry),
    .vanishes(byte_if_zero_replace_2carry_11_vanishes),
    .carry_1_carry(byte_if_zero_replace_2carry_11_carry_1_carry), .out_7(byte_if_zero_replace_2carry_11_out_7));
  byte_if_zero_replace_2carry byte_if_zero_replace_2carry_12 (
    .if_zero(or_18_out), .carryover(or_29_out), .carryover_2(8'h80), .candidate_1({8{1'b0}}),
    .carry_1(byte_if_zero_replace_2carry_11_vanishes),
    .carry_2(byte_if_zero_replace_2carry_11_carry_1_carry), .out_7(byte_if_zero_replace_2carry_12_out_7));  // open: vanishes, carry_1_carry
  assign or_29_out = and_89_out | and_90_out;  // OR_Gate or_29, 8 bits wide
  byte_gate byte_gate_1 (.in_2(byte_if_zero_replace_2carry_5_out_7), .in_1(and_4_out[6]), .out_3(byte_gate_1_out_3));
  byte_gate byte_gate_2 (.in_2(byte_if_zero_replace_2carry_6_out_7), .in_1(and_4_out[7]), .out_3(byte_gate_2_out_3));
  byte_gate byte_gate_3 (.in_2(byte_if_zero_replace_2carry_7_out_7), .in_1(and_4_out[8]), .out_3(byte_gate_3_out_3));
  byte_gate byte_gate_4 (.in_2(byte_if_zero_replace_2carry_8_out_7), .in_1(and_4_out[9]), .out_3(byte_gate_4_out_3));
  byte_gate byte_gate_5 (.in_2(byte_if_zero_replace_2carry_9_out_7), .in_1(and_4_out[10]), .out_3(byte_gate_5_out_3));
  byte_gate byte_gate_6 (.in_2(byte_if_zero_replace_2carry_10_out_7), .in_1(and_4_out[11]), .out_3(byte_gate_6_out_3));
  byte_gate byte_gate_7 (.in_2(byte_if_zero_replace_2carry_11_out_7), .in_1(and_4_out[12]), .out_3(byte_gate_7_out_3));
  byte_gate byte_gate_8 (.in_2(byte_if_zero_replace_2carry_12_out_7), .in_1(and_4_out[13]), .out_3(byte_gate_8_out_3));
  or or_30 (or_30_out, and_4_out[14], and_4_out[15]);
  byte_gate byte_gate_9 (.in_2(8'h80), .in_1(or_30_out), .out_3(byte_gate_9_out_3));
  byte_gate byte_gate_10 (.in_2(or_10_out), .in_1(and_4_out[0]), .out_3(byte_gate_10_out_3));
  byte_gate byte_gate_11 (.in_2(or_19_out), .in_1(and_4_out[1]), .out_3(byte_gate_11_out_3));
  byte_gate byte_gate_12 (.in_2(byte_if_zero_replace_2carry_1_out_7), .in_1(and_4_out[2]), .out_3(byte_gate_12_out_3));
  byte_gate byte_gate_13 (.in_2(byte_if_zero_replace_2carry_2_out_7), .in_1(and_4_out[3]), .out_3(byte_gate_13_out_3));
  byte_gate byte_gate_14 (.in_2(byte_if_zero_replace_2carry_3_out_7), .in_1(and_4_out[4]), .out_3(byte_gate_14_out_3));
  byte_gate byte_gate_15 (.in_2(byte_if_zero_replace_2carry_4_out_7), .in_1(and_4_out[5]), .out_3(byte_gate_15_out_3));
  assign ascii_out = byte_gate_10_out_3 | byte_gate_11_out_3 | byte_gate_12_out_3 | byte_gate_13_out_3 | byte_gate_14_out_3 | byte_gate_15_out_3 | byte_gate_1_out_3 | byte_gate_2_out_3 | byte_gate_3_out_3 | byte_gate_4_out_3 | byte_gate_5_out_3 | byte_gate_6_out_3 | byte_gate_7_out_3 | byte_gate_8_out_3 | byte_gate_9_out_3;  // OR_Gate or_31, 8 bits wide
endmodule

module hex_digits_ascii (
  input  [15:0] in_1,
  output [7:0] out_2,
  output [7:0] out_3,
  output [7:0] out_4,
  output [7:0] out_5
);

  wire comparator_1_gt, comparator_2_gt, comparator_3_gt, comparator_4_gt;
  wire [7:0] adder_1_out, adder_2_out, adder_3_out, adder_4_out, adder_5_out, adder_6_out, adder_7_out,
       adder_8_out, bit_extender_1_out, bit_extender_2_out, bit_extender_3_out, bit_extender_4_out;
  wire [15:0] divider_1_out, divider_1_rem, divider_2_out, divider_2_rem, divider_3_out, divider_3_rem,
       divider_4_rem;

  Divider #(.width(16)) divider_1 (.a(in_1), .b(16'h10), .out(divider_1_out), .rem(divider_1_rem));  // open: upper
  Divider #(.width(16)) divider_2 (
    .a(divider_1_out), .b(16'h10), .out(divider_2_out), .rem(divider_2_rem));  // open: upper
  Divider #(.width(16)) divider_3 (
    .a(divider_2_out), .b(16'h10), .out(divider_3_out), .rem(divider_3_rem));  // open: upper
  Divider #(.width(16)) divider_4 (.a(divider_3_out), .b(16'h10), .rem(divider_4_rem));  // open: out, upper
  Comparator #(.mode("unsigned"), .width(4)) comparator_1 (
    .a(divider_4_rem[3:0]), .b(4'b1001), .gt(comparator_1_gt));  // open: eq, lt
  assign bit_extender_1_out = {{4{1'b0}}, divider_4_rem[3:0]};  // Bit_Extender bit_extender_1
  Comparator #(.mode("unsigned"), .width(4)) comparator_2 (
    .a(divider_3_rem[3:0]), .b(4'b1001), .gt(comparator_2_gt));  // open: eq, lt
  assign bit_extender_2_out = {{4{1'b0}}, divider_3_rem[3:0]};  // Bit_Extender bit_extender_2
  Comparator #(.mode("unsigned"), .width(4)) comparator_3 (
    .a(divider_2_rem[3:0]), .b(4'b1001), .gt(comparator_3_gt));  // open: eq, lt
  assign bit_extender_3_out = {{4{1'b0}}, divider_2_rem[3:0]};  // Bit_Extender bit_extender_3
  Comparator #(.mode("unsigned"), .width(4)) comparator_4 (
    .a(divider_1_rem[3:0]), .b(4'b1001), .gt(comparator_4_gt));  // open: eq, lt
  assign bit_extender_4_out = {{4{1'b0}}, divider_1_rem[3:0]};  // Bit_Extender bit_extender_4
  Adder adder_1 (.a(8'h30), .b(bit_extender_1_out), .out(adder_1_out));  // open: cin, cout
  Multiplexer #(.width(8)) multiplexer_1 (.in0(adder_1_out), .in1(adder_2_out), .out(out_2), .sel(comparator_1_gt));
  Adder adder_2 (.a(bit_extender_1_out), .b(8'h61), .out(adder_2_out));  // open: cin, cout
  Adder adder_3 (.a(8'h30), .b(bit_extender_2_out), .out(adder_3_out));  // open: cin, cout
  Multiplexer #(.width(8)) multiplexer_2 (.in0(adder_3_out), .in1(adder_4_out), .out(out_3), .sel(comparator_2_gt));
  Adder adder_4 (.a(bit_extender_2_out), .b(8'h61), .out(adder_4_out));  // open: cin, cout
  Adder adder_5 (.a(8'h30), .b(bit_extender_3_out), .out(adder_5_out));  // open: cin, cout
  Multiplexer #(.width(8)) multiplexer_3 (.in0(adder_5_out), .in1(adder_6_out), .out(out_4), .sel(comparator_3_gt));
  Adder adder_6 (.a(bit_extender_3_out), .b(8'h61), .out(adder_6_out));  // open: cin, cout
  Adder adder_7 (.a(8'h30), .b(bit_extender_4_out), .out(adder_7_out));  // open: cin, cout
  Multiplexer #(.width(8)) multiplexer_4 (.in0(adder_7_out), .in1(adder_8_out), .out(out_5), .sel(comparator_4_gt));
  Adder adder_8 (.a(bit_extender_4_out), .b(8'h61), .out(adder_8_out));  // open: cin, cout
endmodule

module hex_digit_to_ascii (
  input  [3:0] in_1,
  output [7:0] out_2
);

  wire [7:0] adder_1_out, adder_2_out, and_1_out, and_2_out;
  wire [7:7] comparator_1_gt;

  Comparator #(.mode("unsigned"), .width(4)) comparator_1 (
    .a(in_1), .b(4'b1001), .gt(comparator_1_gt[7]));  // open: eq, lt
  Adder adder_1 (.a(8'h30), .b({4'b0000, in_1}), .out(adder_1_out));  // open: cin, cout
  Adder adder_2 (.a({4'b0000, in_1}), .b(8'h57), .out(adder_2_out));  // open: cin, cout
  assign and_1_out = ~{8{comparator_1_gt[7]}} & adder_1_out;  // AND_Gate and_1, 8 bits wide
  assign out_2 = and_1_out | and_2_out;  // OR_Gate or_1, 8 bits wide
  assign and_2_out = {8{comparator_1_gt[7]}} & adder_2_out;  // AND_Gate and_2, 8 bits wide
endmodule

module immediate_printer (
  input  [4:0] step,
  input  [15:0] value,
  output done,
  output [6:0] out_4
);

  wire [7:0] and_8_out, and_9_out, and_10_out, and_11_out, and_12_out, and_13_out, hex_digits_ascii_1_p2,
       hex_digits_ascii_1_p3, hex_digits_ascii_1_p4, hex_digits_ascii_1_p5;
  wire [7:7] and_2_out, and_3_out, and_4_out, and_5_out, and_6_out, and_7_out, or_1_out;

  // hex_digits_ascii hex_digits_ascii_1: pin names not known; wires that end beside it: value, hex_digits_ascii_1_p2, hex_digits_ascii_1_p3, hex_digits_ascii_1_p4, hex_digits_ascii_1_p5
  and and_1 (done, ~step[0], step[1], step[2], ~step[3], ~step[4]);  // AND_Gate
  and and_2 (and_2_out[7], ~step[0], ~step[1], ~step[2]);  // AND_Gate
  and and_3 (and_3_out[7], step[0], ~step[1], ~step[2]);  // AND_Gate
  and and_4 (and_4_out[7], ~step[0], step[1], ~step[2]);  // AND_Gate
  and and_5 (and_5_out[7], step[0], step[1], ~step[2]);  // AND_Gate
  and and_6 (and_6_out[7], ~step[0], ~step[1], step[2]);  // AND_Gate
  and and_7 (and_7_out[7], step[0], ~step[1], step[2]);  // AND_Gate
  assign and_8_out = {8{and_2_out[7]}} & 8'h30;  // AND_Gate and_8, 8 bits wide
  assign and_9_out = {8{and_3_out[7]}} & 8'h78;  // AND_Gate and_9, 8 bits wide
  assign and_10_out = {8{and_4_out[7]}} & hex_digits_ascii_1_p2;  // AND_Gate and_10, 8 bits wide
  assign and_11_out = {8{and_5_out[7]}} & hex_digits_ascii_1_p3;  // AND_Gate and_11, 8 bits wide
  assign and_12_out = {8{and_6_out[7]}} & hex_digits_ascii_1_p4;  // AND_Gate and_12, 8 bits wide
  assign and_13_out = {8{and_7_out[7]}} & hex_digits_ascii_1_p5;  // AND_Gate and_13, 8 bits wide
  assign {or_1_out[7], out_4} = and_8_out | and_9_out | and_10_out | and_11_out | and_12_out | and_13_out;  // OR_Gate or_1, 8 bits wide
endmodule

module microclock_delay (
  input  in_1,
  output out_2
);

  wire buffer_1_out, buffer_2_out, buffer_3_out, buffer_4_out, buffer_6_out, buffer_7_out, buffer_8_out,
       buffer_9_out, buffer_10_out, buffer_11_out, buffer_12_out, buffer_13_out, buffer_14_out,
       buffer_15_out, buffer_16_out, buffer_17_out, buffer_18_out, buffer_19_out, buffer_20_out,
       buffer_21_out, buffer_22_out, buffer_23_out, buffer_24_out, buffer_25_out;

  buf buffer_1 (buffer_1_out, buffer_6_out);
  buf buffer_2 (buffer_2_out, buffer_1_out);
  buf buffer_3 (buffer_3_out, buffer_14_out);
  buf buffer_4 (buffer_4_out, buffer_3_out);
  buf buffer_5 (out_2, buffer_22_out);
  buf buffer_6 (buffer_6_out, buffer_8_out);
  buf buffer_7 (buffer_7_out, buffer_9_out);
  buf buffer_8 (buffer_8_out, buffer_7_out);
  buf buffer_9 (buffer_9_out, in_1);
  buf buffer_10 (buffer_10_out, buffer_2_out);
  buf buffer_11 (buffer_11_out, buffer_12_out);
  buf buffer_12 (buffer_12_out, buffer_10_out);
  buf buffer_13 (buffer_13_out, buffer_11_out);
  buf buffer_14 (buffer_14_out, buffer_16_out);
  buf buffer_15 (buffer_15_out, buffer_17_out);
  buf buffer_16 (buffer_16_out, buffer_15_out);
  buf buffer_17 (buffer_17_out, buffer_13_out);
  buf buffer_18 (buffer_18_out, buffer_4_out);
  buf buffer_19 (buffer_19_out, buffer_20_out);
  buf buffer_20 (buffer_20_out, buffer_18_out);
  buf buffer_21 (buffer_21_out, buffer_19_out);
  buf buffer_22 (buffer_22_out, buffer_24_out);
  buf buffer_23 (buffer_23_out, buffer_25_out);
  buf buffer_24 (buffer_24_out, buffer_23_out);
  buf buffer_25 (buffer_25_out, buffer_21_out);
endmodule

module hex_digits_ascii_2 (
  input  [15:0] in_1,
  output [7:0] out_2,
  output [7:0] out_3,
  output [7:0] out_4,
  output [7:0] out_5
);

  wire comparator_1_gt, comparator_2_gt, comparator_3_gt, comparator_4_gt;
  wire [7:0] adder_1_out, adder_2_out, adder_3_out, adder_4_out, adder_5_out, adder_6_out, adder_7_out,
       adder_8_out, bit_extender_1_out, bit_extender_2_out, bit_extender_3_out, bit_extender_4_out;

  Comparator #(.mode("unsigned"), .width(4)) comparator_1 (
    .a(in_1[3:0]), .b(4'b1001), .gt(comparator_1_gt));  // open: eq, lt
  assign bit_extender_1_out = {{4{1'b0}}, in_1[3:0]};  // Bit_Extender bit_extender_1
  Comparator #(.mode("unsigned"), .width(4)) comparator_2 (
    .a(in_1[7:4]), .b(4'b1001), .gt(comparator_2_gt));  // open: eq, lt
  assign bit_extender_2_out = {{4{1'b0}}, in_1[7:4]};  // Bit_Extender bit_extender_2
  Comparator #(.mode("unsigned"), .width(4)) comparator_3 (
    .a(in_1[11:8]), .b(4'b1001), .gt(comparator_3_gt));  // open: eq, lt
  Adder adder_1 (.a(8'h30), .b(bit_extender_3_out), .out(adder_1_out));  // open: cin, cout
  assign bit_extender_3_out = {{4{1'b0}}, in_1[11:8]};  // Bit_Extender bit_extender_3
  Adder adder_2 (.a(bit_extender_3_out), .b(8'h57), .out(adder_2_out));  // open: cin, cout
  Comparator #(.mode("unsigned"), .width(4)) comparator_4 (
    .a(in_1[15:12]), .b(4'b1001), .gt(comparator_4_gt));  // open: eq, lt
  Adder adder_3 (.a(8'h30), .b(bit_extender_4_out), .out(adder_3_out));  // open: cin, cout
  assign bit_extender_4_out = {{4{1'b0}}, in_1[15:12]};  // Bit_Extender bit_extender_4
  Adder adder_4 (.a(bit_extender_4_out), .b(8'h57), .out(adder_4_out));  // open: cin, cout
  Adder adder_5 (.a(8'h30), .b(bit_extender_1_out), .out(adder_5_out));  // open: cin, cout
  Multiplexer #(.width(8)) multiplexer_1 (.in0(adder_5_out), .in1(adder_6_out), .out(out_2), .sel(comparator_1_gt));
  Adder adder_6 (.a(bit_extender_1_out), .b(8'h57), .out(adder_6_out));  // open: cin, cout
  Adder adder_7 (.a(8'h30), .b(bit_extender_2_out), .out(adder_7_out));  // open: cin, cout
  Multiplexer #(.width(8)) multiplexer_2 (.in0(adder_7_out), .in1(adder_8_out), .out(out_3), .sel(comparator_2_gt));
  Adder adder_8 (.a(bit_extender_2_out), .b(8'h57), .out(adder_8_out));  // open: cin, cout
  Multiplexer #(.width(8)) multiplexer_3 (.in0(adder_1_out), .in1(adder_2_out), .out(out_4), .sel(comparator_3_gt));
  Multiplexer #(.width(8)) multiplexer_4 (.in0(adder_3_out), .in1(adder_4_out), .out(out_5), .sel(comparator_4_gt));
endmodule

module byte_if_zero_replace (
  input  [7:0] in_1,
  input  [7:0] if_zero,
  input  [7:0] carryover,
  input  [7:0] candidate_1,
  output [7:0] out_5,
  output [7:0] out_6
);

  wire [7:0] and_1_out, and_2_out, and_3_out, and_4_out, or_1_out;

  nor nor_1 (out_6[7], candidate_1[7], candidate_1[6], candidate_1[5], candidate_1[4], candidate_1[3], candidate_1[2], candidate_1[1], candidate_1[0]);
  assign and_1_out = candidate_1 & ~{8{out_6[7]}};  // AND_Gate and_1, 8 bits wide
  assign and_2_out = if_zero & {8{out_6[7]}};  // AND_Gate and_2, 8 bits wide
  Pull_Resistor pull_resistor_1 (.node(in_1));
  assign and_3_out = carryover & in_1;  // AND_Gate and_3, 8 bits wide
  assign and_4_out = ~in_1 & or_1_out;  // AND_Gate and_4, 8 bits wide
  assign or_1_out = and_1_out | and_2_out;  // OR_Gate or_1, 8 bits wide
  assign out_5 = and_3_out | and_4_out;  // OR_Gate or_2, 8 bits wide

  assign out_6[6:0] = {7{out_6[7]}};
endmodule

module byte_gate (
  input  in_1,
  input  [7:0] in_2,
  output [7:0] out_3
);

  assign out_3 = {8{in_1}} & in_2;  // AND_Gate and_1, 8 bits wide
endmodule

module byte_if_zero_replace_2carry (
  input  [7:0] carry_1,
  input  [7:0] carry_2,
  input  [7:0] if_zero,
  input  [7:0] carryover,
  input  [7:0] carryover_2,
  input  [7:0] candidate_1,
  output [7:0] out_7,
  output [7:0] vanishes,
  output [7:0] carry_1_carry
);

  wire [7:0] and_1_out, and_2_out, and_3_out, and_4_out, and_5_out, and_6_out, or_1_out, or_2_out;

  nor nor_1 (vanishes[7], candidate_1[7], candidate_1[6], candidate_1[5], candidate_1[4], candidate_1[3], candidate_1[2], candidate_1[1], candidate_1[0]);
  assign and_1_out = candidate_1 & ~{8{vanishes[7]}};  // AND_Gate and_1, 8 bits wide
  assign and_2_out = if_zero & {8{vanishes[7]}};  // AND_Gate and_2, 8 bits wide
  Pull_Resistor pull_resistor_1 (.node(carry_1));
  assign or_1_out = and_1_out | and_2_out;  // OR_Gate or_1, 8 bits wide
  Pull_Resistor pull_resistor_2 (.node(carry_2));
  assign and_3_out = carryover & carry_1;  // AND_Gate and_3, 8 bits wide
  assign or_2_out = and_3_out | and_4_out;  // OR_Gate or_2, 8 bits wide
  assign and_4_out = ~carry_1 & or_1_out;  // AND_Gate and_4, 8 bits wide
  assign and_5_out = carryover_2 & carry_2;  // AND_Gate and_5, 8 bits wide
  assign and_6_out = ~carry_2 & or_2_out;  // AND_Gate and_6, 8 bits wide
  assign out_7 = and_5_out | and_6_out;  // OR_Gate or_3, 8 bits wide

  assign carry_1_carry = carry_1;
  assign vanishes[6:0] = {7{vanishes[7]}};
endmodule

module five_bit_subtractor (
  input  in_1,
  input  [4:0] a,
  input  [4:0] b,
  output [4:0] out_4,
  output out_5
);

  wire and_1_out, and_2_out, and_3_out, and_4_out, and_5_out, and_6_out, and_7_out, and_8_out, and_9_out,
       and_10_out, not_2_out, xor_1_out, xor_2_out, xor_3_out, xor_4_out, xor_5_out, xor_11_out, xor_12_out,
       xor_13_out, xor_14_out;
  wire [4:0] not_1_out;

  assign not_1_out = ~b;  // NOT_Gate not_1, 5 bits wide
  xor xor_1 (xor_1_out, a[0], not_1_out[0]);
  and and_1 (and_1_out, a[0], not_1_out[0]);
  xor xor_2 (xor_2_out, a[1], not_1_out[1]);
  and and_2 (and_2_out, a[1], not_1_out[1]);
  xor xor_3 (xor_3_out, a[2], not_1_out[2]);
  and and_3 (and_3_out, a[2], not_1_out[2]);
  xor xor_4 (xor_4_out, a[3], not_1_out[3]);
  and and_4 (and_4_out, a[3], not_1_out[3]);
  xor xor_5 (xor_5_out, a[4], not_1_out[4]);
  and and_5 (and_5_out, a[4], not_1_out[4]);
  Pull_Resistor pull_resistor_1 (.node(in_1));
  not not_2 (not_2_out, in_1);
  xor xor_6 (out_4[0], xor_1_out, not_2_out);
  and and_6 (and_6_out, xor_1_out, not_2_out);
  xor xor_7 (out_4[1], xor_2_out, xor_11_out);
  and and_7 (and_7_out, xor_2_out, xor_11_out);
  xor xor_8 (out_4[2], xor_3_out, xor_12_out);
  and and_8 (and_8_out, xor_3_out, xor_12_out);
  xor xor_9 (out_4[3], xor_4_out, xor_13_out);
  and and_9 (and_9_out, xor_4_out, xor_13_out);
  xor xor_10 (out_4[4], xor_5_out, xor_14_out);
  and and_10 (and_10_out, xor_5_out, xor_14_out);
  xor xor_11 (xor_11_out, and_1_out, and_6_out);
  xor xor_12 (xor_12_out, and_2_out, and_7_out);
  xor xor_13 (xor_13_out, and_3_out, and_8_out);
  xor xor_14 (xor_14_out, and_4_out, and_9_out);
  xor xor_15 (out_5, and_5_out, and_10_out);
endmodule

module register_unstacker (
  input  enable,
  input  [15:0] unstacking_mask,
  input  [3:0] id,
  input  clk,
  input  reset,
  input  active_below,
  output active_carry,
  output [15:0] control_bus_1_out,
  output [15:0] control_bus_2_out,
  output enable_carry
);

  wire bitselector_1_out, d_ff_1_q, d_ff_3_q, d_ff_4_q, or_1_out;
  wire [1:0] d_ff_2_q;

  BitSelector #(.width(16)) bitselector_1 (.in(unstacking_mask), .out(bitselector_1_out), .sel(id));
  D_Flip_Flop d_ff_1 (.D(bitselector_1_out), .clk(enable), .Q(d_ff_1_q), .reset(d_ff_3_q));  // open: Qn, preset
  and and_1 (active_carry, or_1_out, ~d_ff_3_q);  // AND_Gate
  or or_1 (or_1_out, active_below, d_ff_2_q[1]);
  Pull_Resistor pull_resistor_1 (.node(active_below));
  D_Flip_Flop d_ff_2 (.D(d_ff_2_q[1]), .clk(clk), .Q(d_ff_2_q[0]), .reset(reset));  // open: Qn, preset
  and and_2 (d_ff_2_q[1], d_ff_1_q, enable, ~active_below);  // AND_Gate
  D_Flip_Flop d_ff_3 (.D(d_ff_2_q[0]), .clk(clk), .Q(d_ff_3_q), .reset(reset));  // open: Qn, preset
  D_Flip_Flop #(.trigger("falling")) d_ff_4 (.D(d_ff_3_q), .clk(clk), .Q(d_ff_4_q), .reset(reset));  // open: Qn, preset
  Multiplexer #(.select(2), .width(16)) multiplexer_1 (
    .in0({16{1'b0}}), .in1({16{1'b0}}), .in2(16'h1004), .in3({id, 12'h24}), .out(control_bus_1_out));  // open: sel
  Multiplexer #(.select(2), .width(16)) multiplexer_2 (
    .in0({16{1'b0}}), .in1({16{1'b0}}), .in2({16{1'b0}}), .in3(16'h1010), .out(control_bus_2_out));  // open: sel

  assign enable_carry = enable;
endmodule

module unstacker_2 (
  input  enable,
  input  load_unstacking_mask,
  input  [15:0] unstacking_mask,
  input  clk,
  input  reset,
  output active,
  output [15:0] control_bus_1_out,
  output [15:0] control_bus_2_out
);

  wire and_1_out, and_2_out, button_1_out, d_ff_1_q, d_ff_2_q, or_1_out, or_2_out, or_3_out,
       register_unstacker_1_enable_carry, register_unstacker_2_active_carry,
       register_unstacker_2_enable_carry, register_unstacker_3_active_carry,
       register_unstacker_3_enable_carry, register_unstacker_4_active_carry,
       register_unstacker_4_enable_carry, register_unstacker_5_active_carry,
       register_unstacker_5_enable_carry, register_unstacker_6_active_carry,
       register_unstacker_6_enable_carry, register_unstacker_7_active_carry,
       register_unstacker_7_enable_carry, register_unstacker_8_active_carry,
       register_unstacker_8_enable_carry, register_unstacker_9_active_carry,
       register_unstacker_9_enable_carry, register_unstacker_10_active_carry,
       register_unstacker_10_enable_carry, register_unstacker_11_active_carry,
       register_unstacker_11_enable_carry, register_unstacker_12_active_carry,
       register_unstacker_12_enable_carry, register_unstacker_13_active_carry,
       register_unstacker_13_enable_carry, register_unstacker_14_active_carry,
       register_unstacker_14_enable_carry, register_unstacker_15_active_carry,
       register_unstacker_15_enable_carry, register_unstacker_16_active_carry;
  wire [15:0] or_5_out, or_6_out, or_7_out, or_8_out, or_9_out, or_10_out, or_11_out, or_12_out, or_13_out,
       or_14_out, or_15_out, or_16_out, or_17_out, or_18_out, or_19_out, or_21_out, or_22_out, or_23_out,
       or_24_out, or_25_out, or_26_out, or_27_out, or_28_out, or_29_out, or_30_out, or_31_out, or_32_out,
       or_33_out, or_34_out, or_35_out, register_1_q, register_unstacker_1_control_bus_1_out,
       register_unstacker_1_control_bus_2_out, register_unstacker_2_control_bus_1_out,
       register_unstacker_2_control_bus_2_out, register_unstacker_3_control_bus_1_out,
       register_unstacker_3_control_bus_2_out, register_unstacker_4_control_bus_1_out,
       register_unstacker_4_control_bus_2_out, register_unstacker_5_control_bus_1_out,
       register_unstacker_5_control_bus_2_out, register_unstacker_6_control_bus_1_out,
       register_unstacker_6_control_bus_2_out, register_unstacker_7_control_bus_1_out,
       register_unstacker_7_control_bus_2_out, register_unstacker_8_control_bus_1_out,
       register_unstacker_8_control_bus_2_out, register_unstacker_9_control_bus_1_out,
       register_unstacker_9_control_bus_2_out, register_unstacker_10_control_bus_1_out,
       register_unstacker_10_control_bus_2_out, register_unstacker_11_control_bus_1_out,
       register_unstacker_11_control_bus_2_out, register_unstacker_12_control_bus_1_out,
       register_unstacker_12_control_bus_2_out, register_unstacker_13_control_bus_1_out,
       register_unstacker_13_control_bus_2_out, register_unstacker_14_control_bus_1_out,
       register_unstacker_14_control_bus_2_out, register_unstacker_15_control_bus_1_out,
       register_unstacker_15_control_bus_2_out, register_unstacker_16_control_bus_1_out,
       register_unstacker_16_control_bus_2_out;

  Button button_1 (.out(button_1_out));
  Register #(.trigger("falling"), .width(16)) register_1 (
    .D(unstacking_mask), .en(load_unstacking_mask), .clk(clk), .Q(register_1_q), .clr(or_3_out));
  or or_1 (or_1_out, load_unstacking_mask, enable);
  and and_1 (and_1_out, ~or_1_out, d_ff_2_q);  // AND_Gate
  D_Flip_Flop #(.trigger("falling")) d_ff_1 (
    .D(or_2_out), .clk(clk), .Q(d_ff_1_q), .preset(enable));  // open: Qn, reset
  or or_2 (or_2_out, enable, active);
  or or_3 (or_3_out, reset, and_1_out, button_1_out);
  D_Flip_Flop d_ff_2 (.D(and_2_out), .clk(clk), .Q(d_ff_2_q));  // open: Qn, preset, reset
  and and_2 (and_2_out, ~d_ff_2_q, ~active);  // AND_Gate
  assign control_bus_2_out = register_unstacker_1_control_bus_2_out | or_5_out;  // OR_Gate or_4, 16 bits wide
  register_unstacker register_unstacker_1 (
    .unstacking_mask(register_1_q), .id(4'b0000), .clk(clk), .reset(or_3_out), .enable(d_ff_1_q),
    .active_below(register_unstacker_2_active_carry),
    .control_bus_1_out(register_unstacker_1_control_bus_1_out),
    .control_bus_2_out(register_unstacker_1_control_bus_2_out),
    .enable_carry(register_unstacker_1_enable_carry), .active_carry(active));
  assign or_5_out = register_unstacker_2_control_bus_2_out | or_6_out;  // OR_Gate or_5, 16 bits wide
  register_unstacker register_unstacker_2 (
    .unstacking_mask(register_1_q), .id(4'b0001), .clk(clk), .reset(or_3_out),
    .enable(register_unstacker_1_enable_carry), .active_below(register_unstacker_3_active_carry),
    .control_bus_1_out(register_unstacker_2_control_bus_1_out),
    .control_bus_2_out(register_unstacker_2_control_bus_2_out),
    .enable_carry(register_unstacker_2_enable_carry), .active_carry(register_unstacker_2_active_carry));
  assign or_6_out = register_unstacker_3_control_bus_2_out | or_7_out;  // OR_Gate or_6, 16 bits wide
  register_unstacker register_unstacker_3 (
    .unstacking_mask(register_1_q), .id(4'b0010), .clk(clk), .reset(or_3_out),
    .enable(register_unstacker_2_enable_carry), .active_below(register_unstacker_4_active_carry),
    .control_bus_1_out(register_unstacker_3_control_bus_1_out),
    .control_bus_2_out(register_unstacker_3_control_bus_2_out),
    .enable_carry(register_unstacker_3_enable_carry), .active_carry(register_unstacker_3_active_carry));
  assign or_7_out = register_unstacker_4_control_bus_2_out | or_8_out;  // OR_Gate or_7, 16 bits wide
  register_unstacker register_unstacker_4 (
    .unstacking_mask(register_1_q), .id(4'b0011), .clk(clk), .reset(or_3_out),
    .enable(register_unstacker_3_enable_carry), .active_below(register_unstacker_5_active_carry),
    .control_bus_1_out(register_unstacker_4_control_bus_1_out),
    .control_bus_2_out(register_unstacker_4_control_bus_2_out),
    .enable_carry(register_unstacker_4_enable_carry), .active_carry(register_unstacker_4_active_carry));
  assign or_8_out = register_unstacker_5_control_bus_2_out | or_9_out;  // OR_Gate or_8, 16 bits wide
  register_unstacker register_unstacker_5 (
    .unstacking_mask(register_1_q), .id(4'b0100), .clk(clk), .reset(or_3_out),
    .enable(register_unstacker_4_enable_carry), .active_below(register_unstacker_6_active_carry),
    .control_bus_1_out(register_unstacker_5_control_bus_1_out),
    .control_bus_2_out(register_unstacker_5_control_bus_2_out),
    .enable_carry(register_unstacker_5_enable_carry), .active_carry(register_unstacker_5_active_carry));
  assign or_9_out = register_unstacker_6_control_bus_2_out | or_10_out;  // OR_Gate or_9, 16 bits wide
  register_unstacker register_unstacker_6 (
    .unstacking_mask(register_1_q), .id(4'b0101), .clk(clk), .reset(or_3_out),
    .enable(register_unstacker_5_enable_carry), .active_below(register_unstacker_7_active_carry),
    .control_bus_1_out(register_unstacker_6_control_bus_1_out),
    .control_bus_2_out(register_unstacker_6_control_bus_2_out),
    .enable_carry(register_unstacker_6_enable_carry), .active_carry(register_unstacker_6_active_carry));
  assign or_10_out = register_unstacker_7_control_bus_2_out | or_11_out;  // OR_Gate or_10, 16 bits wide
  register_unstacker register_unstacker_7 (
    .unstacking_mask(register_1_q), .id(4'b0110), .clk(clk), .reset(or_3_out),
    .enable(register_unstacker_6_enable_carry), .active_below(register_unstacker_8_active_carry),
    .control_bus_1_out(register_unstacker_7_control_bus_1_out),
    .control_bus_2_out(register_unstacker_7_control_bus_2_out),
    .enable_carry(register_unstacker_7_enable_carry), .active_carry(register_unstacker_7_active_carry));
  assign or_11_out = register_unstacker_8_control_bus_2_out | or_12_out;  // OR_Gate or_11, 16 bits wide
  register_unstacker register_unstacker_8 (
    .unstacking_mask(register_1_q), .id(4'b0111), .clk(clk), .reset(or_3_out),
    .enable(register_unstacker_7_enable_carry), .active_below(register_unstacker_9_active_carry),
    .control_bus_1_out(register_unstacker_8_control_bus_1_out),
    .control_bus_2_out(register_unstacker_8_control_bus_2_out),
    .enable_carry(register_unstacker_8_enable_carry), .active_carry(register_unstacker_8_active_carry));
  assign or_12_out = register_unstacker_9_control_bus_2_out | or_13_out;  // OR_Gate or_12, 16 bits wide
  register_unstacker register_unstacker_9 (
    .unstacking_mask(register_1_q), .id(4'b1000), .clk(clk), .reset(or_3_out),
    .enable(register_unstacker_8_enable_carry), .active_below(register_unstacker_10_active_carry),
    .control_bus_1_out(register_unstacker_9_control_bus_1_out),
    .control_bus_2_out(register_unstacker_9_control_bus_2_out),
    .enable_carry(register_unstacker_9_enable_carry), .active_carry(register_unstacker_9_active_carry));
  assign or_13_out = register_unstacker_10_control_bus_2_out | or_14_out;  // OR_Gate or_13, 16 bits wide
  register_unstacker register_unstacker_10 (
    .unstacking_mask(register_1_q), .id(4'b1001), .clk(clk), .reset(or_3_out),
    .enable(register_unstacker_9_enable_carry), .active_below(register_unstacker_11_active_carry),
    .control_bus_1_out(register_unstacker_10_control_bus_1_out),
    .control_bus_2_out(register_unstacker_10_control_bus_2_out),
    .enable_carry(register_unstacker_10_enable_carry), .active_carry(register_unstacker_10_active_carry));
  assign or_14_out = register_unstacker_11_control_bus_2_out | or_15_out;  // OR_Gate or_14, 16 bits wide
  register_unstacker register_unstacker_11 (
    .unstacking_mask(register_1_q), .id(4'b1010), .clk(clk), .reset(or_3_out),
    .enable(register_unstacker_10_enable_carry), .active_below(register_unstacker_12_active_carry),
    .control_bus_1_out(register_unstacker_11_control_bus_1_out),
    .control_bus_2_out(register_unstacker_11_control_bus_2_out),
    .enable_carry(register_unstacker_11_enable_carry), .active_carry(register_unstacker_11_active_carry));
  assign or_15_out = register_unstacker_12_control_bus_2_out | or_16_out;  // OR_Gate or_15, 16 bits wide
  register_unstacker register_unstacker_12 (
    .unstacking_mask(register_1_q), .id(4'b1011), .clk(clk), .reset(or_3_out),
    .enable(register_unstacker_11_enable_carry), .active_below(register_unstacker_13_active_carry),
    .control_bus_1_out(register_unstacker_12_control_bus_1_out),
    .control_bus_2_out(register_unstacker_12_control_bus_2_out),
    .enable_carry(register_unstacker_12_enable_carry), .active_carry(register_unstacker_12_active_carry));
  assign or_16_out = register_unstacker_13_control_bus_2_out | or_17_out;  // OR_Gate or_16, 16 bits wide
  register_unstacker register_unstacker_13 (
    .unstacking_mask(register_1_q), .id(4'b1100), .clk(clk), .reset(or_3_out),
    .enable(register_unstacker_12_enable_carry), .active_below(register_unstacker_14_active_carry),
    .control_bus_1_out(register_unstacker_13_control_bus_1_out),
    .control_bus_2_out(register_unstacker_13_control_bus_2_out),
    .enable_carry(register_unstacker_13_enable_carry), .active_carry(register_unstacker_13_active_carry));
  assign or_17_out = register_unstacker_14_control_bus_2_out | or_18_out;  // OR_Gate or_17, 16 bits wide
  register_unstacker register_unstacker_14 (
    .unstacking_mask(register_1_q), .id(4'b1101), .clk(clk), .reset(or_3_out),
    .enable(register_unstacker_13_enable_carry), .active_below(register_unstacker_15_active_carry),
    .control_bus_1_out(register_unstacker_14_control_bus_1_out),
    .control_bus_2_out(register_unstacker_14_control_bus_2_out),
    .enable_carry(register_unstacker_14_enable_carry), .active_carry(register_unstacker_14_active_carry));
  assign or_18_out = register_unstacker_15_control_bus_2_out | or_19_out;  // OR_Gate or_18, 16 bits wide
  register_unstacker register_unstacker_15 (
    .unstacking_mask(register_1_q), .id(4'b1110), .clk(clk), .reset(or_3_out),
    .enable(register_unstacker_14_enable_carry), .active_below(register_unstacker_16_active_carry),
    .control_bus_1_out(register_unstacker_15_control_bus_1_out),
    .control_bus_2_out(register_unstacker_15_control_bus_2_out),
    .enable_carry(register_unstacker_15_enable_carry), .active_carry(register_unstacker_15_active_carry));
  assign or_19_out = register_unstacker_16_control_bus_2_out;  // OR_Gate or_19, 16 bits wide OR_Gate
  register_unstacker register_unstacker_16 (
    .unstacking_mask(register_1_q), .id(4'b1111), .clk(clk), .reset(or_3_out),
    .enable(register_unstacker_15_enable_carry), .control_bus_1_out(register_unstacker_16_control_bus_1_out),
    .control_bus_2_out(register_unstacker_16_control_bus_2_out),
    .active_carry(register_unstacker_16_active_carry));  // open: active_below, enable_carry
  assign control_bus_1_out = register_unstacker_1_control_bus_1_out | or_21_out;  // OR_Gate or_20, 16 bits wide
  assign or_21_out = register_unstacker_2_control_bus_1_out | or_22_out;  // OR_Gate or_21, 16 bits wide
  assign or_22_out = register_unstacker_3_control_bus_1_out | or_23_out;  // OR_Gate or_22, 16 bits wide
  assign or_23_out = register_unstacker_4_control_bus_1_out | or_24_out;  // OR_Gate or_23, 16 bits wide
  assign or_24_out = register_unstacker_5_control_bus_1_out | or_25_out;  // OR_Gate or_24, 16 bits wide
  assign or_25_out = register_unstacker_6_control_bus_1_out | or_26_out;  // OR_Gate or_25, 16 bits wide
  assign or_26_out = register_unstacker_7_control_bus_1_out | or_27_out;  // OR_Gate or_26, 16 bits wide
  assign or_27_out = register_unstacker_8_control_bus_1_out | or_28_out;  // OR_Gate or_27, 16 bits wide
  assign or_28_out = register_unstacker_9_control_bus_1_out | or_29_out;  // OR_Gate or_28, 16 bits wide
  assign or_29_out = register_unstacker_10_control_bus_1_out | or_30_out;  // OR_Gate or_29, 16 bits wide
  assign or_30_out = register_unstacker_11_control_bus_1_out | or_31_out;  // OR_Gate or_30, 16 bits wide
  assign or_31_out = register_unstacker_12_control_bus_1_out | or_32_out;  // OR_Gate or_31, 16 bits wide
  assign or_32_out = register_unstacker_13_control_bus_1_out | or_33_out;  // OR_Gate or_32, 16 bits wide
  assign or_33_out = register_unstacker_14_control_bus_1_out | or_34_out;  // OR_Gate or_33, 16 bits wide
  assign or_34_out = register_unstacker_15_control_bus_1_out | or_35_out;  // OR_Gate or_34, 16 bits wide
  assign or_35_out = register_unstacker_16_control_bus_1_out;  // OR_Gate or_35, 16 bits wide OR_Gate
endmodule
